// Logisim project 1bit_Full_Adder.circ as structural Verilog: 1 circuit, main circuit main
module main (
  input  Cin,
  input  Bit_A,
  input  Bit_B,
  output Sum,
  output Cout
);

  wire and_1_out, and_2_out, and_3_out, and_4_out, and_5_out, and_6_out, and_7_out;

  and and_1 (and_1_out, ~Cin, ~Bit_A, Bit_B);  // AND_Gate
  and and_2 (and_2_out, ~Cin, Bit_A, ~Bit_B);  // AND_Gate
  and and_3 (and_3_out, Cin, ~Bit_A, ~Bit_B);  // AND_Gate
  and and_4 (and_4_out, Cin, Bit_A, Bit_B);
  and and_5 (and_5_out, Cin, ~Bit_A, Bit_B);  // AND_Gate
  and and_6 (and_6_out, ~Cin, Bit_A, Bit_B);  // AND_Gate
  and and_7 (and_7_out, Cin, Bit_A, ~Bit_B);  // AND_Gate
  or or_1 (Sum, and_1_out, and_2_out, and_3_out, and_4_out);
  or or_2 (Cout, and_4_out, and_5_out, and_6_out, and_7_out);
endmodule
