// Logisim project 8bit_Full_Adder.circ as structural Verilog: 1 circuit, main circuit main
module main (
  input  Cin,
  input  Bit_8A,
  input  Bit_7A,
  input  Bit_6A,
  input  Bit_5A,
  input  Bit_4A,
  input  Bit_3A,
  input  Bit_2A,
  input  Bit_1A,
  input  Bit_8B,
  input  Bit_7B,
  input  Bit_6B,
  input  Bit_5B,
  input  Bit_4B,
  input  Bit_3B,
  input  Bit_2B,
  input  Bit_1B,
  input  Bit_8A_2,
  input  Bit_7A_2,
  input  Bit_6A_2,
  input  Bit_5A_2,
  input  Bit_4A_2,
  input  Bit_3A_2,
  input  Bit_2A_2,
  input  Bit_1A_2,
  input  Bit_8B_2,
  input  Bit_7B_2,
  input  Bit_6B_2,
  input  Bit_5B_2,
  input  Bit_4B_2,
  input  Bit_3B_2,
  input  Bit_2B_2,
  input  Bit_1B_2,
  input  in_34,
  input  Bit_8A_3,
  input  Bit_7A_3,
  input  Bit_6A_3,
  input  Bit_5A_3,
  input  Bit_4A_3,
  input  Bit_3A_3,
  input  Bit_2A_3,
  input  Bit_1A_3,
  input  Bit_8B_3,
  input  Bit_7B_3,
  input  Bit_6B_3,
  input  Bit_5B_3,
  input  Bit_4B_3,
  input  Bit_3B_3,
  input  Bit_2B_3,
  input  Bit_1B_3,
  input  Cin_2,
  output Bit_8out,
  output Bit_7out,
  output Bit_6out,
  output Bit_5out,
  output Bit_4out,
  output Bit_3out,
  output Bit_2out,
  output Bit_1out,
  output Cout,
  output Cout_2,
  output Bit_8out_2,
  output Bit_7out_2,
  output Bit_6out_2,
  output Bit_5out_2,
  output Bit_4out_2,
  output Bit_3out_2,
  output Bit_2out_2,
  output Bit_1out_2,
  output Cout_3,
  output Bit_8out_3,
  output Bit_7out_3,
  output Bit_6out_3,
  output Bit_5out_3,
  output Bit_4out_3,
  output Bit_3out_3,
  output Bit_2out_3,
  output Bit_1out_3
);

  wire adder_2_cout, adder_3_cout, adder_4_cout, adder_5_cout, adder_6_cout, adder_7_cout, adder_8_cout,
       adder_9_cout, adder_10_cout, adder_11_cout, adder_12_cout, adder_13_cout, adder_14_cout,
       adder_15_cout, and_1_out, and_2_out, and_3_out, and_4_out, and_5_out, and_6_out, and_7_out, and_8_out,
       and_9_out, and_10_out, and_11_out, and_12_out, and_13_out, and_14_out, and_15_out, and_16_out,
       and_17_out, and_18_out, and_19_out, and_20_out, and_21_out, and_22_out, and_23_out, and_24_out,
       and_25_out, and_26_out, and_27_out, and_28_out, and_29_out, and_30_out, and_31_out, and_32_out,
       and_33_out, and_34_out, and_35_out, and_36_out, and_37_out, and_38_out, and_39_out, and_40_out,
       and_41_out, and_42_out, and_43_out, and_44_out, and_45_out, and_46_out, and_47_out, and_48_out,
       and_49_out, and_50_out, and_51_out, and_52_out, and_53_out, and_54_out, and_55_out, and_56_out,
       or_2_out, or_4_out, or_6_out, or_8_out, or_10_out, or_12_out, or_14_out;

  Adder #(.width(1)) adder_1 (.a(Bit_8A_3), .b(Bit_8B_3), .out(Bit_8out_3), .cin(adder_2_cout), .cout(Cout_3));
  Adder #(.width(1)) adder_2 (.a(Bit_7A_3), .b(Bit_7B_3), .out(Bit_7out_3), .cin(adder_3_cout), .cout(adder_2_cout));
  and and_1 (and_1_out, ~Cin, ~Bit_1A, Bit_1B);  // AND_Gate
  and and_2 (and_2_out, ~Cin, Bit_1A, ~Bit_1B);  // AND_Gate
  and and_3 (and_3_out, Cin, ~Bit_1A, ~Bit_1B);  // AND_Gate
  and and_4 (and_4_out, Cin, Bit_1A, Bit_1B);
  and and_5 (and_5_out, Cin, ~Bit_1A, Bit_1B);  // AND_Gate
  and and_6 (and_6_out, ~Cin, Bit_1A, Bit_1B);  // AND_Gate
  and and_7 (and_7_out, Cin, Bit_1A, ~Bit_1B);  // AND_Gate
  and and_8 (and_8_out, ~or_2_out, ~Bit_2A, Bit_2B);  // AND_Gate
  and and_9 (and_9_out, ~or_2_out, Bit_2A, ~Bit_2B);  // AND_Gate
  and and_10 (and_10_out, or_2_out, ~Bit_2A, ~Bit_2B);  // AND_Gate
  and and_11 (and_11_out, or_2_out, Bit_2A, Bit_2B);
  and and_12 (and_12_out, or_2_out, ~Bit_2A, Bit_2B);  // AND_Gate
  and and_13 (and_13_out, ~or_2_out, Bit_2A, Bit_2B);  // AND_Gate
  and and_14 (and_14_out, or_2_out, Bit_2A, ~Bit_2B);  // AND_Gate
  and and_15 (and_15_out, ~or_4_out, ~Bit_3A, Bit_3B);  // AND_Gate
  and and_16 (and_16_out, ~or_4_out, Bit_3A, ~Bit_3B);  // AND_Gate
  and and_17 (and_17_out, or_4_out, ~Bit_3A, ~Bit_3B);  // AND_Gate
  and and_18 (and_18_out, or_4_out, Bit_3A, Bit_3B);
  and and_19 (and_19_out, or_4_out, ~Bit_3A, Bit_3B);  // AND_Gate
  and and_20 (and_20_out, ~or_4_out, Bit_3A, Bit_3B);  // AND_Gate
  and and_21 (and_21_out, or_4_out, Bit_3A, ~Bit_3B);  // AND_Gate
  and and_22 (and_22_out, ~or_6_out, ~Bit_4A, Bit_4B);  // AND_Gate
  and and_23 (and_23_out, ~or_6_out, Bit_4A, ~Bit_4B);  // AND_Gate
  and and_24 (and_24_out, or_6_out, ~Bit_4A, ~Bit_4B);  // AND_Gate
  and and_25 (and_25_out, or_6_out, Bit_4A, Bit_4B);
  and and_26 (and_26_out, or_6_out, ~Bit_4A, Bit_4B);  // AND_Gate
  and and_27 (and_27_out, ~or_6_out, Bit_4A, Bit_4B);  // AND_Gate
  and and_28 (and_28_out, or_6_out, Bit_4A, ~Bit_4B);  // AND_Gate
  Adder #(.width(1)) adder_3 (.a(Bit_6A_3), .b(Bit_6B_3), .out(Bit_6out_3), .cin(adder_4_cout), .cout(adder_3_cout));
  or or_1 (Bit_1out, and_1_out, and_2_out, and_3_out, and_4_out);
  or or_2 (or_2_out, and_4_out, and_5_out, and_6_out, and_7_out);
  or or_3 (Bit_2out, and_8_out, and_9_out, and_10_out, and_11_out);
  or or_4 (or_4_out, and_11_out, and_12_out, and_13_out, and_14_out);
  or or_5 (Bit_3out, and_15_out, and_16_out, and_17_out, and_18_out);
  or or_6 (or_6_out, and_18_out, and_19_out, and_20_out, and_21_out);
  or or_7 (Bit_4out, and_22_out, and_23_out, and_24_out, and_25_out);
  or or_8 (or_8_out, and_25_out, and_26_out, and_27_out, and_28_out);
  Adder #(.width(1)) adder_4 (.a(Bit_5A_3), .b(Bit_5B_3), .out(Bit_5out_3), .cin(adder_5_cout), .cout(adder_4_cout));
  Adder #(.width(1)) adder_5 (.a(Bit_4A_3), .b(Bit_4B_3), .out(Bit_4out_3), .cin(adder_6_cout), .cout(adder_5_cout));
  and and_29 (and_29_out, ~or_8_out, ~Bit_5A, Bit_5B);  // AND_Gate
  and and_30 (and_30_out, ~or_8_out, Bit_5A, ~Bit_5B);  // AND_Gate
  and and_31 (and_31_out, or_8_out, ~Bit_5A, ~Bit_5B);  // AND_Gate
  and and_32 (and_32_out, or_8_out, Bit_5A, Bit_5B);
  and and_33 (and_33_out, or_8_out, ~Bit_5A, Bit_5B);  // AND_Gate
  and and_34 (and_34_out, ~or_8_out, Bit_5A, Bit_5B);  // AND_Gate
  and and_35 (and_35_out, or_8_out, Bit_5A, ~Bit_5B);  // AND_Gate
  and and_36 (and_36_out, ~or_10_out, ~Bit_6A, Bit_6B);  // AND_Gate
  and and_37 (and_37_out, ~or_10_out, Bit_6A, ~Bit_6B);  // AND_Gate
  and and_38 (and_38_out, or_10_out, ~Bit_6A, ~Bit_6B);  // AND_Gate
  and and_39 (and_39_out, or_10_out, Bit_6A, Bit_6B);
  and and_40 (and_40_out, or_10_out, ~Bit_6A, Bit_6B);  // AND_Gate
  and and_41 (and_41_out, ~or_10_out, Bit_6A, Bit_6B);  // AND_Gate
  and and_42 (and_42_out, or_10_out, Bit_6A, ~Bit_6B);  // AND_Gate
  and and_43 (and_43_out, or_12_out, Bit_7A, ~Bit_7B);  // AND_Gate
  Adder #(.width(1)) adder_6 (.a(Bit_3A_3), .b(Bit_3B_3), .out(Bit_3out_3), .cin(adder_7_cout), .cout(adder_6_cout));
  and and_44 (and_44_out, ~or_12_out, ~Bit_7A, Bit_7B);  // AND_Gate
  and and_45 (and_45_out, ~or_12_out, Bit_7A, ~Bit_7B);  // AND_Gate
  and and_46 (and_46_out, or_12_out, ~Bit_7A, ~Bit_7B);  // AND_Gate
  and and_47 (and_47_out, or_12_out, Bit_7A, Bit_7B);
  and and_48 (and_48_out, or_12_out, ~Bit_7A, Bit_7B);  // AND_Gate
  and and_49 (and_49_out, ~or_12_out, Bit_7A, Bit_7B);  // AND_Gate
  and and_50 (and_50_out, ~or_14_out, ~Bit_8A, Bit_8B);  // AND_Gate
  and and_51 (and_51_out, ~or_14_out, Bit_8A, ~Bit_8B);  // AND_Gate
  and and_52 (and_52_out, or_14_out, ~Bit_8A, ~Bit_8B);  // AND_Gate
  and and_53 (and_53_out, or_14_out, Bit_8A, Bit_8B);
  and and_54 (and_54_out, or_14_out, ~Bit_8A, Bit_8B);  // AND_Gate
  and and_55 (and_55_out, ~or_14_out, Bit_8A, Bit_8B);  // AND_Gate
  and and_56 (and_56_out, or_14_out, Bit_8A, ~Bit_8B);  // AND_Gate
  Adder #(.width(1)) adder_7 (.a(Bit_2A_3), .b(Bit_2B_3), .out(Bit_2out_3), .cin(adder_8_cout), .cout(adder_7_cout));
  or or_9 (Bit_5out, and_29_out, and_30_out, and_31_out, and_32_out);
  or or_10 (or_10_out, and_32_out, and_33_out, and_34_out, and_35_out);
  or or_11 (Bit_6out, and_36_out, and_37_out, and_38_out, and_39_out);
  or or_12 (or_12_out, and_39_out, and_40_out, and_41_out, and_42_out);
  or or_13 (Bit_7out, and_44_out, and_45_out, and_46_out, and_47_out);
  or or_14 (or_14_out, and_47_out, and_48_out, and_49_out, and_43_out);
  or or_15 (Bit_8out, and_50_out, and_51_out, and_52_out, and_53_out);
  or or_16 (Cout, and_53_out, and_54_out, and_55_out, and_56_out);
  Adder #(.width(1)) adder_8 (.a(Bit_1A_3), .b(Bit_1B_3), .out(Bit_1out_3), .cin(Cin_2), .cout(adder_8_cout));
  Adder #(.width(1)) adder_9 (.a(Bit_1A_2), .b(Bit_1B_2), .out(Bit_1out_2), .cin(in_34), .cout(adder_9_cout));
  Adder #(.width(1)) adder_10 (.a(Bit_2A_2), .b(Bit_2B_2), .out(Bit_2out_2), .cin(adder_9_cout), .cout(adder_10_cout));
  Adder #(.width(1)) adder_11 (.a(Bit_3A_2), .b(Bit_3B_2), .out(Bit_3out_2), .cin(adder_10_cout), .cout(adder_11_cout));
  Adder #(.width(1)) adder_12 (.a(Bit_4A_2), .b(Bit_4B_2), .out(Bit_4out_2), .cin(adder_11_cout), .cout(adder_12_cout));
  Adder #(.width(1)) adder_13 (.a(Bit_5A_2), .b(Bit_5B_2), .out(Bit_5out_2), .cin(adder_12_cout), .cout(adder_13_cout));
  Adder #(.width(1)) adder_14 (.a(Bit_6A_2), .b(Bit_6B_2), .out(Bit_6out_2), .cin(adder_13_cout), .cout(adder_14_cout));
  Adder #(.width(1)) adder_15 (.a(Bit_7A_2), .b(Bit_7B_2), .out(Bit_7out_2), .cin(adder_14_cout), .cout(adder_15_cout));
  Adder #(.width(1)) adder_16 (.a(Bit_8A_2), .b(Bit_8B_2), .out(Bit_8out_2), .cin(adder_15_cout), .cout(Cout_2));
endmodule
