// Logisim project full_arithmatic_with_decoder_selector _ORIGINAL.circ as structural Verilog: 3 circuits, main circuit main
module main (
  input  in_1,
  input  in_2,
  input  in_3,
  input  in_4,
  input  in_5,
  input  in_6,
  input  in_7,
  input  in_8,
  input  in_9,
  input  in_10,
  input  in_11,
  input  in_12,
  input  in_13,
  input  in_14,
  input  in_15,
  input  in_16,
  input  in_17,
  input  in_18,
  input  in_19,
  output out_20,
  output out_21,
  output out_22,
  output out_23,
  output out_24,
  output out_25,
  output out_26,
  output out_27,
  output out_28,
  output out_29,
  output out_30,
  output out_31,
  output out_32,
  output out_33,
  output out_34
);

  wire adder_2_cout, adder_3_cout, adder_4_cout, adder_5_cout, adder_6_cout, adder_7_cout, adder_8_cout,
       and_1_out, and_2_out, and_3_out, and_4_out, and_5_out, and_6_out, and_7_out, and_8_out, and_9_out,
       and_10_out, and_11_out, and_12_out, and_13_out, and_14_out, and_15_out, and_16_out,
       arithmaticselector_1_out_4, or_1_out, or_2_out, or_3_out, or_4_out, or_5_out, or_6_out, or_7_out,
       or_8_out;

  ArithmaticSelector arithmaticselector_1 (
    .in_1(in_1), .in_2(in_2), .in_3(in_3), .out_4(arithmaticselector_1_out_4), .out_5(out_20),
    .out_6(out_21), .out_7(out_22), .out_8(out_23), .out_9(out_24), .out_10(out_25));
  AddSubtract addsubtract_1 ();  // open: Cout, Sub, Ain, Bin, out, Cin
  and and_1 (and_1_out, in_12, ~arithmaticselector_1_out_4);  // AND_Gate
  and and_2 (and_2_out, arithmaticselector_1_out_4, ~in_12);  // AND_Gate
  or or_1 (or_1_out, and_2_out, and_1_out);
  Adder #(.width(1)) adder_1 (.a(in_4), .b(or_1_out), .out(out_27), .cin(adder_2_cout), .cout(out_26));
  and and_3 (and_3_out, in_13, ~arithmaticselector_1_out_4);  // AND_Gate
  and and_4 (and_4_out, arithmaticselector_1_out_4, ~in_13);  // AND_Gate
  or or_2 (or_2_out, and_4_out, and_3_out);
  Adder #(.width(1)) adder_2 (.a(in_5), .b(or_2_out), .out(out_28), .cin(adder_3_cout), .cout(adder_2_cout));
  and and_5 (and_5_out, arithmaticselector_1_out_4, ~in_14);  // AND_Gate
  and and_6 (and_6_out, in_14, ~arithmaticselector_1_out_4);  // AND_Gate
  or or_3 (or_3_out, and_5_out, and_6_out);
  Adder #(.width(1)) adder_3 (.a(in_6), .b(or_3_out), .out(out_29), .cin(adder_4_cout), .cout(adder_3_cout));
  and and_7 (and_7_out, in_15, ~arithmaticselector_1_out_4);  // AND_Gate
  and and_8 (and_8_out, arithmaticselector_1_out_4, ~in_15);  // AND_Gate
  or or_4 (or_4_out, and_8_out, and_7_out);
  Adder #(.width(1)) adder_4 (.a(in_7), .b(or_4_out), .out(out_30), .cin(adder_5_cout), .cout(adder_4_cout));
  and and_9 (and_9_out, arithmaticselector_1_out_4, ~in_16);  // AND_Gate
  and and_10 (and_10_out, in_16, ~arithmaticselector_1_out_4);  // AND_Gate
  or or_5 (or_5_out, and_9_out, and_10_out);
  Adder #(.width(1)) adder_5 (.a(in_8), .b(or_5_out), .out(out_31), .cin(adder_6_cout), .cout(adder_5_cout));
  and and_11 (and_11_out, in_17, ~arithmaticselector_1_out_4);  // AND_Gate
  and and_12 (and_12_out, arithmaticselector_1_out_4, ~in_17);  // AND_Gate
  or or_6 (or_6_out, and_12_out, and_11_out);
  Adder #(.width(1)) adder_6 (.a(in_9), .b(or_6_out), .out(out_32), .cin(adder_7_cout), .cout(adder_6_cout));
  and and_13 (and_13_out, arithmaticselector_1_out_4, ~in_18);  // AND_Gate
  and and_14 (and_14_out, in_18, ~arithmaticselector_1_out_4);  // AND_Gate
  or or_7 (or_7_out, and_13_out, and_14_out);
  Adder #(.width(1)) adder_7 (.a(in_10), .b(or_7_out), .out(out_33), .cin(adder_8_cout), .cout(adder_7_cout));
  and and_15 (and_15_out, in_19, ~arithmaticselector_1_out_4);  // AND_Gate
  and and_16 (and_16_out, arithmaticselector_1_out_4, ~in_19);  // AND_Gate
  or or_8 (or_8_out, and_16_out, and_15_out);
  Adder #(.width(1)) adder_8 (
    .a(in_11), .b(or_8_out), .out(out_34), .cin(arithmaticselector_1_out_4), .cout(adder_8_cout));

  // Notes on the sheet:
  //   000 == Addition
  //   001 == Subtraction
  //   011 == Division
  //   100 == Modulus
  //   101 == Equal To
  //   111 == Less Than
  //   010 == Multiplication
  //   110 == Greater Than
endmodule

module ArithmaticSelector (
  input  in_1,
  input  in_2,
  input  in_3,
  output out_4,
  output out_5,
  output out_6,
  output out_7,
  output out_8,
  output out_9,
  output out_10
);

  wire and_1_out, and_2_out;

  and and_1 (and_1_out, ~in_1, ~in_2, ~in_3);  // AND_Gate
  and and_2 (and_2_out, ~in_1, ~in_2, in_3);  // AND_Gate
  or or_1 (out_4, ~and_1_out, and_2_out);  // OR_Gate
  and and_3 (out_6, ~in_1, in_2, in_3);  // AND_Gate
  and and_4 (out_5, ~in_1, in_2, ~in_3);  // AND_Gate
  and and_5 (out_7, in_1, ~in_2, ~in_3);  // AND_Gate
  and and_6 (out_9, in_1, in_2, ~in_3);  // AND_Gate
  and and_7 (out_8, in_1, ~in_2, in_3);  // AND_Gate
  and and_8 (out_10, in_1, in_2, in_3);

  // Notes on the sheet:
  //   000 == Addition
  //   011 == Division
  //   100 == Modulus
  //   101 == Equal To
  //   001 == Subtraction
  //   010 == Multiplication
  //   110 == Greater Than
  //   111 == Less Than
endmodule

module AddSubtract (
  input  Ain,
  input  Sub,
  input  Bin,
  output Cin,
  output Cout,
  output out
);

  wire and_1_out, and_2_out, or_1_out;

  and and_1 (and_1_out, Sub, ~Bin);  // AND_Gate
  and and_2 (and_2_out, Bin, ~Sub);  // AND_Gate
  or or_1 (or_1_out, and_1_out, and_2_out);
  Adder #(.width(1)) adder_1 (.a(Ain), .b(or_1_out), .out(out), .cin(Cin), .cout(Cout));
endmodule
