// Logisim project full_arithmatic_with_decoder_selector.circ as structural Verilog: 6 circuits, main circuit main
module main (
  input  [3:0] in_1,
  input  [7:0] Ain,
  input  [7:0] Bin,
  output out_4,
  output out_5,
  output out_6,
  output out_7,
  output out_8,
  output out_9,
  output out_10,
  output out_11,
  output out_12,
  output out_13,
  output out_14,
  output out_15,
  output out_16,
  output out_17,
  output out_18,
  output [7:0] out
);

  wire addsubtractselector_1_out_3, n3bit_arithmaticselector_1_out_16, n3bit_arithmaticselector_1_out_17;

  _8bit_AddSubtract u_8bit_addsubtract_1 (
    .Cout(out_18), .Sub(addsubtractselector_1_out_3), .Ain(Ain), .Bin(Bin), .out_5(out));
  AddSubtractSelector addsubtractselector_1 (
    .in_1(n3bit_arithmaticselector_1_out_16), .in_2(n3bit_arithmaticselector_1_out_17),
    .out_3(addsubtractselector_1_out_3));
  _3bit_ArithmaticSelector u_3bit_arithmaticselector_1 (
    .in_1(in_1), .out_2(out_4), .out_3(out_5), .out_4(out_6), .out_5(out_7), .out_6(out_8), .out_7(out_9),
    .out_8(out_10), .out_9(out_11), .out_10(out_12), .out_11(out_13), .out_12(out_14), .out_13(out_15),
    .out_14(out_16), .out_15(out_17), .out_16(n3bit_arithmaticselector_1_out_16),
    .out_17(n3bit_arithmaticselector_1_out_17));

  // Notes on the sheet:
  //   0000 == Addition
  //   0001 == Subtraction
  //   0010 == Multiplication
  //   0011 == Division
  //   0100 == Modulus
  //   0101 == Equal To
  //   0110 == Greater Than
  //   0111 == Less Than
  //   1000 == FREE
  //   1001 == FREE
  //   1010 == FREE
  //   1011 == FREE
  //   1100 == FREE
  //   1101 == FREE
  //   1110 == FREE
  //   1111 == FREE
endmodule

module _3bit_ArithmaticSelector (
  input  [3:0] in_1,
  output out_2,
  output out_3,
  output out_4,
  output out_5,
  output out_6,
  output out_7,
  output out_8,
  output out_9,
  output out_10,
  output out_11,
  output out_12,
  output out_13,
  output out_14,
  output out_15,
  output out_16,
  output out_17
);

  and and_1 (out_2, in_1[3], in_1[2], in_1[1], in_1[0]);
  and and_2 (out_3, in_1[3], in_1[2], in_1[1], ~in_1[0]);  // AND_Gate
  and and_3 (out_5, in_1[3], in_1[2], ~in_1[1], ~in_1[0]);  // AND_Gate
  and and_4 (out_4, in_1[3], in_1[2], ~in_1[1], in_1[0]);  // AND_Gate
  and and_5 (out_6, in_1[3], ~in_1[2], in_1[1], in_1[0]);  // AND_Gate
  and and_6 (out_8, in_1[3], ~in_1[2], ~in_1[1], in_1[0]);  // AND_Gate
  and and_7 (out_7, in_1[3], ~in_1[2], in_1[1], ~in_1[0]);  // AND_Gate
  and and_8 (out_9, in_1[3], ~in_1[2], ~in_1[1], ~in_1[0]);  // AND_Gate
  and and_9 (out_11, ~in_1[3], in_1[2], in_1[1], ~in_1[0]);  // AND_Gate
  and and_10 (out_10, ~in_1[3], in_1[2], in_1[1], in_1[0]);  // AND_Gate
  and and_11 (out_12, ~in_1[3], in_1[2], ~in_1[1], in_1[0]);  // AND_Gate
  and and_12 (out_13, ~in_1[3], in_1[2], ~in_1[1], ~in_1[0]);  // AND_Gate
  and and_13 (out_14, ~in_1[3], ~in_1[2], in_1[1], in_1[0]);  // AND_Gate
  and and_14 (out_15, ~in_1[3], ~in_1[2], in_1[1], ~in_1[0]);  // AND_Gate
  and and_15 (out_16, ~in_1[3], ~in_1[2], ~in_1[1], in_1[0]);  // AND_Gate
  and and_16 (out_17, ~in_1[3], ~in_1[2], ~in_1[1], ~in_1[0]);  // AND_Gate

  // Notes on the sheet:
  //   0000 == Addition
  //   0001 == Subtraction
  //   0010 == Multiplication
  //   0011 == Division
  //   0100 == Modulus
  //   0101 == Equal To
  //   0110 == Greater Than
  //   0111 == Less Than
  //   1000 == FREE
  //   1001 == FREE
  //   1010 == FREE
  //   1011 == FREE
  //   1100 == FREE
  //   1101 == FREE
  //   1110 == FREE
  //   1111 == FREE
endmodule

module _1bit_AddSubtract (
  input  Ain,
  input  Sub,
  input  Bin,
  input  Cin,
  output Cout,
  output out
);

  wire and_1_out, and_2_out, or_1_out;

  and and_1 (and_1_out, Bin, ~Sub);  // AND_Gate
  and and_2 (and_2_out, Sub, ~Bin);  // AND_Gate
  or or_1 (or_1_out, and_2_out, and_1_out);
  Adder #(.width(1)) adder_1 (.a(Ain), .b(or_1_out), .out(out), .cin(Cin), .cout(Cout));
endmodule

module _8bit_AddSubtract (
  input  [7:0] Ain,
  input  [7:0] Bin,
  input  Sub,
  output Cout,
  output [7:0] out_5
);

  wire n1bit_addsubtract_2_cout, n1bit_addsubtract_3_cout, n1bit_addsubtract_4_cout,
       n1bit_addsubtract_5_cout, n1bit_addsubtract_6_cout, n1bit_addsubtract_7_cout, n1bit_addsubtract_8_cout;

  _1bit_AddSubtract u_1bit_addsubtract_1 (
    .Cout(Cout), .Sub(Sub), .Ain(Ain[7]), .Bin(Bin[7]), .out(out_5[7]), .Cin(n1bit_addsubtract_2_cout));
  _1bit_AddSubtract u_1bit_addsubtract_2 (
    .Cout(n1bit_addsubtract_2_cout), .Sub(Sub), .Ain(Ain[6]), .Bin(Bin[6]), .out(out_5[6]),
    .Cin(n1bit_addsubtract_3_cout));
  _1bit_AddSubtract u_1bit_addsubtract_3 (
    .Cout(n1bit_addsubtract_3_cout), .Sub(Sub), .Ain(Ain[5]), .Bin(Bin[5]), .out(out_5[5]),
    .Cin(n1bit_addsubtract_4_cout));
  _1bit_AddSubtract u_1bit_addsubtract_4 (
    .Cout(n1bit_addsubtract_4_cout), .Sub(Sub), .Ain(Ain[4]), .Bin(Bin[4]), .out(out_5[4]),
    .Cin(n1bit_addsubtract_5_cout));
  _1bit_AddSubtract u_1bit_addsubtract_5 (
    .Cout(n1bit_addsubtract_5_cout), .Sub(Sub), .Ain(Ain[3]), .Bin(Bin[3]), .out(out_5[3]),
    .Cin(n1bit_addsubtract_6_cout));
  _1bit_AddSubtract u_1bit_addsubtract_6 (
    .Cout(n1bit_addsubtract_6_cout), .Sub(Sub), .Ain(Ain[2]), .Bin(Bin[2]), .out(out_5[2]),
    .Cin(n1bit_addsubtract_7_cout));
  _1bit_AddSubtract u_1bit_addsubtract_7 (
    .Cout(n1bit_addsubtract_7_cout), .Sub(Sub), .Ain(Ain[1]), .Bin(Bin[1]), .out(out_5[1]),
    .Cin(n1bit_addsubtract_8_cout));
  _1bit_AddSubtract u_1bit_addsubtract_8 (
    .Cout(n1bit_addsubtract_8_cout), .Sub(Sub), .Ain(Ain[0]), .Bin(Bin[0]), .out(out_5[0]), .Cin(Sub));
endmodule

module _8bit_EqualTo (
  input  [7:0] in_1,
  input  [7:0] in_2,
  output out_3
);

  wire [7:0] xnor_1_out;

  assign xnor_1_out = ~(in_1 ^ in_2);  // XNOR_Gate xnor_1, 8 bits wide
  and and_1 (out_3, xnor_1_out[7], xnor_1_out[6], xnor_1_out[5], xnor_1_out[4], xnor_1_out[3], xnor_1_out[2], xnor_1_out[1], xnor_1_out[0]);
endmodule

module AddSubtractSelector (
  input  in_1,
  input  in_2,
  output out_3
);

  and and_1 (out_3, in_1, ~in_2);  // AND_Gate
endmodule
