// Logisim project gated-d-latch.circ as structural Verilog: 1 circuit, main circuit main
module main (
  input  Input,
  input  Write_Enable__WE,
  output Stored_Data,
  output out_4
);

  wire nand_1_out, nand_2_out;

  nand nand_1 (nand_1_out, Input, Write_Enable__WE);
  nand nand_2 (nand_2_out, Write_Enable__WE, ~Input);  // NAND_Gate
  nand nand_3 (Stored_Data, nand_1_out, out_4);
  nand nand_4 (out_4, Stored_Data, nand_2_out);
endmodule
