// Logisim project not_nor_or_nand_and.circ as structural Verilog: 1 circuit, main circuit main
module main (
  input  Input,
  input  Input_2,
  input  Input_3,
  input  A,
  input  A_2,
  input  in_6,
  input  B,
  input  B_2,
  input  A_3,
  input  _1in,
  input  _2in,
  input  _1in_2,
  input  _2in_2,
  input  _1in_3,
  input  _2in_3,
  input  _3in,
  input  A_4,
  input  _3in_2,
  input  A_5,
  input  A_6,
  input  B_3,
  input  _3in_3,
  input  B_4,
  input  B_5,
  input  C,
  input  Input_4,
  input  A_7,
  input  A_8,
  output _1out,
  output _1out_2,
  output _1out_3,
  output _1out_4,
  output _1out_5,
  output _1out_6,
  output _1out_7,
  output _1out_8
);

  wire transistor_6_out, transistor_7_out, transistor_12_out, transistor_15_out, transistor_18_out,
       transistor_23_out, transistor_24_out, transistor_29_out, transistor_32_out, transistor_33_out;

  Transistor transistor_1 (.in(Input_3), .out(_1out), .gate(A_3));
  Transistor #(.\type ("n")) transistor_2 (.in(1'b0), .out(_1out), .gate(A_3));
  Transistor transistor_3 (.in(_1in), .out(_1out_4), .gate(A_4));
  Transistor transistor_4 (.in(_2in), .out(_1out_4), .gate(B_3));
  Transistor #(.\type ("n")) transistor_5 (.in(transistor_6_out), .out(_1out_4), .gate(A_4));
  Transistor #(.\type ("n")) transistor_6 (.in(1'b0), .out(transistor_6_out), .gate(B_3));
  Transistor transistor_7 (.in(Input_4), .out(transistor_7_out), .gate(A_8));
  Transistor transistor_8 (.in(A_8), .out(_1out_7), .gate(Input_4));
  Transistor #(.\type ("n")) transistor_9 (.in(1'b0), .out(transistor_7_out), .gate(A_8));
  Transistor #(.\type ("n")) transistor_10 (.in(1'b0), .out(_1out_2), .gate(B_2));
  Transistor #(.\type ("n")) transistor_11 (.in(transistor_7_out), .out(_1out_7), .gate(Input_4));
  Transistor transistor_12 (.in(Input_2), .out(transistor_12_out), .gate(A_2));
  Transistor transistor_13 (.in(transistor_12_out), .out(_1out_2), .gate(B_2));
  Transistor #(.\type ("n")) transistor_14 (.in(1'b0), .out(_1out_2), .gate(A_2));
  Transistor transistor_15 (.in(_1in_2), .out(transistor_15_out), .gate(A_5));
  Transistor transistor_16 (.in(_2in_2), .out(transistor_15_out), .gate(B_4));
  Transistor #(.\type ("n")) transistor_17 (.in(transistor_18_out), .out(transistor_15_out), .gate(A_5));
  Transistor #(.\type ("n")) transistor_18 (.in(1'b0), .out(transistor_18_out), .gate(B_4));
  Transistor transistor_19 (.in(_3in_2), .out(_1out_5), .gate(transistor_15_out));
  Transistor #(.\type ("n")) transistor_20 (.in(1'b0), .out(_1out_5), .gate(transistor_15_out));
  Transistor transistor_21 (.in(1'b1), .out(_1out_8), .gate(A_7));
  Transistor #(.\type ("n")) transistor_22 (.in(1'b0), .out(_1out_8), .gate(A_7));
  Transistor transistor_23 (.in(Input), .out(transistor_23_out), .gate(A));
  Transistor transistor_24 (.in(transistor_23_out), .out(transistor_24_out), .gate(B));
  Transistor #(.\type ("n")) transistor_25 (.in(1'b0), .out(transistor_24_out), .gate(B));
  Transistor transistor_26 (.in(in_6), .out(_1out_3), .gate(transistor_24_out));
  Transistor #(.\type ("n")) transistor_27 (.in(1'b0), .out(_1out_3), .gate(transistor_24_out));
  Transistor #(.\type ("n")) transistor_28 (.in(1'b0), .out(transistor_24_out), .gate(A));
  Transistor transistor_29 (.in(_2in_3), .out(transistor_29_out), .gate(B_5));
  Transistor transistor_30 (.in(_1in_3), .out(transistor_29_out), .gate(A_6));
  Transistor #(.\type ("n")) transistor_31 (.in(transistor_32_out), .out(transistor_29_out), .gate(A_6));
  Transistor #(.\type ("n")) transistor_32 (.in(transistor_33_out), .out(transistor_32_out), .gate(B_5));
  Transistor #(.\type ("n")) transistor_33 (.in(1'b0), .out(transistor_33_out), .gate(C));
  Transistor transistor_34 (.in(_3in), .out(transistor_29_out), .gate(C));
  Transistor transistor_35 (.in(_3in_3), .out(_1out_6), .gate(transistor_29_out));
  Transistor #(.\type ("n")) transistor_36 (.in(1'b0), .out(_1out_6), .gate(transistor_29_out));

  // Notes on the sheet:
  //   NOT Logic Gate
  //   NAND Logic Gate
  //   Custom Double-NOT Inverter
  //   NOR Logic Gate
  //   AND Logic Gate
  //   OR Logic Gate
  //   3bit AND Logic Gate
endmodule
