// Logisim project project_adder_subtracter.circ as structural Verilog: 1 circuit, main circuit main
module main (
  input  B32,
  input  B31,
  input  B30,
  input  B29,
  input  B28,
  input  B24,
  input  B20,
  input  B27,
  input  B26,
  input  B25,
  input  B23,
  input  B22,
  input  B21,
  input  B19,
  input  B18,
  input  B17,
  input  Subtract_Enable,
  input  A32,
  input  A31,
  input  A30,
  input  A29,
  input  A28,
  input  A24,
  input  A20,
  input  A27,
  input  A26,
  input  A25,
  input  A23,
  input  A22,
  input  A21,
  input  A19,
  input  A18,
  input  A17,
  input  B16,
  input  B15,
  input  B14,
  input  B13,
  input  B12,
  input  B8,
  input  B4,
  input  B11,
  input  B10,
  input  B9,
  input  B7,
  input  B6,
  input  B5,
  input  B3,
  input  B2,
  input  B1,
  input  A16,
  input  A15,
  input  A14,
  input  A13,
  input  A12,
  input  A8,
  input  A4,
  input  A11,
  input  A10,
  input  A9,
  input  A7,
  input  A6,
  input  A5,
  input  A3,
  input  A2,
  input  A1,
  output SUM32,
  output SUM31,
  output SUM30,
  output SUM29,
  output SUM28,
  output SUM27,
  output SUM26,
  output SUM25,
  output SUM24,
  output SUM23,
  output SUM22,
  output SUM21,
  output SUM20,
  output SUM19,
  output SUM18,
  output SUM17,
  output SUM16,
  output SUM15,
  output SUM14,
  output SUM13,
  output SUM12,
  output SUM11,
  output SUM10,
  output SUM8,
  output SUM8_2,
  output SUM7,
  output SUM6,
  output SUM5,
  output SUM4,
  output SUM3,
  output SUM2,
  output SUM1,
  output Final_Carry_Discarded
);

  wire and_1_out, and_2_out, and_3_out, and_4_out, and_5_out, and_6_out, and_7_out, and_8_out, and_9_out,
       and_10_out, and_11_out, and_12_out, and_13_out, and_14_out, and_15_out, and_16_out, and_17_out,
       and_18_out, and_19_out, and_20_out, and_21_out, and_22_out, and_23_out, and_24_out, and_25_out,
       and_26_out, and_27_out, and_28_out, and_29_out, and_30_out, and_31_out, and_32_out, and_33_out,
       and_34_out, and_35_out, and_36_out, and_37_out, and_38_out, and_39_out, and_40_out, and_41_out,
       and_42_out, and_43_out, and_44_out, and_45_out, and_46_out, and_47_out, and_48_out, and_49_out,
       and_50_out, and_51_out, and_52_out, and_53_out, and_54_out, and_55_out, and_56_out, and_57_out,
       and_58_out, and_59_out, and_60_out, and_61_out, and_62_out, and_63_out, and_64_out, and_65_out,
       and_66_out, and_67_out, and_68_out, and_69_out, and_70_out, and_71_out, and_72_out, and_73_out,
       and_74_out, and_75_out, and_76_out, and_77_out, and_78_out, and_79_out, and_80_out, and_81_out,
       and_82_out, and_83_out, and_84_out, and_85_out, and_86_out, and_87_out, and_88_out, and_89_out,
       and_90_out, and_91_out, and_92_out, and_93_out, and_94_out, and_95_out, and_96_out, and_97_out,
       and_98_out, and_99_out, and_100_out, and_101_out, and_102_out, and_103_out, and_104_out, and_105_out,
       and_106_out, and_107_out, and_108_out, and_109_out, and_110_out, and_111_out, and_112_out,
       and_113_out, and_114_out, and_115_out, and_116_out, and_117_out, and_118_out, and_119_out,
       and_120_out, and_121_out, and_122_out, and_123_out, and_124_out, and_125_out, and_126_out,
       and_127_out, and_128_out, and_129_out, and_130_out, and_131_out, and_132_out, and_133_out,
       and_134_out, and_135_out, and_136_out, and_137_out, and_138_out, and_139_out, and_140_out,
       and_141_out, and_142_out, and_143_out, and_144_out, and_145_out, and_146_out, and_147_out,
       and_148_out, and_149_out, and_150_out, and_151_out, and_152_out, and_153_out, and_154_out,
       and_155_out, and_156_out, and_157_out, and_158_out, and_159_out, and_160_out, and_161_out,
       and_162_out, and_163_out, and_164_out, and_165_out, and_166_out, and_167_out, and_168_out,
       and_169_out, and_170_out, and_171_out, and_172_out, and_173_out, and_174_out, and_175_out,
       and_176_out, and_177_out, and_178_out, and_179_out, and_180_out, and_181_out, and_182_out,
       and_183_out, and_184_out, and_185_out, and_186_out, and_187_out, and_188_out, and_189_out,
       and_190_out, and_191_out, and_192_out, and_193_out, and_194_out, and_195_out, and_196_out,
       and_197_out, and_198_out, and_199_out, and_200_out, and_201_out, and_202_out, and_203_out,
       and_204_out, and_205_out, and_206_out, and_207_out, and_208_out, and_209_out, and_210_out,
       and_211_out, and_212_out, and_213_out, and_214_out, and_215_out, and_216_out, and_217_out,
       and_218_out, and_219_out, and_220_out, and_221_out, and_222_out, and_223_out, and_224_out, or_4_out,
       or_6_out, or_8_out, or_10_out, or_12_out, or_14_out, or_16_out, or_18_out, or_20_out, or_22_out,
       or_24_out, or_26_out, or_28_out, or_30_out, or_32_out, or_34_out, or_36_out, or_38_out, or_40_out,
       or_42_out, or_44_out, or_46_out, or_48_out, or_50_out, or_52_out, or_54_out, or_56_out, or_58_out,
       or_60_out, or_62_out, or_64_out, transistor_1_out, transistor_2_out, transistor_3_out,
       transistor_6_out, transistor_7_out, transistor_9_out, transistor_12_out, transistor_13_out,
       transistor_17_out, transistor_18_out, transistor_21_out, transistor_22_out, transistor_23_out,
       transistor_24_out, transistor_27_out, transistor_30_out, transistor_33_out, transistor_34_out,
       transistor_37_out, transistor_38_out, transistor_39_out, transistor_42_out, transistor_45_out,
       transistor_46_out, transistor_49_out, transistor_50_out, transistor_53_out, transistor_54_out,
       transistor_56_out, transistor_57_out, transistor_61_out, transistor_62_out, transistor_65_out,
       transistor_66_out, transistor_68_out, transistor_69_out, transistor_72_out, transistor_73_out,
       transistor_77_out, transistor_78_out, transistor_81_out, transistor_82_out, transistor_84_out,
       transistor_85_out, transistor_88_out, transistor_89_out, transistor_92_out, transistor_93_out,
       transistor_96_out, transistor_97_out, transistor_100_out, transistor_101_out, transistor_104_out,
       transistor_105_out, transistor_108_out, transistor_109_out, transistor_113_out, transistor_114_out,
       transistor_116_out, transistor_117_out, transistor_119_out, transistor_120_out, transistor_124_out,
       transistor_125_out, transistor_128_out, transistor_129_out, transistor_131_out, transistor_134_out,
       transistor_135_out, transistor_137_out, transistor_140_out, transistor_141_out, transistor_145_out,
       transistor_146_out, transistor_149_out, transistor_150_out, transistor_151_out, transistor_152_out,
       transistor_155_out, transistor_158_out, transistor_161_out, transistor_162_out, transistor_165_out,
       transistor_166_out, transistor_167_out, transistor_170_out, transistor_173_out, transistor_174_out,
       transistor_177_out, transistor_178_out, transistor_181_out, transistor_182_out, transistor_184_out,
       transistor_185_out, transistor_189_out, transistor_190_out, transistor_193_out, transistor_194_out,
       transistor_196_out, transistor_197_out, transistor_200_out, transistor_201_out, transistor_205_out,
       transistor_206_out, transistor_209_out, transistor_210_out, transistor_212_out, transistor_213_out,
       transistor_216_out, transistor_217_out, transistor_220_out, transistor_221_out, transistor_224_out,
       transistor_225_out, transistor_228_out, transistor_229_out, transistor_232_out, transistor_233_out,
       transistor_236_out, transistor_237_out, transistor_241_out, transistor_242_out, transistor_244_out,
       transistor_245_out, transistor_247_out, transistor_248_out, transistor_252_out, transistor_253_out;

  Transistor transistor_1 (.in(Subtract_Enable), .out(transistor_1_out), .gate(B16));
  Transistor #(.\type ("n")) transistor_2 (.in(1'b0), .out(transistor_2_out), .gate(Subtract_Enable));
  Transistor transistor_3 (.in(Subtract_Enable), .out(transistor_3_out), .gate(B32));
  Transistor transistor_4 (.in(B16), .out(transistor_2_out), .gate(Subtract_Enable));
  Transistor #(.\type ("n")) transistor_5 (.in(transistor_2_out), .out(transistor_1_out), .gate(B16));
  Transistor transistor_6 (.in(A16), .out(transistor_6_out), .gate(Subtract_Enable));
  Transistor transistor_7 (.in(Subtract_Enable), .out(transistor_7_out), .gate(A16));
  Transistor #(.\type ("n")) transistor_8 (.in(1'b0), .out(transistor_6_out), .gate(Subtract_Enable));
  Transistor transistor_9 (.in(B32), .out(transistor_9_out), .gate(Subtract_Enable));
  Transistor #(.\type ("n")) transistor_10 (.in(transistor_9_out), .out(transistor_3_out), .gate(B32));
  Transistor #(.\type ("n")) transistor_11 (.in(1'b0), .out(transistor_9_out), .gate(Subtract_Enable));
  Transistor transistor_12 (.in(Subtract_Enable), .out(transistor_12_out), .gate(A32));
  Transistor #(.\type ("n")) transistor_13 (.in(1'b0), .out(transistor_13_out), .gate(Subtract_Enable));
  Transistor #(.\type ("n")) transistor_14 (.in(transistor_6_out), .out(transistor_7_out), .gate(A16));
  Transistor transistor_15 (.in(A32), .out(transistor_13_out), .gate(Subtract_Enable));
  Transistor #(.\type ("n")) transistor_16 (.in(transistor_13_out), .out(transistor_12_out), .gate(A32));
  Transistor transistor_17 (.in(Subtract_Enable), .out(transistor_17_out), .gate(B15));
  and and_1 (and_1_out, ~or_6_out, ~transistor_12_out, transistor_3_out);  // AND_Gate
  and and_2 (and_2_out, ~or_6_out, transistor_12_out, ~transistor_3_out);  // AND_Gate
  and and_3 (and_3_out, or_6_out, ~transistor_12_out, ~transistor_3_out);  // AND_Gate
  and and_4 (and_4_out, or_6_out, transistor_12_out, transistor_3_out);
  and and_5 (and_5_out, or_6_out, ~transistor_12_out, transistor_3_out);  // AND_Gate
  and and_6 (and_6_out, ~or_6_out, transistor_12_out, transistor_3_out);  // AND_Gate
  and and_7 (and_7_out, or_6_out, transistor_12_out, ~transistor_3_out);  // AND_Gate
  and and_8 (and_8_out, ~or_8_out, ~transistor_7_out, transistor_1_out);  // AND_Gate
  and and_9 (and_9_out, ~or_8_out, transistor_7_out, ~transistor_1_out);  // AND_Gate
  and and_10 (and_10_out, or_8_out, ~transistor_7_out, ~transistor_1_out);  // AND_Gate
  and and_11 (and_11_out, or_8_out, transistor_7_out, transistor_1_out);
  and and_12 (and_12_out, or_8_out, ~transistor_7_out, transistor_1_out);  // AND_Gate
  and and_13 (and_13_out, ~or_8_out, transistor_7_out, transistor_1_out);  // AND_Gate
  and and_14 (and_14_out, or_8_out, transistor_7_out, ~transistor_1_out);  // AND_Gate
  Transistor transistor_18 (.in(B15), .out(transistor_18_out), .gate(Subtract_Enable));
  Transistor #(.\type ("n")) transistor_19 (.in(transistor_18_out), .out(transistor_17_out), .gate(B15));
  Transistor #(.\type ("n")) transistor_20 (.in(1'b0), .out(transistor_18_out), .gate(Subtract_Enable));
  Transistor transistor_21 (.in(Subtract_Enable), .out(transistor_21_out), .gate(A15));
  Transistor #(.\type ("n")) transistor_22 (.in(1'b0), .out(transistor_22_out), .gate(Subtract_Enable));
  or or_1 (SUM32, and_1_out, and_2_out, and_3_out, and_4_out);
  or or_2 (Final_Carry_Discarded, and_4_out, and_5_out, and_6_out, and_7_out);
  or or_3 (SUM16, and_8_out, and_9_out, and_10_out, and_11_out);
  or or_4 (or_4_out, and_11_out, and_12_out, and_13_out, and_14_out);
  Transistor transistor_23 (.in(B31), .out(transistor_23_out), .gate(Subtract_Enable));
  Transistor #(.\type ("n")) transistor_24 (.in(transistor_23_out), .out(transistor_24_out), .gate(B31));
  Transistor transistor_25 (.in(Subtract_Enable), .out(transistor_24_out), .gate(B31));
  Transistor #(.\type ("n")) transistor_26 (.in(1'b0), .out(transistor_23_out), .gate(Subtract_Enable));
  Transistor transistor_27 (.in(Subtract_Enable), .out(transistor_27_out), .gate(A31));
  Transistor transistor_28 (.in(A15), .out(transistor_22_out), .gate(Subtract_Enable));
  Transistor #(.\type ("n")) transistor_29 (.in(transistor_22_out), .out(transistor_21_out), .gate(A15));
  Transistor transistor_30 (.in(A31), .out(transistor_30_out), .gate(Subtract_Enable));
  Transistor #(.\type ("n")) transistor_31 (.in(transistor_30_out), .out(transistor_27_out), .gate(A31));
  Transistor #(.\type ("n")) transistor_32 (.in(1'b0), .out(transistor_30_out), .gate(Subtract_Enable));
  and and_15 (and_15_out, ~or_10_out, ~transistor_27_out, transistor_24_out);  // AND_Gate
  and and_16 (and_16_out, ~or_10_out, transistor_27_out, ~transistor_24_out);  // AND_Gate
  and and_17 (and_17_out, or_10_out, ~transistor_27_out, ~transistor_24_out);  // AND_Gate
  and and_18 (and_18_out, or_10_out, transistor_27_out, transistor_24_out);
  and and_19 (and_19_out, or_10_out, ~transistor_27_out, transistor_24_out);  // AND_Gate
  and and_20 (and_20_out, ~or_10_out, transistor_27_out, transistor_24_out);  // AND_Gate
  and and_21 (and_21_out, or_10_out, transistor_27_out, ~transistor_24_out);  // AND_Gate
  and and_22 (and_22_out, ~or_12_out, ~transistor_21_out, transistor_17_out);  // AND_Gate
  and and_23 (and_23_out, ~or_12_out, transistor_21_out, ~transistor_17_out);  // AND_Gate
  and and_24 (and_24_out, or_12_out, ~transistor_21_out, ~transistor_17_out);  // AND_Gate
  and and_25 (and_25_out, or_12_out, transistor_21_out, transistor_17_out);
  and and_26 (and_26_out, or_12_out, ~transistor_21_out, transistor_17_out);  // AND_Gate
  and and_27 (and_27_out, ~or_12_out, transistor_21_out, transistor_17_out);  // AND_Gate
  and and_28 (and_28_out, or_12_out, transistor_21_out, ~transistor_17_out);  // AND_Gate
  Transistor transistor_33 (.in(B14), .out(transistor_33_out), .gate(Subtract_Enable));
  Transistor #(.\type ("n")) transistor_34 (.in(transistor_33_out), .out(transistor_34_out), .gate(B14));
  Transistor transistor_35 (.in(Subtract_Enable), .out(transistor_34_out), .gate(B14));
  Transistor #(.\type ("n")) transistor_36 (.in(1'b0), .out(transistor_33_out), .gate(Subtract_Enable));
  Transistor transistor_37 (.in(Subtract_Enable), .out(transistor_37_out), .gate(A14));
  or or_5 (SUM31, and_15_out, and_16_out, and_17_out, and_18_out);
  or or_6 (or_6_out, and_18_out, and_19_out, and_20_out, and_21_out);
  or or_7 (SUM15, and_22_out, and_23_out, and_24_out, and_25_out);
  or or_8 (or_8_out, and_25_out, and_26_out, and_27_out, and_28_out);
  Transistor transistor_38 (.in(B30), .out(transistor_38_out), .gate(Subtract_Enable));
  Transistor #(.\type ("n")) transistor_39 (.in(transistor_38_out), .out(transistor_39_out), .gate(B30));
  Transistor transistor_40 (.in(Subtract_Enable), .out(transistor_39_out), .gate(B30));
  Transistor #(.\type ("n")) transistor_41 (.in(1'b0), .out(transistor_38_out), .gate(Subtract_Enable));
  Transistor transistor_42 (.in(A14), .out(transistor_42_out), .gate(Subtract_Enable));
  Transistor #(.\type ("n")) transistor_43 (.in(transistor_42_out), .out(transistor_37_out), .gate(A14));
  Transistor #(.\type ("n")) transistor_44 (.in(1'b0), .out(transistor_42_out), .gate(Subtract_Enable));
  Transistor transistor_45 (.in(A30), .out(transistor_45_out), .gate(Subtract_Enable));
  Transistor transistor_46 (.in(Subtract_Enable), .out(transistor_46_out), .gate(A30));
  Transistor #(.\type ("n")) transistor_47 (.in(transistor_45_out), .out(transistor_46_out), .gate(A30));
  Transistor #(.\type ("n")) transistor_48 (.in(1'b0), .out(transistor_45_out), .gate(Subtract_Enable));
  and and_29 (and_29_out, ~or_14_out, ~transistor_46_out, transistor_39_out);  // AND_Gate
  and and_30 (and_30_out, ~or_14_out, transistor_46_out, ~transistor_39_out);  // AND_Gate
  and and_31 (and_31_out, or_14_out, ~transistor_46_out, ~transistor_39_out);  // AND_Gate
  and and_32 (and_32_out, or_14_out, transistor_46_out, transistor_39_out);
  and and_33 (and_33_out, or_14_out, ~transistor_46_out, transistor_39_out);  // AND_Gate
  and and_34 (and_34_out, ~or_14_out, transistor_46_out, transistor_39_out);  // AND_Gate
  and and_35 (and_35_out, or_14_out, transistor_46_out, ~transistor_39_out);  // AND_Gate
  and and_36 (and_36_out, ~or_16_out, ~transistor_37_out, transistor_34_out);  // AND_Gate
  and and_37 (and_37_out, ~or_16_out, transistor_37_out, ~transistor_34_out);  // AND_Gate
  and and_38 (and_38_out, or_16_out, ~transistor_37_out, ~transistor_34_out);  // AND_Gate
  and and_39 (and_39_out, or_16_out, transistor_37_out, transistor_34_out);
  and and_40 (and_40_out, or_16_out, ~transistor_37_out, transistor_34_out);  // AND_Gate
  and and_41 (and_41_out, ~or_16_out, transistor_37_out, transistor_34_out);  // AND_Gate
  and and_42 (and_42_out, or_16_out, transistor_37_out, ~transistor_34_out);  // AND_Gate
  Transistor transistor_49 (.in(B13), .out(transistor_49_out), .gate(Subtract_Enable));
  Transistor #(.\type ("n")) transistor_50 (.in(transistor_49_out), .out(transistor_50_out), .gate(B13));
  Transistor transistor_51 (.in(Subtract_Enable), .out(transistor_50_out), .gate(B13));
  Transistor #(.\type ("n")) transistor_52 (.in(1'b0), .out(transistor_49_out), .gate(Subtract_Enable));
  or or_9 (SUM30, and_29_out, and_30_out, and_31_out, and_32_out);
  or or_10 (or_10_out, and_32_out, and_33_out, and_34_out, and_35_out);
  or or_11 (SUM14, and_36_out, and_37_out, and_38_out, and_39_out);
  or or_12 (or_12_out, and_39_out, and_40_out, and_41_out, and_42_out);
  Transistor transistor_53 (.in(B29), .out(transistor_53_out), .gate(Subtract_Enable));
  Transistor transistor_54 (.in(Subtract_Enable), .out(transistor_54_out), .gate(B29));
  Transistor #(.\type ("n")) transistor_55 (.in(1'b0), .out(transistor_53_out), .gate(Subtract_Enable));
  Transistor transistor_56 (.in(A13), .out(transistor_56_out), .gate(Subtract_Enable));
  Transistor transistor_57 (.in(Subtract_Enable), .out(transistor_57_out), .gate(A13));
  Transistor #(.\type ("n")) transistor_58 (.in(transistor_56_out), .out(transistor_57_out), .gate(A13));
  Transistor #(.\type ("n")) transistor_59 (.in(1'b0), .out(transistor_56_out), .gate(Subtract_Enable));
  Transistor #(.\type ("n")) transistor_60 (.in(transistor_53_out), .out(transistor_54_out), .gate(B29));
  Transistor transistor_61 (.in(A29), .out(transistor_61_out), .gate(Subtract_Enable));
  Transistor transistor_62 (.in(Subtract_Enable), .out(transistor_62_out), .gate(A29));
  Transistor #(.\type ("n")) transistor_63 (.in(transistor_61_out), .out(transistor_62_out), .gate(A29));
  Transistor #(.\type ("n")) transistor_64 (.in(1'b0), .out(transistor_61_out), .gate(Subtract_Enable));
  and and_43 (and_43_out, ~or_18_out, ~transistor_62_out, transistor_54_out);  // AND_Gate
  and and_44 (and_44_out, ~or_18_out, transistor_62_out, ~transistor_54_out);  // AND_Gate
  and and_45 (and_45_out, or_18_out, ~transistor_62_out, ~transistor_54_out);  // AND_Gate
  and and_46 (and_46_out, or_18_out, transistor_62_out, transistor_54_out);
  and and_47 (and_47_out, or_18_out, ~transistor_62_out, transistor_54_out);  // AND_Gate
  and and_48 (and_48_out, ~or_18_out, transistor_62_out, transistor_54_out);  // AND_Gate
  and and_49 (and_49_out, or_18_out, transistor_62_out, ~transistor_54_out);  // AND_Gate
  and and_50 (and_50_out, ~or_20_out, ~transistor_57_out, transistor_50_out);  // AND_Gate
  and and_51 (and_51_out, ~or_20_out, transistor_57_out, ~transistor_50_out);  // AND_Gate
  and and_52 (and_52_out, or_20_out, ~transistor_57_out, ~transistor_50_out);  // AND_Gate
  and and_53 (and_53_out, or_20_out, transistor_57_out, transistor_50_out);
  and and_54 (and_54_out, or_20_out, ~transistor_57_out, transistor_50_out);  // AND_Gate
  and and_55 (and_55_out, ~or_20_out, transistor_57_out, transistor_50_out);  // AND_Gate
  and and_56 (and_56_out, or_20_out, transistor_57_out, ~transistor_50_out);  // AND_Gate
  Transistor transistor_65 (.in(B12), .out(transistor_65_out), .gate(Subtract_Enable));
  Transistor transistor_66 (.in(Subtract_Enable), .out(transistor_66_out), .gate(B12));
  Transistor #(.\type ("n")) transistor_67 (.in(1'b0), .out(transistor_65_out), .gate(Subtract_Enable));
  or or_13 (SUM29, and_43_out, and_44_out, and_45_out, and_46_out);
  or or_14 (or_14_out, and_46_out, and_47_out, and_48_out, and_49_out);
  or or_15 (SUM13, and_50_out, and_51_out, and_52_out, and_53_out);
  or or_16 (or_16_out, and_53_out, and_54_out, and_55_out, and_56_out);
  Transistor transistor_68 (.in(B28), .out(transistor_68_out), .gate(Subtract_Enable));
  Transistor transistor_69 (.in(Subtract_Enable), .out(transistor_69_out), .gate(B28));
  Transistor #(.\type ("n")) transistor_70 (.in(1'b0), .out(transistor_68_out), .gate(Subtract_Enable));
  Transistor #(.\type ("n")) transistor_71 (.in(transistor_65_out), .out(transistor_66_out), .gate(B12));
  Transistor transistor_72 (.in(A12), .out(transistor_72_out), .gate(Subtract_Enable));
  Transistor #(.\type ("n")) transistor_73 (.in(transistor_72_out), .out(transistor_73_out), .gate(A12));
  Transistor transistor_74 (.in(Subtract_Enable), .out(transistor_73_out), .gate(A12));
  Transistor #(.\type ("n")) transistor_75 (.in(1'b0), .out(transistor_72_out), .gate(Subtract_Enable));
  Transistor #(.\type ("n")) transistor_76 (.in(transistor_68_out), .out(transistor_69_out), .gate(B28));
  Transistor transistor_77 (.in(A28), .out(transistor_77_out), .gate(Subtract_Enable));
  Transistor transistor_78 (.in(Subtract_Enable), .out(transistor_78_out), .gate(A28));
  Transistor #(.\type ("n")) transistor_79 (.in(1'b0), .out(transistor_77_out), .gate(Subtract_Enable));
  and and_57 (and_57_out, ~or_22_out, ~transistor_73_out, transistor_66_out);  // AND_Gate
  and and_58 (and_58_out, ~or_22_out, transistor_73_out, ~transistor_66_out);  // AND_Gate
  and and_59 (and_59_out, or_22_out, ~transistor_73_out, ~transistor_66_out);  // AND_Gate
  and and_60 (and_60_out, or_22_out, transistor_73_out, transistor_66_out);
  and and_61 (and_61_out, or_22_out, ~transistor_73_out, transistor_66_out);  // AND_Gate
  and and_62 (and_62_out, ~or_22_out, transistor_73_out, transistor_66_out);  // AND_Gate
  and and_63 (and_63_out, or_22_out, transistor_73_out, ~transistor_66_out);  // AND_Gate
  Transistor #(.\type ("n")) transistor_80 (.in(transistor_77_out), .out(transistor_78_out), .gate(A28));
  Transistor transistor_81 (.in(B11), .out(transistor_81_out), .gate(Subtract_Enable));
  Transistor transistor_82 (.in(Subtract_Enable), .out(transistor_82_out), .gate(B11));
  Transistor #(.\type ("n")) transistor_83 (.in(1'b0), .out(transistor_81_out), .gate(Subtract_Enable));
  and and_64 (and_64_out, ~or_24_out, ~transistor_78_out, transistor_69_out);  // AND_Gate
  and and_65 (and_65_out, ~or_24_out, transistor_78_out, ~transistor_69_out);  // AND_Gate
  or or_17 (SUM28, and_64_out, and_65_out, and_66_out, and_67_out);
  and and_66 (and_66_out, or_24_out, ~transistor_78_out, ~transistor_69_out);  // AND_Gate
  and and_67 (and_67_out, or_24_out, transistor_78_out, transistor_69_out);
  and and_68 (and_68_out, or_24_out, ~transistor_78_out, transistor_69_out);  // AND_Gate
  or or_18 (or_18_out, and_67_out, and_68_out, and_69_out, and_70_out);
  and and_69 (and_69_out, ~or_24_out, transistor_78_out, transistor_69_out);  // AND_Gate
  and and_70 (and_70_out, or_24_out, transistor_78_out, ~transistor_69_out);  // AND_Gate
  or or_19 (SUM12, and_57_out, and_58_out, and_59_out, and_60_out);
  or or_20 (or_20_out, and_60_out, and_61_out, and_62_out, and_63_out);
  Transistor transistor_84 (.in(B27), .out(transistor_84_out), .gate(Subtract_Enable));
  Transistor transistor_85 (.in(Subtract_Enable), .out(transistor_85_out), .gate(B27));
  Transistor #(.\type ("n")) transistor_86 (.in(1'b0), .out(transistor_84_out), .gate(Subtract_Enable));
  Transistor #(.\type ("n")) transistor_87 (.in(transistor_81_out), .out(transistor_82_out), .gate(B11));
  Transistor transistor_88 (.in(A11), .out(transistor_88_out), .gate(Subtract_Enable));
  Transistor transistor_89 (.in(Subtract_Enable), .out(transistor_89_out), .gate(A11));
  Transistor #(.\type ("n")) transistor_90 (.in(1'b0), .out(transistor_88_out), .gate(Subtract_Enable));
  Transistor #(.\type ("n")) transistor_91 (.in(transistor_84_out), .out(transistor_85_out), .gate(B27));
  Transistor transistor_92 (.in(A27), .out(transistor_92_out), .gate(Subtract_Enable));
  Transistor transistor_93 (.in(Subtract_Enable), .out(transistor_93_out), .gate(A27));
  Transistor #(.\type ("n")) transistor_94 (.in(1'b0), .out(transistor_92_out), .gate(Subtract_Enable));
  Transistor #(.\type ("n")) transistor_95 (.in(transistor_88_out), .out(transistor_89_out), .gate(A11));
  and and_71 (and_71_out, ~or_26_out, ~transistor_89_out, transistor_82_out);  // AND_Gate
  and and_72 (and_72_out, ~or_26_out, transistor_89_out, ~transistor_82_out);  // AND_Gate
  and and_73 (and_73_out, or_26_out, ~transistor_89_out, ~transistor_82_out);  // AND_Gate
  and and_74 (and_74_out, or_26_out, transistor_89_out, transistor_82_out);
  and and_75 (and_75_out, or_26_out, ~transistor_89_out, transistor_82_out);  // AND_Gate
  and and_76 (and_76_out, ~or_26_out, transistor_89_out, transistor_82_out);  // AND_Gate
  and and_77 (and_77_out, or_26_out, transistor_89_out, ~transistor_82_out);  // AND_Gate
  Transistor transistor_96 (.in(B10), .out(transistor_96_out), .gate(Subtract_Enable));
  Transistor transistor_97 (.in(Subtract_Enable), .out(transistor_97_out), .gate(B10));
  Transistor #(.\type ("n")) transistor_98 (.in(1'b0), .out(transistor_96_out), .gate(Subtract_Enable));
  Transistor #(.\type ("n")) transistor_99 (.in(transistor_92_out), .out(transistor_93_out), .gate(A27));
  and and_78 (and_78_out, ~or_28_out, ~transistor_93_out, transistor_85_out);  // AND_Gate
  and and_79 (and_79_out, ~or_28_out, transistor_93_out, ~transistor_85_out);  // AND_Gate
  and and_80 (and_80_out, or_28_out, ~transistor_93_out, ~transistor_85_out);  // AND_Gate
  and and_81 (and_81_out, or_28_out, transistor_93_out, transistor_85_out);
  and and_82 (and_82_out, or_28_out, ~transistor_93_out, transistor_85_out);  // AND_Gate
  and and_83 (and_83_out, ~or_28_out, transistor_93_out, transistor_85_out);  // AND_Gate
  and and_84 (and_84_out, or_28_out, transistor_93_out, ~transistor_85_out);  // AND_Gate
  or or_21 (SUM11, and_71_out, and_72_out, and_73_out, and_74_out);
  or or_22 (or_22_out, and_74_out, and_75_out, and_76_out, and_77_out);
  Transistor transistor_100 (.in(B26), .out(transistor_100_out), .gate(Subtract_Enable));
  Transistor transistor_101 (.in(Subtract_Enable), .out(transistor_101_out), .gate(B26));
  Transistor #(.\type ("n")) transistor_102 (.in(1'b0), .out(transistor_100_out), .gate(Subtract_Enable));
  Transistor #(.\type ("n")) transistor_103 (.in(transistor_96_out), .out(transistor_97_out), .gate(B10));
  Transistor transistor_104 (.in(A10), .out(transistor_104_out), .gate(Subtract_Enable));
  Transistor transistor_105 (.in(Subtract_Enable), .out(transistor_105_out), .gate(A10));
  Transistor #(.\type ("n")) transistor_106 (.in(1'b0), .out(transistor_104_out), .gate(Subtract_Enable));
  or or_23 (SUM27, and_78_out, and_79_out, and_80_out, and_81_out);
  or or_24 (or_24_out, and_81_out, and_82_out, and_83_out, and_84_out);
  Transistor #(.\type ("n")) transistor_107 (.in(transistor_100_out), .out(transistor_101_out), .gate(B26));
  Transistor transistor_108 (.in(A26), .out(transistor_108_out), .gate(Subtract_Enable));
  Transistor transistor_109 (.in(Subtract_Enable), .out(transistor_109_out), .gate(A26));
  Transistor #(.\type ("n")) transistor_110 (.in(1'b0), .out(transistor_108_out), .gate(Subtract_Enable));
  Transistor #(.\type ("n")) transistor_111 (.in(transistor_104_out), .out(transistor_105_out), .gate(A10));
  Transistor #(.\type ("n")) transistor_112 (.in(transistor_108_out), .out(transistor_109_out), .gate(A26));
  Transistor transistor_113 (.in(B9), .out(transistor_113_out), .gate(Subtract_Enable));
  Transistor transistor_114 (.in(Subtract_Enable), .out(transistor_114_out), .gate(B9));
  Transistor #(.\type ("n")) transistor_115 (.in(1'b0), .out(transistor_113_out), .gate(Subtract_Enable));
  and and_85 (and_85_out, ~or_30_out, ~transistor_109_out, transistor_101_out);  // AND_Gate
  and and_86 (and_86_out, ~or_30_out, transistor_109_out, ~transistor_101_out);  // AND_Gate
  and and_87 (and_87_out, or_30_out, ~transistor_109_out, ~transistor_101_out);  // AND_Gate
  and and_88 (and_88_out, or_30_out, transistor_109_out, transistor_101_out);
  and and_89 (and_89_out, or_30_out, ~transistor_109_out, transistor_101_out);  // AND_Gate
  and and_90 (and_90_out, ~or_30_out, transistor_109_out, transistor_101_out);  // AND_Gate
  and and_91 (and_91_out, or_30_out, transistor_109_out, ~transistor_101_out);  // AND_Gate
  and and_92 (and_92_out, ~or_32_out, ~transistor_105_out, transistor_97_out);  // AND_Gate
  and and_93 (and_93_out, ~or_32_out, transistor_105_out, ~transistor_97_out);  // AND_Gate
  or or_25 (SUM10, and_92_out, and_93_out, and_94_out, and_95_out);
  and and_94 (and_94_out, or_32_out, ~transistor_105_out, ~transistor_97_out);  // AND_Gate
  and and_95 (and_95_out, or_32_out, transistor_105_out, transistor_97_out);
  and and_96 (and_96_out, or_32_out, ~transistor_105_out, transistor_97_out);  // AND_Gate
  or or_26 (or_26_out, and_95_out, and_96_out, and_97_out, and_98_out);
  and and_97 (and_97_out, ~or_32_out, transistor_105_out, transistor_97_out);  // AND_Gate
  and and_98 (and_98_out, or_32_out, transistor_105_out, ~transistor_97_out);  // AND_Gate
  Transistor transistor_116 (.in(Subtract_Enable), .out(transistor_116_out), .gate(B25));
  Transistor #(.\type ("n")) transistor_117 (.in(1'b0), .out(transistor_117_out), .gate(Subtract_Enable));
  Transistor #(.\type ("n")) transistor_118 (.in(transistor_113_out), .out(transistor_114_out), .gate(B9));
  Transistor transistor_119 (.in(A9), .out(transistor_119_out), .gate(Subtract_Enable));
  Transistor transistor_120 (.in(Subtract_Enable), .out(transistor_120_out), .gate(A9));
  Transistor #(.\type ("n")) transistor_121 (.in(1'b0), .out(transistor_119_out), .gate(Subtract_Enable));
  or or_27 (SUM26, and_85_out, and_86_out, and_87_out, and_88_out);
  or or_28 (or_28_out, and_88_out, and_89_out, and_90_out, and_91_out);
  Transistor transistor_122 (.in(B25), .out(transistor_117_out), .gate(Subtract_Enable));
  Transistor #(.\type ("n")) transistor_123 (.in(transistor_117_out), .out(transistor_116_out), .gate(B25));
  Transistor transistor_124 (.in(A25), .out(transistor_124_out), .gate(Subtract_Enable));
  Transistor transistor_125 (.in(Subtract_Enable), .out(transistor_125_out), .gate(A25));
  Transistor #(.\type ("n")) transistor_126 (.in(1'b0), .out(transistor_124_out), .gate(Subtract_Enable));
  Transistor #(.\type ("n")) transistor_127 (.in(transistor_119_out), .out(transistor_120_out), .gate(A9));
  Transistor transistor_128 (.in(Subtract_Enable), .out(transistor_128_out), .gate(B8));
  Transistor #(.\type ("n")) transistor_129 (.in(1'b0), .out(transistor_129_out), .gate(Subtract_Enable));
  Transistor #(.\type ("n")) transistor_130 (.in(transistor_124_out), .out(transistor_125_out), .gate(A25));
  and and_99 (and_99_out, ~or_34_out, ~transistor_125_out, transistor_116_out);  // AND_Gate
  and and_100 (and_100_out, ~or_34_out, transistor_125_out, ~transistor_116_out);  // AND_Gate
  and and_101 (and_101_out, or_34_out, ~transistor_125_out, ~transistor_116_out);  // AND_Gate
  and and_102 (and_102_out, or_34_out, transistor_125_out, transistor_116_out);
  and and_103 (and_103_out, or_34_out, ~transistor_125_out, transistor_116_out);  // AND_Gate
  and and_104 (and_104_out, ~or_34_out, transistor_125_out, transistor_116_out);  // AND_Gate
  and and_105 (and_105_out, or_34_out, transistor_125_out, ~transistor_116_out);  // AND_Gate
  and and_106 (and_106_out, ~or_36_out, ~transistor_120_out, transistor_114_out);  // AND_Gate
  and and_107 (and_107_out, ~or_36_out, transistor_120_out, ~transistor_114_out);  // AND_Gate
  and and_108 (and_108_out, or_36_out, ~transistor_120_out, ~transistor_114_out);  // AND_Gate
  and and_109 (and_109_out, or_36_out, transistor_120_out, transistor_114_out);
  and and_110 (and_110_out, or_36_out, ~transistor_120_out, transistor_114_out);  // AND_Gate
  and and_111 (and_111_out, ~or_36_out, transistor_120_out, transistor_114_out);  // AND_Gate
  and and_112 (and_112_out, or_36_out, transistor_120_out, ~transistor_114_out);  // AND_Gate
  Transistor transistor_131 (.in(Subtract_Enable), .out(transistor_131_out), .gate(B24));
  Transistor transistor_132 (.in(B8), .out(transistor_129_out), .gate(Subtract_Enable));
  Transistor #(.\type ("n")) transistor_133 (.in(transistor_129_out), .out(transistor_128_out), .gate(B8));
  Transistor transistor_134 (.in(A8), .out(transistor_134_out), .gate(Subtract_Enable));
  Transistor transistor_135 (.in(Subtract_Enable), .out(transistor_135_out), .gate(A8));
  Transistor #(.\type ("n")) transistor_136 (.in(1'b0), .out(transistor_134_out), .gate(Subtract_Enable));
  or or_29 (SUM25, and_99_out, and_100_out, and_101_out, and_102_out);
  or or_30 (or_30_out, and_102_out, and_103_out, and_104_out, and_105_out);
  or or_31 (SUM8, and_106_out, and_107_out, and_108_out, and_109_out);
  or or_32 (or_32_out, and_109_out, and_110_out, and_111_out, and_112_out);
  Transistor transistor_137 (.in(B24), .out(transistor_137_out), .gate(Subtract_Enable));
  Transistor #(.\type ("n")) transistor_138 (.in(transistor_137_out), .out(transistor_131_out), .gate(B24));
  Transistor #(.\type ("n")) transistor_139 (.in(1'b0), .out(transistor_137_out), .gate(Subtract_Enable));
  Transistor transistor_140 (.in(Subtract_Enable), .out(transistor_140_out), .gate(A24));
  Transistor #(.\type ("n")) transistor_141 (.in(1'b0), .out(transistor_141_out), .gate(Subtract_Enable));
  Transistor #(.\type ("n")) transistor_142 (.in(transistor_134_out), .out(transistor_135_out), .gate(A8));
  Transistor transistor_143 (.in(A24), .out(transistor_141_out), .gate(Subtract_Enable));
  Transistor #(.\type ("n")) transistor_144 (.in(transistor_141_out), .out(transistor_140_out), .gate(A24));
  Transistor transistor_145 (.in(Subtract_Enable), .out(transistor_145_out), .gate(B7));
  and and_113 (and_113_out, ~or_38_out, ~transistor_140_out, transistor_131_out);  // AND_Gate
  and and_114 (and_114_out, ~or_38_out, transistor_140_out, ~transistor_131_out);  // AND_Gate
  and and_115 (and_115_out, or_38_out, ~transistor_140_out, ~transistor_131_out);  // AND_Gate
  and and_116 (and_116_out, or_38_out, transistor_140_out, transistor_131_out);
  and and_117 (and_117_out, or_38_out, ~transistor_140_out, transistor_131_out);  // AND_Gate
  and and_118 (and_118_out, ~or_38_out, transistor_140_out, transistor_131_out);  // AND_Gate
  and and_119 (and_119_out, or_38_out, transistor_140_out, ~transistor_131_out);  // AND_Gate
  and and_120 (and_120_out, ~or_40_out, ~transistor_135_out, transistor_128_out);  // AND_Gate
  and and_121 (and_121_out, ~or_40_out, transistor_135_out, ~transistor_128_out);  // AND_Gate
  and and_122 (and_122_out, or_40_out, ~transistor_135_out, ~transistor_128_out);  // AND_Gate
  and and_123 (and_123_out, or_40_out, transistor_135_out, transistor_128_out);
  and and_124 (and_124_out, or_40_out, ~transistor_135_out, transistor_128_out);  // AND_Gate
  and and_125 (and_125_out, ~or_40_out, transistor_135_out, transistor_128_out);  // AND_Gate
  and and_126 (and_126_out, or_40_out, transistor_135_out, ~transistor_128_out);  // AND_Gate
  Transistor transistor_146 (.in(B7), .out(transistor_146_out), .gate(Subtract_Enable));
  Transistor #(.\type ("n")) transistor_147 (.in(transistor_146_out), .out(transistor_145_out), .gate(B7));
  Transistor #(.\type ("n")) transistor_148 (.in(1'b0), .out(transistor_146_out), .gate(Subtract_Enable));
  Transistor transistor_149 (.in(Subtract_Enable), .out(transistor_149_out), .gate(A7));
  Transistor #(.\type ("n")) transistor_150 (.in(1'b0), .out(transistor_150_out), .gate(Subtract_Enable));
  or or_33 (SUM24, and_113_out, and_114_out, and_115_out, and_116_out);
  or or_34 (or_34_out, and_116_out, and_117_out, and_118_out, and_119_out);
  or or_35 (SUM8_2, and_120_out, and_121_out, and_122_out, and_123_out);
  or or_36 (or_36_out, and_123_out, and_124_out, and_125_out, and_126_out);
  Transistor transistor_151 (.in(B23), .out(transistor_151_out), .gate(Subtract_Enable));
  Transistor transistor_152 (.in(Subtract_Enable), .out(transistor_152_out), .gate(B23));
  Transistor #(.\type ("n")) transistor_153 (.in(transistor_151_out), .out(transistor_152_out), .gate(B23));
  Transistor #(.\type ("n")) transistor_154 (.in(1'b0), .out(transistor_151_out), .gate(Subtract_Enable));
  Transistor transistor_155 (.in(Subtract_Enable), .out(transistor_155_out), .gate(A23));
  Transistor transistor_156 (.in(A7), .out(transistor_150_out), .gate(Subtract_Enable));
  Transistor #(.\type ("n")) transistor_157 (.in(transistor_150_out), .out(transistor_149_out), .gate(A7));
  Transistor transistor_158 (.in(A23), .out(transistor_158_out), .gate(Subtract_Enable));
  Transistor #(.\type ("n")) transistor_159 (.in(transistor_158_out), .out(transistor_155_out), .gate(A23));
  Transistor #(.\type ("n")) transistor_160 (.in(1'b0), .out(transistor_158_out), .gate(Subtract_Enable));
  and and_127 (and_127_out, ~or_42_out, ~transistor_155_out, transistor_152_out);  // AND_Gate
  and and_128 (and_128_out, ~or_42_out, transistor_155_out, ~transistor_152_out);  // AND_Gate
  and and_129 (and_129_out, or_42_out, ~transistor_155_out, ~transistor_152_out);  // AND_Gate
  and and_130 (and_130_out, or_42_out, transistor_155_out, transistor_152_out);
  and and_131 (and_131_out, or_42_out, ~transistor_155_out, transistor_152_out);  // AND_Gate
  and and_132 (and_132_out, ~or_42_out, transistor_155_out, transistor_152_out);  // AND_Gate
  and and_133 (and_133_out, or_42_out, transistor_155_out, ~transistor_152_out);  // AND_Gate
  and and_134 (and_134_out, ~or_44_out, ~transistor_149_out, transistor_145_out);  // AND_Gate
  and and_135 (and_135_out, ~or_44_out, transistor_149_out, ~transistor_145_out);  // AND_Gate
  and and_136 (and_136_out, or_44_out, ~transistor_149_out, ~transistor_145_out);  // AND_Gate
  and and_137 (and_137_out, or_44_out, transistor_149_out, transistor_145_out);
  and and_138 (and_138_out, or_44_out, ~transistor_149_out, transistor_145_out);  // AND_Gate
  and and_139 (and_139_out, ~or_44_out, transistor_149_out, transistor_145_out);  // AND_Gate
  and and_140 (and_140_out, or_44_out, transistor_149_out, ~transistor_145_out);  // AND_Gate
  Transistor transistor_161 (.in(B6), .out(transistor_161_out), .gate(Subtract_Enable));
  Transistor #(.\type ("n")) transistor_162 (.in(transistor_161_out), .out(transistor_162_out), .gate(B6));
  Transistor transistor_163 (.in(Subtract_Enable), .out(transistor_162_out), .gate(B6));
  Transistor #(.\type ("n")) transistor_164 (.in(1'b0), .out(transistor_161_out), .gate(Subtract_Enable));
  Transistor transistor_165 (.in(Subtract_Enable), .out(transistor_165_out), .gate(A6));
  or or_37 (SUM23, and_127_out, and_128_out, and_129_out, and_130_out);
  or or_38 (or_38_out, and_130_out, and_131_out, and_132_out, and_133_out);
  or or_39 (SUM7, and_134_out, and_135_out, and_136_out, and_137_out);
  or or_40 (or_40_out, and_137_out, and_138_out, and_139_out, and_140_out);
  Transistor transistor_166 (.in(B22), .out(transistor_166_out), .gate(Subtract_Enable));
  Transistor transistor_167 (.in(Subtract_Enable), .out(transistor_167_out), .gate(B22));
  Transistor #(.\type ("n")) transistor_168 (.in(transistor_166_out), .out(transistor_167_out), .gate(B22));
  Transistor #(.\type ("n")) transistor_169 (.in(1'b0), .out(transistor_166_out), .gate(Subtract_Enable));
  Transistor transistor_170 (.in(A6), .out(transistor_170_out), .gate(Subtract_Enable));
  Transistor #(.\type ("n")) transistor_171 (.in(transistor_170_out), .out(transistor_165_out), .gate(A6));
  Transistor #(.\type ("n")) transistor_172 (.in(1'b0), .out(transistor_170_out), .gate(Subtract_Enable));
  Transistor transistor_173 (.in(A22), .out(transistor_173_out), .gate(Subtract_Enable));
  Transistor transistor_174 (.in(Subtract_Enable), .out(transistor_174_out), .gate(A22));
  Transistor #(.\type ("n")) transistor_175 (.in(transistor_173_out), .out(transistor_174_out), .gate(A22));
  Transistor #(.\type ("n")) transistor_176 (.in(1'b0), .out(transistor_173_out), .gate(Subtract_Enable));
  and and_141 (and_141_out, ~or_46_out, ~transistor_174_out, transistor_167_out);  // AND_Gate
  and and_142 (and_142_out, ~or_46_out, transistor_174_out, ~transistor_167_out);  // AND_Gate
  and and_143 (and_143_out, or_46_out, ~transistor_174_out, ~transistor_167_out);  // AND_Gate
  and and_144 (and_144_out, or_46_out, transistor_174_out, transistor_167_out);
  and and_145 (and_145_out, or_46_out, ~transistor_174_out, transistor_167_out);  // AND_Gate
  and and_146 (and_146_out, ~or_46_out, transistor_174_out, transistor_167_out);  // AND_Gate
  and and_147 (and_147_out, or_46_out, transistor_174_out, ~transistor_167_out);  // AND_Gate
  and and_148 (and_148_out, ~or_48_out, ~transistor_165_out, transistor_162_out);  // AND_Gate
  and and_149 (and_149_out, ~or_48_out, transistor_165_out, ~transistor_162_out);  // AND_Gate
  and and_150 (and_150_out, or_48_out, ~transistor_165_out, ~transistor_162_out);  // AND_Gate
  and and_151 (and_151_out, or_48_out, transistor_165_out, transistor_162_out);
  and and_152 (and_152_out, or_48_out, ~transistor_165_out, transistor_162_out);  // AND_Gate
  and and_153 (and_153_out, ~or_48_out, transistor_165_out, transistor_162_out);  // AND_Gate
  and and_154 (and_154_out, or_48_out, transistor_165_out, ~transistor_162_out);  // AND_Gate
  Transistor transistor_177 (.in(B5), .out(transistor_177_out), .gate(Subtract_Enable));
  Transistor transistor_178 (.in(Subtract_Enable), .out(transistor_178_out), .gate(B5));
  Transistor #(.\type ("n")) transistor_179 (.in(transistor_177_out), .out(transistor_178_out), .gate(B5));
  Transistor #(.\type ("n")) transistor_180 (.in(1'b0), .out(transistor_177_out), .gate(Subtract_Enable));
  or or_41 (SUM22, and_141_out, and_142_out, and_143_out, and_144_out);
  or or_42 (or_42_out, and_144_out, and_145_out, and_146_out, and_147_out);
  or or_43 (SUM6, and_148_out, and_149_out, and_150_out, and_151_out);
  or or_44 (or_44_out, and_151_out, and_152_out, and_153_out, and_154_out);
  Transistor transistor_181 (.in(B21), .out(transistor_181_out), .gate(Subtract_Enable));
  Transistor transistor_182 (.in(Subtract_Enable), .out(transistor_182_out), .gate(B21));
  Transistor #(.\type ("n")) transistor_183 (.in(1'b0), .out(transistor_181_out), .gate(Subtract_Enable));
  Transistor transistor_184 (.in(A5), .out(transistor_184_out), .gate(Subtract_Enable));
  Transistor transistor_185 (.in(Subtract_Enable), .out(transistor_185_out), .gate(A5));
  Transistor #(.\type ("n")) transistor_186 (.in(transistor_184_out), .out(transistor_185_out), .gate(A5));
  Transistor #(.\type ("n")) transistor_187 (.in(1'b0), .out(transistor_184_out), .gate(Subtract_Enable));
  Transistor #(.\type ("n")) transistor_188 (.in(transistor_181_out), .out(transistor_182_out), .gate(B21));
  Transistor transistor_189 (.in(A21), .out(transistor_189_out), .gate(Subtract_Enable));
  Transistor #(.\type ("n")) transistor_190 (.in(transistor_189_out), .out(transistor_190_out), .gate(A21));
  Transistor transistor_191 (.in(Subtract_Enable), .out(transistor_190_out), .gate(A21));
  Transistor #(.\type ("n")) transistor_192 (.in(1'b0), .out(transistor_189_out), .gate(Subtract_Enable));
  and and_155 (and_155_out, ~or_50_out, ~transistor_190_out, transistor_182_out);  // AND_Gate
  and and_156 (and_156_out, ~or_50_out, transistor_190_out, ~transistor_182_out);  // AND_Gate
  and and_157 (and_157_out, or_50_out, ~transistor_190_out, ~transistor_182_out);  // AND_Gate
  and and_158 (and_158_out, or_50_out, transistor_190_out, transistor_182_out);
  and and_159 (and_159_out, or_50_out, ~transistor_190_out, transistor_182_out);  // AND_Gate
  and and_160 (and_160_out, ~or_50_out, transistor_190_out, transistor_182_out);  // AND_Gate
  and and_161 (and_161_out, or_50_out, transistor_190_out, ~transistor_182_out);  // AND_Gate
  and and_162 (and_162_out, ~or_52_out, ~transistor_185_out, transistor_178_out);  // AND_Gate
  and and_163 (and_163_out, ~or_52_out, transistor_185_out, ~transistor_178_out);  // AND_Gate
  and and_164 (and_164_out, or_52_out, ~transistor_185_out, ~transistor_178_out);  // AND_Gate
  and and_165 (and_165_out, or_52_out, transistor_185_out, transistor_178_out);
  and and_166 (and_166_out, or_52_out, ~transistor_185_out, transistor_178_out);  // AND_Gate
  and and_167 (and_167_out, ~or_52_out, transistor_185_out, transistor_178_out);  // AND_Gate
  and and_168 (and_168_out, or_52_out, transistor_185_out, ~transistor_178_out);  // AND_Gate
  Transistor transistor_193 (.in(B4), .out(transistor_193_out), .gate(Subtract_Enable));
  Transistor transistor_194 (.in(Subtract_Enable), .out(transistor_194_out), .gate(B4));
  Transistor #(.\type ("n")) transistor_195 (.in(1'b0), .out(transistor_193_out), .gate(Subtract_Enable));
  or or_45 (SUM21, and_155_out, and_156_out, and_157_out, and_158_out);
  or or_46 (or_46_out, and_158_out, and_159_out, and_160_out, and_161_out);
  or or_47 (SUM5, and_162_out, and_163_out, and_164_out, and_165_out);
  or or_48 (or_48_out, and_165_out, and_166_out, and_167_out, and_168_out);
  Transistor transistor_196 (.in(B20), .out(transistor_196_out), .gate(Subtract_Enable));
  Transistor transistor_197 (.in(Subtract_Enable), .out(transistor_197_out), .gate(B20));
  Transistor #(.\type ("n")) transistor_198 (.in(1'b0), .out(transistor_196_out), .gate(Subtract_Enable));
  Transistor #(.\type ("n")) transistor_199 (.in(transistor_193_out), .out(transistor_194_out), .gate(B4));
  Transistor transistor_200 (.in(A4), .out(transistor_200_out), .gate(Subtract_Enable));
  Transistor #(.\type ("n")) transistor_201 (.in(transistor_200_out), .out(transistor_201_out), .gate(A4));
  Transistor transistor_202 (.in(Subtract_Enable), .out(transistor_201_out), .gate(A4));
  Transistor #(.\type ("n")) transistor_203 (.in(1'b0), .out(transistor_200_out), .gate(Subtract_Enable));
  Transistor #(.\type ("n")) transistor_204 (.in(transistor_196_out), .out(transistor_197_out), .gate(B20));
  Transistor transistor_205 (.in(A20), .out(transistor_205_out), .gate(Subtract_Enable));
  Transistor transistor_206 (.in(Subtract_Enable), .out(transistor_206_out), .gate(A20));
  Transistor #(.\type ("n")) transistor_207 (.in(1'b0), .out(transistor_205_out), .gate(Subtract_Enable));
  and and_169 (and_169_out, ~or_54_out, ~transistor_201_out, transistor_194_out);  // AND_Gate
  and and_170 (and_170_out, ~or_54_out, transistor_201_out, ~transistor_194_out);  // AND_Gate
  and and_171 (and_171_out, or_54_out, ~transistor_201_out, ~transistor_194_out);  // AND_Gate
  and and_172 (and_172_out, or_54_out, transistor_201_out, transistor_194_out);
  and and_173 (and_173_out, or_54_out, ~transistor_201_out, transistor_194_out);  // AND_Gate
  and and_174 (and_174_out, ~or_54_out, transistor_201_out, transistor_194_out);  // AND_Gate
  and and_175 (and_175_out, or_54_out, transistor_201_out, ~transistor_194_out);  // AND_Gate
  Transistor #(.\type ("n")) transistor_208 (.in(transistor_205_out), .out(transistor_206_out), .gate(A20));
  Transistor transistor_209 (.in(B3), .out(transistor_209_out), .gate(Subtract_Enable));
  Transistor transistor_210 (.in(Subtract_Enable), .out(transistor_210_out), .gate(B3));
  Transistor #(.\type ("n")) transistor_211 (.in(1'b0), .out(transistor_209_out), .gate(Subtract_Enable));
  and and_176 (and_176_out, ~or_56_out, ~transistor_206_out, transistor_197_out);  // AND_Gate
  and and_177 (and_177_out, ~or_56_out, transistor_206_out, ~transistor_197_out);  // AND_Gate
  or or_49 (SUM20, and_176_out, and_177_out, and_178_out, and_179_out);
  and and_178 (and_178_out, or_56_out, ~transistor_206_out, ~transistor_197_out);  // AND_Gate
  and and_179 (and_179_out, or_56_out, transistor_206_out, transistor_197_out);
  and and_180 (and_180_out, or_56_out, ~transistor_206_out, transistor_197_out);  // AND_Gate
  or or_50 (or_50_out, and_179_out, and_180_out, and_181_out, and_182_out);
  and and_181 (and_181_out, ~or_56_out, transistor_206_out, transistor_197_out);  // AND_Gate
  and and_182 (and_182_out, or_56_out, transistor_206_out, ~transistor_197_out);  // AND_Gate
  or or_51 (SUM4, and_169_out, and_170_out, and_171_out, and_172_out);
  or or_52 (or_52_out, and_172_out, and_173_out, and_174_out, and_175_out);
  Transistor transistor_212 (.in(B19), .out(transistor_212_out), .gate(Subtract_Enable));
  Transistor transistor_213 (.in(Subtract_Enable), .out(transistor_213_out), .gate(B19));
  Transistor #(.\type ("n")) transistor_214 (.in(1'b0), .out(transistor_212_out), .gate(Subtract_Enable));
  Transistor #(.\type ("n")) transistor_215 (.in(transistor_209_out), .out(transistor_210_out), .gate(B3));
  Transistor transistor_216 (.in(A3), .out(transistor_216_out), .gate(Subtract_Enable));
  Transistor transistor_217 (.in(Subtract_Enable), .out(transistor_217_out), .gate(A3));
  Transistor #(.\type ("n")) transistor_218 (.in(1'b0), .out(transistor_216_out), .gate(Subtract_Enable));
  Transistor #(.\type ("n")) transistor_219 (.in(transistor_212_out), .out(transistor_213_out), .gate(B19));
  Transistor transistor_220 (.in(A19), .out(transistor_220_out), .gate(Subtract_Enable));
  Transistor transistor_221 (.in(Subtract_Enable), .out(transistor_221_out), .gate(A19));
  Transistor #(.\type ("n")) transistor_222 (.in(1'b0), .out(transistor_220_out), .gate(Subtract_Enable));
  Transistor #(.\type ("n")) transistor_223 (.in(transistor_216_out), .out(transistor_217_out), .gate(A3));
  and and_183 (and_183_out, ~or_58_out, ~transistor_217_out, transistor_210_out);  // AND_Gate
  and and_184 (and_184_out, ~or_58_out, transistor_217_out, ~transistor_210_out);  // AND_Gate
  and and_185 (and_185_out, or_58_out, ~transistor_217_out, ~transistor_210_out);  // AND_Gate
  and and_186 (and_186_out, or_58_out, transistor_217_out, transistor_210_out);
  and and_187 (and_187_out, or_58_out, ~transistor_217_out, transistor_210_out);  // AND_Gate
  and and_188 (and_188_out, ~or_58_out, transistor_217_out, transistor_210_out);  // AND_Gate
  and and_189 (and_189_out, or_58_out, transistor_217_out, ~transistor_210_out);  // AND_Gate
  Transistor transistor_224 (.in(B2), .out(transistor_224_out), .gate(Subtract_Enable));
  Transistor transistor_225 (.in(Subtract_Enable), .out(transistor_225_out), .gate(B2));
  Transistor #(.\type ("n")) transistor_226 (.in(1'b0), .out(transistor_224_out), .gate(Subtract_Enable));
  Transistor #(.\type ("n")) transistor_227 (.in(transistor_220_out), .out(transistor_221_out), .gate(A19));
  and and_190 (and_190_out, ~or_60_out, ~transistor_221_out, transistor_213_out);  // AND_Gate
  and and_191 (and_191_out, ~or_60_out, transistor_221_out, ~transistor_213_out);  // AND_Gate
  and and_192 (and_192_out, or_60_out, ~transistor_221_out, ~transistor_213_out);  // AND_Gate
  and and_193 (and_193_out, or_60_out, transistor_221_out, transistor_213_out);
  and and_194 (and_194_out, or_60_out, ~transistor_221_out, transistor_213_out);  // AND_Gate
  and and_195 (and_195_out, ~or_60_out, transistor_221_out, transistor_213_out);  // AND_Gate
  and and_196 (and_196_out, or_60_out, transistor_221_out, ~transistor_213_out);  // AND_Gate
  or or_53 (SUM3, and_183_out, and_184_out, and_185_out, and_186_out);
  or or_54 (or_54_out, and_186_out, and_187_out, and_188_out, and_189_out);
  Transistor transistor_228 (.in(B18), .out(transistor_228_out), .gate(Subtract_Enable));
  Transistor transistor_229 (.in(Subtract_Enable), .out(transistor_229_out), .gate(B18));
  Transistor #(.\type ("n")) transistor_230 (.in(1'b0), .out(transistor_228_out), .gate(Subtract_Enable));
  Transistor #(.\type ("n")) transistor_231 (.in(transistor_224_out), .out(transistor_225_out), .gate(B2));
  Transistor transistor_232 (.in(A2), .out(transistor_232_out), .gate(Subtract_Enable));
  Transistor transistor_233 (.in(Subtract_Enable), .out(transistor_233_out), .gate(A2));
  Transistor #(.\type ("n")) transistor_234 (.in(1'b0), .out(transistor_232_out), .gate(Subtract_Enable));
  or or_55 (SUM19, and_190_out, and_191_out, and_192_out, and_193_out);
  or or_56 (or_56_out, and_193_out, and_194_out, and_195_out, and_196_out);
  Transistor #(.\type ("n")) transistor_235 (.in(transistor_228_out), .out(transistor_229_out), .gate(B18));
  Transistor transistor_236 (.in(A18), .out(transistor_236_out), .gate(Subtract_Enable));
  Transistor transistor_237 (.in(Subtract_Enable), .out(transistor_237_out), .gate(A18));
  Transistor #(.\type ("n")) transistor_238 (.in(1'b0), .out(transistor_236_out), .gate(Subtract_Enable));
  Transistor #(.\type ("n")) transistor_239 (.in(transistor_232_out), .out(transistor_233_out), .gate(A2));
  Transistor #(.\type ("n")) transistor_240 (.in(transistor_236_out), .out(transistor_237_out), .gate(A18));
  Transistor transistor_241 (.in(B1), .out(transistor_241_out), .gate(Subtract_Enable));
  Transistor transistor_242 (.in(Subtract_Enable), .out(transistor_242_out), .gate(B1));
  Transistor #(.\type ("n")) transistor_243 (.in(1'b0), .out(transistor_241_out), .gate(Subtract_Enable));
  and and_197 (and_197_out, ~or_62_out, ~transistor_237_out, transistor_229_out);  // AND_Gate
  and and_198 (and_198_out, ~or_62_out, transistor_237_out, ~transistor_229_out);  // AND_Gate
  and and_199 (and_199_out, or_62_out, ~transistor_237_out, ~transistor_229_out);  // AND_Gate
  and and_200 (and_200_out, or_62_out, transistor_237_out, transistor_229_out);
  and and_201 (and_201_out, or_62_out, ~transistor_237_out, transistor_229_out);  // AND_Gate
  and and_202 (and_202_out, ~or_62_out, transistor_237_out, transistor_229_out);  // AND_Gate
  and and_203 (and_203_out, or_62_out, transistor_237_out, ~transistor_229_out);  // AND_Gate
  and and_204 (and_204_out, ~or_64_out, ~transistor_233_out, transistor_225_out);  // AND_Gate
  and and_205 (and_205_out, ~or_64_out, transistor_233_out, ~transistor_225_out);  // AND_Gate
  or or_57 (SUM2, and_204_out, and_205_out, and_206_out, and_207_out);
  and and_206 (and_206_out, or_64_out, ~transistor_233_out, ~transistor_225_out);  // AND_Gate
  and and_207 (and_207_out, or_64_out, transistor_233_out, transistor_225_out);
  and and_208 (and_208_out, or_64_out, ~transistor_233_out, transistor_225_out);  // AND_Gate
  or or_58 (or_58_out, and_207_out, and_208_out, and_209_out, and_210_out);
  and and_209 (and_209_out, ~or_64_out, transistor_233_out, transistor_225_out);  // AND_Gate
  and and_210 (and_210_out, or_64_out, transistor_233_out, ~transistor_225_out);  // AND_Gate
  Transistor transistor_244 (.in(Subtract_Enable), .out(transistor_244_out), .gate(B17));
  Transistor #(.\type ("n")) transistor_245 (.in(1'b0), .out(transistor_245_out), .gate(Subtract_Enable));
  Transistor #(.\type ("n")) transistor_246 (.in(transistor_241_out), .out(transistor_242_out), .gate(B1));
  Transistor transistor_247 (.in(A1), .out(transistor_247_out), .gate(Subtract_Enable));
  Transistor transistor_248 (.in(Subtract_Enable), .out(transistor_248_out), .gate(A1));
  Transistor #(.\type ("n")) transistor_249 (.in(1'b0), .out(transistor_247_out), .gate(Subtract_Enable));
  or or_59 (SUM18, and_197_out, and_198_out, and_199_out, and_200_out);
  or or_60 (or_60_out, and_200_out, and_201_out, and_202_out, and_203_out);
  Transistor transistor_250 (.in(B17), .out(transistor_245_out), .gate(Subtract_Enable));
  Transistor #(.\type ("n")) transistor_251 (.in(transistor_245_out), .out(transistor_244_out), .gate(B17));
  Transistor transistor_252 (.in(A17), .out(transistor_252_out), .gate(Subtract_Enable));
  Transistor transistor_253 (.in(Subtract_Enable), .out(transistor_253_out), .gate(A17));
  Transistor #(.\type ("n")) transistor_254 (.in(1'b0), .out(transistor_252_out), .gate(Subtract_Enable));
  Transistor #(.\type ("n")) transistor_255 (.in(transistor_247_out), .out(transistor_248_out), .gate(A1));
  Transistor #(.\type ("n")) transistor_256 (.in(transistor_252_out), .out(transistor_253_out), .gate(A17));
  and and_211 (and_211_out, ~or_4_out, ~transistor_253_out, transistor_244_out);  // AND_Gate
  and and_212 (and_212_out, ~or_4_out, transistor_253_out, ~transistor_244_out);  // AND_Gate
  and and_213 (and_213_out, or_4_out, ~transistor_253_out, ~transistor_244_out);  // AND_Gate
  and and_214 (and_214_out, or_4_out, transistor_253_out, transistor_244_out);
  and and_215 (and_215_out, or_4_out, ~transistor_253_out, transistor_244_out);  // AND_Gate
  and and_216 (and_216_out, ~or_4_out, transistor_253_out, transistor_244_out);  // AND_Gate
  and and_217 (and_217_out, or_4_out, transistor_253_out, ~transistor_244_out);  // AND_Gate
  and and_218 (and_218_out, ~Subtract_Enable, ~transistor_248_out, transistor_242_out);  // AND_Gate
  and and_219 (and_219_out, ~Subtract_Enable, transistor_248_out, ~transistor_242_out);  // AND_Gate
  and and_220 (and_220_out, Subtract_Enable, ~transistor_248_out, ~transistor_242_out);  // AND_Gate
  and and_221 (and_221_out, Subtract_Enable, transistor_248_out, transistor_242_out);
  and and_222 (and_222_out, Subtract_Enable, ~transistor_248_out, transistor_242_out);  // AND_Gate
  and and_223 (and_223_out, ~Subtract_Enable, transistor_248_out, transistor_242_out);  // AND_Gate
  and and_224 (and_224_out, Subtract_Enable, transistor_248_out, ~transistor_242_out);  // AND_Gate
  or or_61 (SUM17, and_211_out, and_212_out, and_213_out, and_214_out);
  or or_62 (or_62_out, and_214_out, and_215_out, and_216_out, and_217_out);
  or or_63 (SUM1, and_218_out, and_219_out, and_220_out, and_221_out);
  or or_64 (or_64_out, and_221_out, and_222_out, and_223_out, and_224_out);
endmodule
