// Logisim project project_multiplier.circ as structural Verilog: 1 circuit, main circuit main
module main (
  input  A1,
  input  A2,
  input  B1,
  input  B2,
  output out_5,
  output out_6,
  output out_7,
  output out_8
);

  wire and_1_out, and_3_out, and_4_out, and_5_out;

  and and_1 (and_1_out, A1, B2);
  and and_2 (out_5, A1, B1);
  and and_3 (and_3_out, A2, B1);
  and and_4 (and_4_out, A2, B2);
  xor xor_1 (out_6, and_1_out, and_3_out);
  and and_5 (and_5_out, and_1_out, and_3_out);
  xor xor_2 (out_7, and_5_out, and_4_out);
  and and_6 (out_8, and_5_out, and_4_out);
endmodule
