// Logisim project rs_latch.circ as structural Verilog: 1 circuit, main circuit main
module main (
  input  S,
  input  R,
  output Stored_Value,
  output out_4
);

  nand nand_1 (Stored_Value, S, out_4);
  nand nand_2 (out_4, Stored_Value, R);

  // Notes on the sheet:
  //   R-S Latch for memory storage
endmodule
