// Logisim project sequential_logic_circuit_INCOMPLETE.circ as structural Verilog: 1 circuit, main circuit main
module main (
  input  in_1,
  input  in_2,
  input  in_3,
  output out_4,
  output out_5,
  output out_6,
  output out_7,
  output out_8
);

  wire and_1_out, and_2_out, and_3_out;

  and and_1 (and_1_out, in_1, ~in_2, ~in_2);  // AND_Gate
  and and_2 (and_2_out, in_1, ~in_2, in_2);  // AND_Gate
  and and_3 (and_3_out, in_1, in_2, ~in_2);  // AND_Gate
  and and_4 (out_6, in_1, in_2, in_2);
  or or_1 (out_4, and_2_out, and_3_out, out_6);
  or or_2 (out_5, and_3_out, out_6);
  or or_3 (out_7, and_2_out, and_3_out);
  or or_4 (out_8, and_3_out, and_1_out);

  assign in_3 = in_2;
endmodule
