// Logisim project von_neumann_circuit.circ as structural Verilog
module main (
  input  in_1,
  input  in_2,
  input  [15:0] in_3,
  input  [7:0] in_4,
  input  [2:0] in_5,
  input  in_6,
  input  [3:0] in_7,
  output [7:0] out_8,
  output [3:0] PrcSel,
  output [2:0] D_Reg,
  output [2:0] S1_Reg,
  output [2:0] FILLER,
  output [2:0] S2_Reg
);

  wire [15:0] pc_addr_mem_1_dout;

  PC_Addr_MEM pc_addr_mem_1 (.WE(in_1), .AddrSel(in_7), .Din(in_3), .Dout(pc_addr_mem_1_dout));
  MAR_Reg mar_reg_1 (
    .WE(in_6), .Din(pc_addr_mem_1_dout), .PrcSel(PrcSel), .D_Reg(D_Reg), .S1_Reg(S1_Reg), .FILLER(FILLER),
    .S2_Reg(S2_Reg));
  MDR_Reg mdr_reg_1 ();  // open: WE, Din, AddrSel, Dout
  PC_Data_MEM pc_data_mem_1 (.WE(in_2), .Din(in_4), .AddrSel(in_5), .Dout(out_8));

  // Notes on the sheet:
  //   Instruction Write Enabling
  //   Instruction Programming
  //   PU MAR Write Enabling
  //   PU Instruction Selection
endmodule

module _3bit_ArithmaticSelector (
  input  [3:0] in_1,
  output out_2,
  output out_3,
  output out_4,
  output out_5,
  output out_6,
  output out_7,
  output out_8,
  output out_9,
  output out_10,
  output out_11,
  output out_12,
  output out_13,
  output out_14,
  output out_15,
  output out_16,
  output out_17
);

  and and_1 (out_2, in_1[3], in_1[2], in_1[1], in_1[0]);
  and and_2 (out_3, in_1[3], in_1[2], in_1[1], ~in_1[0]);  // AND_Gate
  and and_3 (out_4, in_1[3], in_1[2], ~in_1[1], in_1[0]);  // AND_Gate
  and and_4 (out_5, in_1[3], in_1[2], ~in_1[1], ~in_1[0]);  // AND_Gate
  and and_5 (out_6, in_1[3], ~in_1[2], in_1[1], in_1[0]);  // AND_Gate
  and and_6 (out_7, in_1[3], ~in_1[2], in_1[1], ~in_1[0]);  // AND_Gate
  and and_7 (out_8, in_1[3], ~in_1[2], ~in_1[1], in_1[0]);  // AND_Gate
  and and_8 (out_9, in_1[3], ~in_1[2], ~in_1[1], ~in_1[0]);  // AND_Gate
  and and_9 (out_11, ~in_1[3], in_1[2], in_1[1], ~in_1[0]);  // AND_Gate
  and and_10 (out_10, ~in_1[3], in_1[2], in_1[1], in_1[0]);  // AND_Gate
  and and_11 (out_12, ~in_1[3], in_1[2], ~in_1[1], in_1[0]);  // AND_Gate
  and and_12 (out_13, ~in_1[3], in_1[2], ~in_1[1], ~in_1[0]);  // AND_Gate
  and and_13 (out_14, ~in_1[3], ~in_1[2], in_1[1], in_1[0]);  // AND_Gate
  and and_14 (out_16, ~in_1[3], ~in_1[2], ~in_1[1], in_1[0]);  // AND_Gate
  and and_15 (out_15, ~in_1[3], ~in_1[2], in_1[1], ~in_1[0]);  // AND_Gate
  and and_16 (out_17, ~in_1[3], ~in_1[2], ~in_1[1], ~in_1[0]);  // AND_Gate

  // Notes on the sheet:
  //   0000 == Addition
  //   0001 == Subtraction
  //   0010 == Multiplication
  //   0011 == Division
  //   0100 == Modulus
  //   0101 == Equal To
  //   0110 == Greater Than
  //   0111 == Less Than
  //   1000 == FREE
  //   1001 == FREE
  //   1010 == FREE
  //   1011 == FREE
  //   1100 == FREE
  //   1101 == FREE
  //   1110 == FREE
  //   1111 == FREE
endmodule

module _1bit_AddSubtract (
  input  Ain,
  input  Sub,
  input  Bin,
  input  Cin,
  output Cout,
  output out
);

  wire and_1_out, and_2_out, or_1_out;

  and and_1 (and_1_out, Sub, ~Bin);  // AND_Gate
  and and_2 (and_2_out, Bin, ~Sub);  // AND_Gate
  or or_1 (or_1_out, and_1_out, and_2_out);
  Adder #(.width(1)) adder_1 (.a(Ain), .b(or_1_out), .out(out), .cin(Cin), .cout(Cout));
endmodule

module _8bit_AddSubtract (
  input  [7:0] Ain,
  input  [7:0] Bin,
  input  Sub,
  output Cout,
  output [7:0] out_5
);

  wire n1bit_addsubtract_2_cout, n1bit_addsubtract_3_cout, n1bit_addsubtract_4_cout,
       n1bit_addsubtract_5_cout, n1bit_addsubtract_6_cout, n1bit_addsubtract_7_cout, n1bit_addsubtract_8_cout;

  _1bit_AddSubtract u_1bit_addsubtract_1 (
    .Cout(Cout), .Sub(Sub), .Ain(Ain[7]), .Bin(Bin[7]), .out(out_5[7]), .Cin(n1bit_addsubtract_2_cout));
  _1bit_AddSubtract u_1bit_addsubtract_2 (
    .Cout(n1bit_addsubtract_2_cout), .Sub(Sub), .Ain(Ain[6]), .Bin(Bin[6]), .out(out_5[6]),
    .Cin(n1bit_addsubtract_3_cout));
  _1bit_AddSubtract u_1bit_addsubtract_3 (
    .Cout(n1bit_addsubtract_3_cout), .Sub(Sub), .Ain(Ain[5]), .Bin(Bin[5]), .out(out_5[5]),
    .Cin(n1bit_addsubtract_4_cout));
  _1bit_AddSubtract u_1bit_addsubtract_4 (
    .Cout(n1bit_addsubtract_4_cout), .Sub(Sub), .Ain(Ain[4]), .Bin(Bin[4]), .out(out_5[4]),
    .Cin(n1bit_addsubtract_5_cout));
  _1bit_AddSubtract u_1bit_addsubtract_5 (
    .Cout(n1bit_addsubtract_5_cout), .Sub(Sub), .Ain(Ain[3]), .Bin(Bin[3]), .out(out_5[3]),
    .Cin(n1bit_addsubtract_6_cout));
  _1bit_AddSubtract u_1bit_addsubtract_6 (
    .Cout(n1bit_addsubtract_6_cout), .Sub(Sub), .Ain(Ain[2]), .Bin(Bin[2]), .out(out_5[2]),
    .Cin(n1bit_addsubtract_7_cout));
  _1bit_AddSubtract u_1bit_addsubtract_7 (
    .Cout(n1bit_addsubtract_7_cout), .Sub(Sub), .Ain(Ain[1]), .Bin(Bin[1]), .out(out_5[1]),
    .Cin(n1bit_addsubtract_8_cout));
  _1bit_AddSubtract u_1bit_addsubtract_8 (
    .Cout(n1bit_addsubtract_8_cout), .Sub(Sub), .Ain(Ain[0]), .Bin(Bin[0]), .out(out_5[0]), .Cin(Sub));
endmodule

module _8bit_EqualTo (
  input  [7:0] in_1,
  input  [7:0] in_2,
  output out_3
);

  wire [7:0] xnor_1_out;

  assign xnor_1_out = ~(in_1 ^ in_2);  // XNOR_Gate xnor_1, 8 bits wide
  and and_1 (out_3, xnor_1_out[7], xnor_1_out[6], xnor_1_out[5], xnor_1_out[4], xnor_1_out[3], xnor_1_out[2], xnor_1_out[1], xnor_1_out[0]);
endmodule

module _1x8_Reg (
  input  [7:0] Din,
  input  WEin,
  output out_3,
  output out_4,
  output out_5,
  output out_6,
  output out_7,
  output out_8,
  output out_9,
  output out_10
);

  wire nand_1_out, nand_2_out, nand_3_out, nand_4_out, nand_5_out, nand_7_out, nand_9_out, nand_10_out,
       nand_11_out, nand_13_out, nand_14_out, nand_15_out, nand_16_out, nand_18_out, nand_19_out,
       nand_20_out, nand_22_out, nand_23_out, nand_25_out, nand_26_out, nand_28_out, nand_29_out,
       nand_30_out, nand_31_out;

  nand nand_1 (nand_1_out, WEin, ~Din[7]);  // NAND_Gate
  nand nand_2 (nand_2_out, nand_1_out, out_3);
  nand nand_3 (nand_3_out, WEin, ~Din[6]);  // NAND_Gate
  nand nand_4 (nand_4_out, Din[7], WEin);
  nand nand_5 (nand_5_out, nand_3_out, out_4);
  nand nand_6 (out_3, nand_2_out, nand_4_out);
  nand nand_7 (nand_7_out, Din[6], WEin);
  nand nand_8 (out_4, nand_5_out, nand_7_out);
  nand nand_9 (nand_9_out, WEin, ~Din[5]);  // NAND_Gate
  nand nand_10 (nand_10_out, Din[5], WEin);
  nand nand_11 (nand_11_out, nand_9_out, out_5);
  nand nand_12 (out_5, nand_11_out, nand_10_out);
  nand nand_13 (nand_13_out, WEin, ~Din[4]);  // NAND_Gate
  nand nand_14 (nand_14_out, nand_13_out, out_6);
  nand nand_15 (nand_15_out, WEin, ~Din[3]);  // NAND_Gate
  nand nand_16 (nand_16_out, Din[4], WEin);
  nand nand_17 (out_6, nand_14_out, nand_16_out);
  nand nand_18 (nand_18_out, nand_15_out, out_7);
  nand nand_19 (nand_19_out, Din[3], WEin);
  nand nand_20 (nand_20_out, WEin, ~Din[2]);  // NAND_Gate
  nand nand_21 (out_7, nand_18_out, nand_19_out);
  nand nand_22 (nand_22_out, nand_20_out, out_8);
  nand nand_23 (nand_23_out, Din[2], WEin);
  nand nand_24 (out_8, nand_22_out, nand_23_out);
  nand nand_25 (nand_25_out, WEin, ~Din[1]);  // NAND_Gate
  nand nand_26 (nand_26_out, Din[1], WEin);
  nand nand_27 (out_9, nand_28_out, nand_26_out);
  nand nand_28 (nand_28_out, nand_25_out, out_9);
  nand nand_29 (nand_29_out, WEin, ~Din[0]);  // NAND_Gate
  nand nand_30 (nand_30_out, nand_29_out, out_10);
  nand nand_31 (nand_31_out, Din[0], WEin);
  nand nand_32 (out_10, nand_30_out, nand_31_out);
endmodule

module _8_RegSelector_Mux (
  input  in_1,
  input  in_2,
  input  in_3,
  input  in_4,
  input  in_5,
  input  in_6,
  input  in_7,
  input  in_8,
  input  in_9,
  output [7:0] out_10
);

  and and_1 (out_10[7], in_9, in_1);
  and and_2 (out_10[4], in_9, in_4);
  and and_3 (out_10[5], in_9, in_3);
  and and_4 (out_10[6], in_9, in_2);
  and and_5 (out_10[1], in_9, in_7);
  and and_6 (out_10[3], in_9, in_5);
  and and_7 (out_10[2], in_9, in_6);
  and and_8 (out_10[0], in_9, in_8);
endmodule

module _2x8_Reg (
  input  WE,
  input  AddrSel,
  input  [7:0] Din,
  output [7:0] Dout
);

  wire and_1_out, and_2_out, n1x8_reg_1_out_3, n1x8_reg_1_out_4, n1x8_reg_1_out_5, n1x8_reg_1_out_6,
       n1x8_reg_1_out_7, n1x8_reg_1_out_8, n1x8_reg_1_out_9, n1x8_reg_1_out_10, n1x8_reg_2_out_3,
       n1x8_reg_2_out_4, n1x8_reg_2_out_5, n1x8_reg_2_out_6, n1x8_reg_2_out_7, n1x8_reg_2_out_8,
       n1x8_reg_2_out_9, n1x8_reg_2_out_10, not_1_out;
  wire [7:0] n8_regselector_mux_1_out_10, n8_regselector_mux_2_out_10;

  not not_1 (not_1_out, AddrSel);
  and and_1 (and_1_out, not_1_out, WE);
  and and_2 (and_2_out, AddrSel, WE);
  _1x8_Reg u_1x8_reg_1 (
    .WEin(and_1_out), .Din(Din), .out_3(n1x8_reg_1_out_3), .out_4(n1x8_reg_1_out_4),
    .out_5(n1x8_reg_1_out_5), .out_6(n1x8_reg_1_out_6), .out_7(n1x8_reg_1_out_7), .out_8(n1x8_reg_1_out_8),
    .out_9(n1x8_reg_1_out_9), .out_10(n1x8_reg_1_out_10));
  _8_RegSelector_Mux u_8_regselector_mux_1 (
    .in_9(not_1_out), .in_1(n1x8_reg_1_out_3), .in_2(n1x8_reg_1_out_4), .in_3(n1x8_reg_1_out_5),
    .in_4(n1x8_reg_1_out_6), .in_5(n1x8_reg_1_out_7), .in_6(n1x8_reg_1_out_8), .in_7(n1x8_reg_1_out_9),
    .in_8(n1x8_reg_1_out_10), .out_10(n8_regselector_mux_1_out_10));
  _1x8_Reg u_1x8_reg_2 (
    .WEin(and_2_out), .Din(Din), .out_3(n1x8_reg_2_out_3), .out_4(n1x8_reg_2_out_4),
    .out_5(n1x8_reg_2_out_5), .out_6(n1x8_reg_2_out_6), .out_7(n1x8_reg_2_out_7), .out_8(n1x8_reg_2_out_8),
    .out_9(n1x8_reg_2_out_9), .out_10(n1x8_reg_2_out_10));
  _8_RegSelector_Mux u_8_regselector_mux_2 (
    .in_9(AddrSel), .in_1(n1x8_reg_2_out_3), .in_2(n1x8_reg_2_out_4), .in_3(n1x8_reg_2_out_5),
    .in_4(n1x8_reg_2_out_6), .in_5(n1x8_reg_2_out_7), .in_6(n1x8_reg_2_out_8), .in_7(n1x8_reg_2_out_9),
    .in_8(n1x8_reg_2_out_10), .out_10(n8_regselector_mux_2_out_10));
  assign Dout = n8_regselector_mux_1_out_10 | n8_regselector_mux_2_out_10;  // OR_Gate or_1, 8 bits wide
endmodule

module PC_Data_MEM (
  input  WE,
  input  [2:0] AddrSel,
  input  [7:0] Din,
  output [7:0] Dout
);

  wire and_1_out, and_2_out, and_3_out, and_4_out, and_5_out, and_6_out, and_7_out, and_8_out, and_9_out,
       and_10_out, and_11_out, and_12_out, and_13_out, and_14_out, and_15_out, and_16_out, n1x8_reg_1_out_3,
       n1x8_reg_1_out_4, n1x8_reg_1_out_5, n1x8_reg_1_out_6, n1x8_reg_1_out_7, n1x8_reg_1_out_8,
       n1x8_reg_1_out_9, n1x8_reg_1_out_10, n1x8_reg_2_out_3, n1x8_reg_2_out_4, n1x8_reg_2_out_5,
       n1x8_reg_2_out_6, n1x8_reg_2_out_7, n1x8_reg_2_out_8, n1x8_reg_2_out_9, n1x8_reg_2_out_10,
       n1x8_reg_3_out_3, n1x8_reg_3_out_4, n1x8_reg_3_out_5, n1x8_reg_3_out_6, n1x8_reg_3_out_7,
       n1x8_reg_3_out_8, n1x8_reg_3_out_9, n1x8_reg_3_out_10, n1x8_reg_4_out_3, n1x8_reg_4_out_4,
       n1x8_reg_4_out_5, n1x8_reg_4_out_6, n1x8_reg_4_out_7, n1x8_reg_4_out_8, n1x8_reg_4_out_9,
       n1x8_reg_4_out_10, n1x8_reg_5_out_3, n1x8_reg_5_out_4, n1x8_reg_5_out_5, n1x8_reg_5_out_6,
       n1x8_reg_5_out_7, n1x8_reg_5_out_8, n1x8_reg_5_out_9, n1x8_reg_5_out_10, n1x8_reg_6_out_3,
       n1x8_reg_6_out_4, n1x8_reg_6_out_5, n1x8_reg_6_out_6, n1x8_reg_6_out_7, n1x8_reg_6_out_8,
       n1x8_reg_6_out_9, n1x8_reg_6_out_10, n1x8_reg_7_out_3, n1x8_reg_7_out_4, n1x8_reg_7_out_5,
       n1x8_reg_7_out_6, n1x8_reg_7_out_7, n1x8_reg_7_out_8, n1x8_reg_7_out_9, n1x8_reg_7_out_10,
       n1x8_reg_8_out_3, n1x8_reg_8_out_4, n1x8_reg_8_out_5, n1x8_reg_8_out_6, n1x8_reg_8_out_7,
       n1x8_reg_8_out_8, n1x8_reg_8_out_9, n1x8_reg_8_out_10;
  wire [7:0] n8_regselector_mux_1_out_10, n8_regselector_mux_2_out_10, n8_regselector_mux_3_out_10,
       n8_regselector_mux_4_out_10, n8_regselector_mux_5_out_10, n8_regselector_mux_6_out_10,
       n8_regselector_mux_7_out_10, n8_regselector_mux_8_out_10;

  and and_1 (and_1_out, ~AddrSel[0], ~AddrSel[1], ~AddrSel[2]);  // AND_Gate
  and and_2 (and_2_out, AddrSel[0], ~AddrSel[1], ~AddrSel[2]);  // AND_Gate
  and and_3 (and_3_out, ~AddrSel[0], AddrSel[1], ~AddrSel[2]);  // AND_Gate
  and and_4 (and_4_out, AddrSel[0], AddrSel[1], ~AddrSel[2]);  // AND_Gate
  and and_5 (and_5_out, ~AddrSel[0], ~AddrSel[1], AddrSel[2]);  // AND_Gate
  and and_6 (and_6_out, AddrSel[0], ~AddrSel[1], AddrSel[2]);  // AND_Gate
  and and_7 (and_7_out, ~AddrSel[0], AddrSel[1], AddrSel[2]);  // AND_Gate
  and and_8 (and_8_out, AddrSel[0], AddrSel[1], AddrSel[2]);
  and and_9 (and_9_out, and_1_out, WE);
  and and_10 (and_10_out, and_2_out, WE);
  and and_11 (and_11_out, and_3_out, WE);
  and and_12 (and_12_out, and_4_out, WE);
  and and_13 (and_13_out, and_5_out, WE);
  and and_14 (and_14_out, and_6_out, WE);
  and and_15 (and_15_out, and_7_out, WE);
  and and_16 (and_16_out, and_8_out, WE);
  _1x8_Reg u_1x8_reg_1 (
    .WEin(and_9_out), .Din(Din), .out_3(n1x8_reg_1_out_3), .out_4(n1x8_reg_1_out_4),
    .out_5(n1x8_reg_1_out_5), .out_6(n1x8_reg_1_out_6), .out_7(n1x8_reg_1_out_7), .out_8(n1x8_reg_1_out_8),
    .out_9(n1x8_reg_1_out_9), .out_10(n1x8_reg_1_out_10));
  _8_RegSelector_Mux u_8_regselector_mux_1 (
    .in_9(and_1_out), .in_1(n1x8_reg_1_out_3), .in_2(n1x8_reg_1_out_4), .in_3(n1x8_reg_1_out_5),
    .in_4(n1x8_reg_1_out_6), .in_5(n1x8_reg_1_out_7), .in_6(n1x8_reg_1_out_8), .in_7(n1x8_reg_1_out_9),
    .in_8(n1x8_reg_1_out_10), .out_10(n8_regselector_mux_1_out_10));
  _1x8_Reg u_1x8_reg_2 (
    .WEin(and_10_out), .Din(Din), .out_3(n1x8_reg_2_out_3), .out_4(n1x8_reg_2_out_4),
    .out_5(n1x8_reg_2_out_5), .out_6(n1x8_reg_2_out_6), .out_7(n1x8_reg_2_out_7), .out_8(n1x8_reg_2_out_8),
    .out_9(n1x8_reg_2_out_9), .out_10(n1x8_reg_2_out_10));
  _8_RegSelector_Mux u_8_regselector_mux_2 (
    .in_9(and_2_out), .in_1(n1x8_reg_2_out_3), .in_2(n1x8_reg_2_out_4), .in_3(n1x8_reg_2_out_5),
    .in_4(n1x8_reg_2_out_6), .in_5(n1x8_reg_2_out_7), .in_6(n1x8_reg_2_out_8), .in_7(n1x8_reg_2_out_9),
    .in_8(n1x8_reg_2_out_10), .out_10(n8_regselector_mux_2_out_10));
  _1x8_Reg u_1x8_reg_3 (
    .WEin(and_11_out), .Din(Din), .out_3(n1x8_reg_3_out_3), .out_4(n1x8_reg_3_out_4),
    .out_5(n1x8_reg_3_out_5), .out_6(n1x8_reg_3_out_6), .out_7(n1x8_reg_3_out_7), .out_8(n1x8_reg_3_out_8),
    .out_9(n1x8_reg_3_out_9), .out_10(n1x8_reg_3_out_10));
  _8_RegSelector_Mux u_8_regselector_mux_3 (
    .in_9(and_3_out), .in_1(n1x8_reg_3_out_3), .in_2(n1x8_reg_3_out_4), .in_3(n1x8_reg_3_out_5),
    .in_4(n1x8_reg_3_out_6), .in_5(n1x8_reg_3_out_7), .in_6(n1x8_reg_3_out_8), .in_7(n1x8_reg_3_out_9),
    .in_8(n1x8_reg_3_out_10), .out_10(n8_regselector_mux_3_out_10));
  _1x8_Reg u_1x8_reg_4 (
    .WEin(and_12_out), .Din(Din), .out_3(n1x8_reg_4_out_3), .out_4(n1x8_reg_4_out_4),
    .out_5(n1x8_reg_4_out_5), .out_6(n1x8_reg_4_out_6), .out_7(n1x8_reg_4_out_7), .out_8(n1x8_reg_4_out_8),
    .out_9(n1x8_reg_4_out_9), .out_10(n1x8_reg_4_out_10));
  _8_RegSelector_Mux u_8_regselector_mux_4 (
    .in_9(and_4_out), .in_1(n1x8_reg_4_out_3), .in_2(n1x8_reg_4_out_4), .in_3(n1x8_reg_4_out_5),
    .in_4(n1x8_reg_4_out_6), .in_5(n1x8_reg_4_out_7), .in_6(n1x8_reg_4_out_8), .in_7(n1x8_reg_4_out_9),
    .in_8(n1x8_reg_4_out_10), .out_10(n8_regselector_mux_4_out_10));
  _1x8_Reg u_1x8_reg_5 (
    .WEin(and_13_out), .Din(Din), .out_3(n1x8_reg_5_out_3), .out_4(n1x8_reg_5_out_4),
    .out_5(n1x8_reg_5_out_5), .out_6(n1x8_reg_5_out_6), .out_7(n1x8_reg_5_out_7), .out_8(n1x8_reg_5_out_8),
    .out_9(n1x8_reg_5_out_9), .out_10(n1x8_reg_5_out_10));
  _8_RegSelector_Mux u_8_regselector_mux_5 (
    .in_9(and_5_out), .in_1(n1x8_reg_5_out_3), .in_2(n1x8_reg_5_out_4), .in_3(n1x8_reg_5_out_5),
    .in_4(n1x8_reg_5_out_6), .in_5(n1x8_reg_5_out_7), .in_6(n1x8_reg_5_out_8), .in_7(n1x8_reg_5_out_9),
    .in_8(n1x8_reg_5_out_10), .out_10(n8_regselector_mux_5_out_10));
  _1x8_Reg u_1x8_reg_6 (
    .WEin(and_14_out), .Din(Din), .out_3(n1x8_reg_6_out_3), .out_4(n1x8_reg_6_out_4),
    .out_5(n1x8_reg_6_out_5), .out_6(n1x8_reg_6_out_6), .out_7(n1x8_reg_6_out_7), .out_8(n1x8_reg_6_out_8),
    .out_9(n1x8_reg_6_out_9), .out_10(n1x8_reg_6_out_10));
  _8_RegSelector_Mux u_8_regselector_mux_6 (
    .in_9(and_6_out), .in_1(n1x8_reg_6_out_3), .in_2(n1x8_reg_6_out_4), .in_3(n1x8_reg_6_out_5),
    .in_4(n1x8_reg_6_out_6), .in_5(n1x8_reg_6_out_7), .in_6(n1x8_reg_6_out_8), .in_7(n1x8_reg_6_out_9),
    .in_8(n1x8_reg_6_out_10), .out_10(n8_regselector_mux_6_out_10));
  _1x8_Reg u_1x8_reg_7 (
    .WEin(and_15_out), .Din(Din), .out_3(n1x8_reg_7_out_3), .out_4(n1x8_reg_7_out_4),
    .out_5(n1x8_reg_7_out_5), .out_6(n1x8_reg_7_out_6), .out_7(n1x8_reg_7_out_7), .out_8(n1x8_reg_7_out_8),
    .out_9(n1x8_reg_7_out_9), .out_10(n1x8_reg_7_out_10));
  _8_RegSelector_Mux u_8_regselector_mux_7 (
    .in_9(and_7_out), .in_1(n1x8_reg_7_out_3), .in_2(n1x8_reg_7_out_4), .in_3(n1x8_reg_7_out_5),
    .in_4(n1x8_reg_7_out_6), .in_5(n1x8_reg_7_out_7), .in_6(n1x8_reg_7_out_8), .in_7(n1x8_reg_7_out_9),
    .in_8(n1x8_reg_7_out_10), .out_10(n8_regselector_mux_7_out_10));
  _1x8_Reg u_1x8_reg_8 (
    .WEin(and_16_out), .Din(Din), .out_3(n1x8_reg_8_out_3), .out_4(n1x8_reg_8_out_4),
    .out_5(n1x8_reg_8_out_5), .out_6(n1x8_reg_8_out_6), .out_7(n1x8_reg_8_out_7), .out_8(n1x8_reg_8_out_8),
    .out_9(n1x8_reg_8_out_9), .out_10(n1x8_reg_8_out_10));
  _8_RegSelector_Mux u_8_regselector_mux_8 (
    .in_9(and_8_out), .in_1(n1x8_reg_8_out_3), .in_2(n1x8_reg_8_out_4), .in_3(n1x8_reg_8_out_5),
    .in_4(n1x8_reg_8_out_6), .in_5(n1x8_reg_8_out_7), .in_6(n1x8_reg_8_out_8), .in_7(n1x8_reg_8_out_9),
    .in_8(n1x8_reg_8_out_10), .out_10(n8_regselector_mux_8_out_10));
  assign Dout = n8_regselector_mux_1_out_10 | n8_regselector_mux_2_out_10 | n8_regselector_mux_3_out_10 | n8_regselector_mux_4_out_10 | n8_regselector_mux_5_out_10 | n8_regselector_mux_6_out_10 | n8_regselector_mux_7_out_10 | n8_regselector_mux_8_out_10;  // OR_Gate or_1, 8 bits wide
endmodule

module _8bit_Multiplier (
  input  [7:0] Ain,
  input  [7:0] Bin,
  output [7:0] out_3,
  output [7:0] out_4
);

  wire adder_2_cout, adder_2_out, adder_4_cout, adder_4_out, adder_5_cout, adder_5_out, adder_7_cout,
       adder_7_out, adder_8_cout, adder_8_out, adder_9_cout, adder_9_out, adder_11_cout, adder_11_out,
       adder_12_cout, adder_12_out, adder_13_cout, adder_13_out, adder_14_cout, adder_14_out, adder_16_cout,
       adder_16_out, adder_17_cout, adder_17_out, adder_18_cout, adder_18_out, adder_19_cout, adder_19_out,
       adder_20_cout, adder_20_out, adder_22_cout, adder_22_out, adder_23_cout, adder_23_out, adder_24_cout,
       adder_24_out, adder_25_cout, adder_25_out, adder_26_cout, adder_26_out, adder_27_cout, adder_27_out,
       adder_28_cout, adder_28_out, adder_29_cout, adder_29_out, adder_31_cout, adder_31_out, adder_32_cout,
       adder_32_out, adder_33_cout, adder_33_out, adder_34_cout, adder_34_out, adder_35_cout, adder_35_out,
       adder_36_cout, adder_36_out, adder_37_cout, adder_37_out, adder_39_cout, adder_39_out, adder_40_cout,
       adder_40_out, adder_41_cout, adder_41_out, adder_42_cout, adder_42_out, adder_43_cout, adder_43_out,
       adder_44_cout, adder_44_out, adder_45_cout, adder_45_out, adder_46_cout, adder_47_cout, adder_47_out,
       adder_48_cout, adder_48_out, adder_49_cout, adder_50_cout, adder_50_out, adder_51_cout, adder_51_out,
       adder_52_cout, adder_52_out, adder_53_cout, adder_53_out, adder_54_cout, adder_55_cout, adder_55_out,
       adder_56_cout, adder_56_out, adder_57_cout, adder_57_out, adder_58_cout, adder_59_cout, adder_59_out,
       adder_60_cout, adder_60_out, adder_61_cout, adder_62_cout, adder_62_out, adder_63_cout, adder_64_cout,
       and_1_out, and_2_out, and_3_out, and_4_out, and_5_out, and_6_out, and_7_out, and_8_out, and_9_out,
       and_10_out, and_11_out, and_12_out, and_13_out, and_14_out, and_15_out, and_16_out, and_17_out,
       and_18_out, and_19_out, and_20_out, and_21_out, and_22_out, and_23_out, and_24_out, and_25_out,
       and_26_out, and_27_out, and_28_out, and_29_out, and_30_out, and_31_out, and_32_out, and_33_out,
       and_34_out, and_35_out, and_36_out, and_37_out, and_38_out, and_39_out, and_40_out, and_41_out,
       and_42_out, and_43_out, and_44_out, and_45_out, and_46_out, and_47_out, and_48_out, and_49_out,
       and_50_out, and_51_out, and_52_out, and_53_out, and_54_out, and_55_out, and_56_out, and_57_out,
       and_58_out, and_59_out, and_60_out, and_61_out, and_62_out, and_63_out, and_64_out;

  and and_1 (and_1_out, Ain[7], Bin[7]);
  Adder #(.width(1)) adder_1 (.a(1'b0), .b(and_1_out), .out(out_3[6]), .cin(adder_2_cout), .cout(out_3[7]));
  and and_2 (and_2_out, Ain[7], Bin[6]);
  Adder #(.width(1)) adder_2 (.a(1'b0), .b(and_2_out), .out(adder_2_out), .cin(adder_4_cout), .cout(adder_2_cout));
  and and_3 (and_3_out, Ain[6], Bin[7]);
  and and_4 (and_4_out, Ain[7], Bin[5]);
  Adder #(.width(1)) adder_3 (.a(adder_2_out), .b(and_3_out), .out(out_3[5]), .cin(adder_5_cout));  // open: cout
  Adder #(.width(1)) adder_4 (.a(1'b0), .b(and_4_out), .out(adder_4_out), .cin(adder_7_cout), .cout(adder_4_cout));
  and and_5 (and_5_out, Ain[6], Bin[6]);
  Adder #(.width(1)) adder_5 (
    .a(adder_4_out), .b(and_5_out), .out(adder_5_out), .cin(adder_8_cout), .cout(adder_5_cout));
  and and_6 (and_6_out, Ain[5], Bin[7]);
  and and_7 (and_7_out, Ain[7], Bin[4]);
  and and_8 (and_8_out, Ain[6], Bin[5]);
  and and_9 (and_9_out, Ain[5], Bin[6]);
  Adder #(.width(1)) adder_6 (.a(adder_5_out), .b(and_6_out), .out(out_3[4]), .cin(adder_9_cout));  // open: cout
  Adder #(.width(1)) adder_7 (.a(1'b0), .b(and_7_out), .out(adder_7_out), .cin(adder_11_cout), .cout(adder_7_cout));
  Adder #(.width(1)) adder_8 (
    .a(adder_7_out), .b(and_8_out), .out(adder_8_out), .cin(adder_12_cout), .cout(adder_8_cout));
  Adder #(.width(1)) adder_9 (
    .a(adder_8_out), .b(and_9_out), .out(adder_9_out), .cin(adder_13_cout), .cout(adder_9_cout));
  and and_10 (and_10_out, Ain[4], Bin[7]);
  Adder #(.width(1)) adder_10 (.a(adder_9_out), .b(and_10_out), .out(out_3[3]), .cin(adder_14_cout));  // open: cout
  and and_11 (and_11_out, Ain[7], Bin[3]);
  Adder #(.width(1)) adder_11 (.a(1'b0), .b(and_11_out), .out(adder_11_out), .cin(adder_16_cout), .cout(adder_11_cout));
  and and_12 (and_12_out, Ain[6], Bin[4]);
  and and_13 (and_13_out, Ain[5], Bin[5]);
  and and_14 (and_14_out, Ain[4], Bin[6]);
  and and_15 (and_15_out, Ain[7], Bin[2]);
  and and_16 (and_16_out, Ain[6], Bin[3]);
  Adder #(.width(1)) adder_12 (
    .a(adder_11_out), .b(and_12_out), .out(adder_12_out), .cin(adder_17_cout), .cout(adder_12_cout));
  Adder #(.width(1)) adder_13 (
    .a(adder_12_out), .b(and_13_out), .out(adder_13_out), .cin(adder_18_cout), .cout(adder_13_cout));
  Adder #(.width(1)) adder_14 (
    .a(adder_13_out), .b(and_14_out), .out(adder_14_out), .cin(adder_19_cout), .cout(adder_14_cout));
  and and_17 (and_17_out, Ain[3], Bin[7]);
  Adder #(.width(1)) adder_15 (.a(adder_14_out), .b(and_17_out), .out(out_3[2]), .cin(adder_20_cout));  // open: cout
  Adder #(.width(1)) adder_16 (.a(1'b0), .b(and_15_out), .out(adder_16_out), .cin(adder_22_cout), .cout(adder_16_cout));
  Adder #(.width(1)) adder_17 (
    .a(adder_16_out), .b(and_16_out), .out(adder_17_out), .cin(adder_23_cout), .cout(adder_17_cout));
  and and_18 (and_18_out, Ain[5], Bin[4]);
  Adder #(.width(1)) adder_18 (
    .a(adder_17_out), .b(and_18_out), .out(adder_18_out), .cin(adder_24_cout), .cout(adder_18_cout));
  and and_19 (and_19_out, Ain[4], Bin[5]);
  and and_20 (and_20_out, Ain[3], Bin[6]);
  and and_21 (and_21_out, Ain[2], Bin[7]);
  and and_22 (and_22_out, Ain[7], Bin[1]);
  and and_23 (and_23_out, Ain[6], Bin[2]);
  and and_24 (and_24_out, Ain[5], Bin[3]);
  Adder #(.width(1)) adder_19 (
    .a(adder_18_out), .b(and_19_out), .out(adder_19_out), .cin(adder_25_cout), .cout(adder_19_cout));
  Adder #(.width(1)) adder_20 (
    .a(adder_19_out), .b(and_20_out), .out(adder_20_out), .cin(adder_28_cout), .cout(adder_20_cout));
  Adder #(.width(1)) adder_21 (.a(adder_20_out), .b(and_21_out), .out(out_3[1]), .cin(adder_29_cout));  // open: cout
  and and_25 (and_25_out, Ain[7], Bin[0]);
  Adder #(.width(1)) adder_22 (.a(1'b0), .b(and_22_out), .out(adder_22_out), .cin(adder_26_cout), .cout(adder_22_cout));
  Adder #(.width(1)) adder_23 (
    .a(adder_22_out), .b(and_23_out), .out(adder_23_out), .cin(adder_27_cout), .cout(adder_23_cout));
  Adder #(.width(1)) adder_24 (
    .a(adder_23_out), .b(and_24_out), .out(adder_24_out), .cin(adder_31_cout), .cout(adder_24_cout));
  and and_26 (and_26_out, Ain[4], Bin[4]);
  Adder #(.width(1)) adder_25 (
    .a(adder_24_out), .b(and_26_out), .out(adder_25_out), .cin(adder_32_cout), .cout(adder_25_cout));
  and and_27 (and_27_out, Ain[3], Bin[5]);
  and and_28 (and_28_out, Ain[2], Bin[6]);
  and and_29 (and_29_out, Ain[1], Bin[7]);
  Adder #(.width(1)) adder_26 (.a(1'b0), .b(and_25_out), .out(adder_26_out), .cin(1'b0), .cout(adder_26_cout));
  and and_30 (and_30_out, Ain[6], Bin[1]);
  Adder #(.width(1)) adder_27 (
    .a(adder_26_out), .b(and_30_out), .out(adder_27_out), .cin(adder_35_cout), .cout(adder_27_cout));
  and and_31 (and_31_out, Ain[5], Bin[2]);
  and and_32 (and_32_out, Ain[4], Bin[3]);
  and and_33 (and_33_out, Ain[3], Bin[4]);
  Adder #(.width(1)) adder_28 (
    .a(adder_25_out), .b(and_27_out), .out(adder_28_out), .cin(adder_33_cout), .cout(adder_28_cout));
  Adder #(.width(1)) adder_29 (
    .a(adder_28_out), .b(and_28_out), .out(adder_29_out), .cin(adder_34_cout), .cout(adder_29_cout));
  Adder #(.width(1)) adder_30 (.a(adder_29_out), .b(and_29_out), .out(out_3[0]), .cin(adder_37_cout));  // open: cout
  and and_34 (and_34_out, Ain[6], Bin[0]);
  Adder #(.width(1)) adder_31 (
    .a(adder_27_out), .b(and_31_out), .out(adder_31_out), .cin(adder_36_cout), .cout(adder_31_cout));
  Adder #(.width(1)) adder_32 (
    .a(adder_31_out), .b(and_32_out), .out(adder_32_out), .cin(adder_39_cout), .cout(adder_32_cout));
  Adder #(.width(1)) adder_33 (
    .a(adder_32_out), .b(and_33_out), .out(adder_33_out), .cin(adder_40_cout), .cout(adder_33_cout));
  and and_35 (and_35_out, Ain[2], Bin[5]);
  Adder #(.width(1)) adder_34 (
    .a(adder_33_out), .b(and_35_out), .out(adder_34_out), .cin(adder_41_cout), .cout(adder_34_cout));
  and and_36 (and_36_out, Ain[1], Bin[6]);
  and and_37 (and_37_out, Ain[0], Bin[7]);
  Adder #(.width(1)) adder_35 (.a(1'b0), .b(and_34_out), .out(adder_35_out), .cin(1'b0), .cout(adder_35_cout));
  and and_38 (and_38_out, Ain[5], Bin[1]);
  Adder #(.width(1)) adder_36 (
    .a(adder_35_out), .b(and_38_out), .out(adder_36_out), .cin(adder_43_cout), .cout(adder_36_cout));
  and and_39 (and_39_out, Ain[4], Bin[2]);
  and and_40 (and_40_out, Ain[3], Bin[3]);
  and and_41 (and_41_out, Ain[2], Bin[4]);
  Adder #(.width(1)) adder_37 (
    .a(adder_34_out), .b(and_36_out), .out(adder_37_out), .cin(adder_42_cout), .cout(adder_37_cout));
  Adder #(.width(1)) adder_38 (.a(adder_37_out), .b(and_37_out), .out(out_4[7]), .cin(adder_46_cout));  // open: cout
  and and_42 (and_42_out, Ain[5], Bin[0]);
  and and_43 (and_43_out, Ain[4], Bin[1]);
  Adder #(.width(1)) adder_39 (
    .a(adder_36_out), .b(and_39_out), .out(adder_39_out), .cin(adder_44_cout), .cout(adder_39_cout));
  Adder #(.width(1)) adder_40 (
    .a(adder_39_out), .b(and_40_out), .out(adder_40_out), .cin(adder_45_cout), .cout(adder_40_cout));
  Adder #(.width(1)) adder_41 (
    .a(adder_40_out), .b(and_41_out), .out(adder_41_out), .cin(adder_47_cout), .cout(adder_41_cout));
  and and_44 (and_44_out, Ain[1], Bin[5]);
  Adder #(.width(1)) adder_42 (
    .a(adder_41_out), .b(and_44_out), .out(adder_42_out), .cin(adder_48_cout), .cout(adder_42_cout));
  and and_45 (and_45_out, Ain[0], Bin[6]);
  Adder #(.width(1)) adder_43 (.a(1'b0), .b(and_42_out), .out(adder_43_out), .cin(1'b0), .cout(adder_43_cout));
  Adder #(.width(1)) adder_44 (
    .a(adder_43_out), .b(and_43_out), .out(adder_44_out), .cin(adder_50_cout), .cout(adder_44_cout));
  and and_46 (and_46_out, Ain[3], Bin[2]);
  Adder #(.width(1)) adder_45 (
    .a(adder_44_out), .b(and_46_out), .out(adder_45_out), .cin(adder_51_cout), .cout(adder_45_cout));
  and and_47 (and_47_out, Ain[2], Bin[3]);
  and and_48 (and_48_out, Ain[1], Bin[4]);
  and and_49 (and_49_out, Ain[0], Bin[5]);
  Adder #(.width(1)) adder_46 (
    .a(adder_42_out), .b(and_45_out), .out(out_4[6]), .cin(adder_49_cout), .cout(adder_46_cout));
  and and_50 (and_50_out, Ain[4], Bin[0]);
  and and_51 (and_51_out, Ain[3], Bin[1]);
  Adder #(.width(1)) adder_47 (
    .a(adder_45_out), .b(and_47_out), .out(adder_47_out), .cin(adder_52_cout), .cout(adder_47_cout));
  Adder #(.width(1)) adder_48 (
    .a(adder_47_out), .b(and_48_out), .out(adder_48_out), .cin(adder_53_cout), .cout(adder_48_cout));
  Adder #(.width(1)) adder_49 (
    .a(adder_48_out), .b(and_49_out), .out(out_4[5]), .cin(adder_54_cout), .cout(adder_49_cout));
  Adder #(.width(1)) adder_50 (.a(1'b0), .b(and_50_out), .out(adder_50_out), .cin(1'b0), .cout(adder_50_cout));
  Adder #(.width(1)) adder_51 (
    .a(adder_50_out), .b(and_51_out), .out(adder_51_out), .cin(adder_55_cout), .cout(adder_51_cout));
  and and_52 (and_52_out, Ain[2], Bin[2]);
  Adder #(.width(1)) adder_52 (
    .a(adder_51_out), .b(and_52_out), .out(adder_52_out), .cin(adder_56_cout), .cout(adder_52_cout));
  and and_53 (and_53_out, Ain[1], Bin[3]);
  and and_54 (and_54_out, Ain[0], Bin[4]);
  and and_55 (and_55_out, Ain[3], Bin[0]);
  and and_56 (and_56_out, Ain[2], Bin[1]);
  and and_57 (and_57_out, Ain[1], Bin[2]);
  Adder #(.width(1)) adder_53 (
    .a(adder_52_out), .b(and_53_out), .out(adder_53_out), .cin(adder_57_cout), .cout(adder_53_cout));
  Adder #(.width(1)) adder_54 (
    .a(adder_53_out), .b(and_54_out), .out(out_4[4]), .cin(adder_58_cout), .cout(adder_54_cout));
  Adder #(.width(1)) adder_55 (.a(1'b0), .b(and_55_out), .out(adder_55_out), .cin(1'b0), .cout(adder_55_cout));
  Adder #(.width(1)) adder_56 (
    .a(adder_55_out), .b(and_56_out), .out(adder_56_out), .cin(adder_59_cout), .cout(adder_56_cout));
  Adder #(.width(1)) adder_57 (
    .a(adder_56_out), .b(and_57_out), .out(adder_57_out), .cin(adder_60_cout), .cout(adder_57_cout));
  and and_58 (and_58_out, Ain[0], Bin[3]);
  Adder #(.width(1)) adder_58 (
    .a(adder_57_out), .b(and_58_out), .out(out_4[3]), .cin(adder_61_cout), .cout(adder_58_cout));
  and and_59 (and_59_out, Ain[2], Bin[0]);
  and and_60 (and_60_out, Ain[1], Bin[1]);
  and and_61 (and_61_out, Ain[0], Bin[2]);
  Adder #(.width(1)) adder_59 (.a(1'b0), .b(and_59_out), .out(adder_59_out), .cin(1'b0), .cout(adder_59_cout));
  Adder #(.width(1)) adder_60 (
    .a(adder_59_out), .b(and_60_out), .out(adder_60_out), .cin(adder_62_cout), .cout(adder_60_cout));
  Adder #(.width(1)) adder_61 (
    .a(adder_60_out), .b(and_61_out), .out(out_4[2]), .cin(adder_63_cout), .cout(adder_61_cout));
  and and_62 (and_62_out, Ain[1], Bin[0]);
  Adder #(.width(1)) adder_62 (.a(1'b0), .b(and_62_out), .out(adder_62_out), .cin(1'b0), .cout(adder_62_cout));
  and and_63 (and_63_out, Ain[0], Bin[1]);
  Adder #(.width(1)) adder_63 (
    .a(adder_62_out), .b(and_63_out), .out(out_4[1]), .cin(adder_64_cout), .cout(adder_63_cout));
  and and_64 (and_64_out, Ain[0], Bin[0]);
  Adder #(.width(1)) adder_64 (.a(1'b0), .b(and_64_out), .out(out_4[0]), .cin(1'b0), .cout(adder_64_cout));
endmodule

module _8bit_Divider (
  input  [7:0] in_1,
  input  [7:0] in_2,
  input  [7:0] in_3,
  output [7:0] out_4,
  output [7:0] out_5
);

  Divider divider_1 (.a(in_2), .b(in_3), .out(out_4), .upper(in_1), .rem(out_5));

  // Notes on the sheet:
  //   Sorry, ths one's sad...
  //   I wanted to still be able to contiue with the projects.
endmodule

module AddSubtractSelector (
  input  in_1,
  input  in_2,
  output out_3
);

  and and_1 (out_3, in_1, ~in_2);  // AND_Gate
endmodule

module _1by16bit_Registry (
  input  [15:0] Din,
  input  WEin,
  output out_3,
  output out_4,
  output out_5,
  output out_6,
  output out_7,
  output out_8,
  output out_9,
  output out_10,
  output out_11,
  output out_12,
  output out_13,
  output out_14,
  output out_15,
  output out_16,
  output out_17,
  output out_18
);

  wire nand_1_out, nand_2_out, nand_3_out, nand_4_out, nand_6_out, nand_7_out, nand_9_out, nand_10_out,
       nand_12_out, nand_13_out, nand_14_out, nand_15_out, nand_16_out, nand_18_out, nand_19_out,
       nand_20_out, nand_21_out, nand_23_out, nand_25_out, nand_26_out, nand_28_out, nand_29_out,
       nand_30_out, nand_31_out, nand_32_out, nand_33_out, nand_35_out, nand_36_out, nand_38_out,
       nand_39_out, nand_41_out, nand_42_out, nand_44_out, nand_45_out, nand_46_out, nand_47_out,
       nand_48_out, nand_50_out, nand_51_out, nand_52_out, nand_54_out, nand_55_out, nand_57_out,
       nand_58_out, nand_60_out, nand_61_out, nand_62_out, nand_63_out;

  nand nand_1 (nand_1_out, WEin, ~Din[15]);  // NAND_Gate
  nand nand_2 (nand_2_out, nand_1_out, out_3);
  nand nand_3 (nand_3_out, Din[15], WEin);
  nand nand_4 (nand_4_out, WEin, ~Din[14]);  // NAND_Gate
  nand nand_5 (out_3, nand_2_out, nand_3_out);
  nand nand_6 (nand_6_out, nand_4_out, out_4);
  nand nand_7 (nand_7_out, Din[14], WEin);
  nand nand_8 (out_4, nand_6_out, nand_7_out);
  nand nand_9 (nand_9_out, WEin, ~Din[13]);  // NAND_Gate
  nand nand_10 (nand_10_out, Din[13], WEin);
  nand nand_11 (out_5, nand_12_out, nand_10_out);
  nand nand_12 (nand_12_out, nand_9_out, out_5);
  nand nand_13 (nand_13_out, WEin, ~Din[12]);  // NAND_Gate
  nand nand_14 (nand_14_out, nand_13_out, out_6);
  nand nand_15 (nand_15_out, Din[12], WEin);
  nand nand_16 (nand_16_out, WEin, ~Din[11]);  // NAND_Gate
  nand nand_17 (out_6, nand_14_out, nand_15_out);
  nand nand_18 (nand_18_out, nand_16_out, out_7);
  nand nand_19 (nand_19_out, Din[11], WEin);
  nand nand_20 (nand_20_out, WEin, ~Din[10]);  // NAND_Gate
  nand nand_21 (nand_21_out, nand_20_out, out_8);
  nand nand_22 (out_7, nand_18_out, nand_19_out);
  nand nand_23 (nand_23_out, Din[10], WEin);
  nand nand_24 (out_8, nand_21_out, nand_23_out);
  nand nand_25 (nand_25_out, WEin, ~Din[9]);  // NAND_Gate
  nand nand_26 (nand_26_out, Din[9], WEin);
  nand nand_27 (out_9, nand_28_out, nand_26_out);
  nand nand_28 (nand_28_out, nand_25_out, out_9);
  nand nand_29 (nand_29_out, WEin, ~Din[8]);  // NAND_Gate
  nand nand_30 (nand_30_out, nand_29_out, out_10);
  nand nand_31 (nand_31_out, Din[8], WEin);
  nand nand_32 (nand_32_out, WEin, ~Din[7]);  // NAND_Gate
  nand nand_33 (nand_33_out, nand_32_out, out_11);
  nand nand_34 (out_10, nand_30_out, nand_31_out);
  nand nand_35 (nand_35_out, WEin, ~Din[6]);  // NAND_Gate
  nand nand_36 (nand_36_out, Din[7], WEin);
  nand nand_37 (out_11, nand_33_out, nand_36_out);
  nand nand_38 (nand_38_out, nand_35_out, out_12);
  nand nand_39 (nand_39_out, Din[6], WEin);
  nand nand_40 (out_12, nand_38_out, nand_39_out);
  nand nand_41 (nand_41_out, WEin, ~Din[5]);  // NAND_Gate
  nand nand_42 (nand_42_out, Din[5], WEin);
  nand nand_43 (out_13, nand_44_out, nand_42_out);
  nand nand_44 (nand_44_out, nand_41_out, out_13);
  nand nand_45 (nand_45_out, WEin, ~Din[4]);  // NAND_Gate
  nand nand_46 (nand_46_out, nand_45_out, out_14);
  nand nand_47 (nand_47_out, WEin, ~Din[3]);  // NAND_Gate
  nand nand_48 (nand_48_out, Din[4], WEin);
  nand nand_49 (out_14, nand_46_out, nand_48_out);
  nand nand_50 (nand_50_out, nand_47_out, out_15);
  nand nand_51 (nand_51_out, Din[3], WEin);
  nand nand_52 (nand_52_out, WEin, ~Din[2]);  // NAND_Gate
  nand nand_53 (out_15, nand_50_out, nand_51_out);
  nand nand_54 (nand_54_out, nand_52_out, out_16);
  nand nand_55 (nand_55_out, Din[2], WEin);
  nand nand_56 (out_16, nand_54_out, nand_55_out);
  nand nand_57 (nand_57_out, Din[1], WEin);
  nand nand_58 (nand_58_out, WEin, ~Din[1]);  // NAND_Gate
  nand nand_59 (out_17, nand_60_out, nand_57_out);
  nand nand_60 (nand_60_out, nand_58_out, out_17);
  nand nand_61 (nand_61_out, WEin, ~Din[0]);  // NAND_Gate
  nand nand_62 (nand_62_out, nand_61_out, out_18);
  nand nand_63 (nand_63_out, Din[0], WEin);
  nand nand_64 (out_18, nand_62_out, nand_63_out);
endmodule

module _16bit_RegSelector_Mux (
  input  in_1,
  input  in_2,
  input  in_3,
  input  in_4,
  input  in_5,
  input  in_6,
  input  in_7,
  input  in_8,
  input  in_9,
  input  in_10,
  input  in_11,
  input  in_12,
  input  in_13,
  input  in_14,
  input  in_15,
  input  in_16,
  input  in_17,
  output [15:0] Dout
);

  and and_1 (Dout[15], in_17, in_1);
  and and_2 (Dout[14], in_17, in_2);
  and and_3 (Dout[11], in_17, in_5);
  and and_4 (Dout[13], in_17, in_3);
  and and_5 (Dout[12], in_17, in_4);
  and and_6 (Dout[9], in_17, in_7);
  and and_7 (Dout[10], in_17, in_6);
  and and_8 (Dout[6], in_17, in_10);
  and and_9 (Dout[8], in_17, in_8);
  and and_10 (Dout[7], in_17, in_9);
  and and_11 (Dout[5], in_17, in_11);
  and and_12 (Dout[3], in_17, in_13);
  and and_13 (Dout[4], in_17, in_12);
  and and_14 (Dout[1], in_17, in_15);
  and and_15 (Dout[2], in_17, in_14);
  and and_16 (Dout[0], in_17, in_16);
endmodule

module PC_Addr_MEM (
  input  [3:0] AddrSel,
  input  WE,
  input  [15:0] Din,
  output [15:0] Dout
);

  wire and_1_out, and_2_out, and_3_out, and_4_out, and_5_out, and_6_out, and_7_out, and_8_out, and_9_out,
       and_10_out, and_11_out, and_12_out, and_13_out, and_14_out, and_15_out, and_16_out, and_17_out,
       and_18_out, and_19_out, and_20_out, and_21_out, and_22_out, and_23_out, and_24_out, and_25_out,
       and_26_out, and_27_out, and_28_out, and_29_out, and_30_out, and_31_out, and_32_out,
       n1by16bit_registry_1_out_3, n1by16bit_registry_1_out_4, n1by16bit_registry_1_out_5,
       n1by16bit_registry_1_out_6, n1by16bit_registry_1_out_7, n1by16bit_registry_1_out_8,
       n1by16bit_registry_1_out_9, n1by16bit_registry_1_out_10, n1by16bit_registry_1_out_11,
       n1by16bit_registry_1_out_12, n1by16bit_registry_1_out_13, n1by16bit_registry_1_out_14,
       n1by16bit_registry_1_out_15, n1by16bit_registry_1_out_16, n1by16bit_registry_1_out_17,
       n1by16bit_registry_1_out_18, n1by16bit_registry_2_out_3, n1by16bit_registry_2_out_4,
       n1by16bit_registry_2_out_5, n1by16bit_registry_2_out_6, n1by16bit_registry_2_out_7,
       n1by16bit_registry_2_out_8, n1by16bit_registry_2_out_9, n1by16bit_registry_2_out_10,
       n1by16bit_registry_2_out_11, n1by16bit_registry_2_out_12, n1by16bit_registry_2_out_13,
       n1by16bit_registry_2_out_14, n1by16bit_registry_2_out_15, n1by16bit_registry_2_out_16,
       n1by16bit_registry_2_out_17, n1by16bit_registry_2_out_18, n1by16bit_registry_3_out_3,
       n1by16bit_registry_3_out_4, n1by16bit_registry_3_out_5, n1by16bit_registry_3_out_6,
       n1by16bit_registry_3_out_7, n1by16bit_registry_3_out_8, n1by16bit_registry_3_out_9,
       n1by16bit_registry_3_out_10, n1by16bit_registry_3_out_11, n1by16bit_registry_3_out_12,
       n1by16bit_registry_3_out_13, n1by16bit_registry_3_out_14, n1by16bit_registry_3_out_15,
       n1by16bit_registry_3_out_16, n1by16bit_registry_3_out_17, n1by16bit_registry_3_out_18,
       n1by16bit_registry_4_out_3, n1by16bit_registry_4_out_4, n1by16bit_registry_4_out_5,
       n1by16bit_registry_4_out_6, n1by16bit_registry_4_out_7, n1by16bit_registry_4_out_8,
       n1by16bit_registry_4_out_9, n1by16bit_registry_4_out_10, n1by16bit_registry_4_out_11,
       n1by16bit_registry_4_out_12, n1by16bit_registry_4_out_13, n1by16bit_registry_4_out_14,
       n1by16bit_registry_4_out_15, n1by16bit_registry_4_out_16, n1by16bit_registry_4_out_17,
       n1by16bit_registry_4_out_18, n1by16bit_registry_5_out_3, n1by16bit_registry_5_out_4,
       n1by16bit_registry_5_out_5, n1by16bit_registry_5_out_6, n1by16bit_registry_5_out_7,
       n1by16bit_registry_5_out_8, n1by16bit_registry_5_out_9, n1by16bit_registry_5_out_10,
       n1by16bit_registry_5_out_11, n1by16bit_registry_5_out_12, n1by16bit_registry_5_out_13,
       n1by16bit_registry_5_out_14, n1by16bit_registry_5_out_15, n1by16bit_registry_5_out_16,
       n1by16bit_registry_5_out_17, n1by16bit_registry_5_out_18, n1by16bit_registry_6_out_3,
       n1by16bit_registry_6_out_4, n1by16bit_registry_6_out_5, n1by16bit_registry_6_out_6,
       n1by16bit_registry_6_out_7, n1by16bit_registry_6_out_8, n1by16bit_registry_6_out_9,
       n1by16bit_registry_6_out_10, n1by16bit_registry_6_out_11, n1by16bit_registry_6_out_12,
       n1by16bit_registry_6_out_13, n1by16bit_registry_6_out_14, n1by16bit_registry_6_out_15,
       n1by16bit_registry_6_out_16, n1by16bit_registry_6_out_17, n1by16bit_registry_6_out_18,
       n1by16bit_registry_7_out_3, n1by16bit_registry_7_out_4, n1by16bit_registry_7_out_5,
       n1by16bit_registry_7_out_6, n1by16bit_registry_7_out_7, n1by16bit_registry_7_out_8,
       n1by16bit_registry_7_out_9, n1by16bit_registry_7_out_10, n1by16bit_registry_7_out_11,
       n1by16bit_registry_7_out_12, n1by16bit_registry_7_out_13, n1by16bit_registry_7_out_14,
       n1by16bit_registry_7_out_15, n1by16bit_registry_7_out_16, n1by16bit_registry_7_out_17,
       n1by16bit_registry_7_out_18, n1by16bit_registry_8_out_3, n1by16bit_registry_8_out_4,
       n1by16bit_registry_8_out_5, n1by16bit_registry_8_out_6, n1by16bit_registry_8_out_7,
       n1by16bit_registry_8_out_8, n1by16bit_registry_8_out_9, n1by16bit_registry_8_out_10,
       n1by16bit_registry_8_out_11, n1by16bit_registry_8_out_12, n1by16bit_registry_8_out_13,
       n1by16bit_registry_8_out_14, n1by16bit_registry_8_out_15, n1by16bit_registry_8_out_16,
       n1by16bit_registry_8_out_17, n1by16bit_registry_8_out_18, n1by16bit_registry_9_out_3,
       n1by16bit_registry_9_out_4, n1by16bit_registry_9_out_5, n1by16bit_registry_9_out_6,
       n1by16bit_registry_9_out_7, n1by16bit_registry_9_out_8, n1by16bit_registry_9_out_9,
       n1by16bit_registry_9_out_10, n1by16bit_registry_9_out_11, n1by16bit_registry_9_out_12,
       n1by16bit_registry_9_out_13, n1by16bit_registry_9_out_14, n1by16bit_registry_9_out_15,
       n1by16bit_registry_9_out_16, n1by16bit_registry_9_out_17, n1by16bit_registry_9_out_18,
       n1by16bit_registry_10_out_3, n1by16bit_registry_10_out_4, n1by16bit_registry_10_out_5,
       n1by16bit_registry_10_out_6, n1by16bit_registry_10_out_7, n1by16bit_registry_10_out_8,
       n1by16bit_registry_10_out_9, n1by16bit_registry_10_out_10, n1by16bit_registry_10_out_11,
       n1by16bit_registry_10_out_12, n1by16bit_registry_10_out_13, n1by16bit_registry_10_out_14,
       n1by16bit_registry_10_out_15, n1by16bit_registry_10_out_16, n1by16bit_registry_10_out_17,
       n1by16bit_registry_10_out_18, n1by16bit_registry_11_out_3, n1by16bit_registry_11_out_4,
       n1by16bit_registry_11_out_5, n1by16bit_registry_11_out_6, n1by16bit_registry_11_out_7,
       n1by16bit_registry_11_out_8, n1by16bit_registry_11_out_9, n1by16bit_registry_11_out_10,
       n1by16bit_registry_11_out_11, n1by16bit_registry_11_out_12, n1by16bit_registry_11_out_13,
       n1by16bit_registry_11_out_14, n1by16bit_registry_11_out_15, n1by16bit_registry_11_out_16,
       n1by16bit_registry_11_out_17, n1by16bit_registry_11_out_18, n1by16bit_registry_12_out_3,
       n1by16bit_registry_12_out_4, n1by16bit_registry_12_out_5, n1by16bit_registry_12_out_6,
       n1by16bit_registry_12_out_7, n1by16bit_registry_12_out_8, n1by16bit_registry_12_out_9,
       n1by16bit_registry_12_out_10, n1by16bit_registry_12_out_11, n1by16bit_registry_12_out_12,
       n1by16bit_registry_12_out_13, n1by16bit_registry_12_out_14, n1by16bit_registry_12_out_15,
       n1by16bit_registry_12_out_16, n1by16bit_registry_12_out_17, n1by16bit_registry_12_out_18,
       n1by16bit_registry_13_out_3, n1by16bit_registry_13_out_4, n1by16bit_registry_13_out_5,
       n1by16bit_registry_13_out_6, n1by16bit_registry_13_out_7, n1by16bit_registry_13_out_8,
       n1by16bit_registry_13_out_9, n1by16bit_registry_13_out_10, n1by16bit_registry_13_out_11,
       n1by16bit_registry_13_out_12, n1by16bit_registry_13_out_13, n1by16bit_registry_13_out_14,
       n1by16bit_registry_13_out_15, n1by16bit_registry_13_out_16, n1by16bit_registry_13_out_17,
       n1by16bit_registry_13_out_18, n1by16bit_registry_14_out_3, n1by16bit_registry_14_out_4,
       n1by16bit_registry_14_out_5, n1by16bit_registry_14_out_6, n1by16bit_registry_14_out_7,
       n1by16bit_registry_14_out_8, n1by16bit_registry_14_out_9, n1by16bit_registry_14_out_10,
       n1by16bit_registry_14_out_11, n1by16bit_registry_14_out_12, n1by16bit_registry_14_out_13,
       n1by16bit_registry_14_out_14, n1by16bit_registry_14_out_15, n1by16bit_registry_14_out_16,
       n1by16bit_registry_14_out_17, n1by16bit_registry_14_out_18, n1by16bit_registry_15_out_3,
       n1by16bit_registry_15_out_4, n1by16bit_registry_15_out_5, n1by16bit_registry_15_out_6,
       n1by16bit_registry_15_out_7, n1by16bit_registry_15_out_8, n1by16bit_registry_15_out_9,
       n1by16bit_registry_15_out_10, n1by16bit_registry_15_out_11, n1by16bit_registry_15_out_12,
       n1by16bit_registry_15_out_13, n1by16bit_registry_15_out_14, n1by16bit_registry_15_out_15,
       n1by16bit_registry_15_out_16, n1by16bit_registry_15_out_17, n1by16bit_registry_15_out_18,
       n1by16bit_registry_16_out_3, n1by16bit_registry_16_out_4, n1by16bit_registry_16_out_5,
       n1by16bit_registry_16_out_6, n1by16bit_registry_16_out_7, n1by16bit_registry_16_out_8,
       n1by16bit_registry_16_out_9, n1by16bit_registry_16_out_10, n1by16bit_registry_16_out_11,
       n1by16bit_registry_16_out_12, n1by16bit_registry_16_out_13, n1by16bit_registry_16_out_14,
       n1by16bit_registry_16_out_15, n1by16bit_registry_16_out_16, n1by16bit_registry_16_out_17,
       n1by16bit_registry_16_out_18;
  wire [15:0] n16bit_regselector_mux_1_dout, n16bit_regselector_mux_2_dout, n16bit_regselector_mux_3_dout,
       n16bit_regselector_mux_4_dout, n16bit_regselector_mux_5_dout, n16bit_regselector_mux_6_dout,
       n16bit_regselector_mux_7_dout, n16bit_regselector_mux_8_dout, n16bit_regselector_mux_9_dout,
       n16bit_regselector_mux_10_dout, n16bit_regselector_mux_11_dout, n16bit_regselector_mux_12_dout,
       n16bit_regselector_mux_13_dout, n16bit_regselector_mux_14_dout, n16bit_regselector_mux_15_dout,
       n16bit_regselector_mux_16_dout;

  and and_1 (and_1_out, ~AddrSel[0], ~AddrSel[1], ~AddrSel[2], ~AddrSel[3]);  // AND_Gate
  and and_2 (and_2_out, AddrSel[0], ~AddrSel[1], ~AddrSel[2], ~AddrSel[3]);  // AND_Gate
  and and_3 (and_3_out, ~AddrSel[0], AddrSel[1], ~AddrSel[2], ~AddrSel[3]);  // AND_Gate
  and and_4 (and_4_out, AddrSel[0], AddrSel[1], ~AddrSel[2], ~AddrSel[3]);  // AND_Gate
  and and_5 (and_5_out, ~AddrSel[0], ~AddrSel[1], AddrSel[2], ~AddrSel[3]);  // AND_Gate
  and and_6 (and_6_out, AddrSel[0], ~AddrSel[1], AddrSel[2], ~AddrSel[3]);  // AND_Gate
  and and_7 (and_7_out, ~AddrSel[0], AddrSel[1], AddrSel[2], ~AddrSel[3]);  // AND_Gate
  and and_8 (and_8_out, AddrSel[0], AddrSel[1], AddrSel[2], ~AddrSel[3]);  // AND_Gate
  and and_9 (and_9_out, ~AddrSel[0], ~AddrSel[1], ~AddrSel[2], AddrSel[3]);  // AND_Gate
  and and_10 (and_10_out, AddrSel[0], ~AddrSel[1], ~AddrSel[2], AddrSel[3]);  // AND_Gate
  and and_11 (and_11_out, ~AddrSel[0], AddrSel[1], ~AddrSel[2], AddrSel[3]);  // AND_Gate
  and and_12 (and_12_out, AddrSel[0], AddrSel[1], ~AddrSel[2], AddrSel[3]);  // AND_Gate
  and and_13 (and_13_out, ~AddrSel[0], ~AddrSel[1], AddrSel[2], AddrSel[3]);  // AND_Gate
  and and_14 (and_14_out, AddrSel[0], ~AddrSel[1], AddrSel[2], AddrSel[3]);  // AND_Gate
  and and_15 (and_15_out, ~AddrSel[0], AddrSel[1], AddrSel[2], AddrSel[3]);  // AND_Gate
  and and_16 (and_16_out, AddrSel[0], AddrSel[1], AddrSel[2], AddrSel[3]);
  and and_17 (and_17_out, and_1_out, WE);
  and and_18 (and_18_out, and_2_out, WE);
  and and_19 (and_19_out, and_3_out, WE);
  and and_20 (and_20_out, and_4_out, WE);
  and and_21 (and_21_out, and_5_out, WE);
  and and_22 (and_22_out, and_6_out, WE);
  and and_23 (and_23_out, and_7_out, WE);
  and and_24 (and_24_out, and_8_out, WE);
  and and_25 (and_25_out, and_9_out, WE);
  and and_26 (and_26_out, and_10_out, WE);
  and and_27 (and_27_out, and_11_out, WE);
  and and_28 (and_28_out, and_12_out, WE);
  and and_29 (and_29_out, and_13_out, WE);
  and and_30 (and_30_out, and_14_out, WE);
  and and_31 (and_31_out, and_15_out, WE);
  and and_32 (and_32_out, and_16_out, WE);
  _16bit_RegSelector_Mux u_16bit_regselector_mux_1 (
    .in_17(and_1_out), .in_1(n1by16bit_registry_1_out_3), .in_2(n1by16bit_registry_1_out_4),
    .in_3(n1by16bit_registry_1_out_5), .in_4(n1by16bit_registry_1_out_6), .in_5(n1by16bit_registry_1_out_7),
    .in_6(n1by16bit_registry_1_out_8), .in_7(n1by16bit_registry_1_out_9), .in_8(n1by16bit_registry_1_out_10),
    .in_9(n1by16bit_registry_1_out_11), .in_10(n1by16bit_registry_1_out_12),
    .in_11(n1by16bit_registry_1_out_13), .in_12(n1by16bit_registry_1_out_14),
    .in_13(n1by16bit_registry_1_out_15), .in_14(n1by16bit_registry_1_out_16),
    .in_15(n1by16bit_registry_1_out_17), .in_16(n1by16bit_registry_1_out_18),
    .Dout(n16bit_regselector_mux_1_dout));
  _16bit_RegSelector_Mux u_16bit_regselector_mux_2 (
    .in_17(and_2_out), .in_1(n1by16bit_registry_2_out_3), .in_2(n1by16bit_registry_2_out_4),
    .in_3(n1by16bit_registry_2_out_5), .in_4(n1by16bit_registry_2_out_6), .in_5(n1by16bit_registry_2_out_7),
    .in_6(n1by16bit_registry_2_out_8), .in_7(n1by16bit_registry_2_out_9), .in_8(n1by16bit_registry_2_out_10),
    .in_9(n1by16bit_registry_2_out_11), .in_10(n1by16bit_registry_2_out_12),
    .in_11(n1by16bit_registry_2_out_13), .in_12(n1by16bit_registry_2_out_14),
    .in_13(n1by16bit_registry_2_out_15), .in_14(n1by16bit_registry_2_out_16),
    .in_15(n1by16bit_registry_2_out_17), .in_16(n1by16bit_registry_2_out_18),
    .Dout(n16bit_regselector_mux_2_dout));
  _16bit_RegSelector_Mux u_16bit_regselector_mux_3 (
    .in_17(and_3_out), .in_1(n1by16bit_registry_3_out_3), .in_2(n1by16bit_registry_3_out_4),
    .in_3(n1by16bit_registry_3_out_5), .in_4(n1by16bit_registry_3_out_6), .in_5(n1by16bit_registry_3_out_7),
    .in_6(n1by16bit_registry_3_out_8), .in_7(n1by16bit_registry_3_out_9), .in_8(n1by16bit_registry_3_out_10),
    .in_9(n1by16bit_registry_3_out_11), .in_10(n1by16bit_registry_3_out_12),
    .in_11(n1by16bit_registry_3_out_13), .in_12(n1by16bit_registry_3_out_14),
    .in_13(n1by16bit_registry_3_out_15), .in_14(n1by16bit_registry_3_out_16),
    .in_15(n1by16bit_registry_3_out_17), .in_16(n1by16bit_registry_3_out_18),
    .Dout(n16bit_regselector_mux_3_dout));
  _16bit_RegSelector_Mux u_16bit_regselector_mux_4 (
    .in_17(and_4_out), .in_1(n1by16bit_registry_4_out_3), .in_2(n1by16bit_registry_4_out_4),
    .in_3(n1by16bit_registry_4_out_5), .in_4(n1by16bit_registry_4_out_6), .in_5(n1by16bit_registry_4_out_7),
    .in_6(n1by16bit_registry_4_out_8), .in_7(n1by16bit_registry_4_out_9), .in_8(n1by16bit_registry_4_out_10),
    .in_9(n1by16bit_registry_4_out_11), .in_10(n1by16bit_registry_4_out_12),
    .in_11(n1by16bit_registry_4_out_13), .in_12(n1by16bit_registry_4_out_14),
    .in_13(n1by16bit_registry_4_out_15), .in_14(n1by16bit_registry_4_out_16),
    .in_15(n1by16bit_registry_4_out_17), .in_16(n1by16bit_registry_4_out_18),
    .Dout(n16bit_regselector_mux_4_dout));
  _16bit_RegSelector_Mux u_16bit_regselector_mux_5 (
    .in_17(and_5_out), .in_1(n1by16bit_registry_5_out_3), .in_2(n1by16bit_registry_5_out_4),
    .in_3(n1by16bit_registry_5_out_5), .in_4(n1by16bit_registry_5_out_6), .in_5(n1by16bit_registry_5_out_7),
    .in_6(n1by16bit_registry_5_out_8), .in_7(n1by16bit_registry_5_out_9), .in_8(n1by16bit_registry_5_out_10),
    .in_9(n1by16bit_registry_5_out_11), .in_10(n1by16bit_registry_5_out_12),
    .in_11(n1by16bit_registry_5_out_13), .in_12(n1by16bit_registry_5_out_14),
    .in_13(n1by16bit_registry_5_out_15), .in_14(n1by16bit_registry_5_out_16),
    .in_15(n1by16bit_registry_5_out_17), .in_16(n1by16bit_registry_5_out_18),
    .Dout(n16bit_regselector_mux_5_dout));
  _16bit_RegSelector_Mux u_16bit_regselector_mux_6 (
    .in_17(and_6_out), .in_1(n1by16bit_registry_6_out_3), .in_2(n1by16bit_registry_6_out_4),
    .in_3(n1by16bit_registry_6_out_5), .in_4(n1by16bit_registry_6_out_6), .in_5(n1by16bit_registry_6_out_7),
    .in_6(n1by16bit_registry_6_out_8), .in_7(n1by16bit_registry_6_out_9), .in_8(n1by16bit_registry_6_out_10),
    .in_9(n1by16bit_registry_6_out_11), .in_10(n1by16bit_registry_6_out_12),
    .in_11(n1by16bit_registry_6_out_13), .in_12(n1by16bit_registry_6_out_14),
    .in_13(n1by16bit_registry_6_out_15), .in_14(n1by16bit_registry_6_out_16),
    .in_15(n1by16bit_registry_6_out_17), .in_16(n1by16bit_registry_6_out_18),
    .Dout(n16bit_regselector_mux_6_dout));
  _16bit_RegSelector_Mux u_16bit_regselector_mux_7 (
    .in_17(and_7_out), .in_1(n1by16bit_registry_7_out_3), .in_2(n1by16bit_registry_7_out_4),
    .in_3(n1by16bit_registry_7_out_5), .in_4(n1by16bit_registry_7_out_6), .in_5(n1by16bit_registry_7_out_7),
    .in_6(n1by16bit_registry_7_out_8), .in_7(n1by16bit_registry_7_out_9), .in_8(n1by16bit_registry_7_out_10),
    .in_9(n1by16bit_registry_7_out_11), .in_10(n1by16bit_registry_7_out_12),
    .in_11(n1by16bit_registry_7_out_13), .in_12(n1by16bit_registry_7_out_14),
    .in_13(n1by16bit_registry_7_out_15), .in_14(n1by16bit_registry_7_out_16),
    .in_15(n1by16bit_registry_7_out_17), .in_16(n1by16bit_registry_7_out_18),
    .Dout(n16bit_regselector_mux_7_dout));
  _16bit_RegSelector_Mux u_16bit_regselector_mux_8 (
    .in_17(and_8_out), .in_1(n1by16bit_registry_8_out_3), .in_2(n1by16bit_registry_8_out_4),
    .in_3(n1by16bit_registry_8_out_5), .in_4(n1by16bit_registry_8_out_6), .in_5(n1by16bit_registry_8_out_7),
    .in_6(n1by16bit_registry_8_out_8), .in_7(n1by16bit_registry_8_out_9), .in_8(n1by16bit_registry_8_out_10),
    .in_9(n1by16bit_registry_8_out_11), .in_10(n1by16bit_registry_8_out_12),
    .in_11(n1by16bit_registry_8_out_13), .in_12(n1by16bit_registry_8_out_14),
    .in_13(n1by16bit_registry_8_out_15), .in_14(n1by16bit_registry_8_out_16),
    .in_15(n1by16bit_registry_8_out_17), .in_16(n1by16bit_registry_8_out_18),
    .Dout(n16bit_regselector_mux_8_dout));
  _16bit_RegSelector_Mux u_16bit_regselector_mux_9 (
    .in_17(and_9_out), .in_1(n1by16bit_registry_9_out_3), .in_2(n1by16bit_registry_9_out_4),
    .in_3(n1by16bit_registry_9_out_5), .in_4(n1by16bit_registry_9_out_6), .in_5(n1by16bit_registry_9_out_7),
    .in_6(n1by16bit_registry_9_out_8), .in_7(n1by16bit_registry_9_out_9), .in_8(n1by16bit_registry_9_out_10),
    .in_9(n1by16bit_registry_9_out_11), .in_10(n1by16bit_registry_9_out_12),
    .in_11(n1by16bit_registry_9_out_13), .in_12(n1by16bit_registry_9_out_14),
    .in_13(n1by16bit_registry_9_out_15), .in_14(n1by16bit_registry_9_out_16),
    .in_15(n1by16bit_registry_9_out_17), .in_16(n1by16bit_registry_9_out_18),
    .Dout(n16bit_regselector_mux_9_dout));
  _16bit_RegSelector_Mux u_16bit_regselector_mux_10 (
    .in_17(and_10_out), .in_1(n1by16bit_registry_10_out_3), .in_2(n1by16bit_registry_10_out_4),
    .in_3(n1by16bit_registry_10_out_5), .in_4(n1by16bit_registry_10_out_6),
    .in_5(n1by16bit_registry_10_out_7), .in_6(n1by16bit_registry_10_out_8),
    .in_7(n1by16bit_registry_10_out_9), .in_8(n1by16bit_registry_10_out_10),
    .in_9(n1by16bit_registry_10_out_11), .in_10(n1by16bit_registry_10_out_12),
    .in_11(n1by16bit_registry_10_out_13), .in_12(n1by16bit_registry_10_out_14),
    .in_13(n1by16bit_registry_10_out_15), .in_14(n1by16bit_registry_10_out_16),
    .in_15(n1by16bit_registry_10_out_17), .in_16(n1by16bit_registry_10_out_18),
    .Dout(n16bit_regselector_mux_10_dout));
  _16bit_RegSelector_Mux u_16bit_regselector_mux_11 (
    .in_17(and_11_out), .in_1(n1by16bit_registry_11_out_3), .in_2(n1by16bit_registry_11_out_4),
    .in_3(n1by16bit_registry_11_out_5), .in_4(n1by16bit_registry_11_out_6),
    .in_5(n1by16bit_registry_11_out_7), .in_6(n1by16bit_registry_11_out_8),
    .in_7(n1by16bit_registry_11_out_9), .in_8(n1by16bit_registry_11_out_10),
    .in_9(n1by16bit_registry_11_out_11), .in_10(n1by16bit_registry_11_out_12),
    .in_11(n1by16bit_registry_11_out_13), .in_12(n1by16bit_registry_11_out_14),
    .in_13(n1by16bit_registry_11_out_15), .in_14(n1by16bit_registry_11_out_16),
    .in_15(n1by16bit_registry_11_out_17), .in_16(n1by16bit_registry_11_out_18),
    .Dout(n16bit_regselector_mux_11_dout));
  _16bit_RegSelector_Mux u_16bit_regselector_mux_12 (
    .in_17(and_12_out), .in_1(n1by16bit_registry_12_out_3), .in_2(n1by16bit_registry_12_out_4),
    .in_3(n1by16bit_registry_12_out_5), .in_4(n1by16bit_registry_12_out_6),
    .in_5(n1by16bit_registry_12_out_7), .in_6(n1by16bit_registry_12_out_8),
    .in_7(n1by16bit_registry_12_out_9), .in_8(n1by16bit_registry_12_out_10),
    .in_9(n1by16bit_registry_12_out_11), .in_10(n1by16bit_registry_12_out_12),
    .in_11(n1by16bit_registry_12_out_13), .in_12(n1by16bit_registry_12_out_14),
    .in_13(n1by16bit_registry_12_out_15), .in_14(n1by16bit_registry_12_out_16),
    .in_15(n1by16bit_registry_12_out_17), .in_16(n1by16bit_registry_12_out_18),
    .Dout(n16bit_regselector_mux_12_dout));
  _16bit_RegSelector_Mux u_16bit_regselector_mux_13 (
    .in_17(and_13_out), .in_1(n1by16bit_registry_13_out_3), .in_2(n1by16bit_registry_13_out_4),
    .in_3(n1by16bit_registry_13_out_5), .in_4(n1by16bit_registry_13_out_6),
    .in_5(n1by16bit_registry_13_out_7), .in_6(n1by16bit_registry_13_out_8),
    .in_7(n1by16bit_registry_13_out_9), .in_8(n1by16bit_registry_13_out_10),
    .in_9(n1by16bit_registry_13_out_11), .in_10(n1by16bit_registry_13_out_12),
    .in_11(n1by16bit_registry_13_out_13), .in_12(n1by16bit_registry_13_out_14),
    .in_13(n1by16bit_registry_13_out_15), .in_14(n1by16bit_registry_13_out_16),
    .in_15(n1by16bit_registry_13_out_17), .in_16(n1by16bit_registry_13_out_18),
    .Dout(n16bit_regselector_mux_13_dout));
  _16bit_RegSelector_Mux u_16bit_regselector_mux_14 (
    .in_17(and_14_out), .in_1(n1by16bit_registry_14_out_3), .in_2(n1by16bit_registry_14_out_4),
    .in_3(n1by16bit_registry_14_out_5), .in_4(n1by16bit_registry_14_out_6),
    .in_5(n1by16bit_registry_14_out_7), .in_6(n1by16bit_registry_14_out_8),
    .in_7(n1by16bit_registry_14_out_9), .in_8(n1by16bit_registry_14_out_10),
    .in_9(n1by16bit_registry_14_out_11), .in_10(n1by16bit_registry_14_out_12),
    .in_11(n1by16bit_registry_14_out_13), .in_12(n1by16bit_registry_14_out_14),
    .in_13(n1by16bit_registry_14_out_15), .in_14(n1by16bit_registry_14_out_16),
    .in_15(n1by16bit_registry_14_out_17), .in_16(n1by16bit_registry_14_out_18),
    .Dout(n16bit_regselector_mux_14_dout));
  _16bit_RegSelector_Mux u_16bit_regselector_mux_15 (
    .in_17(and_15_out), .in_1(n1by16bit_registry_15_out_3), .in_2(n1by16bit_registry_15_out_4),
    .in_3(n1by16bit_registry_15_out_5), .in_4(n1by16bit_registry_15_out_6),
    .in_5(n1by16bit_registry_15_out_7), .in_6(n1by16bit_registry_15_out_8),
    .in_7(n1by16bit_registry_15_out_9), .in_8(n1by16bit_registry_15_out_10),
    .in_9(n1by16bit_registry_15_out_11), .in_10(n1by16bit_registry_15_out_12),
    .in_11(n1by16bit_registry_15_out_13), .in_12(n1by16bit_registry_15_out_14),
    .in_13(n1by16bit_registry_15_out_15), .in_14(n1by16bit_registry_15_out_16),
    .in_15(n1by16bit_registry_15_out_17), .in_16(n1by16bit_registry_15_out_18),
    .Dout(n16bit_regselector_mux_15_dout));
  _16bit_RegSelector_Mux u_16bit_regselector_mux_16 (
    .in_17(and_16_out), .in_1(n1by16bit_registry_16_out_3), .in_2(n1by16bit_registry_16_out_4),
    .in_3(n1by16bit_registry_16_out_5), .in_4(n1by16bit_registry_16_out_6),
    .in_5(n1by16bit_registry_16_out_7), .in_6(n1by16bit_registry_16_out_8),
    .in_7(n1by16bit_registry_16_out_9), .in_8(n1by16bit_registry_16_out_10),
    .in_9(n1by16bit_registry_16_out_11), .in_10(n1by16bit_registry_16_out_12),
    .in_11(n1by16bit_registry_16_out_13), .in_12(n1by16bit_registry_16_out_14),
    .in_13(n1by16bit_registry_16_out_15), .in_14(n1by16bit_registry_16_out_16),
    .in_15(n1by16bit_registry_16_out_17), .in_16(n1by16bit_registry_16_out_18),
    .Dout(n16bit_regselector_mux_16_dout));
  _1by16bit_Registry u_1by16bit_registry_1 (
    .WEin(and_17_out), .Din(Din), .out_3(n1by16bit_registry_1_out_3), .out_4(n1by16bit_registry_1_out_4),
    .out_5(n1by16bit_registry_1_out_5), .out_6(n1by16bit_registry_1_out_6),
    .out_7(n1by16bit_registry_1_out_7), .out_8(n1by16bit_registry_1_out_8),
    .out_9(n1by16bit_registry_1_out_9), .out_10(n1by16bit_registry_1_out_10),
    .out_11(n1by16bit_registry_1_out_11), .out_12(n1by16bit_registry_1_out_12),
    .out_13(n1by16bit_registry_1_out_13), .out_14(n1by16bit_registry_1_out_14),
    .out_15(n1by16bit_registry_1_out_15), .out_16(n1by16bit_registry_1_out_16),
    .out_17(n1by16bit_registry_1_out_17), .out_18(n1by16bit_registry_1_out_18));
  _1by16bit_Registry u_1by16bit_registry_2 (
    .WEin(and_18_out), .Din(Din), .out_3(n1by16bit_registry_2_out_3), .out_4(n1by16bit_registry_2_out_4),
    .out_5(n1by16bit_registry_2_out_5), .out_6(n1by16bit_registry_2_out_6),
    .out_7(n1by16bit_registry_2_out_7), .out_8(n1by16bit_registry_2_out_8),
    .out_9(n1by16bit_registry_2_out_9), .out_10(n1by16bit_registry_2_out_10),
    .out_11(n1by16bit_registry_2_out_11), .out_12(n1by16bit_registry_2_out_12),
    .out_13(n1by16bit_registry_2_out_13), .out_14(n1by16bit_registry_2_out_14),
    .out_15(n1by16bit_registry_2_out_15), .out_16(n1by16bit_registry_2_out_16),
    .out_17(n1by16bit_registry_2_out_17), .out_18(n1by16bit_registry_2_out_18));
  _1by16bit_Registry u_1by16bit_registry_3 (
    .WEin(and_19_out), .Din(Din), .out_3(n1by16bit_registry_3_out_3), .out_4(n1by16bit_registry_3_out_4),
    .out_5(n1by16bit_registry_3_out_5), .out_6(n1by16bit_registry_3_out_6),
    .out_7(n1by16bit_registry_3_out_7), .out_8(n1by16bit_registry_3_out_8),
    .out_9(n1by16bit_registry_3_out_9), .out_10(n1by16bit_registry_3_out_10),
    .out_11(n1by16bit_registry_3_out_11), .out_12(n1by16bit_registry_3_out_12),
    .out_13(n1by16bit_registry_3_out_13), .out_14(n1by16bit_registry_3_out_14),
    .out_15(n1by16bit_registry_3_out_15), .out_16(n1by16bit_registry_3_out_16),
    .out_17(n1by16bit_registry_3_out_17), .out_18(n1by16bit_registry_3_out_18));
  _1by16bit_Registry u_1by16bit_registry_4 (
    .WEin(and_20_out), .Din(Din), .out_3(n1by16bit_registry_4_out_3), .out_4(n1by16bit_registry_4_out_4),
    .out_5(n1by16bit_registry_4_out_5), .out_6(n1by16bit_registry_4_out_6),
    .out_7(n1by16bit_registry_4_out_7), .out_8(n1by16bit_registry_4_out_8),
    .out_9(n1by16bit_registry_4_out_9), .out_10(n1by16bit_registry_4_out_10),
    .out_11(n1by16bit_registry_4_out_11), .out_12(n1by16bit_registry_4_out_12),
    .out_13(n1by16bit_registry_4_out_13), .out_14(n1by16bit_registry_4_out_14),
    .out_15(n1by16bit_registry_4_out_15), .out_16(n1by16bit_registry_4_out_16),
    .out_17(n1by16bit_registry_4_out_17), .out_18(n1by16bit_registry_4_out_18));
  _1by16bit_Registry u_1by16bit_registry_5 (
    .WEin(and_21_out), .Din(Din), .out_3(n1by16bit_registry_5_out_3), .out_4(n1by16bit_registry_5_out_4),
    .out_5(n1by16bit_registry_5_out_5), .out_6(n1by16bit_registry_5_out_6),
    .out_7(n1by16bit_registry_5_out_7), .out_8(n1by16bit_registry_5_out_8),
    .out_9(n1by16bit_registry_5_out_9), .out_10(n1by16bit_registry_5_out_10),
    .out_11(n1by16bit_registry_5_out_11), .out_12(n1by16bit_registry_5_out_12),
    .out_13(n1by16bit_registry_5_out_13), .out_14(n1by16bit_registry_5_out_14),
    .out_15(n1by16bit_registry_5_out_15), .out_16(n1by16bit_registry_5_out_16),
    .out_17(n1by16bit_registry_5_out_17), .out_18(n1by16bit_registry_5_out_18));
  _1by16bit_Registry u_1by16bit_registry_6 (
    .WEin(and_22_out), .Din(Din), .out_3(n1by16bit_registry_6_out_3), .out_4(n1by16bit_registry_6_out_4),
    .out_5(n1by16bit_registry_6_out_5), .out_6(n1by16bit_registry_6_out_6),
    .out_7(n1by16bit_registry_6_out_7), .out_8(n1by16bit_registry_6_out_8),
    .out_9(n1by16bit_registry_6_out_9), .out_10(n1by16bit_registry_6_out_10),
    .out_11(n1by16bit_registry_6_out_11), .out_12(n1by16bit_registry_6_out_12),
    .out_13(n1by16bit_registry_6_out_13), .out_14(n1by16bit_registry_6_out_14),
    .out_15(n1by16bit_registry_6_out_15), .out_16(n1by16bit_registry_6_out_16),
    .out_17(n1by16bit_registry_6_out_17), .out_18(n1by16bit_registry_6_out_18));
  _1by16bit_Registry u_1by16bit_registry_7 (
    .WEin(and_23_out), .Din(Din), .out_3(n1by16bit_registry_7_out_3), .out_4(n1by16bit_registry_7_out_4),
    .out_5(n1by16bit_registry_7_out_5), .out_6(n1by16bit_registry_7_out_6),
    .out_7(n1by16bit_registry_7_out_7), .out_8(n1by16bit_registry_7_out_8),
    .out_9(n1by16bit_registry_7_out_9), .out_10(n1by16bit_registry_7_out_10),
    .out_11(n1by16bit_registry_7_out_11), .out_12(n1by16bit_registry_7_out_12),
    .out_13(n1by16bit_registry_7_out_13), .out_14(n1by16bit_registry_7_out_14),
    .out_15(n1by16bit_registry_7_out_15), .out_16(n1by16bit_registry_7_out_16),
    .out_17(n1by16bit_registry_7_out_17), .out_18(n1by16bit_registry_7_out_18));
  _1by16bit_Registry u_1by16bit_registry_8 (
    .WEin(and_24_out), .Din(Din), .out_3(n1by16bit_registry_8_out_3), .out_4(n1by16bit_registry_8_out_4),
    .out_5(n1by16bit_registry_8_out_5), .out_6(n1by16bit_registry_8_out_6),
    .out_7(n1by16bit_registry_8_out_7), .out_8(n1by16bit_registry_8_out_8),
    .out_9(n1by16bit_registry_8_out_9), .out_10(n1by16bit_registry_8_out_10),
    .out_11(n1by16bit_registry_8_out_11), .out_12(n1by16bit_registry_8_out_12),
    .out_13(n1by16bit_registry_8_out_13), .out_14(n1by16bit_registry_8_out_14),
    .out_15(n1by16bit_registry_8_out_15), .out_16(n1by16bit_registry_8_out_16),
    .out_17(n1by16bit_registry_8_out_17), .out_18(n1by16bit_registry_8_out_18));
  _1by16bit_Registry u_1by16bit_registry_9 (
    .WEin(and_25_out), .Din(Din), .out_3(n1by16bit_registry_9_out_3), .out_4(n1by16bit_registry_9_out_4),
    .out_5(n1by16bit_registry_9_out_5), .out_6(n1by16bit_registry_9_out_6),
    .out_7(n1by16bit_registry_9_out_7), .out_8(n1by16bit_registry_9_out_8),
    .out_9(n1by16bit_registry_9_out_9), .out_10(n1by16bit_registry_9_out_10),
    .out_11(n1by16bit_registry_9_out_11), .out_12(n1by16bit_registry_9_out_12),
    .out_13(n1by16bit_registry_9_out_13), .out_14(n1by16bit_registry_9_out_14),
    .out_15(n1by16bit_registry_9_out_15), .out_16(n1by16bit_registry_9_out_16),
    .out_17(n1by16bit_registry_9_out_17), .out_18(n1by16bit_registry_9_out_18));
  _1by16bit_Registry u_1by16bit_registry_10 (
    .WEin(and_26_out), .Din(Din), .out_3(n1by16bit_registry_10_out_3), .out_4(n1by16bit_registry_10_out_4),
    .out_5(n1by16bit_registry_10_out_5), .out_6(n1by16bit_registry_10_out_6),
    .out_7(n1by16bit_registry_10_out_7), .out_8(n1by16bit_registry_10_out_8),
    .out_9(n1by16bit_registry_10_out_9), .out_10(n1by16bit_registry_10_out_10),
    .out_11(n1by16bit_registry_10_out_11), .out_12(n1by16bit_registry_10_out_12),
    .out_13(n1by16bit_registry_10_out_13), .out_14(n1by16bit_registry_10_out_14),
    .out_15(n1by16bit_registry_10_out_15), .out_16(n1by16bit_registry_10_out_16),
    .out_17(n1by16bit_registry_10_out_17), .out_18(n1by16bit_registry_10_out_18));
  _1by16bit_Registry u_1by16bit_registry_11 (
    .WEin(and_27_out), .Din(Din), .out_3(n1by16bit_registry_11_out_3), .out_4(n1by16bit_registry_11_out_4),
    .out_5(n1by16bit_registry_11_out_5), .out_6(n1by16bit_registry_11_out_6),
    .out_7(n1by16bit_registry_11_out_7), .out_8(n1by16bit_registry_11_out_8),
    .out_9(n1by16bit_registry_11_out_9), .out_10(n1by16bit_registry_11_out_10),
    .out_11(n1by16bit_registry_11_out_11), .out_12(n1by16bit_registry_11_out_12),
    .out_13(n1by16bit_registry_11_out_13), .out_14(n1by16bit_registry_11_out_14),
    .out_15(n1by16bit_registry_11_out_15), .out_16(n1by16bit_registry_11_out_16),
    .out_17(n1by16bit_registry_11_out_17), .out_18(n1by16bit_registry_11_out_18));
  _1by16bit_Registry u_1by16bit_registry_12 (
    .WEin(and_28_out), .Din(Din), .out_3(n1by16bit_registry_12_out_3), .out_4(n1by16bit_registry_12_out_4),
    .out_5(n1by16bit_registry_12_out_5), .out_6(n1by16bit_registry_12_out_6),
    .out_7(n1by16bit_registry_12_out_7), .out_8(n1by16bit_registry_12_out_8),
    .out_9(n1by16bit_registry_12_out_9), .out_10(n1by16bit_registry_12_out_10),
    .out_11(n1by16bit_registry_12_out_11), .out_12(n1by16bit_registry_12_out_12),
    .out_13(n1by16bit_registry_12_out_13), .out_14(n1by16bit_registry_12_out_14),
    .out_15(n1by16bit_registry_12_out_15), .out_16(n1by16bit_registry_12_out_16),
    .out_17(n1by16bit_registry_12_out_17), .out_18(n1by16bit_registry_12_out_18));
  _1by16bit_Registry u_1by16bit_registry_13 (
    .WEin(and_29_out), .Din(Din), .out_3(n1by16bit_registry_13_out_3), .out_4(n1by16bit_registry_13_out_4),
    .out_5(n1by16bit_registry_13_out_5), .out_6(n1by16bit_registry_13_out_6),
    .out_7(n1by16bit_registry_13_out_7), .out_8(n1by16bit_registry_13_out_8),
    .out_9(n1by16bit_registry_13_out_9), .out_10(n1by16bit_registry_13_out_10),
    .out_11(n1by16bit_registry_13_out_11), .out_12(n1by16bit_registry_13_out_12),
    .out_13(n1by16bit_registry_13_out_13), .out_14(n1by16bit_registry_13_out_14),
    .out_15(n1by16bit_registry_13_out_15), .out_16(n1by16bit_registry_13_out_16),
    .out_17(n1by16bit_registry_13_out_17), .out_18(n1by16bit_registry_13_out_18));
  _1by16bit_Registry u_1by16bit_registry_14 (
    .WEin(and_30_out), .Din(Din), .out_3(n1by16bit_registry_14_out_3), .out_4(n1by16bit_registry_14_out_4),
    .out_5(n1by16bit_registry_14_out_5), .out_6(n1by16bit_registry_14_out_6),
    .out_7(n1by16bit_registry_14_out_7), .out_8(n1by16bit_registry_14_out_8),
    .out_9(n1by16bit_registry_14_out_9), .out_10(n1by16bit_registry_14_out_10),
    .out_11(n1by16bit_registry_14_out_11), .out_12(n1by16bit_registry_14_out_12),
    .out_13(n1by16bit_registry_14_out_13), .out_14(n1by16bit_registry_14_out_14),
    .out_15(n1by16bit_registry_14_out_15), .out_16(n1by16bit_registry_14_out_16),
    .out_17(n1by16bit_registry_14_out_17), .out_18(n1by16bit_registry_14_out_18));
  _1by16bit_Registry u_1by16bit_registry_15 (
    .WEin(and_31_out), .Din(Din), .out_3(n1by16bit_registry_15_out_3), .out_4(n1by16bit_registry_15_out_4),
    .out_5(n1by16bit_registry_15_out_5), .out_6(n1by16bit_registry_15_out_6),
    .out_7(n1by16bit_registry_15_out_7), .out_8(n1by16bit_registry_15_out_8),
    .out_9(n1by16bit_registry_15_out_9), .out_10(n1by16bit_registry_15_out_10),
    .out_11(n1by16bit_registry_15_out_11), .out_12(n1by16bit_registry_15_out_12),
    .out_13(n1by16bit_registry_15_out_13), .out_14(n1by16bit_registry_15_out_14),
    .out_15(n1by16bit_registry_15_out_15), .out_16(n1by16bit_registry_15_out_16),
    .out_17(n1by16bit_registry_15_out_17), .out_18(n1by16bit_registry_15_out_18));
  _1by16bit_Registry u_1by16bit_registry_16 (
    .WEin(and_32_out), .Din(Din), .out_3(n1by16bit_registry_16_out_3), .out_4(n1by16bit_registry_16_out_4),
    .out_5(n1by16bit_registry_16_out_5), .out_6(n1by16bit_registry_16_out_6),
    .out_7(n1by16bit_registry_16_out_7), .out_8(n1by16bit_registry_16_out_8),
    .out_9(n1by16bit_registry_16_out_9), .out_10(n1by16bit_registry_16_out_10),
    .out_11(n1by16bit_registry_16_out_11), .out_12(n1by16bit_registry_16_out_12),
    .out_13(n1by16bit_registry_16_out_13), .out_14(n1by16bit_registry_16_out_14),
    .out_15(n1by16bit_registry_16_out_15), .out_16(n1by16bit_registry_16_out_16),
    .out_17(n1by16bit_registry_16_out_17), .out_18(n1by16bit_registry_16_out_18));
  assign Dout = n16bit_regselector_mux_1_dout | n16bit_regselector_mux_2_dout | n16bit_regselector_mux_3_dout | n16bit_regselector_mux_4_dout | n16bit_regselector_mux_5_dout | n16bit_regselector_mux_6_dout | n16bit_regselector_mux_7_dout | n16bit_regselector_mux_8_dout | n16bit_regselector_mux_9_dout | n16bit_regselector_mux_10_dout | n16bit_regselector_mux_11_dout | n16bit_regselector_mux_12_dout | n16bit_regselector_mux_13_dout | n16bit_regselector_mux_14_dout | n16bit_regselector_mux_15_dout | n16bit_regselector_mux_16_dout;  // OR_Gate or_1, 16 bits wide
endmodule

module MAR_Reg (
  input  [15:0] Din,
  input  WE,
  output [3:0] PrcSel,
  output [2:0] D_Reg,
  output [2:0] S1_Reg,
  output [2:0] FILLER,
  output [2:0] S2_Reg
);

  wire n1by16bit_registry_1_out_3, n1by16bit_registry_1_out_4, n1by16bit_registry_1_out_5,
       n1by16bit_registry_1_out_6, n1by16bit_registry_1_out_7, n1by16bit_registry_1_out_8,
       n1by16bit_registry_1_out_9, n1by16bit_registry_1_out_10, n1by16bit_registry_1_out_11,
       n1by16bit_registry_1_out_12, n1by16bit_registry_1_out_13, n1by16bit_registry_1_out_14,
       n1by16bit_registry_1_out_15, n1by16bit_registry_1_out_16, n1by16bit_registry_1_out_17,
       n1by16bit_registry_1_out_18;

  _16bit_RegSelector_Mux u_16bit_regselector_mux_1 (
    .in_17(1'b1), .in_1(n1by16bit_registry_1_out_3), .in_2(n1by16bit_registry_1_out_4),
    .in_3(n1by16bit_registry_1_out_5), .in_4(n1by16bit_registry_1_out_6), .in_5(n1by16bit_registry_1_out_7),
    .in_6(n1by16bit_registry_1_out_8), .in_7(n1by16bit_registry_1_out_9), .in_8(n1by16bit_registry_1_out_10),
    .in_9(n1by16bit_registry_1_out_11), .in_10(n1by16bit_registry_1_out_12),
    .in_11(n1by16bit_registry_1_out_13), .in_12(n1by16bit_registry_1_out_14),
    .in_13(n1by16bit_registry_1_out_15), .in_14(n1by16bit_registry_1_out_16),
    .in_15(n1by16bit_registry_1_out_17), .in_16(n1by16bit_registry_1_out_18),
    .Dout({PrcSel, D_Reg, S1_Reg, FILLER, S2_Reg}));
  _1by16bit_Registry u_1by16bit_registry_1 (
    .WEin(WE), .Din(Din), .out_3(n1by16bit_registry_1_out_3), .out_4(n1by16bit_registry_1_out_4),
    .out_5(n1by16bit_registry_1_out_5), .out_6(n1by16bit_registry_1_out_6),
    .out_7(n1by16bit_registry_1_out_7), .out_8(n1by16bit_registry_1_out_8),
    .out_9(n1by16bit_registry_1_out_9), .out_10(n1by16bit_registry_1_out_10),
    .out_11(n1by16bit_registry_1_out_11), .out_12(n1by16bit_registry_1_out_12),
    .out_13(n1by16bit_registry_1_out_13), .out_14(n1by16bit_registry_1_out_14),
    .out_15(n1by16bit_registry_1_out_15), .out_16(n1by16bit_registry_1_out_16),
    .out_17(n1by16bit_registry_1_out_17), .out_18(n1by16bit_registry_1_out_18));
endmodule

module MDR_Reg (
  input  WE,
  input  [2:0] AddrSel,
  input  [15:0] Din,
  output [15:0] Dout
);

  wire and_1_out, and_2_out, and_3_out, and_4_out, and_5_out, and_6_out, and_7_out, and_8_out, and_9_out,
       and_10_out, and_11_out, and_12_out, and_13_out, and_14_out, and_15_out, and_16_out,
       n1by16bit_registry_1_out_3, n1by16bit_registry_1_out_4, n1by16bit_registry_1_out_5,
       n1by16bit_registry_1_out_6, n1by16bit_registry_1_out_7, n1by16bit_registry_1_out_8,
       n1by16bit_registry_1_out_9, n1by16bit_registry_1_out_10, n1by16bit_registry_1_out_11,
       n1by16bit_registry_1_out_12, n1by16bit_registry_1_out_13, n1by16bit_registry_1_out_14,
       n1by16bit_registry_1_out_15, n1by16bit_registry_1_out_16, n1by16bit_registry_1_out_17,
       n1by16bit_registry_1_out_18, n1by16bit_registry_2_out_3, n1by16bit_registry_2_out_4,
       n1by16bit_registry_2_out_5, n1by16bit_registry_2_out_6, n1by16bit_registry_2_out_7,
       n1by16bit_registry_2_out_8, n1by16bit_registry_2_out_9, n1by16bit_registry_2_out_10,
       n1by16bit_registry_2_out_11, n1by16bit_registry_2_out_12, n1by16bit_registry_2_out_13,
       n1by16bit_registry_2_out_14, n1by16bit_registry_2_out_15, n1by16bit_registry_2_out_16,
       n1by16bit_registry_2_out_17, n1by16bit_registry_2_out_18, n1by16bit_registry_3_out_3,
       n1by16bit_registry_3_out_4, n1by16bit_registry_3_out_5, n1by16bit_registry_3_out_6,
       n1by16bit_registry_3_out_7, n1by16bit_registry_3_out_8, n1by16bit_registry_3_out_9,
       n1by16bit_registry_3_out_10, n1by16bit_registry_3_out_11, n1by16bit_registry_3_out_12,
       n1by16bit_registry_3_out_13, n1by16bit_registry_3_out_14, n1by16bit_registry_3_out_15,
       n1by16bit_registry_3_out_16, n1by16bit_registry_3_out_17, n1by16bit_registry_3_out_18,
       n1by16bit_registry_4_out_3, n1by16bit_registry_4_out_4, n1by16bit_registry_4_out_5,
       n1by16bit_registry_4_out_6, n1by16bit_registry_4_out_7, n1by16bit_registry_4_out_8,
       n1by16bit_registry_4_out_9, n1by16bit_registry_4_out_10, n1by16bit_registry_4_out_11,
       n1by16bit_registry_4_out_12, n1by16bit_registry_4_out_13, n1by16bit_registry_4_out_14,
       n1by16bit_registry_4_out_15, n1by16bit_registry_4_out_16, n1by16bit_registry_4_out_17,
       n1by16bit_registry_4_out_18, n1by16bit_registry_5_out_3, n1by16bit_registry_5_out_4,
       n1by16bit_registry_5_out_5, n1by16bit_registry_5_out_6, n1by16bit_registry_5_out_7,
       n1by16bit_registry_5_out_8, n1by16bit_registry_5_out_9, n1by16bit_registry_5_out_10,
       n1by16bit_registry_5_out_11, n1by16bit_registry_5_out_12, n1by16bit_registry_5_out_13,
       n1by16bit_registry_5_out_14, n1by16bit_registry_5_out_15, n1by16bit_registry_5_out_16,
       n1by16bit_registry_5_out_17, n1by16bit_registry_5_out_18, n1by16bit_registry_6_out_3,
       n1by16bit_registry_6_out_4, n1by16bit_registry_6_out_5, n1by16bit_registry_6_out_6,
       n1by16bit_registry_6_out_7, n1by16bit_registry_6_out_8, n1by16bit_registry_6_out_9,
       n1by16bit_registry_6_out_10, n1by16bit_registry_6_out_11, n1by16bit_registry_6_out_12,
       n1by16bit_registry_6_out_13, n1by16bit_registry_6_out_14, n1by16bit_registry_6_out_15,
       n1by16bit_registry_6_out_16, n1by16bit_registry_6_out_17, n1by16bit_registry_6_out_18,
       n1by16bit_registry_7_out_3, n1by16bit_registry_7_out_4, n1by16bit_registry_7_out_5,
       n1by16bit_registry_7_out_6, n1by16bit_registry_7_out_7, n1by16bit_registry_7_out_8,
       n1by16bit_registry_7_out_9, n1by16bit_registry_7_out_10, n1by16bit_registry_7_out_11,
       n1by16bit_registry_7_out_12, n1by16bit_registry_7_out_13, n1by16bit_registry_7_out_14,
       n1by16bit_registry_7_out_15, n1by16bit_registry_7_out_16, n1by16bit_registry_7_out_17,
       n1by16bit_registry_7_out_18, n1by16bit_registry_8_out_3, n1by16bit_registry_8_out_4,
       n1by16bit_registry_8_out_5, n1by16bit_registry_8_out_6, n1by16bit_registry_8_out_7,
       n1by16bit_registry_8_out_8, n1by16bit_registry_8_out_9, n1by16bit_registry_8_out_10,
       n1by16bit_registry_8_out_11, n1by16bit_registry_8_out_12, n1by16bit_registry_8_out_13,
       n1by16bit_registry_8_out_14, n1by16bit_registry_8_out_15, n1by16bit_registry_8_out_16,
       n1by16bit_registry_8_out_17, n1by16bit_registry_8_out_18;
  wire [15:0] n16bit_regselector_mux_1_dout, n16bit_regselector_mux_2_dout, n16bit_regselector_mux_3_dout,
       n16bit_regselector_mux_4_dout, n16bit_regselector_mux_5_dout, n16bit_regselector_mux_6_dout,
       n16bit_regselector_mux_7_dout, n16bit_regselector_mux_8_dout;

  and and_1 (and_1_out, ~AddrSel[0], ~AddrSel[1], ~AddrSel[2]);  // AND_Gate
  and and_2 (and_2_out, AddrSel[0], ~AddrSel[1], ~AddrSel[2]);  // AND_Gate
  and and_3 (and_3_out, ~AddrSel[0], AddrSel[1], ~AddrSel[2]);  // AND_Gate
  and and_4 (and_4_out, AddrSel[0], AddrSel[1], ~AddrSel[2]);  // AND_Gate
  and and_5 (and_5_out, ~AddrSel[0], ~AddrSel[1], AddrSel[2]);  // AND_Gate
  and and_6 (and_6_out, AddrSel[0], ~AddrSel[1], AddrSel[2]);  // AND_Gate
  and and_7 (and_7_out, ~AddrSel[0], AddrSel[1], AddrSel[2]);  // AND_Gate
  and and_8 (and_8_out, AddrSel[0], AddrSel[1], AddrSel[2]);
  and and_9 (and_9_out, and_1_out, WE);
  and and_10 (and_10_out, and_2_out, WE);
  and and_11 (and_11_out, and_3_out, WE);
  and and_12 (and_12_out, and_4_out, WE);
  and and_13 (and_13_out, and_5_out, WE);
  and and_14 (and_14_out, and_6_out, WE);
  and and_15 (and_15_out, and_7_out, WE);
  and and_16 (and_16_out, and_8_out, WE);
  _16bit_RegSelector_Mux u_16bit_regselector_mux_1 (
    .in_17(and_1_out), .in_1(n1by16bit_registry_1_out_3), .in_2(n1by16bit_registry_1_out_4),
    .in_3(n1by16bit_registry_1_out_5), .in_4(n1by16bit_registry_1_out_6), .in_5(n1by16bit_registry_1_out_7),
    .in_6(n1by16bit_registry_1_out_8), .in_7(n1by16bit_registry_1_out_9), .in_8(n1by16bit_registry_1_out_10),
    .in_9(n1by16bit_registry_1_out_11), .in_10(n1by16bit_registry_1_out_12),
    .in_11(n1by16bit_registry_1_out_13), .in_12(n1by16bit_registry_1_out_14),
    .in_13(n1by16bit_registry_1_out_15), .in_14(n1by16bit_registry_1_out_16),
    .in_15(n1by16bit_registry_1_out_17), .in_16(n1by16bit_registry_1_out_18),
    .Dout(n16bit_regselector_mux_1_dout));
  _16bit_RegSelector_Mux u_16bit_regselector_mux_2 (
    .in_17(and_2_out), .in_1(n1by16bit_registry_2_out_3), .in_2(n1by16bit_registry_2_out_4),
    .in_3(n1by16bit_registry_2_out_5), .in_4(n1by16bit_registry_2_out_6), .in_5(n1by16bit_registry_2_out_7),
    .in_6(n1by16bit_registry_2_out_8), .in_7(n1by16bit_registry_2_out_9), .in_8(n1by16bit_registry_2_out_10),
    .in_9(n1by16bit_registry_2_out_11), .in_10(n1by16bit_registry_2_out_12),
    .in_11(n1by16bit_registry_2_out_13), .in_12(n1by16bit_registry_2_out_14),
    .in_13(n1by16bit_registry_2_out_15), .in_14(n1by16bit_registry_2_out_16),
    .in_15(n1by16bit_registry_2_out_17), .in_16(n1by16bit_registry_2_out_18),
    .Dout(n16bit_regselector_mux_2_dout));
  _16bit_RegSelector_Mux u_16bit_regselector_mux_3 (
    .in_17(and_3_out), .in_1(n1by16bit_registry_3_out_3), .in_2(n1by16bit_registry_3_out_4),
    .in_3(n1by16bit_registry_3_out_5), .in_4(n1by16bit_registry_3_out_6), .in_5(n1by16bit_registry_3_out_7),
    .in_6(n1by16bit_registry_3_out_8), .in_7(n1by16bit_registry_3_out_9), .in_8(n1by16bit_registry_3_out_10),
    .in_9(n1by16bit_registry_3_out_11), .in_10(n1by16bit_registry_3_out_12),
    .in_11(n1by16bit_registry_3_out_13), .in_12(n1by16bit_registry_3_out_14),
    .in_13(n1by16bit_registry_3_out_15), .in_14(n1by16bit_registry_3_out_16),
    .in_15(n1by16bit_registry_3_out_17), .in_16(n1by16bit_registry_3_out_18),
    .Dout(n16bit_regselector_mux_3_dout));
  _16bit_RegSelector_Mux u_16bit_regselector_mux_4 (
    .in_17(and_4_out), .in_1(n1by16bit_registry_4_out_3), .in_2(n1by16bit_registry_4_out_4),
    .in_3(n1by16bit_registry_4_out_5), .in_4(n1by16bit_registry_4_out_6), .in_5(n1by16bit_registry_4_out_7),
    .in_6(n1by16bit_registry_4_out_8), .in_7(n1by16bit_registry_4_out_9), .in_8(n1by16bit_registry_4_out_10),
    .in_9(n1by16bit_registry_4_out_11), .in_10(n1by16bit_registry_4_out_12),
    .in_11(n1by16bit_registry_4_out_13), .in_12(n1by16bit_registry_4_out_14),
    .in_13(n1by16bit_registry_4_out_15), .in_14(n1by16bit_registry_4_out_16),
    .in_15(n1by16bit_registry_4_out_17), .in_16(n1by16bit_registry_4_out_18),
    .Dout(n16bit_regselector_mux_4_dout));
  _16bit_RegSelector_Mux u_16bit_regselector_mux_5 (
    .in_17(and_5_out), .in_1(n1by16bit_registry_5_out_3), .in_2(n1by16bit_registry_5_out_4),
    .in_3(n1by16bit_registry_5_out_5), .in_4(n1by16bit_registry_5_out_6), .in_5(n1by16bit_registry_5_out_7),
    .in_6(n1by16bit_registry_5_out_8), .in_7(n1by16bit_registry_5_out_9), .in_8(n1by16bit_registry_5_out_10),
    .in_9(n1by16bit_registry_5_out_11), .in_10(n1by16bit_registry_5_out_12),
    .in_11(n1by16bit_registry_5_out_13), .in_12(n1by16bit_registry_5_out_14),
    .in_13(n1by16bit_registry_5_out_15), .in_14(n1by16bit_registry_5_out_16),
    .in_15(n1by16bit_registry_5_out_17), .in_16(n1by16bit_registry_5_out_18),
    .Dout(n16bit_regselector_mux_5_dout));
  _16bit_RegSelector_Mux u_16bit_regselector_mux_6 (
    .in_17(and_6_out), .in_1(n1by16bit_registry_6_out_3), .in_2(n1by16bit_registry_6_out_4),
    .in_3(n1by16bit_registry_6_out_5), .in_4(n1by16bit_registry_6_out_6), .in_5(n1by16bit_registry_6_out_7),
    .in_6(n1by16bit_registry_6_out_8), .in_7(n1by16bit_registry_6_out_9), .in_8(n1by16bit_registry_6_out_10),
    .in_9(n1by16bit_registry_6_out_11), .in_10(n1by16bit_registry_6_out_12),
    .in_11(n1by16bit_registry_6_out_13), .in_12(n1by16bit_registry_6_out_14),
    .in_13(n1by16bit_registry_6_out_15), .in_14(n1by16bit_registry_6_out_16),
    .in_15(n1by16bit_registry_6_out_17), .in_16(n1by16bit_registry_6_out_18),
    .Dout(n16bit_regselector_mux_6_dout));
  _16bit_RegSelector_Mux u_16bit_regselector_mux_7 (
    .in_17(and_7_out), .in_1(n1by16bit_registry_7_out_3), .in_2(n1by16bit_registry_7_out_4),
    .in_3(n1by16bit_registry_7_out_5), .in_4(n1by16bit_registry_7_out_6), .in_5(n1by16bit_registry_7_out_7),
    .in_6(n1by16bit_registry_7_out_8), .in_7(n1by16bit_registry_7_out_9), .in_8(n1by16bit_registry_7_out_10),
    .in_9(n1by16bit_registry_7_out_11), .in_10(n1by16bit_registry_7_out_12),
    .in_11(n1by16bit_registry_7_out_13), .in_12(n1by16bit_registry_7_out_14),
    .in_13(n1by16bit_registry_7_out_15), .in_14(n1by16bit_registry_7_out_16),
    .in_15(n1by16bit_registry_7_out_17), .in_16(n1by16bit_registry_7_out_18),
    .Dout(n16bit_regselector_mux_7_dout));
  _16bit_RegSelector_Mux u_16bit_regselector_mux_8 (
    .in_17(and_8_out), .in_1(n1by16bit_registry_8_out_3), .in_2(n1by16bit_registry_8_out_4),
    .in_3(n1by16bit_registry_8_out_5), .in_4(n1by16bit_registry_8_out_6), .in_5(n1by16bit_registry_8_out_7),
    .in_6(n1by16bit_registry_8_out_8), .in_7(n1by16bit_registry_8_out_9), .in_8(n1by16bit_registry_8_out_10),
    .in_9(n1by16bit_registry_8_out_11), .in_10(n1by16bit_registry_8_out_12),
    .in_11(n1by16bit_registry_8_out_13), .in_12(n1by16bit_registry_8_out_14),
    .in_13(n1by16bit_registry_8_out_15), .in_14(n1by16bit_registry_8_out_16),
    .in_15(n1by16bit_registry_8_out_17), .in_16(n1by16bit_registry_8_out_18),
    .Dout(n16bit_regselector_mux_8_dout));
  _1by16bit_Registry u_1by16bit_registry_1 (
    .WEin(and_9_out), .Din(Din), .out_3(n1by16bit_registry_1_out_3), .out_4(n1by16bit_registry_1_out_4),
    .out_5(n1by16bit_registry_1_out_5), .out_6(n1by16bit_registry_1_out_6),
    .out_7(n1by16bit_registry_1_out_7), .out_8(n1by16bit_registry_1_out_8),
    .out_9(n1by16bit_registry_1_out_9), .out_10(n1by16bit_registry_1_out_10),
    .out_11(n1by16bit_registry_1_out_11), .out_12(n1by16bit_registry_1_out_12),
    .out_13(n1by16bit_registry_1_out_13), .out_14(n1by16bit_registry_1_out_14),
    .out_15(n1by16bit_registry_1_out_15), .out_16(n1by16bit_registry_1_out_16),
    .out_17(n1by16bit_registry_1_out_17), .out_18(n1by16bit_registry_1_out_18));
  _1by16bit_Registry u_1by16bit_registry_2 (
    .WEin(and_10_out), .Din(Din), .out_3(n1by16bit_registry_2_out_3), .out_4(n1by16bit_registry_2_out_4),
    .out_5(n1by16bit_registry_2_out_5), .out_6(n1by16bit_registry_2_out_6),
    .out_7(n1by16bit_registry_2_out_7), .out_8(n1by16bit_registry_2_out_8),
    .out_9(n1by16bit_registry_2_out_9), .out_10(n1by16bit_registry_2_out_10),
    .out_11(n1by16bit_registry_2_out_11), .out_12(n1by16bit_registry_2_out_12),
    .out_13(n1by16bit_registry_2_out_13), .out_14(n1by16bit_registry_2_out_14),
    .out_15(n1by16bit_registry_2_out_15), .out_16(n1by16bit_registry_2_out_16),
    .out_17(n1by16bit_registry_2_out_17), .out_18(n1by16bit_registry_2_out_18));
  _1by16bit_Registry u_1by16bit_registry_3 (
    .WEin(and_11_out), .Din(Din), .out_3(n1by16bit_registry_3_out_3), .out_4(n1by16bit_registry_3_out_4),
    .out_5(n1by16bit_registry_3_out_5), .out_6(n1by16bit_registry_3_out_6),
    .out_7(n1by16bit_registry_3_out_7), .out_8(n1by16bit_registry_3_out_8),
    .out_9(n1by16bit_registry_3_out_9), .out_10(n1by16bit_registry_3_out_10),
    .out_11(n1by16bit_registry_3_out_11), .out_12(n1by16bit_registry_3_out_12),
    .out_13(n1by16bit_registry_3_out_13), .out_14(n1by16bit_registry_3_out_14),
    .out_15(n1by16bit_registry_3_out_15), .out_16(n1by16bit_registry_3_out_16),
    .out_17(n1by16bit_registry_3_out_17), .out_18(n1by16bit_registry_3_out_18));
  _1by16bit_Registry u_1by16bit_registry_4 (
    .WEin(and_12_out), .Din(Din), .out_3(n1by16bit_registry_4_out_3), .out_4(n1by16bit_registry_4_out_4),
    .out_5(n1by16bit_registry_4_out_5), .out_6(n1by16bit_registry_4_out_6),
    .out_7(n1by16bit_registry_4_out_7), .out_8(n1by16bit_registry_4_out_8),
    .out_9(n1by16bit_registry_4_out_9), .out_10(n1by16bit_registry_4_out_10),
    .out_11(n1by16bit_registry_4_out_11), .out_12(n1by16bit_registry_4_out_12),
    .out_13(n1by16bit_registry_4_out_13), .out_14(n1by16bit_registry_4_out_14),
    .out_15(n1by16bit_registry_4_out_15), .out_16(n1by16bit_registry_4_out_16),
    .out_17(n1by16bit_registry_4_out_17), .out_18(n1by16bit_registry_4_out_18));
  _1by16bit_Registry u_1by16bit_registry_5 (
    .WEin(and_13_out), .Din(Din), .out_3(n1by16bit_registry_5_out_3), .out_4(n1by16bit_registry_5_out_4),
    .out_5(n1by16bit_registry_5_out_5), .out_6(n1by16bit_registry_5_out_6),
    .out_7(n1by16bit_registry_5_out_7), .out_8(n1by16bit_registry_5_out_8),
    .out_9(n1by16bit_registry_5_out_9), .out_10(n1by16bit_registry_5_out_10),
    .out_11(n1by16bit_registry_5_out_11), .out_12(n1by16bit_registry_5_out_12),
    .out_13(n1by16bit_registry_5_out_13), .out_14(n1by16bit_registry_5_out_14),
    .out_15(n1by16bit_registry_5_out_15), .out_16(n1by16bit_registry_5_out_16),
    .out_17(n1by16bit_registry_5_out_17), .out_18(n1by16bit_registry_5_out_18));
  _1by16bit_Registry u_1by16bit_registry_6 (
    .WEin(and_14_out), .Din(Din), .out_3(n1by16bit_registry_6_out_3), .out_4(n1by16bit_registry_6_out_4),
    .out_5(n1by16bit_registry_6_out_5), .out_6(n1by16bit_registry_6_out_6),
    .out_7(n1by16bit_registry_6_out_7), .out_8(n1by16bit_registry_6_out_8),
    .out_9(n1by16bit_registry_6_out_9), .out_10(n1by16bit_registry_6_out_10),
    .out_11(n1by16bit_registry_6_out_11), .out_12(n1by16bit_registry_6_out_12),
    .out_13(n1by16bit_registry_6_out_13), .out_14(n1by16bit_registry_6_out_14),
    .out_15(n1by16bit_registry_6_out_15), .out_16(n1by16bit_registry_6_out_16),
    .out_17(n1by16bit_registry_6_out_17), .out_18(n1by16bit_registry_6_out_18));
  _1by16bit_Registry u_1by16bit_registry_7 (
    .WEin(and_15_out), .Din(Din), .out_3(n1by16bit_registry_7_out_3), .out_4(n1by16bit_registry_7_out_4),
    .out_5(n1by16bit_registry_7_out_5), .out_6(n1by16bit_registry_7_out_6),
    .out_7(n1by16bit_registry_7_out_7), .out_8(n1by16bit_registry_7_out_8),
    .out_9(n1by16bit_registry_7_out_9), .out_10(n1by16bit_registry_7_out_10),
    .out_11(n1by16bit_registry_7_out_11), .out_12(n1by16bit_registry_7_out_12),
    .out_13(n1by16bit_registry_7_out_13), .out_14(n1by16bit_registry_7_out_14),
    .out_15(n1by16bit_registry_7_out_15), .out_16(n1by16bit_registry_7_out_16),
    .out_17(n1by16bit_registry_7_out_17), .out_18(n1by16bit_registry_7_out_18));
  _1by16bit_Registry u_1by16bit_registry_8 (
    .WEin(and_16_out), .Din(Din), .out_3(n1by16bit_registry_8_out_3), .out_4(n1by16bit_registry_8_out_4),
    .out_5(n1by16bit_registry_8_out_5), .out_6(n1by16bit_registry_8_out_6),
    .out_7(n1by16bit_registry_8_out_7), .out_8(n1by16bit_registry_8_out_8),
    .out_9(n1by16bit_registry_8_out_9), .out_10(n1by16bit_registry_8_out_10),
    .out_11(n1by16bit_registry_8_out_11), .out_12(n1by16bit_registry_8_out_12),
    .out_13(n1by16bit_registry_8_out_13), .out_14(n1by16bit_registry_8_out_14),
    .out_15(n1by16bit_registry_8_out_15), .out_16(n1by16bit_registry_8_out_16),
    .out_17(n1by16bit_registry_8_out_17), .out_18(n1by16bit_registry_8_out_18));
  assign Dout = n16bit_regselector_mux_1_dout | n16bit_regselector_mux_2_dout | n16bit_regselector_mux_3_dout | n16bit_regselector_mux_4_dout | n16bit_regselector_mux_5_dout | n16bit_regselector_mux_6_dout | n16bit_regselector_mux_7_dout | n16bit_regselector_mux_8_dout;  // OR_Gate or_1, 16 bits wide
endmodule

module MDR_Copy_Loop (
  input  [2:0] AddrIn1,
  input  [2:0] AddrIn2,
  output out_3,
  output out_4,
  output out_5,
  output out_6,
  output out_7,
  output out_8
);

  wire nand_1_out, nand_3_out, nand_4_out, nand_5_out, nand_7_out, nand_8_out, nand_9_out, nand_11_out,
       nand_12_out, nand_14_out, nand_16_out, nand_18_out, nand_19_out, nand_20_out, nand_21_out,
       nand_22_out, nand_23_out, nand_24_out, not_1_out, not_2_out, not_3_out, undriven, undriven_2;

  nand nand_1 (nand_1_out, AddrIn1[0], undriven);
  nand nand_2 (out_4, nand_1_out, nand_3_out);
  nand nand_3 (nand_3_out, out_4, nand_4_out);
  nand nand_4 (nand_4_out, undriven, AddrIn1[0]);
  nand nand_5 (nand_5_out, AddrIn1[1], undriven);
  nand nand_6 (out_6, nand_5_out, nand_7_out);
  nand nand_7 (nand_7_out, out_6, nand_8_out);
  nand nand_8 (nand_8_out, undriven, AddrIn1[1]);
  nand nand_9 (nand_9_out, AddrIn1[2], undriven_2);
  nand nand_10 (out_8, nand_9_out, nand_11_out);
  nand nand_11 (nand_11_out, out_8, nand_12_out);
  nand nand_12 (nand_12_out, undriven_2, AddrIn1[2]);
  nand nand_13 (out_3, nand_19_out, nand_14_out);
  nand nand_14 (nand_14_out, out_3, nand_20_out);
  nand nand_15 (out_5, nand_21_out, nand_16_out);
  nand nand_16 (nand_16_out, out_5, nand_22_out);
  nand nand_17 (out_7, nand_23_out, nand_18_out);
  nand nand_18 (nand_18_out, out_7, nand_24_out);
  nand nand_19 (nand_19_out, AddrIn2[0], not_1_out);
  nand nand_20 (nand_20_out, not_1_out, AddrIn2[0]);
  not not_1 (not_1_out, undriven);
  nand nand_21 (nand_21_out, AddrIn2[1], not_2_out);
  nand nand_22 (nand_22_out, not_2_out, AddrIn2[1]);
  not not_2 (not_2_out, undriven);
  nand nand_23 (nand_23_out, AddrIn2[2], not_3_out);
  nand nand_24 (nand_24_out, not_3_out, AddrIn2[2]);
  not not_3 (not_3_out, undriven_2);
endmodule
