// Logisim project Project 4 - Von Neumann.circ as structural Verilog: 23 circuits, main circuit Main
module Main (
  input  Clear_Ctr,
  input  [15:0] Instruction_Address,
  input  Switch,
  output [15:0] TEST___Incremented_PP,
  output [15:0] TEST___Address_to_PP,
  output [15:0] TEST___PP_to_MAR,
  output [15:0] TEST___Data_from_Memory,
  output [15:0] TEST___Saved_to_Registry,
  output [2:0] DR,
  output ADD_Out___In_Progress
);

  wire Automatic_Clock_out, control_unit_1_out_3, control_unit_1_out_4, control_unit_1_out_5,
       control_unit_1_out_6, control_unit_1_out_7, control_unit_1_out_8, control_unit_1_out_9,
       control_unit_1_out_10, INITIAL_INST_ADDR____PP_out, Manual_Clock_out, operation_multiplexer_1_ldr_out,
       or_1_out, or_2_out, or_4_out, or_5_out, or_6_out, or_7_out, or_8_out, or_9_out, or_10_out;
  wire [2:0] instruction_decoder_1_sr1;
  wire [3:0] instruction_decoder_1_opcode;
  wire [5:0] instruction_decoder_1_opdepndnt;
  wire [15:0] evaluate_address_1_out_5, instruction_registry_ir_1_data_out,
       memory_address_registry_mar_1_data_out, memory_data_registry_mdr_1_out_3, n16bit_decoder_1_out,
       n16bit_decoder_1_out_2, or_3_out, program_pointer_pp_1_data_out;

  Button Manual_Clock (.out(Manual_Clock_out));
  Clock Automatic_Clock (.out(Automatic_Clock_out));
  Button INITIAL_INST_ADDR____PP (.out(INITIAL_INST_ADDR____PP_out));
  or or_1 (or_1_out, Manual_Clock_out, Automatic_Clock_out);
  or or_2 (or_2_out, or_1_out, INITIAL_INST_ADDR____PP_out);
  Control_Unit control_unit_1 (
    .Activate(Switch), .Clock(or_2_out), .out_3(control_unit_1_out_3), .out_4(control_unit_1_out_4),
    .out_5(control_unit_1_out_5), .out_6(control_unit_1_out_6), .out_7(control_unit_1_out_7),
    .out_8(control_unit_1_out_8), .out_9(control_unit_1_out_9), .out_10(control_unit_1_out_10));  // open: BLANK
  assign or_3_out = Instruction_Address | TEST___Incremented_PP;  // OR_Gate or_3, 16 bits wide
  or or_4 (or_4_out, Clear_Ctr, INITIAL_INST_ADDR____PP_out);
  Operation_Multiplexer operation_multiplexer_1 (
    .Op_In(instruction_decoder_1_opcode), .LDR_Out(operation_multiplexer_1_ldr_out),
    .ADD_Out(ADD_Out___In_Progress));
  Incrementer incrementer_1 (
    .Out(TEST___Incremented_PP), .Clear(Clear_Ctr), .Increment(or_5_out), .In(program_pointer_pp_1_data_out),
    .Mem_Load(control_unit_1_out_3), .Load(control_unit_1_out_4));
  or or_5 (or_5_out, control_unit_1_out_5, Clear_Ctr);
  Initial_Instruction_Address initial_instruction_address_1 (.WE(or_6_out), .Out(TEST___Address_to_PP), .In(or_3_out));
  or or_6 (or_6_out, control_unit_1_out_5, or_4_out);
  Program_Pointer__PP program_pointer_pp_1 (
    .WE(or_7_out), .In(TEST___Address_to_PP), .Data_Out(program_pointer_pp_1_data_out),
    .Read_Enable(control_unit_1_out_3));
  or or_7 (or_7_out, or_4_out, control_unit_1_out_3);
  or or_8 (or_8_out, control_unit_1_out_4, control_unit_1_out_8);
  Instruction_Decoder instruction_decoder_1 (
    .Decoder_In(instruction_registry_ir_1_data_out), .Opcode(instruction_decoder_1_opcode), .DR(DR),
    .SR1(instruction_decoder_1_sr1), .OpDepndnt(instruction_decoder_1_opdepndnt));
  Evaluate_Address evaluate_address_1 (
    .Activate(operation_multiplexer_1_ldr_out), .Evaluate(control_unit_1_out_7),
    .SR(instruction_decoder_1_sr1), ._2s_Comp_Offset(instruction_decoder_1_opdepndnt),
    .out_5(evaluate_address_1_out_5));
  or or_9 (or_9_out, control_unit_1_out_5, control_unit_1_out_9);
  or or_10 (or_10_out, control_unit_1_out_3, control_unit_1_out_7);
  General_Purpose_Registries general_purpose_registries_1 (
    .in_3(control_unit_1_out_10), .Address(DR), .Data_In(n16bit_decoder_1_out_2),
    .Data_Out(TEST___Saved_to_Registry));
  _16bit_Multiplexer u_16bit_multiplexer_1 (
    .In_1(program_pointer_pp_1_data_out), .In_2(evaluate_address_1_out_5), .in_3(control_unit_1_out_7),
    .Out(TEST___PP_to_MAR));
  Memory_Address_Registry__MAR memory_address_registry_mar_1 (
    .In(TEST___PP_to_MAR), .WE(or_10_out), .Data_Out(memory_address_registry_mar_1_data_out),
    .Read_Enable(or_8_out));
  Memory memory_1 (
    .Instruction_Out(TEST___Data_from_Memory), .in_2(or_8_out),
    .Memory_Address(memory_address_registry_mar_1_data_out));
  Memory_Data_Registry__MDR memory_data_registry_mdr_1 (
    .WE(or_9_out), .In(TEST___Data_from_Memory), .out_3(memory_data_registry_mdr_1_out_3));
  _16bit_Decoder u_16bit_decoder_1 (
    .In(memory_data_registry_mdr_1_out_3), .To_IR(or_9_out), .Out(n16bit_decoder_1_out),
    .Out_2(n16bit_decoder_1_out_2), .To_Reg(control_unit_1_out_10));
  Instruction_Registry__IR instruction_registry_ir_1 (
    .WE(control_unit_1_out_6), .In(n16bit_decoder_1_out), .Data_Out(instruction_registry_ir_1_data_out));

  // Notes on the sheet:
  //   FETCH >>>
  //   EVALUATE >>>
  //   FETCH OP >>>
  //   STORE >>>
  //   3 - MDR INST > IR
  //   DECODE >>>>>>>>>>>>>>>>>>>>>>>>>>>>>>>>>>>>
  //   4 - EVAL
  //   7 - STORE
  //   0 - PP ADDR > MAR
  //   1 - MAR > MAR ADDR > MDR
  //   2 - MEM INST > MDR
  //   5 - MAR ADDR > MEM
  //   6 - MEM INST > MDR
endmodule

module _8bit_Registry__1_1 (
  input  [7:0] Data_In,
  input  WE,
  output [7:0] Data_Out
);

  wire nand_1_out, nand_2_out, nand_3_out, nand_4_out, nand_5_out, nand_7_out, nand_8_out, nand_9_out,
       nand_11_out, nand_12_out, nand_13_out, nand_15_out, nand_16_out, nand_17_out, nand_19_out,
       nand_21_out, nand_22_out, nand_23_out, nand_25_out, nand_26_out, nand_27_out, nand_29_out,
       nand_30_out, nand_31_out;

  nand nand_1 (nand_1_out, WE, ~Data_In[7]);  // NAND_Gate
  nand nand_2 (nand_2_out, nand_1_out, Data_Out[7]);
  nand nand_3 (nand_3_out, WE, ~Data_In[6]);  // NAND_Gate
  nand nand_4 (nand_4_out, Data_In[7], WE);
  nand nand_5 (nand_5_out, nand_3_out, Data_Out[6]);
  nand nand_6 (Data_Out[7], nand_2_out, nand_4_out);
  nand nand_7 (nand_7_out, WE, ~Data_In[5]);  // NAND_Gate
  nand nand_8 (nand_8_out, Data_In[6], WE);
  nand nand_9 (nand_9_out, nand_7_out, Data_Out[5]);
  nand nand_10 (Data_Out[6], nand_5_out, nand_8_out);
  nand nand_11 (nand_11_out, Data_In[5], WE);
  nand nand_12 (nand_12_out, WE, ~Data_In[4]);  // NAND_Gate
  nand nand_13 (nand_13_out, nand_12_out, Data_Out[4]);
  nand nand_14 (Data_Out[5], nand_9_out, nand_11_out);
  nand nand_15 (nand_15_out, Data_In[4], WE);
  nand nand_16 (nand_16_out, WE, ~Data_In[3]);  // NAND_Gate
  nand nand_17 (nand_17_out, nand_16_out, Data_Out[3]);
  nand nand_18 (Data_Out[4], nand_13_out, nand_15_out);
  nand nand_19 (nand_19_out, Data_In[3], WE);
  nand nand_20 (Data_Out[3], nand_17_out, nand_19_out);
  nand nand_21 (nand_21_out, Data_In[2], WE);
  nand nand_22 (nand_22_out, WE, ~Data_In[2]);  // NAND_Gate
  nand nand_23 (nand_23_out, nand_22_out, Data_Out[2]);
  nand nand_24 (Data_Out[2], nand_23_out, nand_21_out);
  nand nand_25 (nand_25_out, Data_In[1], WE);
  nand nand_26 (nand_26_out, WE, ~Data_In[1]);  // NAND_Gate
  nand nand_27 (nand_27_out, nand_26_out, Data_Out[1]);
  nand nand_28 (Data_Out[1], nand_27_out, nand_25_out);
  nand nand_29 (nand_29_out, WE, ~Data_In[0]);  // NAND_Gate
  nand nand_30 (nand_30_out, Data_In[0], WE);
  nand nand_31 (nand_31_out, nand_29_out, Data_Out[0]);
  nand nand_32 (Data_Out[0], nand_31_out, nand_30_out);
endmodule

module _16bit_Registry__1_1 (
  input  [15:0] In,
  input  WE,
  output Out15,
  output Out13,
  output Out11,
  output Out9,
  output Out7,
  output Out5,
  output Out3,
  output Out1,
  output Out14,
  output Out12,
  output Out10,
  output Out8,
  output Out6,
  output Out4,
  output Out2,
  output Out0
);

  wire nand_1_out, nand_2_out, nand_3_out, nand_4_out, nand_6_out, nand_7_out, nand_8_out, nand_9_out,
       nand_11_out, nand_12_out, nand_13_out, nand_15_out, nand_16_out, nand_18_out, nand_19_out,
       nand_21_out, nand_22_out, nand_24_out, nand_25_out, nand_26_out, nand_27_out, nand_29_out,
       nand_30_out, nand_32_out, nand_33_out, nand_34_out, nand_35_out, nand_36_out, nand_38_out,
       nand_39_out, nand_40_out, nand_42_out, nand_43_out, nand_44_out, nand_46_out, nand_47_out,
       nand_48_out, nand_49_out, nand_51_out, nand_53_out, nand_54_out, nand_55_out, nand_57_out,
       nand_58_out, nand_59_out, nand_61_out, nand_62_out, nand_63_out;

  nand nand_1 (nand_1_out, WE, ~In[15]);  // NAND_Gate
  nand nand_2 (nand_2_out, nand_1_out, Out15);
  nand nand_3 (nand_3_out, In[15], WE);
  nand nand_4 (nand_4_out, WE, ~In[14]);  // NAND_Gate
  nand nand_5 (Out15, nand_2_out, nand_3_out);
  nand nand_6 (nand_6_out, nand_4_out, Out14);
  nand nand_7 (nand_7_out, In[14], WE);
  nand nand_8 (nand_8_out, WE, ~In[13]);  // NAND_Gate
  nand nand_9 (nand_9_out, nand_8_out, Out13);
  nand nand_10 (Out14, nand_6_out, nand_7_out);
  nand nand_11 (nand_11_out, In[13], WE);
  nand nand_12 (nand_12_out, WE, ~In[12]);  // NAND_Gate
  nand nand_13 (nand_13_out, nand_12_out, Out12);
  nand nand_14 (Out13, nand_9_out, nand_11_out);
  nand nand_15 (nand_15_out, In[12], WE);
  nand nand_16 (nand_16_out, WE, ~In[11]);  // NAND_Gate
  nand nand_17 (Out12, nand_13_out, nand_15_out);
  nand nand_18 (nand_18_out, nand_16_out, Out11);
  nand nand_19 (nand_19_out, In[11], WE);
  nand nand_20 (Out11, nand_18_out, nand_19_out);
  nand nand_21 (nand_21_out, WE, ~In[10]);  // NAND_Gate
  nand nand_22 (nand_22_out, In[10], WE);
  nand nand_23 (Out10, nand_24_out, nand_22_out);
  nand nand_24 (nand_24_out, nand_21_out, Out10);
  nand nand_25 (nand_25_out, WE, ~In[9]);  // NAND_Gate
  nand nand_26 (nand_26_out, In[9], WE);
  nand nand_27 (nand_27_out, nand_25_out, Out9);
  nand nand_28 (Out9, nand_27_out, nand_26_out);
  nand nand_29 (nand_29_out, WE, ~In[8]);  // NAND_Gate
  nand nand_30 (nand_30_out, In[8], WE);
  nand nand_31 (Out8, nand_32_out, nand_30_out);
  nand nand_32 (nand_32_out, nand_29_out, Out8);
  nand nand_33 (nand_33_out, WE, ~In[7]);  // NAND_Gate
  nand nand_34 (nand_34_out, nand_33_out, Out7);
  nand nand_35 (nand_35_out, In[7], WE);
  nand nand_36 (nand_36_out, WE, ~In[6]);  // NAND_Gate
  nand nand_37 (Out7, nand_34_out, nand_35_out);
  nand nand_38 (nand_38_out, nand_36_out, Out6);
  nand nand_39 (nand_39_out, WE, ~In[5]);  // NAND_Gate
  nand nand_40 (nand_40_out, In[6], WE);
  nand nand_41 (Out6, nand_38_out, nand_40_out);
  nand nand_42 (nand_42_out, nand_39_out, Out5);
  nand nand_43 (nand_43_out, WE, ~In[4]);  // NAND_Gate
  nand nand_44 (nand_44_out, In[5], WE);
  nand nand_45 (Out5, nand_42_out, nand_44_out);
  nand nand_46 (nand_46_out, nand_43_out, Out4);
  nand nand_47 (nand_47_out, WE, ~In[3]);  // NAND_Gate
  nand nand_48 (nand_48_out, In[4], WE);
  nand nand_49 (nand_49_out, nand_47_out, Out3);
  nand nand_50 (Out4, nand_46_out, nand_48_out);
  nand nand_51 (nand_51_out, In[3], WE);
  nand nand_52 (Out3, nand_49_out, nand_51_out);
  nand nand_53 (nand_53_out, In[2], WE);
  nand nand_54 (nand_54_out, WE, ~In[2]);  // NAND_Gate
  nand nand_55 (nand_55_out, nand_54_out, Out2);
  nand nand_56 (Out2, nand_55_out, nand_53_out);
  nand nand_57 (nand_57_out, WE, ~In[1]);  // NAND_Gate
  nand nand_58 (nand_58_out, In[1], WE);
  nand nand_59 (nand_59_out, nand_57_out, Out1);
  nand nand_60 (Out1, nand_59_out, nand_58_out);
  nand nand_61 (nand_61_out, WE, ~In[0]);  // NAND_Gate
  nand nand_62 (nand_62_out, In[0], WE);
  nand nand_63 (nand_63_out, nand_61_out, Out0);
  nand nand_64 (Out0, nand_63_out, nand_62_out);
endmodule

module _16bit_Registry_Selector (
  input  In,
  input  In_2,
  input  In_3,
  input  In_4,
  input  In_5,
  input  In_6,
  input  In_7,
  input  In_8,
  input  In_9,
  input  In_10,
  input  In_11,
  input  In_12,
  input  In_13,
  input  In_14,
  input  In_15,
  input  In_16,
  input  WE,
  output [15:0] Out
);

  and and_1 (Out[15], WE, In);
  and and_2 (Out[14], WE, In_2);
  and and_3 (Out[13], WE, In_3);
  and and_4 (Out[12], WE, In_4);
  and and_5 (Out[10], WE, In_6);
  and and_6 (Out[11], WE, In_5);
  and and_7 (Out[7], WE, In_9);
  and and_8 (Out[9], WE, In_7);
  and and_9 (Out[8], WE, In_8);
  and and_10 (Out[5], WE, In_11);
  and and_11 (Out[6], WE, In_10);
  and and_12 (Out[3], WE, In_13);
  and and_13 (Out[2], WE, In_14);
  and and_14 (Out[4], WE, In_12);
  and and_15 (Out[1], WE, In_15);
  and and_16 (Out[0], WE, In_16);
endmodule

module Initial_Instruction_Address (
  input  [15:0] In,
  input  WE,
  output [15:0] Out
);

  wire nand_1_out, nand_2_out, nand_3_out, nand_4_out, nand_6_out, nand_7_out, nand_8_out, nand_10_out,
       nand_11_out, nand_12_out, nand_14_out, nand_15_out, nand_16_out, nand_17_out, nand_19_out,
       nand_21_out, nand_22_out, nand_24_out, nand_25_out, nand_26_out, nand_28_out, nand_29_out,
       nand_30_out, nand_31_out, nand_33_out, nand_34_out, nand_35_out, nand_36_out, nand_38_out,
       nand_39_out, nand_40_out, nand_41_out, nand_43_out, nand_44_out, nand_46_out, nand_47_out,
       nand_48_out, nand_49_out, nand_51_out, nand_53_out, nand_54_out, nand_55_out, nand_57_out,
       nand_58_out, nand_60_out, nand_61_out, nand_62_out, nand_64_out;

  nand nand_1 (nand_1_out, WE, ~In[15]);  // NAND_Gate
  nand nand_2 (nand_2_out, nand_1_out, Out[15]);
  nand nand_3 (nand_3_out, In[15], WE);
  nand nand_4 (nand_4_out, WE, ~In[14]);  // NAND_Gate
  nand nand_5 (Out[15], nand_2_out, nand_3_out);
  nand nand_6 (nand_6_out, nand_4_out, Out[14]);
  nand nand_7 (nand_7_out, WE, ~In[13]);  // NAND_Gate
  nand nand_8 (nand_8_out, In[14], WE);
  nand nand_9 (Out[14], nand_6_out, nand_8_out);
  nand nand_10 (nand_10_out, nand_7_out, Out[13]);
  nand nand_11 (nand_11_out, In[13], WE);
  nand nand_12 (nand_12_out, WE, ~In[12]);  // NAND_Gate
  nand nand_13 (Out[13], nand_10_out, nand_11_out);
  nand nand_14 (nand_14_out, nand_12_out, Out[12]);
  nand nand_15 (nand_15_out, In[12], WE);
  nand nand_16 (nand_16_out, WE, ~In[11]);  // NAND_Gate
  nand nand_17 (nand_17_out, nand_16_out, Out[11]);
  nand nand_18 (Out[12], nand_14_out, nand_15_out);
  nand nand_19 (nand_19_out, In[11], WE);
  nand nand_20 (Out[11], nand_17_out, nand_19_out);
  nand nand_21 (nand_21_out, In[10], WE);
  nand nand_22 (nand_22_out, WE, ~In[10]);  // NAND_Gate
  nand nand_23 (Out[10], nand_24_out, nand_21_out);
  nand nand_24 (nand_24_out, nand_22_out, Out[10]);
  nand nand_25 (nand_25_out, WE, ~In[9]);  // NAND_Gate
  nand nand_26 (nand_26_out, In[9], WE);
  nand nand_27 (Out[9], nand_28_out, nand_26_out);
  nand nand_28 (nand_28_out, nand_25_out, Out[9]);
  nand nand_29 (nand_29_out, WE, ~In[8]);  // NAND_Gate
  nand nand_30 (nand_30_out, In[8], WE);
  nand nand_31 (nand_31_out, nand_29_out, Out[8]);
  nand nand_32 (Out[8], nand_31_out, nand_30_out);
  nand nand_33 (nand_33_out, WE, ~In[7]);  // NAND_Gate
  nand nand_34 (nand_34_out, nand_33_out, Out[7]);
  nand nand_35 (nand_35_out, WE, ~In[6]);  // NAND_Gate
  nand nand_36 (nand_36_out, In[7], WE);
  nand nand_37 (Out[7], nand_34_out, nand_36_out);
  nand nand_38 (nand_38_out, nand_35_out, Out[6]);
  nand nand_39 (nand_39_out, WE, ~In[5]);  // NAND_Gate
  nand nand_40 (nand_40_out, In[6], WE);
  nand nand_41 (nand_41_out, nand_39_out, Out[5]);
  nand nand_42 (Out[6], nand_38_out, nand_40_out);
  nand nand_43 (nand_43_out, WE, ~In[4]);  // NAND_Gate
  nand nand_44 (nand_44_out, In[5], WE);
  nand nand_45 (Out[5], nand_41_out, nand_44_out);
  nand nand_46 (nand_46_out, nand_43_out, Out[4]);
  nand nand_47 (nand_47_out, In[4], WE);
  nand nand_48 (nand_48_out, WE, ~In[3]);  // NAND_Gate
  nand nand_49 (nand_49_out, nand_48_out, Out[3]);
  nand nand_50 (Out[4], nand_46_out, nand_47_out);
  nand nand_51 (nand_51_out, In[3], WE);
  nand nand_52 (Out[3], nand_49_out, nand_51_out);
  nand nand_53 (nand_53_out, WE, ~In[2]);  // NAND_Gate
  nand nand_54 (nand_54_out, In[2], WE);
  nand nand_55 (nand_55_out, nand_53_out, Out[2]);
  nand nand_56 (Out[2], nand_55_out, nand_54_out);
  nand nand_57 (nand_57_out, WE, ~In[1]);  // NAND_Gate
  nand nand_58 (nand_58_out, In[1], WE);
  nand nand_59 (Out[1], nand_60_out, nand_58_out);
  nand nand_60 (nand_60_out, nand_57_out, Out[1]);
  nand nand_61 (nand_61_out, WE, ~In[0]);  // NAND_Gate
  nand nand_62 (nand_62_out, In[0], WE);
  nand nand_63 (Out[0], nand_64_out, nand_62_out);
  nand nand_64 (nand_64_out, nand_61_out, Out[0]);
endmodule

module Incrementer (
  input  [15:0] In,
  input  Clear,
  input  Load,
  input  Increment,
  input  Mem_Load,
  output [15:0] Out
);

  wire counter_1_carry, or_1_out;
  wire [15:0] n16bit_registry_1_1_1_out0, or_2_out;

  or or_1 (or_1_out, Increment, Load);
  Counter #(.width(16), .max('hffff)) counter_1 (
    .load(Load), .D(n16bit_registry_1_1_1_out0), .count(Increment), .Q(Out), .carry(counter_1_carry),
    .clk(or_1_out), .clr(Clear));
  _16bit_Registry__1_1 u_16bit_registry_1_1_1 (
    .WE(Mem_Load), .In(or_2_out), .Out15(n16bit_registry_1_1_1_out0[15]),
    .Out14(n16bit_registry_1_1_1_out0[14]), .Out13(n16bit_registry_1_1_1_out0[13]),
    .Out12(n16bit_registry_1_1_1_out0[12]), .Out11(n16bit_registry_1_1_1_out0[11]),
    .Out10(n16bit_registry_1_1_1_out0[10]), .Out9(n16bit_registry_1_1_1_out0[9]),
    .Out8(n16bit_registry_1_1_1_out0[8]), .Out7(n16bit_registry_1_1_1_out0[7]),
    .Out6(n16bit_registry_1_1_1_out0[6]), .Out5(n16bit_registry_1_1_1_out0[5]),
    .Out4(n16bit_registry_1_1_1_out0[4]), .Out3(n16bit_registry_1_1_1_out0[3]),
    .Out2(n16bit_registry_1_1_1_out0[2]), .Out1(n16bit_registry_1_1_1_out0[1]),
    .Out0(n16bit_registry_1_1_1_out0[0]));
  assign or_2_out = Out | In;  // OR_Gate or_2, 16 bits wide
  // also tied to GND on the sheet: counter_1_carry
endmodule

module Temp_OR (
  input  [15:0] in_1,
  input  [15:0] in_2,
  output [15:0] out_3
);

  wire [15:0] n16bit_registry_1_1_1_out0;

  _16bit_Registry__1_1 u_16bit_registry_1_1_1 (
    .WE(1'b1), .In(in_2), .Out15(n16bit_registry_1_1_1_out0[15]), .Out14(n16bit_registry_1_1_1_out0[14]),
    .Out13(n16bit_registry_1_1_1_out0[13]), .Out12(n16bit_registry_1_1_1_out0[12]),
    .Out11(n16bit_registry_1_1_1_out0[11]), .Out10(n16bit_registry_1_1_1_out0[10]),
    .Out9(n16bit_registry_1_1_1_out0[9]), .Out8(n16bit_registry_1_1_1_out0[8]),
    .Out7(n16bit_registry_1_1_1_out0[7]), .Out6(n16bit_registry_1_1_1_out0[6]),
    .Out5(n16bit_registry_1_1_1_out0[5]), .Out4(n16bit_registry_1_1_1_out0[4]),
    .Out3(n16bit_registry_1_1_1_out0[3]), .Out2(n16bit_registry_1_1_1_out0[2]),
    .Out1(n16bit_registry_1_1_1_out0[1]), .Out0(n16bit_registry_1_1_1_out0[0]));
  assign out_3 = in_1 | n16bit_registry_1_1_1_out0;  // OR_Gate or_1, 16 bits wide
endmodule

module Memory (
  input  [15:0] Memory_Address,
  input  in_2,
  output [15:0] Instruction_Out
);

  wire and_1_out, and_2_out, and_3_out, and_4_out, and_5_out, and_6_out, and_7_out, and_8_out, and_9_out,
       and_10_out, and_11_out, and_12_out, and_13_out, and_14_out, and_15_out, and_16_out, and_17_out,
       and_18_out, and_19_out, and_20_out, and_21_out, and_22_out, and_23_out, and_24_out, and_25_out,
       and_26_out, and_27_out, and_28_out, and_29_out, and_30_out, and_31_out, and_32_out,
       n16bit_registry_1_1_1_out0, n16bit_registry_1_1_1_out1, n16bit_registry_1_1_1_out2,
       n16bit_registry_1_1_1_out3, n16bit_registry_1_1_1_out4, n16bit_registry_1_1_1_out5,
       n16bit_registry_1_1_1_out6, n16bit_registry_1_1_1_out7, n16bit_registry_1_1_1_out8,
       n16bit_registry_1_1_1_out9, n16bit_registry_1_1_1_out10, n16bit_registry_1_1_1_out11,
       n16bit_registry_1_1_1_out12, n16bit_registry_1_1_1_out13, n16bit_registry_1_1_1_out14,
       n16bit_registry_1_1_1_out15, n16bit_registry_1_1_2_out0, n16bit_registry_1_1_2_out1,
       n16bit_registry_1_1_2_out2, n16bit_registry_1_1_2_out3, n16bit_registry_1_1_2_out4,
       n16bit_registry_1_1_2_out5, n16bit_registry_1_1_2_out6, n16bit_registry_1_1_2_out7,
       n16bit_registry_1_1_2_out8, n16bit_registry_1_1_2_out9, n16bit_registry_1_1_2_out10,
       n16bit_registry_1_1_2_out11, n16bit_registry_1_1_2_out12, n16bit_registry_1_1_2_out13,
       n16bit_registry_1_1_2_out14, n16bit_registry_1_1_2_out15, n16bit_registry_1_1_3_out0,
       n16bit_registry_1_1_3_out1, n16bit_registry_1_1_3_out2, n16bit_registry_1_1_3_out3,
       n16bit_registry_1_1_3_out4, n16bit_registry_1_1_3_out5, n16bit_registry_1_1_3_out6,
       n16bit_registry_1_1_3_out7, n16bit_registry_1_1_3_out8, n16bit_registry_1_1_3_out9,
       n16bit_registry_1_1_3_out10, n16bit_registry_1_1_3_out11, n16bit_registry_1_1_3_out12,
       n16bit_registry_1_1_3_out13, n16bit_registry_1_1_3_out14, n16bit_registry_1_1_3_out15,
       n16bit_registry_1_1_4_out0, n16bit_registry_1_1_4_out1, n16bit_registry_1_1_4_out2,
       n16bit_registry_1_1_4_out3, n16bit_registry_1_1_4_out4, n16bit_registry_1_1_4_out5,
       n16bit_registry_1_1_4_out6, n16bit_registry_1_1_4_out7, n16bit_registry_1_1_4_out8,
       n16bit_registry_1_1_4_out9, n16bit_registry_1_1_4_out10, n16bit_registry_1_1_4_out11,
       n16bit_registry_1_1_4_out12, n16bit_registry_1_1_4_out13, n16bit_registry_1_1_4_out14,
       n16bit_registry_1_1_4_out15, n16bit_registry_1_1_5_out0, n16bit_registry_1_1_5_out1,
       n16bit_registry_1_1_5_out2, n16bit_registry_1_1_5_out3, n16bit_registry_1_1_5_out4,
       n16bit_registry_1_1_5_out5, n16bit_registry_1_1_5_out6, n16bit_registry_1_1_5_out7,
       n16bit_registry_1_1_5_out8, n16bit_registry_1_1_5_out9, n16bit_registry_1_1_5_out10,
       n16bit_registry_1_1_5_out11, n16bit_registry_1_1_5_out12, n16bit_registry_1_1_5_out13,
       n16bit_registry_1_1_5_out14, n16bit_registry_1_1_5_out15, n16bit_registry_1_1_6_out0,
       n16bit_registry_1_1_6_out1, n16bit_registry_1_1_6_out2, n16bit_registry_1_1_6_out3,
       n16bit_registry_1_1_6_out4, n16bit_registry_1_1_6_out5, n16bit_registry_1_1_6_out6,
       n16bit_registry_1_1_6_out7, n16bit_registry_1_1_6_out8, n16bit_registry_1_1_6_out9,
       n16bit_registry_1_1_6_out10, n16bit_registry_1_1_6_out11, n16bit_registry_1_1_6_out12,
       n16bit_registry_1_1_6_out13, n16bit_registry_1_1_6_out14, n16bit_registry_1_1_6_out15,
       n16bit_registry_1_1_7_out0, n16bit_registry_1_1_7_out1, n16bit_registry_1_1_7_out2,
       n16bit_registry_1_1_7_out3, n16bit_registry_1_1_7_out4, n16bit_registry_1_1_7_out5,
       n16bit_registry_1_1_7_out6, n16bit_registry_1_1_7_out7, n16bit_registry_1_1_7_out8,
       n16bit_registry_1_1_7_out9, n16bit_registry_1_1_7_out10, n16bit_registry_1_1_7_out11,
       n16bit_registry_1_1_7_out12, n16bit_registry_1_1_7_out13, n16bit_registry_1_1_7_out14,
       n16bit_registry_1_1_7_out15, n16bit_registry_1_1_8_out0, n16bit_registry_1_1_8_out1,
       n16bit_registry_1_1_8_out2, n16bit_registry_1_1_8_out3, n16bit_registry_1_1_8_out4,
       n16bit_registry_1_1_8_out5, n16bit_registry_1_1_8_out6, n16bit_registry_1_1_8_out7,
       n16bit_registry_1_1_8_out8, n16bit_registry_1_1_8_out9, n16bit_registry_1_1_8_out10,
       n16bit_registry_1_1_8_out11, n16bit_registry_1_1_8_out12, n16bit_registry_1_1_8_out13,
       n16bit_registry_1_1_8_out14, n16bit_registry_1_1_8_out15, n16bit_registry_1_1_9_out0,
       n16bit_registry_1_1_9_out1, n16bit_registry_1_1_9_out2, n16bit_registry_1_1_9_out3,
       n16bit_registry_1_1_9_out4, n16bit_registry_1_1_9_out5, n16bit_registry_1_1_9_out6,
       n16bit_registry_1_1_9_out7, n16bit_registry_1_1_9_out8, n16bit_registry_1_1_9_out9,
       n16bit_registry_1_1_9_out10, n16bit_registry_1_1_9_out11, n16bit_registry_1_1_9_out12,
       n16bit_registry_1_1_9_out13, n16bit_registry_1_1_9_out14, n16bit_registry_1_1_9_out15,
       n16bit_registry_1_1_10_out0, n16bit_registry_1_1_10_out1, n16bit_registry_1_1_10_out2,
       n16bit_registry_1_1_10_out3, n16bit_registry_1_1_10_out4, n16bit_registry_1_1_10_out5,
       n16bit_registry_1_1_10_out6, n16bit_registry_1_1_10_out7, n16bit_registry_1_1_10_out8,
       n16bit_registry_1_1_10_out9, n16bit_registry_1_1_10_out10, n16bit_registry_1_1_10_out11,
       n16bit_registry_1_1_10_out12, n16bit_registry_1_1_10_out13, n16bit_registry_1_1_10_out14,
       n16bit_registry_1_1_10_out15, n16bit_registry_1_1_11_out0, n16bit_registry_1_1_11_out1,
       n16bit_registry_1_1_11_out2, n16bit_registry_1_1_11_out3, n16bit_registry_1_1_11_out4,
       n16bit_registry_1_1_11_out5, n16bit_registry_1_1_11_out6, n16bit_registry_1_1_11_out7,
       n16bit_registry_1_1_11_out8, n16bit_registry_1_1_11_out9, n16bit_registry_1_1_11_out10,
       n16bit_registry_1_1_11_out11, n16bit_registry_1_1_11_out12, n16bit_registry_1_1_11_out13,
       n16bit_registry_1_1_11_out14, n16bit_registry_1_1_11_out15, n16bit_registry_1_1_12_out0,
       n16bit_registry_1_1_12_out1, n16bit_registry_1_1_12_out2, n16bit_registry_1_1_12_out3,
       n16bit_registry_1_1_12_out4, n16bit_registry_1_1_12_out5, n16bit_registry_1_1_12_out6,
       n16bit_registry_1_1_12_out7, n16bit_registry_1_1_12_out8, n16bit_registry_1_1_12_out9,
       n16bit_registry_1_1_12_out10, n16bit_registry_1_1_12_out11, n16bit_registry_1_1_12_out12,
       n16bit_registry_1_1_12_out13, n16bit_registry_1_1_12_out14, n16bit_registry_1_1_12_out15,
       n16bit_registry_1_1_13_out0, n16bit_registry_1_1_13_out1, n16bit_registry_1_1_13_out2,
       n16bit_registry_1_1_13_out3, n16bit_registry_1_1_13_out4, n16bit_registry_1_1_13_out5,
       n16bit_registry_1_1_13_out6, n16bit_registry_1_1_13_out7, n16bit_registry_1_1_13_out8,
       n16bit_registry_1_1_13_out9, n16bit_registry_1_1_13_out10, n16bit_registry_1_1_13_out11,
       n16bit_registry_1_1_13_out12, n16bit_registry_1_1_13_out13, n16bit_registry_1_1_13_out14,
       n16bit_registry_1_1_13_out15, n16bit_registry_1_1_14_out0, n16bit_registry_1_1_14_out1,
       n16bit_registry_1_1_14_out2, n16bit_registry_1_1_14_out3, n16bit_registry_1_1_14_out4,
       n16bit_registry_1_1_14_out5, n16bit_registry_1_1_14_out6, n16bit_registry_1_1_14_out7,
       n16bit_registry_1_1_14_out8, n16bit_registry_1_1_14_out9, n16bit_registry_1_1_14_out10,
       n16bit_registry_1_1_14_out11, n16bit_registry_1_1_14_out12, n16bit_registry_1_1_14_out13,
       n16bit_registry_1_1_14_out14, n16bit_registry_1_1_14_out15, n16bit_registry_1_1_15_out0,
       n16bit_registry_1_1_15_out1, n16bit_registry_1_1_15_out2, n16bit_registry_1_1_15_out3,
       n16bit_registry_1_1_15_out4, n16bit_registry_1_1_15_out5, n16bit_registry_1_1_15_out6,
       n16bit_registry_1_1_15_out7, n16bit_registry_1_1_15_out8, n16bit_registry_1_1_15_out9,
       n16bit_registry_1_1_15_out10, n16bit_registry_1_1_15_out11, n16bit_registry_1_1_15_out12,
       n16bit_registry_1_1_15_out13, n16bit_registry_1_1_15_out14, n16bit_registry_1_1_15_out15,
       n16bit_registry_1_1_16_out0, n16bit_registry_1_1_16_out1, n16bit_registry_1_1_16_out2,
       n16bit_registry_1_1_16_out3, n16bit_registry_1_1_16_out4, n16bit_registry_1_1_16_out5,
       n16bit_registry_1_1_16_out6, n16bit_registry_1_1_16_out7, n16bit_registry_1_1_16_out8,
       n16bit_registry_1_1_16_out9, n16bit_registry_1_1_16_out10, n16bit_registry_1_1_16_out11,
       n16bit_registry_1_1_16_out12, n16bit_registry_1_1_16_out13, n16bit_registry_1_1_16_out14,
       n16bit_registry_1_1_16_out15, n16bit_registry_1_1_17_out0, n16bit_registry_1_1_17_out1,
       n16bit_registry_1_1_17_out2, n16bit_registry_1_1_17_out3, n16bit_registry_1_1_17_out4,
       n16bit_registry_1_1_17_out5, n16bit_registry_1_1_17_out6, n16bit_registry_1_1_17_out7,
       n16bit_registry_1_1_17_out8, n16bit_registry_1_1_17_out9, n16bit_registry_1_1_17_out10,
       n16bit_registry_1_1_17_out11, n16bit_registry_1_1_17_out12, n16bit_registry_1_1_17_out13,
       n16bit_registry_1_1_17_out14, n16bit_registry_1_1_17_out15;
  wire [15:0] n16bit_registry_selector_1_out, n16bit_registry_selector_2_out, n16bit_registry_selector_3_out,
       n16bit_registry_selector_4_out, n16bit_registry_selector_5_out, n16bit_registry_selector_6_out,
       n16bit_registry_selector_7_out, n16bit_registry_selector_8_out, n16bit_registry_selector_9_out,
       n16bit_registry_selector_10_out, n16bit_registry_selector_11_out, n16bit_registry_selector_12_out,
       n16bit_registry_selector_13_out, n16bit_registry_selector_14_out, n16bit_registry_selector_15_out,
       n16bit_registry_selector_16_out;

  _16bit_Registry__1_1 u_16bit_registry_1_1_1 (
    .WE(in_2), .In(Memory_Address), .Out15(n16bit_registry_1_1_1_out15), .Out14(n16bit_registry_1_1_1_out14),
    .Out13(n16bit_registry_1_1_1_out13), .Out12(n16bit_registry_1_1_1_out12),
    .Out11(n16bit_registry_1_1_1_out11), .Out10(n16bit_registry_1_1_1_out10),
    .Out9(n16bit_registry_1_1_1_out9), .Out8(n16bit_registry_1_1_1_out8), .Out7(n16bit_registry_1_1_1_out7),
    .Out6(n16bit_registry_1_1_1_out6), .Out5(n16bit_registry_1_1_1_out5), .Out4(n16bit_registry_1_1_1_out4),
    .Out3(n16bit_registry_1_1_1_out3), .Out2(n16bit_registry_1_1_1_out2), .Out1(n16bit_registry_1_1_1_out1),
    .Out0(n16bit_registry_1_1_1_out0));
  and and_1 (and_1_out, ~n16bit_registry_1_1_1_out0, ~n16bit_registry_1_1_1_out1, ~n16bit_registry_1_1_1_out2, ~n16bit_registry_1_1_1_out3);  // AND_Gate
  and and_2 (and_2_out, n16bit_registry_1_1_1_out0, ~n16bit_registry_1_1_1_out1, ~n16bit_registry_1_1_1_out2, ~n16bit_registry_1_1_1_out3);  // AND_Gate
  and and_3 (and_3_out, ~n16bit_registry_1_1_1_out0, n16bit_registry_1_1_1_out1, ~n16bit_registry_1_1_1_out2, ~n16bit_registry_1_1_1_out3);  // AND_Gate
  and and_4 (and_4_out, n16bit_registry_1_1_1_out0, n16bit_registry_1_1_1_out1, ~n16bit_registry_1_1_1_out2, ~n16bit_registry_1_1_1_out3);  // AND_Gate
  and and_5 (and_5_out, ~n16bit_registry_1_1_1_out0, ~n16bit_registry_1_1_1_out1, n16bit_registry_1_1_1_out2, ~n16bit_registry_1_1_1_out3);  // AND_Gate
  and and_6 (and_6_out, n16bit_registry_1_1_1_out0, ~n16bit_registry_1_1_1_out1, n16bit_registry_1_1_1_out2, ~n16bit_registry_1_1_1_out3);  // AND_Gate
  and and_7 (and_7_out, ~n16bit_registry_1_1_1_out0, n16bit_registry_1_1_1_out1, n16bit_registry_1_1_1_out2, ~n16bit_registry_1_1_1_out3);  // AND_Gate
  and and_8 (and_8_out, n16bit_registry_1_1_1_out0, n16bit_registry_1_1_1_out1, n16bit_registry_1_1_1_out2, ~n16bit_registry_1_1_1_out3);  // AND_Gate
  and and_9 (and_9_out, ~n16bit_registry_1_1_1_out0, ~n16bit_registry_1_1_1_out1, ~n16bit_registry_1_1_1_out2, n16bit_registry_1_1_1_out3);  // AND_Gate
  and and_10 (and_10_out, n16bit_registry_1_1_1_out0, ~n16bit_registry_1_1_1_out1, ~n16bit_registry_1_1_1_out2, n16bit_registry_1_1_1_out3);  // AND_Gate
  and and_11 (and_11_out, ~n16bit_registry_1_1_1_out0, n16bit_registry_1_1_1_out1, ~n16bit_registry_1_1_1_out2, n16bit_registry_1_1_1_out3);  // AND_Gate
  and and_12 (and_12_out, n16bit_registry_1_1_1_out0, n16bit_registry_1_1_1_out1, ~n16bit_registry_1_1_1_out2, n16bit_registry_1_1_1_out3);  // AND_Gate
  and and_13 (and_13_out, ~n16bit_registry_1_1_1_out0, ~n16bit_registry_1_1_1_out1, n16bit_registry_1_1_1_out2, n16bit_registry_1_1_1_out3);  // AND_Gate
  and and_14 (and_14_out, n16bit_registry_1_1_1_out0, ~n16bit_registry_1_1_1_out1, n16bit_registry_1_1_1_out2, n16bit_registry_1_1_1_out3);  // AND_Gate
  and and_15 (and_15_out, ~n16bit_registry_1_1_1_out0, n16bit_registry_1_1_1_out1, n16bit_registry_1_1_1_out2, n16bit_registry_1_1_1_out3);  // AND_Gate
  and and_16 (and_16_out, n16bit_registry_1_1_1_out0, n16bit_registry_1_1_1_out1, n16bit_registry_1_1_1_out2, n16bit_registry_1_1_1_out3);
  _16bit_Registry__1_1 u_16bit_registry_1_1_2 (
    .WE(and_17_out), .In(16'h6203), .Out15(n16bit_registry_1_1_2_out15), .Out14(n16bit_registry_1_1_2_out14),
    .Out13(n16bit_registry_1_1_2_out13), .Out12(n16bit_registry_1_1_2_out12),
    .Out11(n16bit_registry_1_1_2_out11), .Out10(n16bit_registry_1_1_2_out10),
    .Out9(n16bit_registry_1_1_2_out9), .Out8(n16bit_registry_1_1_2_out8), .Out7(n16bit_registry_1_1_2_out7),
    .Out6(n16bit_registry_1_1_2_out6), .Out5(n16bit_registry_1_1_2_out5), .Out4(n16bit_registry_1_1_2_out4),
    .Out3(n16bit_registry_1_1_2_out3), .Out2(n16bit_registry_1_1_2_out2), .Out1(n16bit_registry_1_1_2_out1),
    .Out0(n16bit_registry_1_1_2_out0));
  and and_17 (and_17_out, and_1_out, in_2);
  _16bit_Registry_Selector u_16bit_registry_selector_1 (
    .WE(and_1_out), .In(n16bit_registry_1_1_2_out15), .In_2(n16bit_registry_1_1_2_out14),
    .In_3(n16bit_registry_1_1_2_out13), .In_4(n16bit_registry_1_1_2_out12),
    .In_5(n16bit_registry_1_1_2_out11), .In_6(n16bit_registry_1_1_2_out10),
    .In_7(n16bit_registry_1_1_2_out9), .In_8(n16bit_registry_1_1_2_out8), .In_9(n16bit_registry_1_1_2_out7),
    .In_10(n16bit_registry_1_1_2_out6), .In_11(n16bit_registry_1_1_2_out5),
    .In_12(n16bit_registry_1_1_2_out4), .In_13(n16bit_registry_1_1_2_out3),
    .In_14(n16bit_registry_1_1_2_out2), .In_15(n16bit_registry_1_1_2_out1),
    .In_16(n16bit_registry_1_1_2_out0), .Out(n16bit_registry_selector_1_out));
  _16bit_Registry__1_1 u_16bit_registry_1_1_3 (
    .WE(and_18_out), .In(16'h6404), .Out15(n16bit_registry_1_1_3_out15), .Out14(n16bit_registry_1_1_3_out14),
    .Out13(n16bit_registry_1_1_3_out13), .Out12(n16bit_registry_1_1_3_out12),
    .Out11(n16bit_registry_1_1_3_out11), .Out10(n16bit_registry_1_1_3_out10),
    .Out9(n16bit_registry_1_1_3_out9), .Out8(n16bit_registry_1_1_3_out8), .Out7(n16bit_registry_1_1_3_out7),
    .Out6(n16bit_registry_1_1_3_out6), .Out5(n16bit_registry_1_1_3_out5), .Out4(n16bit_registry_1_1_3_out4),
    .Out3(n16bit_registry_1_1_3_out3), .Out2(n16bit_registry_1_1_3_out2), .Out1(n16bit_registry_1_1_3_out1),
    .Out0(n16bit_registry_1_1_3_out0));
  and and_18 (and_18_out, and_2_out, in_2);
  _16bit_Registry_Selector u_16bit_registry_selector_2 (
    .WE(and_2_out), .In(n16bit_registry_1_1_3_out15), .In_2(n16bit_registry_1_1_3_out14),
    .In_3(n16bit_registry_1_1_3_out13), .In_4(n16bit_registry_1_1_3_out12),
    .In_5(n16bit_registry_1_1_3_out11), .In_6(n16bit_registry_1_1_3_out10),
    .In_7(n16bit_registry_1_1_3_out9), .In_8(n16bit_registry_1_1_3_out8), .In_9(n16bit_registry_1_1_3_out7),
    .In_10(n16bit_registry_1_1_3_out6), .In_11(n16bit_registry_1_1_3_out5),
    .In_12(n16bit_registry_1_1_3_out4), .In_13(n16bit_registry_1_1_3_out3),
    .In_14(n16bit_registry_1_1_3_out2), .In_15(n16bit_registry_1_1_3_out1),
    .In_16(n16bit_registry_1_1_3_out0), .Out(n16bit_registry_selector_2_out));
  _16bit_Registry__1_1 u_16bit_registry_1_1_4 (
    .WE(and_19_out), .In(16'h1042), .Out15(n16bit_registry_1_1_4_out15), .Out14(n16bit_registry_1_1_4_out14),
    .Out13(n16bit_registry_1_1_4_out13), .Out12(n16bit_registry_1_1_4_out12),
    .Out11(n16bit_registry_1_1_4_out11), .Out10(n16bit_registry_1_1_4_out10),
    .Out9(n16bit_registry_1_1_4_out9), .Out8(n16bit_registry_1_1_4_out8), .Out7(n16bit_registry_1_1_4_out7),
    .Out6(n16bit_registry_1_1_4_out6), .Out5(n16bit_registry_1_1_4_out5), .Out4(n16bit_registry_1_1_4_out4),
    .Out3(n16bit_registry_1_1_4_out3), .Out2(n16bit_registry_1_1_4_out2), .Out1(n16bit_registry_1_1_4_out1),
    .Out0(n16bit_registry_1_1_4_out0));
  and and_19 (and_19_out, and_3_out, in_2);
  _16bit_Registry_Selector u_16bit_registry_selector_3 (
    .WE(and_3_out), .In(n16bit_registry_1_1_4_out15), .In_2(n16bit_registry_1_1_4_out14),
    .In_3(n16bit_registry_1_1_4_out13), .In_4(n16bit_registry_1_1_4_out12),
    .In_5(n16bit_registry_1_1_4_out11), .In_6(n16bit_registry_1_1_4_out10),
    .In_7(n16bit_registry_1_1_4_out9), .In_8(n16bit_registry_1_1_4_out8), .In_9(n16bit_registry_1_1_4_out7),
    .In_10(n16bit_registry_1_1_4_out6), .In_11(n16bit_registry_1_1_4_out5),
    .In_12(n16bit_registry_1_1_4_out4), .In_13(n16bit_registry_1_1_4_out3),
    .In_14(n16bit_registry_1_1_4_out2), .In_15(n16bit_registry_1_1_4_out1),
    .In_16(n16bit_registry_1_1_4_out0), .Out(n16bit_registry_selector_3_out));
  _16bit_Registry__1_1 u_16bit_registry_1_1_5 (
    .WE(and_20_out), .In(16'hc), .Out15(n16bit_registry_1_1_5_out15), .Out14(n16bit_registry_1_1_5_out14),
    .Out13(n16bit_registry_1_1_5_out13), .Out12(n16bit_registry_1_1_5_out12),
    .Out11(n16bit_registry_1_1_5_out11), .Out10(n16bit_registry_1_1_5_out10),
    .Out9(n16bit_registry_1_1_5_out9), .Out8(n16bit_registry_1_1_5_out8), .Out7(n16bit_registry_1_1_5_out7),
    .Out6(n16bit_registry_1_1_5_out6), .Out5(n16bit_registry_1_1_5_out5), .Out4(n16bit_registry_1_1_5_out4),
    .Out3(n16bit_registry_1_1_5_out3), .Out2(n16bit_registry_1_1_5_out2), .Out1(n16bit_registry_1_1_5_out1),
    .Out0(n16bit_registry_1_1_5_out0));
  and and_20 (and_20_out, and_4_out, in_2);
  _16bit_Registry_Selector u_16bit_registry_selector_4 (
    .WE(and_4_out), .In(n16bit_registry_1_1_5_out15), .In_2(n16bit_registry_1_1_5_out14),
    .In_3(n16bit_registry_1_1_5_out13), .In_4(n16bit_registry_1_1_5_out12),
    .In_5(n16bit_registry_1_1_5_out11), .In_6(n16bit_registry_1_1_5_out10),
    .In_7(n16bit_registry_1_1_5_out9), .In_8(n16bit_registry_1_1_5_out8), .In_9(n16bit_registry_1_1_5_out7),
    .In_10(n16bit_registry_1_1_5_out6), .In_11(n16bit_registry_1_1_5_out5),
    .In_12(n16bit_registry_1_1_5_out4), .In_13(n16bit_registry_1_1_5_out3),
    .In_14(n16bit_registry_1_1_5_out2), .In_15(n16bit_registry_1_1_5_out1),
    .In_16(n16bit_registry_1_1_5_out0), .Out(n16bit_registry_selector_4_out));
  _16bit_Registry__1_1 u_16bit_registry_1_1_6 (
    .WE(and_21_out), .In(16'h8), .Out15(n16bit_registry_1_1_6_out15), .Out14(n16bit_registry_1_1_6_out14),
    .Out13(n16bit_registry_1_1_6_out13), .Out12(n16bit_registry_1_1_6_out12),
    .Out11(n16bit_registry_1_1_6_out11), .Out10(n16bit_registry_1_1_6_out10),
    .Out9(n16bit_registry_1_1_6_out9), .Out8(n16bit_registry_1_1_6_out8), .Out7(n16bit_registry_1_1_6_out7),
    .Out6(n16bit_registry_1_1_6_out6), .Out5(n16bit_registry_1_1_6_out5), .Out4(n16bit_registry_1_1_6_out4),
    .Out3(n16bit_registry_1_1_6_out3), .Out2(n16bit_registry_1_1_6_out2), .Out1(n16bit_registry_1_1_6_out1),
    .Out0(n16bit_registry_1_1_6_out0));
  and and_21 (and_21_out, and_5_out, in_2);
  _16bit_Registry_Selector u_16bit_registry_selector_5 (
    .WE(and_5_out), .In(n16bit_registry_1_1_6_out15), .In_2(n16bit_registry_1_1_6_out14),
    .In_3(n16bit_registry_1_1_6_out13), .In_4(n16bit_registry_1_1_6_out12),
    .In_5(n16bit_registry_1_1_6_out11), .In_6(n16bit_registry_1_1_6_out10),
    .In_7(n16bit_registry_1_1_6_out9), .In_8(n16bit_registry_1_1_6_out8), .In_9(n16bit_registry_1_1_6_out7),
    .In_10(n16bit_registry_1_1_6_out6), .In_11(n16bit_registry_1_1_6_out5),
    .In_12(n16bit_registry_1_1_6_out4), .In_13(n16bit_registry_1_1_6_out3),
    .In_14(n16bit_registry_1_1_6_out2), .In_15(n16bit_registry_1_1_6_out1),
    .In_16(n16bit_registry_1_1_6_out0), .Out(n16bit_registry_selector_5_out));
  _16bit_Registry__1_1 u_16bit_registry_1_1_7 (
    .WE(and_22_out), .In(16'h1100), .Out15(n16bit_registry_1_1_7_out15), .Out14(n16bit_registry_1_1_7_out14),
    .Out13(n16bit_registry_1_1_7_out13), .Out12(n16bit_registry_1_1_7_out12),
    .Out11(n16bit_registry_1_1_7_out11), .Out10(n16bit_registry_1_1_7_out10),
    .Out9(n16bit_registry_1_1_7_out9), .Out8(n16bit_registry_1_1_7_out8), .Out7(n16bit_registry_1_1_7_out7),
    .Out6(n16bit_registry_1_1_7_out6), .Out5(n16bit_registry_1_1_7_out5), .Out4(n16bit_registry_1_1_7_out4),
    .Out3(n16bit_registry_1_1_7_out3), .Out2(n16bit_registry_1_1_7_out2), .Out1(n16bit_registry_1_1_7_out1),
    .Out0(n16bit_registry_1_1_7_out0));
  and and_22 (and_22_out, and_6_out, in_2);
  _16bit_Registry_Selector u_16bit_registry_selector_6 (
    .WE(and_6_out), .In(n16bit_registry_1_1_7_out15), .In_2(n16bit_registry_1_1_7_out14),
    .In_3(n16bit_registry_1_1_7_out13), .In_4(n16bit_registry_1_1_7_out12),
    .In_5(n16bit_registry_1_1_7_out11), .In_6(n16bit_registry_1_1_7_out10),
    .In_7(n16bit_registry_1_1_7_out9), .In_8(n16bit_registry_1_1_7_out8), .In_9(n16bit_registry_1_1_7_out7),
    .In_10(n16bit_registry_1_1_7_out6), .In_11(n16bit_registry_1_1_7_out5),
    .In_12(n16bit_registry_1_1_7_out4), .In_13(n16bit_registry_1_1_7_out3),
    .In_14(n16bit_registry_1_1_7_out2), .In_15(n16bit_registry_1_1_7_out1),
    .In_16(n16bit_registry_1_1_7_out0), .Out(n16bit_registry_selector_6_out));
  _16bit_Registry__1_1 u_16bit_registry_1_1_8 (
    .WE(and_23_out), .In(16'h1100), .Out15(n16bit_registry_1_1_8_out15), .Out14(n16bit_registry_1_1_8_out14),
    .Out13(n16bit_registry_1_1_8_out13), .Out12(n16bit_registry_1_1_8_out12),
    .Out11(n16bit_registry_1_1_8_out11), .Out10(n16bit_registry_1_1_8_out10),
    .Out9(n16bit_registry_1_1_8_out9), .Out8(n16bit_registry_1_1_8_out8), .Out7(n16bit_registry_1_1_8_out7),
    .Out6(n16bit_registry_1_1_8_out6), .Out5(n16bit_registry_1_1_8_out5), .Out4(n16bit_registry_1_1_8_out4),
    .Out3(n16bit_registry_1_1_8_out3), .Out2(n16bit_registry_1_1_8_out2), .Out1(n16bit_registry_1_1_8_out1),
    .Out0(n16bit_registry_1_1_8_out0));
  and and_23 (and_23_out, and_7_out, in_2);
  _16bit_Registry_Selector u_16bit_registry_selector_7 (
    .WE(and_7_out), .In(n16bit_registry_1_1_8_out15), .In_2(n16bit_registry_1_1_8_out14),
    .In_3(n16bit_registry_1_1_8_out13), .In_4(n16bit_registry_1_1_8_out12),
    .In_5(n16bit_registry_1_1_8_out11), .In_6(n16bit_registry_1_1_8_out10),
    .In_7(n16bit_registry_1_1_8_out9), .In_8(n16bit_registry_1_1_8_out8), .In_9(n16bit_registry_1_1_8_out7),
    .In_10(n16bit_registry_1_1_8_out6), .In_11(n16bit_registry_1_1_8_out5),
    .In_12(n16bit_registry_1_1_8_out4), .In_13(n16bit_registry_1_1_8_out3),
    .In_14(n16bit_registry_1_1_8_out2), .In_15(n16bit_registry_1_1_8_out1),
    .In_16(n16bit_registry_1_1_8_out0), .Out(n16bit_registry_selector_7_out));
  _16bit_Registry__1_1 u_16bit_registry_1_1_9 (
    .WE(and_24_out), .In(16'h1100), .Out15(n16bit_registry_1_1_9_out15), .Out14(n16bit_registry_1_1_9_out14),
    .Out13(n16bit_registry_1_1_9_out13), .Out12(n16bit_registry_1_1_9_out12),
    .Out11(n16bit_registry_1_1_9_out11), .Out10(n16bit_registry_1_1_9_out10),
    .Out9(n16bit_registry_1_1_9_out9), .Out8(n16bit_registry_1_1_9_out8), .Out7(n16bit_registry_1_1_9_out7),
    .Out6(n16bit_registry_1_1_9_out6), .Out5(n16bit_registry_1_1_9_out5), .Out4(n16bit_registry_1_1_9_out4),
    .Out3(n16bit_registry_1_1_9_out3), .Out2(n16bit_registry_1_1_9_out2), .Out1(n16bit_registry_1_1_9_out1),
    .Out0(n16bit_registry_1_1_9_out0));
  and and_24 (and_24_out, and_8_out, in_2);
  _16bit_Registry_Selector u_16bit_registry_selector_8 (
    .WE(and_8_out), .In(n16bit_registry_1_1_9_out15), .In_2(n16bit_registry_1_1_9_out14),
    .In_3(n16bit_registry_1_1_9_out13), .In_4(n16bit_registry_1_1_9_out12),
    .In_5(n16bit_registry_1_1_9_out11), .In_6(n16bit_registry_1_1_9_out10),
    .In_7(n16bit_registry_1_1_9_out9), .In_8(n16bit_registry_1_1_9_out8), .In_9(n16bit_registry_1_1_9_out7),
    .In_10(n16bit_registry_1_1_9_out6), .In_11(n16bit_registry_1_1_9_out5),
    .In_12(n16bit_registry_1_1_9_out4), .In_13(n16bit_registry_1_1_9_out3),
    .In_14(n16bit_registry_1_1_9_out2), .In_15(n16bit_registry_1_1_9_out1),
    .In_16(n16bit_registry_1_1_9_out0), .Out(n16bit_registry_selector_8_out));
  _16bit_Registry__1_1 u_16bit_registry_1_1_10 (
    .WE(and_25_out), .In(16'h1100), .Out15(n16bit_registry_1_1_10_out15),
    .Out14(n16bit_registry_1_1_10_out14), .Out13(n16bit_registry_1_1_10_out13),
    .Out12(n16bit_registry_1_1_10_out12), .Out11(n16bit_registry_1_1_10_out11),
    .Out10(n16bit_registry_1_1_10_out10), .Out9(n16bit_registry_1_1_10_out9),
    .Out8(n16bit_registry_1_1_10_out8), .Out7(n16bit_registry_1_1_10_out7),
    .Out6(n16bit_registry_1_1_10_out6), .Out5(n16bit_registry_1_1_10_out5),
    .Out4(n16bit_registry_1_1_10_out4), .Out3(n16bit_registry_1_1_10_out3),
    .Out2(n16bit_registry_1_1_10_out2), .Out1(n16bit_registry_1_1_10_out1), .Out0(n16bit_registry_1_1_10_out0));
  and and_25 (and_25_out, and_9_out, in_2);
  _16bit_Registry_Selector u_16bit_registry_selector_9 (
    .WE(and_9_out), .In(n16bit_registry_1_1_10_out15), .In_2(n16bit_registry_1_1_10_out14),
    .In_3(n16bit_registry_1_1_10_out13), .In_4(n16bit_registry_1_1_10_out12),
    .In_5(n16bit_registry_1_1_10_out11), .In_6(n16bit_registry_1_1_10_out10),
    .In_7(n16bit_registry_1_1_10_out9), .In_8(n16bit_registry_1_1_10_out8),
    .In_9(n16bit_registry_1_1_10_out7), .In_10(n16bit_registry_1_1_10_out6),
    .In_11(n16bit_registry_1_1_10_out5), .In_12(n16bit_registry_1_1_10_out4),
    .In_13(n16bit_registry_1_1_10_out3), .In_14(n16bit_registry_1_1_10_out2),
    .In_15(n16bit_registry_1_1_10_out1), .In_16(n16bit_registry_1_1_10_out0),
    .Out(n16bit_registry_selector_9_out));
  _16bit_Registry__1_1 u_16bit_registry_1_1_11 (
    .WE(and_26_out), .In(16'h1100), .Out15(n16bit_registry_1_1_11_out15),
    .Out14(n16bit_registry_1_1_11_out14), .Out13(n16bit_registry_1_1_11_out13),
    .Out12(n16bit_registry_1_1_11_out12), .Out11(n16bit_registry_1_1_11_out11),
    .Out10(n16bit_registry_1_1_11_out10), .Out9(n16bit_registry_1_1_11_out9),
    .Out8(n16bit_registry_1_1_11_out8), .Out7(n16bit_registry_1_1_11_out7),
    .Out6(n16bit_registry_1_1_11_out6), .Out5(n16bit_registry_1_1_11_out5),
    .Out4(n16bit_registry_1_1_11_out4), .Out3(n16bit_registry_1_1_11_out3),
    .Out2(n16bit_registry_1_1_11_out2), .Out1(n16bit_registry_1_1_11_out1), .Out0(n16bit_registry_1_1_11_out0));
  and and_26 (and_26_out, and_10_out, in_2);
  _16bit_Registry_Selector u_16bit_registry_selector_10 (
    .WE(and_10_out), .In(n16bit_registry_1_1_11_out15), .In_2(n16bit_registry_1_1_11_out14),
    .In_3(n16bit_registry_1_1_11_out13), .In_4(n16bit_registry_1_1_11_out12),
    .In_5(n16bit_registry_1_1_11_out11), .In_6(n16bit_registry_1_1_11_out10),
    .In_7(n16bit_registry_1_1_11_out9), .In_8(n16bit_registry_1_1_11_out8),
    .In_9(n16bit_registry_1_1_11_out7), .In_10(n16bit_registry_1_1_11_out6),
    .In_11(n16bit_registry_1_1_11_out5), .In_12(n16bit_registry_1_1_11_out4),
    .In_13(n16bit_registry_1_1_11_out3), .In_14(n16bit_registry_1_1_11_out2),
    .In_15(n16bit_registry_1_1_11_out1), .In_16(n16bit_registry_1_1_11_out0),
    .Out(n16bit_registry_selector_10_out));
  _16bit_Registry__1_1 u_16bit_registry_1_1_12 (
    .WE(and_27_out), .In(16'h1100), .Out15(n16bit_registry_1_1_12_out15),
    .Out14(n16bit_registry_1_1_12_out14), .Out13(n16bit_registry_1_1_12_out13),
    .Out12(n16bit_registry_1_1_12_out12), .Out11(n16bit_registry_1_1_12_out11),
    .Out10(n16bit_registry_1_1_12_out10), .Out9(n16bit_registry_1_1_12_out9),
    .Out8(n16bit_registry_1_1_12_out8), .Out7(n16bit_registry_1_1_12_out7),
    .Out6(n16bit_registry_1_1_12_out6), .Out5(n16bit_registry_1_1_12_out5),
    .Out4(n16bit_registry_1_1_12_out4), .Out3(n16bit_registry_1_1_12_out3),
    .Out2(n16bit_registry_1_1_12_out2), .Out1(n16bit_registry_1_1_12_out1), .Out0(n16bit_registry_1_1_12_out0));
  and and_27 (and_27_out, and_11_out, in_2);
  _16bit_Registry_Selector u_16bit_registry_selector_11 (
    .WE(and_11_out), .In(n16bit_registry_1_1_12_out15), .In_2(n16bit_registry_1_1_12_out14),
    .In_3(n16bit_registry_1_1_12_out13), .In_4(n16bit_registry_1_1_12_out12),
    .In_5(n16bit_registry_1_1_12_out11), .In_6(n16bit_registry_1_1_12_out10),
    .In_7(n16bit_registry_1_1_12_out9), .In_8(n16bit_registry_1_1_12_out8),
    .In_9(n16bit_registry_1_1_12_out7), .In_10(n16bit_registry_1_1_12_out6),
    .In_11(n16bit_registry_1_1_12_out5), .In_12(n16bit_registry_1_1_12_out4),
    .In_13(n16bit_registry_1_1_12_out3), .In_14(n16bit_registry_1_1_12_out2),
    .In_15(n16bit_registry_1_1_12_out1), .In_16(n16bit_registry_1_1_12_out0),
    .Out(n16bit_registry_selector_11_out));
  _16bit_Registry__1_1 u_16bit_registry_1_1_13 (
    .WE(and_28_out), .In(16'h1100), .Out15(n16bit_registry_1_1_13_out15),
    .Out14(n16bit_registry_1_1_13_out14), .Out13(n16bit_registry_1_1_13_out13),
    .Out12(n16bit_registry_1_1_13_out12), .Out11(n16bit_registry_1_1_13_out11),
    .Out10(n16bit_registry_1_1_13_out10), .Out9(n16bit_registry_1_1_13_out9),
    .Out8(n16bit_registry_1_1_13_out8), .Out7(n16bit_registry_1_1_13_out7),
    .Out6(n16bit_registry_1_1_13_out6), .Out5(n16bit_registry_1_1_13_out5),
    .Out4(n16bit_registry_1_1_13_out4), .Out3(n16bit_registry_1_1_13_out3),
    .Out2(n16bit_registry_1_1_13_out2), .Out1(n16bit_registry_1_1_13_out1), .Out0(n16bit_registry_1_1_13_out0));
  and and_28 (and_28_out, and_12_out, in_2);
  _16bit_Registry_Selector u_16bit_registry_selector_12 (
    .WE(and_12_out), .In(n16bit_registry_1_1_13_out15), .In_2(n16bit_registry_1_1_13_out14),
    .In_3(n16bit_registry_1_1_13_out13), .In_4(n16bit_registry_1_1_13_out12),
    .In_5(n16bit_registry_1_1_13_out11), .In_6(n16bit_registry_1_1_13_out10),
    .In_7(n16bit_registry_1_1_13_out9), .In_8(n16bit_registry_1_1_13_out8),
    .In_9(n16bit_registry_1_1_13_out7), .In_10(n16bit_registry_1_1_13_out6),
    .In_11(n16bit_registry_1_1_13_out5), .In_12(n16bit_registry_1_1_13_out4),
    .In_13(n16bit_registry_1_1_13_out3), .In_14(n16bit_registry_1_1_13_out2),
    .In_15(n16bit_registry_1_1_13_out1), .In_16(n16bit_registry_1_1_13_out0),
    .Out(n16bit_registry_selector_12_out));
  _16bit_Registry__1_1 u_16bit_registry_1_1_14 (
    .WE(and_29_out), .In(16'h1100), .Out15(n16bit_registry_1_1_14_out15),
    .Out14(n16bit_registry_1_1_14_out14), .Out13(n16bit_registry_1_1_14_out13),
    .Out12(n16bit_registry_1_1_14_out12), .Out11(n16bit_registry_1_1_14_out11),
    .Out10(n16bit_registry_1_1_14_out10), .Out9(n16bit_registry_1_1_14_out9),
    .Out8(n16bit_registry_1_1_14_out8), .Out7(n16bit_registry_1_1_14_out7),
    .Out6(n16bit_registry_1_1_14_out6), .Out5(n16bit_registry_1_1_14_out5),
    .Out4(n16bit_registry_1_1_14_out4), .Out3(n16bit_registry_1_1_14_out3),
    .Out2(n16bit_registry_1_1_14_out2), .Out1(n16bit_registry_1_1_14_out1), .Out0(n16bit_registry_1_1_14_out0));
  and and_29 (and_29_out, and_13_out, in_2);
  _16bit_Registry_Selector u_16bit_registry_selector_13 (
    .WE(and_13_out), .In(n16bit_registry_1_1_14_out15), .In_2(n16bit_registry_1_1_14_out14),
    .In_3(n16bit_registry_1_1_14_out13), .In_4(n16bit_registry_1_1_14_out12),
    .In_5(n16bit_registry_1_1_14_out11), .In_6(n16bit_registry_1_1_14_out10),
    .In_7(n16bit_registry_1_1_14_out9), .In_8(n16bit_registry_1_1_14_out8),
    .In_9(n16bit_registry_1_1_14_out7), .In_10(n16bit_registry_1_1_14_out6),
    .In_11(n16bit_registry_1_1_14_out5), .In_12(n16bit_registry_1_1_14_out4),
    .In_13(n16bit_registry_1_1_14_out3), .In_14(n16bit_registry_1_1_14_out2),
    .In_15(n16bit_registry_1_1_14_out1), .In_16(n16bit_registry_1_1_14_out0),
    .Out(n16bit_registry_selector_13_out));
  _16bit_Registry__1_1 u_16bit_registry_1_1_15 (
    .WE(and_30_out), .In(16'h1100), .Out15(n16bit_registry_1_1_15_out15),
    .Out14(n16bit_registry_1_1_15_out14), .Out13(n16bit_registry_1_1_15_out13),
    .Out12(n16bit_registry_1_1_15_out12), .Out11(n16bit_registry_1_1_15_out11),
    .Out10(n16bit_registry_1_1_15_out10), .Out9(n16bit_registry_1_1_15_out9),
    .Out8(n16bit_registry_1_1_15_out8), .Out7(n16bit_registry_1_1_15_out7),
    .Out6(n16bit_registry_1_1_15_out6), .Out5(n16bit_registry_1_1_15_out5),
    .Out4(n16bit_registry_1_1_15_out4), .Out3(n16bit_registry_1_1_15_out3),
    .Out2(n16bit_registry_1_1_15_out2), .Out1(n16bit_registry_1_1_15_out1), .Out0(n16bit_registry_1_1_15_out0));
  and and_30 (and_30_out, and_14_out, in_2);
  _16bit_Registry_Selector u_16bit_registry_selector_14 (
    .WE(and_14_out), .In(n16bit_registry_1_1_15_out15), .In_2(n16bit_registry_1_1_15_out14),
    .In_3(n16bit_registry_1_1_15_out13), .In_4(n16bit_registry_1_1_15_out12),
    .In_5(n16bit_registry_1_1_15_out11), .In_6(n16bit_registry_1_1_15_out10),
    .In_7(n16bit_registry_1_1_15_out9), .In_8(n16bit_registry_1_1_15_out8),
    .In_9(n16bit_registry_1_1_15_out7), .In_10(n16bit_registry_1_1_15_out6),
    .In_11(n16bit_registry_1_1_15_out5), .In_12(n16bit_registry_1_1_15_out4),
    .In_13(n16bit_registry_1_1_15_out3), .In_14(n16bit_registry_1_1_15_out2),
    .In_15(n16bit_registry_1_1_15_out1), .In_16(n16bit_registry_1_1_15_out0),
    .Out(n16bit_registry_selector_14_out));
  _16bit_Registry__1_1 u_16bit_registry_1_1_16 (
    .WE(and_31_out), .In(16'h1100), .Out15(n16bit_registry_1_1_16_out15),
    .Out14(n16bit_registry_1_1_16_out14), .Out13(n16bit_registry_1_1_16_out13),
    .Out12(n16bit_registry_1_1_16_out12), .Out11(n16bit_registry_1_1_16_out11),
    .Out10(n16bit_registry_1_1_16_out10), .Out9(n16bit_registry_1_1_16_out9),
    .Out8(n16bit_registry_1_1_16_out8), .Out7(n16bit_registry_1_1_16_out7),
    .Out6(n16bit_registry_1_1_16_out6), .Out5(n16bit_registry_1_1_16_out5),
    .Out4(n16bit_registry_1_1_16_out4), .Out3(n16bit_registry_1_1_16_out3),
    .Out2(n16bit_registry_1_1_16_out2), .Out1(n16bit_registry_1_1_16_out1), .Out0(n16bit_registry_1_1_16_out0));
  and and_31 (and_31_out, and_15_out, in_2);
  _16bit_Registry_Selector u_16bit_registry_selector_15 (
    .WE(and_15_out), .In(n16bit_registry_1_1_16_out15), .In_2(n16bit_registry_1_1_16_out14),
    .In_3(n16bit_registry_1_1_16_out13), .In_4(n16bit_registry_1_1_16_out12),
    .In_5(n16bit_registry_1_1_16_out11), .In_6(n16bit_registry_1_1_16_out10),
    .In_7(n16bit_registry_1_1_16_out9), .In_8(n16bit_registry_1_1_16_out8),
    .In_9(n16bit_registry_1_1_16_out7), .In_10(n16bit_registry_1_1_16_out6),
    .In_11(n16bit_registry_1_1_16_out5), .In_12(n16bit_registry_1_1_16_out4),
    .In_13(n16bit_registry_1_1_16_out3), .In_14(n16bit_registry_1_1_16_out2),
    .In_15(n16bit_registry_1_1_16_out1), .In_16(n16bit_registry_1_1_16_out0),
    .Out(n16bit_registry_selector_15_out));
  _16bit_Registry__1_1 u_16bit_registry_1_1_17 (
    .WE(and_32_out), .In(16'h1100), .Out15(n16bit_registry_1_1_17_out15),
    .Out14(n16bit_registry_1_1_17_out14), .Out13(n16bit_registry_1_1_17_out13),
    .Out12(n16bit_registry_1_1_17_out12), .Out11(n16bit_registry_1_1_17_out11),
    .Out10(n16bit_registry_1_1_17_out10), .Out9(n16bit_registry_1_1_17_out9),
    .Out8(n16bit_registry_1_1_17_out8), .Out7(n16bit_registry_1_1_17_out7),
    .Out6(n16bit_registry_1_1_17_out6), .Out5(n16bit_registry_1_1_17_out5),
    .Out4(n16bit_registry_1_1_17_out4), .Out3(n16bit_registry_1_1_17_out3),
    .Out2(n16bit_registry_1_1_17_out2), .Out1(n16bit_registry_1_1_17_out1), .Out0(n16bit_registry_1_1_17_out0));
  and and_32 (and_32_out, and_16_out, in_2);
  _16bit_Registry_Selector u_16bit_registry_selector_16 (
    .WE(and_16_out), .In(n16bit_registry_1_1_17_out15), .In_2(n16bit_registry_1_1_17_out14),
    .In_3(n16bit_registry_1_1_17_out13), .In_4(n16bit_registry_1_1_17_out12),
    .In_5(n16bit_registry_1_1_17_out11), .In_6(n16bit_registry_1_1_17_out10),
    .In_7(n16bit_registry_1_1_17_out9), .In_8(n16bit_registry_1_1_17_out8),
    .In_9(n16bit_registry_1_1_17_out7), .In_10(n16bit_registry_1_1_17_out6),
    .In_11(n16bit_registry_1_1_17_out5), .In_12(n16bit_registry_1_1_17_out4),
    .In_13(n16bit_registry_1_1_17_out3), .In_14(n16bit_registry_1_1_17_out2),
    .In_15(n16bit_registry_1_1_17_out1), .In_16(n16bit_registry_1_1_17_out0),
    .Out(n16bit_registry_selector_16_out));
  assign Instruction_Out = n16bit_registry_selector_1_out | n16bit_registry_selector_2_out | n16bit_registry_selector_3_out | n16bit_registry_selector_4_out | n16bit_registry_selector_5_out | n16bit_registry_selector_6_out | n16bit_registry_selector_7_out | n16bit_registry_selector_8_out | n16bit_registry_selector_9_out | n16bit_registry_selector_10_out | n16bit_registry_selector_11_out | n16bit_registry_selector_12_out | n16bit_registry_selector_13_out | n16bit_registry_selector_14_out | n16bit_registry_selector_15_out | n16bit_registry_selector_16_out;  // OR_Gate or_1, 16 bits wide
  // also tied to GND on the sheet: {n16bit_registry_1_1_1_out15, n16bit_registry_1_1_1_out14, n16bit_registry_1_1_1_out13, n16bit_registry_1_1_1_out12, n16bit_registry_1_1_1_out11, n16bit_registry_1_1_1_out10, n16bit_registry_1_1_1_out9, n16bit_registry_1_1_1_out8, n16bit_registry_1_1_1_out7, n16bit_registry_1_1_1_out6, n16bit_registry_1_1_1_out5, n16bit_registry_1_1_1_out4}

  // Notes on the sheet:
  //   DATA 10
  //   DATA 8
  //   LDR 1
  //   LDR 2
  //   ADD
endmodule

module Memory_Data (
  input  [15:0] Memory_Address,
  input  [15:0] Data_In,
  input  WE,
  output [15:0] Inst_Out
);

  wire and_1_out, and_2_out, and_3_out, and_4_out, and_5_out, and_6_out, and_7_out, and_8_out, and_9_out,
       and_10_out, and_11_out, and_12_out, and_13_out, and_14_out, and_15_out, and_16_out, and_17_out,
       and_18_out, and_19_out, and_20_out, and_21_out, and_22_out, and_23_out, and_24_out, and_25_out,
       and_26_out, and_27_out, and_28_out, and_29_out, and_30_out, and_31_out, and_32_out,
       n16bit_registry_1_1_1_out0, n16bit_registry_1_1_1_out1, n16bit_registry_1_1_1_out2,
       n16bit_registry_1_1_1_out3, n16bit_registry_1_1_1_out4, n16bit_registry_1_1_1_out5,
       n16bit_registry_1_1_1_out6, n16bit_registry_1_1_1_out7, n16bit_registry_1_1_1_out8,
       n16bit_registry_1_1_1_out9, n16bit_registry_1_1_1_out10, n16bit_registry_1_1_1_out11,
       n16bit_registry_1_1_1_out12, n16bit_registry_1_1_1_out13, n16bit_registry_1_1_1_out14,
       n16bit_registry_1_1_1_out15, n16bit_registry_1_1_2_out0, n16bit_registry_1_1_2_out1,
       n16bit_registry_1_1_2_out2, n16bit_registry_1_1_2_out3, n16bit_registry_1_1_2_out4,
       n16bit_registry_1_1_2_out5, n16bit_registry_1_1_2_out6, n16bit_registry_1_1_2_out7,
       n16bit_registry_1_1_2_out8, n16bit_registry_1_1_2_out9, n16bit_registry_1_1_2_out10,
       n16bit_registry_1_1_2_out11, n16bit_registry_1_1_2_out12, n16bit_registry_1_1_2_out13,
       n16bit_registry_1_1_2_out14, n16bit_registry_1_1_2_out15, n16bit_registry_1_1_3_out0,
       n16bit_registry_1_1_3_out1, n16bit_registry_1_1_3_out2, n16bit_registry_1_1_3_out3,
       n16bit_registry_1_1_3_out4, n16bit_registry_1_1_3_out5, n16bit_registry_1_1_3_out6,
       n16bit_registry_1_1_3_out7, n16bit_registry_1_1_3_out8, n16bit_registry_1_1_3_out9,
       n16bit_registry_1_1_3_out10, n16bit_registry_1_1_3_out11, n16bit_registry_1_1_3_out12,
       n16bit_registry_1_1_3_out13, n16bit_registry_1_1_3_out14, n16bit_registry_1_1_3_out15,
       n16bit_registry_1_1_4_out0, n16bit_registry_1_1_4_out1, n16bit_registry_1_1_4_out2,
       n16bit_registry_1_1_4_out3, n16bit_registry_1_1_4_out4, n16bit_registry_1_1_4_out5,
       n16bit_registry_1_1_4_out6, n16bit_registry_1_1_4_out7, n16bit_registry_1_1_4_out8,
       n16bit_registry_1_1_4_out9, n16bit_registry_1_1_4_out10, n16bit_registry_1_1_4_out11,
       n16bit_registry_1_1_4_out12, n16bit_registry_1_1_4_out13, n16bit_registry_1_1_4_out14,
       n16bit_registry_1_1_4_out15, n16bit_registry_1_1_5_out0, n16bit_registry_1_1_5_out1,
       n16bit_registry_1_1_5_out2, n16bit_registry_1_1_5_out3, n16bit_registry_1_1_5_out4,
       n16bit_registry_1_1_5_out5, n16bit_registry_1_1_5_out6, n16bit_registry_1_1_5_out7,
       n16bit_registry_1_1_5_out8, n16bit_registry_1_1_5_out9, n16bit_registry_1_1_5_out10,
       n16bit_registry_1_1_5_out11, n16bit_registry_1_1_5_out12, n16bit_registry_1_1_5_out13,
       n16bit_registry_1_1_5_out14, n16bit_registry_1_1_5_out15, n16bit_registry_1_1_6_out0,
       n16bit_registry_1_1_6_out1, n16bit_registry_1_1_6_out2, n16bit_registry_1_1_6_out3,
       n16bit_registry_1_1_6_out4, n16bit_registry_1_1_6_out5, n16bit_registry_1_1_6_out6,
       n16bit_registry_1_1_6_out7, n16bit_registry_1_1_6_out8, n16bit_registry_1_1_6_out9,
       n16bit_registry_1_1_6_out10, n16bit_registry_1_1_6_out11, n16bit_registry_1_1_6_out12,
       n16bit_registry_1_1_6_out13, n16bit_registry_1_1_6_out14, n16bit_registry_1_1_6_out15,
       n16bit_registry_1_1_7_out0, n16bit_registry_1_1_7_out1, n16bit_registry_1_1_7_out2,
       n16bit_registry_1_1_7_out3, n16bit_registry_1_1_7_out4, n16bit_registry_1_1_7_out5,
       n16bit_registry_1_1_7_out6, n16bit_registry_1_1_7_out7, n16bit_registry_1_1_7_out8,
       n16bit_registry_1_1_7_out9, n16bit_registry_1_1_7_out10, n16bit_registry_1_1_7_out11,
       n16bit_registry_1_1_7_out12, n16bit_registry_1_1_7_out13, n16bit_registry_1_1_7_out14,
       n16bit_registry_1_1_7_out15, n16bit_registry_1_1_8_out0, n16bit_registry_1_1_8_out1,
       n16bit_registry_1_1_8_out2, n16bit_registry_1_1_8_out3, n16bit_registry_1_1_8_out4,
       n16bit_registry_1_1_8_out5, n16bit_registry_1_1_8_out6, n16bit_registry_1_1_8_out7,
       n16bit_registry_1_1_8_out8, n16bit_registry_1_1_8_out9, n16bit_registry_1_1_8_out10,
       n16bit_registry_1_1_8_out11, n16bit_registry_1_1_8_out12, n16bit_registry_1_1_8_out13,
       n16bit_registry_1_1_8_out14, n16bit_registry_1_1_8_out15, n16bit_registry_1_1_9_out0,
       n16bit_registry_1_1_9_out1, n16bit_registry_1_1_9_out2, n16bit_registry_1_1_9_out3,
       n16bit_registry_1_1_9_out4, n16bit_registry_1_1_9_out5, n16bit_registry_1_1_9_out6,
       n16bit_registry_1_1_9_out7, n16bit_registry_1_1_9_out8, n16bit_registry_1_1_9_out9,
       n16bit_registry_1_1_9_out10, n16bit_registry_1_1_9_out11, n16bit_registry_1_1_9_out12,
       n16bit_registry_1_1_9_out13, n16bit_registry_1_1_9_out14, n16bit_registry_1_1_9_out15,
       n16bit_registry_1_1_10_out0, n16bit_registry_1_1_10_out1, n16bit_registry_1_1_10_out2,
       n16bit_registry_1_1_10_out3, n16bit_registry_1_1_10_out4, n16bit_registry_1_1_10_out5,
       n16bit_registry_1_1_10_out6, n16bit_registry_1_1_10_out7, n16bit_registry_1_1_10_out8,
       n16bit_registry_1_1_10_out9, n16bit_registry_1_1_10_out10, n16bit_registry_1_1_10_out11,
       n16bit_registry_1_1_10_out12, n16bit_registry_1_1_10_out13, n16bit_registry_1_1_10_out14,
       n16bit_registry_1_1_10_out15, n16bit_registry_1_1_11_out0, n16bit_registry_1_1_11_out1,
       n16bit_registry_1_1_11_out2, n16bit_registry_1_1_11_out3, n16bit_registry_1_1_11_out4,
       n16bit_registry_1_1_11_out5, n16bit_registry_1_1_11_out6, n16bit_registry_1_1_11_out7,
       n16bit_registry_1_1_11_out8, n16bit_registry_1_1_11_out9, n16bit_registry_1_1_11_out10,
       n16bit_registry_1_1_11_out11, n16bit_registry_1_1_11_out12, n16bit_registry_1_1_11_out13,
       n16bit_registry_1_1_11_out14, n16bit_registry_1_1_11_out15, n16bit_registry_1_1_12_out0,
       n16bit_registry_1_1_12_out1, n16bit_registry_1_1_12_out2, n16bit_registry_1_1_12_out3,
       n16bit_registry_1_1_12_out4, n16bit_registry_1_1_12_out5, n16bit_registry_1_1_12_out6,
       n16bit_registry_1_1_12_out7, n16bit_registry_1_1_12_out8, n16bit_registry_1_1_12_out9,
       n16bit_registry_1_1_12_out10, n16bit_registry_1_1_12_out11, n16bit_registry_1_1_12_out12,
       n16bit_registry_1_1_12_out13, n16bit_registry_1_1_12_out14, n16bit_registry_1_1_12_out15,
       n16bit_registry_1_1_13_out0, n16bit_registry_1_1_13_out1, n16bit_registry_1_1_13_out2,
       n16bit_registry_1_1_13_out3, n16bit_registry_1_1_13_out4, n16bit_registry_1_1_13_out5,
       n16bit_registry_1_1_13_out6, n16bit_registry_1_1_13_out7, n16bit_registry_1_1_13_out8,
       n16bit_registry_1_1_13_out9, n16bit_registry_1_1_13_out10, n16bit_registry_1_1_13_out11,
       n16bit_registry_1_1_13_out12, n16bit_registry_1_1_13_out13, n16bit_registry_1_1_13_out14,
       n16bit_registry_1_1_13_out15, n16bit_registry_1_1_14_out0, n16bit_registry_1_1_14_out1,
       n16bit_registry_1_1_14_out2, n16bit_registry_1_1_14_out3, n16bit_registry_1_1_14_out4,
       n16bit_registry_1_1_14_out5, n16bit_registry_1_1_14_out6, n16bit_registry_1_1_14_out7,
       n16bit_registry_1_1_14_out8, n16bit_registry_1_1_14_out9, n16bit_registry_1_1_14_out10,
       n16bit_registry_1_1_14_out11, n16bit_registry_1_1_14_out12, n16bit_registry_1_1_14_out13,
       n16bit_registry_1_1_14_out14, n16bit_registry_1_1_14_out15, n16bit_registry_1_1_15_out0,
       n16bit_registry_1_1_15_out1, n16bit_registry_1_1_15_out2, n16bit_registry_1_1_15_out3,
       n16bit_registry_1_1_15_out4, n16bit_registry_1_1_15_out5, n16bit_registry_1_1_15_out6,
       n16bit_registry_1_1_15_out7, n16bit_registry_1_1_15_out8, n16bit_registry_1_1_15_out9,
       n16bit_registry_1_1_15_out10, n16bit_registry_1_1_15_out11, n16bit_registry_1_1_15_out12,
       n16bit_registry_1_1_15_out13, n16bit_registry_1_1_15_out14, n16bit_registry_1_1_15_out15,
       n16bit_registry_1_1_16_out0, n16bit_registry_1_1_16_out1, n16bit_registry_1_1_16_out2,
       n16bit_registry_1_1_16_out3, n16bit_registry_1_1_16_out4, n16bit_registry_1_1_16_out5,
       n16bit_registry_1_1_16_out6, n16bit_registry_1_1_16_out7, n16bit_registry_1_1_16_out8,
       n16bit_registry_1_1_16_out9, n16bit_registry_1_1_16_out10, n16bit_registry_1_1_16_out11,
       n16bit_registry_1_1_16_out12, n16bit_registry_1_1_16_out13, n16bit_registry_1_1_16_out14,
       n16bit_registry_1_1_16_out15;
  wire [15:0] n16bit_registry_selector_1_out, n16bit_registry_selector_2_out, n16bit_registry_selector_3_out,
       n16bit_registry_selector_4_out, n16bit_registry_selector_5_out, n16bit_registry_selector_6_out,
       n16bit_registry_selector_7_out, n16bit_registry_selector_8_out, n16bit_registry_selector_9_out,
       n16bit_registry_selector_10_out, n16bit_registry_selector_11_out, n16bit_registry_selector_12_out,
       n16bit_registry_selector_13_out, n16bit_registry_selector_14_out, n16bit_registry_selector_15_out,
       n16bit_registry_selector_16_out;

  and and_1 (and_1_out, ~Memory_Address[0], ~Memory_Address[1], ~Memory_Address[2], ~Memory_Address[3]);  // AND_Gate
  and and_2 (and_2_out, and_1_out, WE);
  and and_3 (and_3_out, Memory_Address[0], ~Memory_Address[1], ~Memory_Address[2], ~Memory_Address[3]);  // AND_Gate
  and and_4 (and_4_out, and_3_out, WE);
  and and_5 (and_5_out, ~Memory_Address[0], Memory_Address[1], ~Memory_Address[2], ~Memory_Address[3]);  // AND_Gate
  and and_6 (and_6_out, and_5_out, WE);
  and and_7 (and_7_out, Memory_Address[0], Memory_Address[1], ~Memory_Address[2], ~Memory_Address[3]);  // AND_Gate
  and and_8 (and_8_out, and_7_out, WE);
  and and_9 (and_9_out, ~Memory_Address[0], ~Memory_Address[1], Memory_Address[2], ~Memory_Address[3]);  // AND_Gate
  and and_10 (and_10_out, and_9_out, WE);
  and and_11 (and_11_out, Memory_Address[0], ~Memory_Address[1], Memory_Address[2], ~Memory_Address[3]);  // AND_Gate
  and and_12 (and_12_out, and_11_out, WE);
  and and_13 (and_13_out, ~Memory_Address[0], Memory_Address[1], Memory_Address[2], ~Memory_Address[3]);  // AND_Gate
  and and_14 (and_14_out, and_13_out, WE);
  and and_15 (and_15_out, Memory_Address[0], Memory_Address[1], Memory_Address[2], ~Memory_Address[3]);  // AND_Gate
  and and_16 (and_16_out, and_15_out, WE);
  and and_17 (and_17_out, ~Memory_Address[0], ~Memory_Address[1], ~Memory_Address[2], Memory_Address[3]);  // AND_Gate
  and and_18 (and_18_out, and_17_out, WE);
  and and_19 (and_19_out, Memory_Address[0], ~Memory_Address[1], ~Memory_Address[2], Memory_Address[3]);  // AND_Gate
  and and_20 (and_20_out, and_19_out, WE);
  and and_21 (and_21_out, ~Memory_Address[0], Memory_Address[1], ~Memory_Address[2], Memory_Address[3]);  // AND_Gate
  and and_22 (and_22_out, and_21_out, WE);
  and and_23 (and_23_out, Memory_Address[0], Memory_Address[1], ~Memory_Address[2], Memory_Address[3]);  // AND_Gate
  and and_24 (and_24_out, and_23_out, WE);
  and and_25 (and_25_out, ~Memory_Address[0], ~Memory_Address[1], Memory_Address[2], Memory_Address[3]);  // AND_Gate
  and and_26 (and_26_out, and_25_out, WE);
  and and_27 (and_27_out, Memory_Address[0], ~Memory_Address[1], Memory_Address[2], Memory_Address[3]);  // AND_Gate
  and and_28 (and_28_out, and_27_out, WE);
  and and_29 (and_29_out, ~Memory_Address[0], Memory_Address[1], Memory_Address[2], Memory_Address[3]);  // AND_Gate
  and and_30 (and_30_out, and_29_out, WE);
  and and_31 (and_31_out, Memory_Address[0], Memory_Address[1], Memory_Address[2], Memory_Address[3]);
  and and_32 (and_32_out, and_31_out, WE);
  _16bit_Registry__1_1 u_16bit_registry_1_1_1 (
    .WE(and_2_out), .In(Data_In), .Out15(n16bit_registry_1_1_1_out15), .Out14(n16bit_registry_1_1_1_out14),
    .Out13(n16bit_registry_1_1_1_out13), .Out12(n16bit_registry_1_1_1_out12),
    .Out11(n16bit_registry_1_1_1_out11), .Out10(n16bit_registry_1_1_1_out10),
    .Out9(n16bit_registry_1_1_1_out9), .Out8(n16bit_registry_1_1_1_out8), .Out7(n16bit_registry_1_1_1_out7),
    .Out6(n16bit_registry_1_1_1_out6), .Out5(n16bit_registry_1_1_1_out5), .Out4(n16bit_registry_1_1_1_out4),
    .Out3(n16bit_registry_1_1_1_out3), .Out2(n16bit_registry_1_1_1_out2), .Out1(n16bit_registry_1_1_1_out1),
    .Out0(n16bit_registry_1_1_1_out0));
  _16bit_Registry_Selector u_16bit_registry_selector_1 (
    .WE(and_1_out), .In(n16bit_registry_1_1_1_out15), .In_2(n16bit_registry_1_1_1_out14),
    .In_3(n16bit_registry_1_1_1_out13), .In_4(n16bit_registry_1_1_1_out12),
    .In_5(n16bit_registry_1_1_1_out11), .In_6(n16bit_registry_1_1_1_out10),
    .In_7(n16bit_registry_1_1_1_out9), .In_8(n16bit_registry_1_1_1_out8), .In_9(n16bit_registry_1_1_1_out7),
    .In_10(n16bit_registry_1_1_1_out6), .In_11(n16bit_registry_1_1_1_out5),
    .In_12(n16bit_registry_1_1_1_out4), .In_13(n16bit_registry_1_1_1_out3),
    .In_14(n16bit_registry_1_1_1_out2), .In_15(n16bit_registry_1_1_1_out1),
    .In_16(n16bit_registry_1_1_1_out0), .Out(n16bit_registry_selector_1_out));
  _16bit_Registry__1_1 u_16bit_registry_1_1_2 (
    .WE(and_4_out), .In(Data_In), .Out15(n16bit_registry_1_1_2_out15), .Out14(n16bit_registry_1_1_2_out14),
    .Out13(n16bit_registry_1_1_2_out13), .Out12(n16bit_registry_1_1_2_out12),
    .Out11(n16bit_registry_1_1_2_out11), .Out10(n16bit_registry_1_1_2_out10),
    .Out9(n16bit_registry_1_1_2_out9), .Out8(n16bit_registry_1_1_2_out8), .Out7(n16bit_registry_1_1_2_out7),
    .Out6(n16bit_registry_1_1_2_out6), .Out5(n16bit_registry_1_1_2_out5), .Out4(n16bit_registry_1_1_2_out4),
    .Out3(n16bit_registry_1_1_2_out3), .Out2(n16bit_registry_1_1_2_out2), .Out1(n16bit_registry_1_1_2_out1),
    .Out0(n16bit_registry_1_1_2_out0));
  _16bit_Registry_Selector u_16bit_registry_selector_2 (
    .WE(and_3_out), .In(n16bit_registry_1_1_2_out15), .In_2(n16bit_registry_1_1_2_out14),
    .In_3(n16bit_registry_1_1_2_out13), .In_4(n16bit_registry_1_1_2_out12),
    .In_5(n16bit_registry_1_1_2_out11), .In_6(n16bit_registry_1_1_2_out10),
    .In_7(n16bit_registry_1_1_2_out9), .In_8(n16bit_registry_1_1_2_out8), .In_9(n16bit_registry_1_1_2_out7),
    .In_10(n16bit_registry_1_1_2_out6), .In_11(n16bit_registry_1_1_2_out5),
    .In_12(n16bit_registry_1_1_2_out4), .In_13(n16bit_registry_1_1_2_out3),
    .In_14(n16bit_registry_1_1_2_out2), .In_15(n16bit_registry_1_1_2_out1),
    .In_16(n16bit_registry_1_1_2_out0), .Out(n16bit_registry_selector_2_out));
  _16bit_Registry__1_1 u_16bit_registry_1_1_3 (
    .WE(and_6_out), .In(Data_In), .Out15(n16bit_registry_1_1_3_out15), .Out14(n16bit_registry_1_1_3_out14),
    .Out13(n16bit_registry_1_1_3_out13), .Out12(n16bit_registry_1_1_3_out12),
    .Out11(n16bit_registry_1_1_3_out11), .Out10(n16bit_registry_1_1_3_out10),
    .Out9(n16bit_registry_1_1_3_out9), .Out8(n16bit_registry_1_1_3_out8), .Out7(n16bit_registry_1_1_3_out7),
    .Out6(n16bit_registry_1_1_3_out6), .Out5(n16bit_registry_1_1_3_out5), .Out4(n16bit_registry_1_1_3_out4),
    .Out3(n16bit_registry_1_1_3_out3), .Out2(n16bit_registry_1_1_3_out2), .Out1(n16bit_registry_1_1_3_out1),
    .Out0(n16bit_registry_1_1_3_out0));
  _16bit_Registry_Selector u_16bit_registry_selector_3 (
    .WE(and_5_out), .In(n16bit_registry_1_1_3_out15), .In_2(n16bit_registry_1_1_3_out14),
    .In_3(n16bit_registry_1_1_3_out13), .In_4(n16bit_registry_1_1_3_out12),
    .In_5(n16bit_registry_1_1_3_out11), .In_6(n16bit_registry_1_1_3_out10),
    .In_7(n16bit_registry_1_1_3_out9), .In_8(n16bit_registry_1_1_3_out8), .In_9(n16bit_registry_1_1_3_out7),
    .In_10(n16bit_registry_1_1_3_out6), .In_11(n16bit_registry_1_1_3_out5),
    .In_12(n16bit_registry_1_1_3_out4), .In_13(n16bit_registry_1_1_3_out3),
    .In_14(n16bit_registry_1_1_3_out2), .In_15(n16bit_registry_1_1_3_out1),
    .In_16(n16bit_registry_1_1_3_out0), .Out(n16bit_registry_selector_3_out));
  _16bit_Registry__1_1 u_16bit_registry_1_1_4 (
    .WE(and_8_out), .In(Data_In), .Out15(n16bit_registry_1_1_4_out15), .Out14(n16bit_registry_1_1_4_out14),
    .Out13(n16bit_registry_1_1_4_out13), .Out12(n16bit_registry_1_1_4_out12),
    .Out11(n16bit_registry_1_1_4_out11), .Out10(n16bit_registry_1_1_4_out10),
    .Out9(n16bit_registry_1_1_4_out9), .Out8(n16bit_registry_1_1_4_out8), .Out7(n16bit_registry_1_1_4_out7),
    .Out6(n16bit_registry_1_1_4_out6), .Out5(n16bit_registry_1_1_4_out5), .Out4(n16bit_registry_1_1_4_out4),
    .Out3(n16bit_registry_1_1_4_out3), .Out2(n16bit_registry_1_1_4_out2), .Out1(n16bit_registry_1_1_4_out1),
    .Out0(n16bit_registry_1_1_4_out0));
  _16bit_Registry_Selector u_16bit_registry_selector_4 (
    .WE(and_7_out), .In(n16bit_registry_1_1_4_out15), .In_2(n16bit_registry_1_1_4_out14),
    .In_3(n16bit_registry_1_1_4_out13), .In_4(n16bit_registry_1_1_4_out12),
    .In_5(n16bit_registry_1_1_4_out11), .In_6(n16bit_registry_1_1_4_out10),
    .In_7(n16bit_registry_1_1_4_out9), .In_8(n16bit_registry_1_1_4_out8), .In_9(n16bit_registry_1_1_4_out7),
    .In_10(n16bit_registry_1_1_4_out6), .In_11(n16bit_registry_1_1_4_out5),
    .In_12(n16bit_registry_1_1_4_out4), .In_13(n16bit_registry_1_1_4_out3),
    .In_14(n16bit_registry_1_1_4_out2), .In_15(n16bit_registry_1_1_4_out1),
    .In_16(n16bit_registry_1_1_4_out0), .Out(n16bit_registry_selector_4_out));
  _16bit_Registry__1_1 u_16bit_registry_1_1_5 (
    .WE(and_10_out), .In(Data_In), .Out15(n16bit_registry_1_1_5_out15), .Out14(n16bit_registry_1_1_5_out14),
    .Out13(n16bit_registry_1_1_5_out13), .Out12(n16bit_registry_1_1_5_out12),
    .Out11(n16bit_registry_1_1_5_out11), .Out10(n16bit_registry_1_1_5_out10),
    .Out9(n16bit_registry_1_1_5_out9), .Out8(n16bit_registry_1_1_5_out8), .Out7(n16bit_registry_1_1_5_out7),
    .Out6(n16bit_registry_1_1_5_out6), .Out5(n16bit_registry_1_1_5_out5), .Out4(n16bit_registry_1_1_5_out4),
    .Out3(n16bit_registry_1_1_5_out3), .Out2(n16bit_registry_1_1_5_out2), .Out1(n16bit_registry_1_1_5_out1),
    .Out0(n16bit_registry_1_1_5_out0));
  _16bit_Registry_Selector u_16bit_registry_selector_5 (
    .WE(and_9_out), .In(n16bit_registry_1_1_5_out15), .In_2(n16bit_registry_1_1_5_out14),
    .In_3(n16bit_registry_1_1_5_out13), .In_4(n16bit_registry_1_1_5_out12),
    .In_5(n16bit_registry_1_1_5_out11), .In_6(n16bit_registry_1_1_5_out10),
    .In_7(n16bit_registry_1_1_5_out9), .In_8(n16bit_registry_1_1_5_out8), .In_9(n16bit_registry_1_1_5_out7),
    .In_10(n16bit_registry_1_1_5_out6), .In_11(n16bit_registry_1_1_5_out5),
    .In_12(n16bit_registry_1_1_5_out4), .In_13(n16bit_registry_1_1_5_out3),
    .In_14(n16bit_registry_1_1_5_out2), .In_15(n16bit_registry_1_1_5_out1),
    .In_16(n16bit_registry_1_1_5_out0), .Out(n16bit_registry_selector_5_out));
  _16bit_Registry__1_1 u_16bit_registry_1_1_6 (
    .WE(and_12_out), .In(Data_In), .Out15(n16bit_registry_1_1_6_out15), .Out14(n16bit_registry_1_1_6_out14),
    .Out13(n16bit_registry_1_1_6_out13), .Out12(n16bit_registry_1_1_6_out12),
    .Out11(n16bit_registry_1_1_6_out11), .Out10(n16bit_registry_1_1_6_out10),
    .Out9(n16bit_registry_1_1_6_out9), .Out8(n16bit_registry_1_1_6_out8), .Out7(n16bit_registry_1_1_6_out7),
    .Out6(n16bit_registry_1_1_6_out6), .Out5(n16bit_registry_1_1_6_out5), .Out4(n16bit_registry_1_1_6_out4),
    .Out3(n16bit_registry_1_1_6_out3), .Out2(n16bit_registry_1_1_6_out2), .Out1(n16bit_registry_1_1_6_out1),
    .Out0(n16bit_registry_1_1_6_out0));
  _16bit_Registry_Selector u_16bit_registry_selector_6 (
    .WE(and_11_out), .In(n16bit_registry_1_1_6_out15), .In_2(n16bit_registry_1_1_6_out14),
    .In_3(n16bit_registry_1_1_6_out13), .In_4(n16bit_registry_1_1_6_out12),
    .In_5(n16bit_registry_1_1_6_out11), .In_6(n16bit_registry_1_1_6_out10),
    .In_7(n16bit_registry_1_1_6_out9), .In_8(n16bit_registry_1_1_6_out8), .In_9(n16bit_registry_1_1_6_out7),
    .In_10(n16bit_registry_1_1_6_out6), .In_11(n16bit_registry_1_1_6_out5),
    .In_12(n16bit_registry_1_1_6_out4), .In_13(n16bit_registry_1_1_6_out3),
    .In_14(n16bit_registry_1_1_6_out2), .In_15(n16bit_registry_1_1_6_out1),
    .In_16(n16bit_registry_1_1_6_out0), .Out(n16bit_registry_selector_6_out));
  _16bit_Registry__1_1 u_16bit_registry_1_1_7 (
    .WE(and_14_out), .In(Data_In), .Out15(n16bit_registry_1_1_7_out15), .Out14(n16bit_registry_1_1_7_out14),
    .Out13(n16bit_registry_1_1_7_out13), .Out12(n16bit_registry_1_1_7_out12),
    .Out11(n16bit_registry_1_1_7_out11), .Out10(n16bit_registry_1_1_7_out10),
    .Out9(n16bit_registry_1_1_7_out9), .Out8(n16bit_registry_1_1_7_out8), .Out7(n16bit_registry_1_1_7_out7),
    .Out6(n16bit_registry_1_1_7_out6), .Out5(n16bit_registry_1_1_7_out5), .Out4(n16bit_registry_1_1_7_out4),
    .Out3(n16bit_registry_1_1_7_out3), .Out2(n16bit_registry_1_1_7_out2), .Out1(n16bit_registry_1_1_7_out1),
    .Out0(n16bit_registry_1_1_7_out0));
  _16bit_Registry_Selector u_16bit_registry_selector_7 (
    .WE(and_13_out), .In(n16bit_registry_1_1_7_out15), .In_2(n16bit_registry_1_1_7_out14),
    .In_3(n16bit_registry_1_1_7_out13), .In_4(n16bit_registry_1_1_7_out12),
    .In_5(n16bit_registry_1_1_7_out11), .In_6(n16bit_registry_1_1_7_out10),
    .In_7(n16bit_registry_1_1_7_out9), .In_8(n16bit_registry_1_1_7_out8), .In_9(n16bit_registry_1_1_7_out7),
    .In_10(n16bit_registry_1_1_7_out6), .In_11(n16bit_registry_1_1_7_out5),
    .In_12(n16bit_registry_1_1_7_out4), .In_13(n16bit_registry_1_1_7_out3),
    .In_14(n16bit_registry_1_1_7_out2), .In_15(n16bit_registry_1_1_7_out1),
    .In_16(n16bit_registry_1_1_7_out0), .Out(n16bit_registry_selector_7_out));
  _16bit_Registry__1_1 u_16bit_registry_1_1_8 (
    .WE(and_16_out), .In(Data_In), .Out15(n16bit_registry_1_1_8_out15), .Out14(n16bit_registry_1_1_8_out14),
    .Out13(n16bit_registry_1_1_8_out13), .Out12(n16bit_registry_1_1_8_out12),
    .Out11(n16bit_registry_1_1_8_out11), .Out10(n16bit_registry_1_1_8_out10),
    .Out9(n16bit_registry_1_1_8_out9), .Out8(n16bit_registry_1_1_8_out8), .Out7(n16bit_registry_1_1_8_out7),
    .Out6(n16bit_registry_1_1_8_out6), .Out5(n16bit_registry_1_1_8_out5), .Out4(n16bit_registry_1_1_8_out4),
    .Out3(n16bit_registry_1_1_8_out3), .Out2(n16bit_registry_1_1_8_out2), .Out1(n16bit_registry_1_1_8_out1),
    .Out0(n16bit_registry_1_1_8_out0));
  _16bit_Registry_Selector u_16bit_registry_selector_8 (
    .WE(and_15_out), .In(n16bit_registry_1_1_8_out15), .In_2(n16bit_registry_1_1_8_out14),
    .In_3(n16bit_registry_1_1_8_out13), .In_4(n16bit_registry_1_1_8_out12),
    .In_5(n16bit_registry_1_1_8_out11), .In_6(n16bit_registry_1_1_8_out10),
    .In_7(n16bit_registry_1_1_8_out9), .In_8(n16bit_registry_1_1_8_out8), .In_9(n16bit_registry_1_1_8_out7),
    .In_10(n16bit_registry_1_1_8_out6), .In_11(n16bit_registry_1_1_8_out5),
    .In_12(n16bit_registry_1_1_8_out4), .In_13(n16bit_registry_1_1_8_out3),
    .In_14(n16bit_registry_1_1_8_out2), .In_15(n16bit_registry_1_1_8_out1),
    .In_16(n16bit_registry_1_1_8_out0), .Out(n16bit_registry_selector_8_out));
  _16bit_Registry__1_1 u_16bit_registry_1_1_9 (
    .WE(and_18_out), .In(Data_In), .Out15(n16bit_registry_1_1_9_out15), .Out14(n16bit_registry_1_1_9_out14),
    .Out13(n16bit_registry_1_1_9_out13), .Out12(n16bit_registry_1_1_9_out12),
    .Out11(n16bit_registry_1_1_9_out11), .Out10(n16bit_registry_1_1_9_out10),
    .Out9(n16bit_registry_1_1_9_out9), .Out8(n16bit_registry_1_1_9_out8), .Out7(n16bit_registry_1_1_9_out7),
    .Out6(n16bit_registry_1_1_9_out6), .Out5(n16bit_registry_1_1_9_out5), .Out4(n16bit_registry_1_1_9_out4),
    .Out3(n16bit_registry_1_1_9_out3), .Out2(n16bit_registry_1_1_9_out2), .Out1(n16bit_registry_1_1_9_out1),
    .Out0(n16bit_registry_1_1_9_out0));
  _16bit_Registry_Selector u_16bit_registry_selector_9 (
    .WE(and_17_out), .In(n16bit_registry_1_1_9_out15), .In_2(n16bit_registry_1_1_9_out14),
    .In_3(n16bit_registry_1_1_9_out13), .In_4(n16bit_registry_1_1_9_out12),
    .In_5(n16bit_registry_1_1_9_out11), .In_6(n16bit_registry_1_1_9_out10),
    .In_7(n16bit_registry_1_1_9_out9), .In_8(n16bit_registry_1_1_9_out8), .In_9(n16bit_registry_1_1_9_out7),
    .In_10(n16bit_registry_1_1_9_out6), .In_11(n16bit_registry_1_1_9_out5),
    .In_12(n16bit_registry_1_1_9_out4), .In_13(n16bit_registry_1_1_9_out3),
    .In_14(n16bit_registry_1_1_9_out2), .In_15(n16bit_registry_1_1_9_out1),
    .In_16(n16bit_registry_1_1_9_out0), .Out(n16bit_registry_selector_9_out));
  _16bit_Registry__1_1 u_16bit_registry_1_1_10 (
    .WE(and_20_out), .In(Data_In), .Out15(n16bit_registry_1_1_10_out15),
    .Out14(n16bit_registry_1_1_10_out14), .Out13(n16bit_registry_1_1_10_out13),
    .Out12(n16bit_registry_1_1_10_out12), .Out11(n16bit_registry_1_1_10_out11),
    .Out10(n16bit_registry_1_1_10_out10), .Out9(n16bit_registry_1_1_10_out9),
    .Out8(n16bit_registry_1_1_10_out8), .Out7(n16bit_registry_1_1_10_out7),
    .Out6(n16bit_registry_1_1_10_out6), .Out5(n16bit_registry_1_1_10_out5),
    .Out4(n16bit_registry_1_1_10_out4), .Out3(n16bit_registry_1_1_10_out3),
    .Out2(n16bit_registry_1_1_10_out2), .Out1(n16bit_registry_1_1_10_out1), .Out0(n16bit_registry_1_1_10_out0));
  _16bit_Registry_Selector u_16bit_registry_selector_10 (
    .WE(and_19_out), .In(n16bit_registry_1_1_10_out15), .In_2(n16bit_registry_1_1_10_out14),
    .In_3(n16bit_registry_1_1_10_out13), .In_4(n16bit_registry_1_1_10_out12),
    .In_5(n16bit_registry_1_1_10_out11), .In_6(n16bit_registry_1_1_10_out10),
    .In_7(n16bit_registry_1_1_10_out9), .In_8(n16bit_registry_1_1_10_out8),
    .In_9(n16bit_registry_1_1_10_out7), .In_10(n16bit_registry_1_1_10_out6),
    .In_11(n16bit_registry_1_1_10_out5), .In_12(n16bit_registry_1_1_10_out4),
    .In_13(n16bit_registry_1_1_10_out3), .In_14(n16bit_registry_1_1_10_out2),
    .In_15(n16bit_registry_1_1_10_out1), .In_16(n16bit_registry_1_1_10_out0),
    .Out(n16bit_registry_selector_10_out));
  _16bit_Registry__1_1 u_16bit_registry_1_1_11 (
    .WE(and_22_out), .In(Data_In), .Out15(n16bit_registry_1_1_11_out15),
    .Out14(n16bit_registry_1_1_11_out14), .Out13(n16bit_registry_1_1_11_out13),
    .Out12(n16bit_registry_1_1_11_out12), .Out11(n16bit_registry_1_1_11_out11),
    .Out10(n16bit_registry_1_1_11_out10), .Out9(n16bit_registry_1_1_11_out9),
    .Out8(n16bit_registry_1_1_11_out8), .Out7(n16bit_registry_1_1_11_out7),
    .Out6(n16bit_registry_1_1_11_out6), .Out5(n16bit_registry_1_1_11_out5),
    .Out4(n16bit_registry_1_1_11_out4), .Out3(n16bit_registry_1_1_11_out3),
    .Out2(n16bit_registry_1_1_11_out2), .Out1(n16bit_registry_1_1_11_out1), .Out0(n16bit_registry_1_1_11_out0));
  _16bit_Registry_Selector u_16bit_registry_selector_11 (
    .WE(and_21_out), .In(n16bit_registry_1_1_11_out15), .In_2(n16bit_registry_1_1_11_out14),
    .In_3(n16bit_registry_1_1_11_out13), .In_4(n16bit_registry_1_1_11_out12),
    .In_5(n16bit_registry_1_1_11_out11), .In_6(n16bit_registry_1_1_11_out10),
    .In_7(n16bit_registry_1_1_11_out9), .In_8(n16bit_registry_1_1_11_out8),
    .In_9(n16bit_registry_1_1_11_out7), .In_10(n16bit_registry_1_1_11_out6),
    .In_11(n16bit_registry_1_1_11_out5), .In_12(n16bit_registry_1_1_11_out4),
    .In_13(n16bit_registry_1_1_11_out3), .In_14(n16bit_registry_1_1_11_out2),
    .In_15(n16bit_registry_1_1_11_out1), .In_16(n16bit_registry_1_1_11_out0),
    .Out(n16bit_registry_selector_11_out));
  _16bit_Registry__1_1 u_16bit_registry_1_1_12 (
    .WE(and_24_out), .In(Data_In), .Out15(n16bit_registry_1_1_12_out15),
    .Out14(n16bit_registry_1_1_12_out14), .Out13(n16bit_registry_1_1_12_out13),
    .Out12(n16bit_registry_1_1_12_out12), .Out11(n16bit_registry_1_1_12_out11),
    .Out10(n16bit_registry_1_1_12_out10), .Out9(n16bit_registry_1_1_12_out9),
    .Out8(n16bit_registry_1_1_12_out8), .Out7(n16bit_registry_1_1_12_out7),
    .Out6(n16bit_registry_1_1_12_out6), .Out5(n16bit_registry_1_1_12_out5),
    .Out4(n16bit_registry_1_1_12_out4), .Out3(n16bit_registry_1_1_12_out3),
    .Out2(n16bit_registry_1_1_12_out2), .Out1(n16bit_registry_1_1_12_out1), .Out0(n16bit_registry_1_1_12_out0));
  _16bit_Registry_Selector u_16bit_registry_selector_12 (
    .WE(and_23_out), .In(n16bit_registry_1_1_12_out15), .In_2(n16bit_registry_1_1_12_out14),
    .In_3(n16bit_registry_1_1_12_out13), .In_4(n16bit_registry_1_1_12_out12),
    .In_5(n16bit_registry_1_1_12_out11), .In_6(n16bit_registry_1_1_12_out10),
    .In_7(n16bit_registry_1_1_12_out9), .In_8(n16bit_registry_1_1_12_out8),
    .In_9(n16bit_registry_1_1_12_out7), .In_10(n16bit_registry_1_1_12_out6),
    .In_11(n16bit_registry_1_1_12_out5), .In_12(n16bit_registry_1_1_12_out4),
    .In_13(n16bit_registry_1_1_12_out3), .In_14(n16bit_registry_1_1_12_out2),
    .In_15(n16bit_registry_1_1_12_out1), .In_16(n16bit_registry_1_1_12_out0),
    .Out(n16bit_registry_selector_12_out));
  _16bit_Registry__1_1 u_16bit_registry_1_1_13 (
    .WE(and_26_out), .In(Data_In), .Out15(n16bit_registry_1_1_13_out15),
    .Out14(n16bit_registry_1_1_13_out14), .Out13(n16bit_registry_1_1_13_out13),
    .Out12(n16bit_registry_1_1_13_out12), .Out11(n16bit_registry_1_1_13_out11),
    .Out10(n16bit_registry_1_1_13_out10), .Out9(n16bit_registry_1_1_13_out9),
    .Out8(n16bit_registry_1_1_13_out8), .Out7(n16bit_registry_1_1_13_out7),
    .Out6(n16bit_registry_1_1_13_out6), .Out5(n16bit_registry_1_1_13_out5),
    .Out4(n16bit_registry_1_1_13_out4), .Out3(n16bit_registry_1_1_13_out3),
    .Out2(n16bit_registry_1_1_13_out2), .Out1(n16bit_registry_1_1_13_out1), .Out0(n16bit_registry_1_1_13_out0));
  _16bit_Registry_Selector u_16bit_registry_selector_13 (
    .WE(and_25_out), .In(n16bit_registry_1_1_13_out15), .In_2(n16bit_registry_1_1_13_out14),
    .In_3(n16bit_registry_1_1_13_out13), .In_4(n16bit_registry_1_1_13_out12),
    .In_5(n16bit_registry_1_1_13_out11), .In_6(n16bit_registry_1_1_13_out10),
    .In_7(n16bit_registry_1_1_13_out9), .In_8(n16bit_registry_1_1_13_out8),
    .In_9(n16bit_registry_1_1_13_out7), .In_10(n16bit_registry_1_1_13_out6),
    .In_11(n16bit_registry_1_1_13_out5), .In_12(n16bit_registry_1_1_13_out4),
    .In_13(n16bit_registry_1_1_13_out3), .In_14(n16bit_registry_1_1_13_out2),
    .In_15(n16bit_registry_1_1_13_out1), .In_16(n16bit_registry_1_1_13_out0),
    .Out(n16bit_registry_selector_13_out));
  _16bit_Registry__1_1 u_16bit_registry_1_1_14 (
    .WE(and_28_out), .In(Data_In), .Out15(n16bit_registry_1_1_14_out15),
    .Out14(n16bit_registry_1_1_14_out14), .Out13(n16bit_registry_1_1_14_out13),
    .Out12(n16bit_registry_1_1_14_out12), .Out11(n16bit_registry_1_1_14_out11),
    .Out10(n16bit_registry_1_1_14_out10), .Out9(n16bit_registry_1_1_14_out9),
    .Out8(n16bit_registry_1_1_14_out8), .Out7(n16bit_registry_1_1_14_out7),
    .Out6(n16bit_registry_1_1_14_out6), .Out5(n16bit_registry_1_1_14_out5),
    .Out4(n16bit_registry_1_1_14_out4), .Out3(n16bit_registry_1_1_14_out3),
    .Out2(n16bit_registry_1_1_14_out2), .Out1(n16bit_registry_1_1_14_out1), .Out0(n16bit_registry_1_1_14_out0));
  _16bit_Registry_Selector u_16bit_registry_selector_14 (
    .WE(and_27_out), .In(n16bit_registry_1_1_14_out15), .In_2(n16bit_registry_1_1_14_out14),
    .In_3(n16bit_registry_1_1_14_out13), .In_4(n16bit_registry_1_1_14_out12),
    .In_5(n16bit_registry_1_1_14_out11), .In_6(n16bit_registry_1_1_14_out10),
    .In_7(n16bit_registry_1_1_14_out9), .In_8(n16bit_registry_1_1_14_out8),
    .In_9(n16bit_registry_1_1_14_out7), .In_10(n16bit_registry_1_1_14_out6),
    .In_11(n16bit_registry_1_1_14_out5), .In_12(n16bit_registry_1_1_14_out4),
    .In_13(n16bit_registry_1_1_14_out3), .In_14(n16bit_registry_1_1_14_out2),
    .In_15(n16bit_registry_1_1_14_out1), .In_16(n16bit_registry_1_1_14_out0),
    .Out(n16bit_registry_selector_14_out));
  _16bit_Registry__1_1 u_16bit_registry_1_1_15 (
    .WE(and_30_out), .In(Data_In), .Out15(n16bit_registry_1_1_15_out15),
    .Out14(n16bit_registry_1_1_15_out14), .Out13(n16bit_registry_1_1_15_out13),
    .Out12(n16bit_registry_1_1_15_out12), .Out11(n16bit_registry_1_1_15_out11),
    .Out10(n16bit_registry_1_1_15_out10), .Out9(n16bit_registry_1_1_15_out9),
    .Out8(n16bit_registry_1_1_15_out8), .Out7(n16bit_registry_1_1_15_out7),
    .Out6(n16bit_registry_1_1_15_out6), .Out5(n16bit_registry_1_1_15_out5),
    .Out4(n16bit_registry_1_1_15_out4), .Out3(n16bit_registry_1_1_15_out3),
    .Out2(n16bit_registry_1_1_15_out2), .Out1(n16bit_registry_1_1_15_out1), .Out0(n16bit_registry_1_1_15_out0));
  _16bit_Registry_Selector u_16bit_registry_selector_15 (
    .WE(and_29_out), .In(n16bit_registry_1_1_15_out15), .In_2(n16bit_registry_1_1_15_out14),
    .In_3(n16bit_registry_1_1_15_out13), .In_4(n16bit_registry_1_1_15_out12),
    .In_5(n16bit_registry_1_1_15_out11), .In_6(n16bit_registry_1_1_15_out10),
    .In_7(n16bit_registry_1_1_15_out9), .In_8(n16bit_registry_1_1_15_out8),
    .In_9(n16bit_registry_1_1_15_out7), .In_10(n16bit_registry_1_1_15_out6),
    .In_11(n16bit_registry_1_1_15_out5), .In_12(n16bit_registry_1_1_15_out4),
    .In_13(n16bit_registry_1_1_15_out3), .In_14(n16bit_registry_1_1_15_out2),
    .In_15(n16bit_registry_1_1_15_out1), .In_16(n16bit_registry_1_1_15_out0),
    .Out(n16bit_registry_selector_15_out));
  _16bit_Registry__1_1 u_16bit_registry_1_1_16 (
    .WE(and_32_out), .In(Data_In), .Out15(n16bit_registry_1_1_16_out15),
    .Out14(n16bit_registry_1_1_16_out14), .Out13(n16bit_registry_1_1_16_out13),
    .Out12(n16bit_registry_1_1_16_out12), .Out11(n16bit_registry_1_1_16_out11),
    .Out10(n16bit_registry_1_1_16_out10), .Out9(n16bit_registry_1_1_16_out9),
    .Out8(n16bit_registry_1_1_16_out8), .Out7(n16bit_registry_1_1_16_out7),
    .Out6(n16bit_registry_1_1_16_out6), .Out5(n16bit_registry_1_1_16_out5),
    .Out4(n16bit_registry_1_1_16_out4), .Out3(n16bit_registry_1_1_16_out3),
    .Out2(n16bit_registry_1_1_16_out2), .Out1(n16bit_registry_1_1_16_out1), .Out0(n16bit_registry_1_1_16_out0));
  _16bit_Registry_Selector u_16bit_registry_selector_16 (
    .WE(and_31_out), .In(n16bit_registry_1_1_16_out15), .In_2(n16bit_registry_1_1_16_out14),
    .In_3(n16bit_registry_1_1_16_out13), .In_4(n16bit_registry_1_1_16_out12),
    .In_5(n16bit_registry_1_1_16_out11), .In_6(n16bit_registry_1_1_16_out10),
    .In_7(n16bit_registry_1_1_16_out9), .In_8(n16bit_registry_1_1_16_out8),
    .In_9(n16bit_registry_1_1_16_out7), .In_10(n16bit_registry_1_1_16_out6),
    .In_11(n16bit_registry_1_1_16_out5), .In_12(n16bit_registry_1_1_16_out4),
    .In_13(n16bit_registry_1_1_16_out3), .In_14(n16bit_registry_1_1_16_out2),
    .In_15(n16bit_registry_1_1_16_out1), .In_16(n16bit_registry_1_1_16_out0),
    .Out(n16bit_registry_selector_16_out));
  assign Inst_Out = n16bit_registry_selector_1_out | n16bit_registry_selector_2_out | n16bit_registry_selector_3_out | n16bit_registry_selector_4_out | n16bit_registry_selector_5_out | n16bit_registry_selector_6_out | n16bit_registry_selector_7_out | n16bit_registry_selector_8_out | n16bit_registry_selector_9_out | n16bit_registry_selector_10_out | n16bit_registry_selector_11_out | n16bit_registry_selector_12_out | n16bit_registry_selector_13_out | n16bit_registry_selector_14_out | n16bit_registry_selector_15_out | n16bit_registry_selector_16_out;  // OR_Gate or_1, 16 bits wide
  // also tied to GND on the sheet: {Memory_Address[4], Memory_Address[5], Memory_Address[6], Memory_Address[7], Memory_Address[8], Memory_Address[9], Memory_Address[10], Memory_Address[11], Memory_Address[12], Memory_Address[13], Memory_Address[14], Memory_Address[15]}
endmodule
module General_Purpose_Registries (
  input  [15:0] Data_In,
  input  [2:0] Address,
  input  in_3,
  output [15:0] Data_Out
);

  wire and_1_out, and_2_out, and_3_out, and_4_out, and_5_out, and_6_out, and_7_out, and_8_out, and_9_out,
       and_10_out, and_11_out, and_12_out, and_13_out, and_14_out, and_15_out, and_16_out,
       n16bit_registry_1_1_1_out0, n16bit_registry_1_1_1_out1, n16bit_registry_1_1_1_out2,
       n16bit_registry_1_1_1_out3, n16bit_registry_1_1_1_out4, n16bit_registry_1_1_1_out5,
       n16bit_registry_1_1_1_out6, n16bit_registry_1_1_1_out7, n16bit_registry_1_1_1_out8,
       n16bit_registry_1_1_1_out9, n16bit_registry_1_1_1_out10, n16bit_registry_1_1_1_out11,
       n16bit_registry_1_1_1_out12, n16bit_registry_1_1_1_out13, n16bit_registry_1_1_1_out14,
       n16bit_registry_1_1_1_out15, n16bit_registry_1_1_2_out0, n16bit_registry_1_1_2_out1,
       n16bit_registry_1_1_2_out2, n16bit_registry_1_1_2_out3, n16bit_registry_1_1_2_out4,
       n16bit_registry_1_1_2_out5, n16bit_registry_1_1_2_out6, n16bit_registry_1_1_2_out7,
       n16bit_registry_1_1_2_out8, n16bit_registry_1_1_2_out9, n16bit_registry_1_1_2_out10,
       n16bit_registry_1_1_2_out11, n16bit_registry_1_1_2_out12, n16bit_registry_1_1_2_out13,
       n16bit_registry_1_1_2_out14, n16bit_registry_1_1_2_out15, n16bit_registry_1_1_3_out0,
       n16bit_registry_1_1_3_out1, n16bit_registry_1_1_3_out2, n16bit_registry_1_1_3_out3,
       n16bit_registry_1_1_3_out4, n16bit_registry_1_1_3_out5, n16bit_registry_1_1_3_out6,
       n16bit_registry_1_1_3_out7, n16bit_registry_1_1_3_out8, n16bit_registry_1_1_3_out9,
       n16bit_registry_1_1_3_out10, n16bit_registry_1_1_3_out11, n16bit_registry_1_1_3_out12,
       n16bit_registry_1_1_3_out13, n16bit_registry_1_1_3_out14, n16bit_registry_1_1_3_out15,
       n16bit_registry_1_1_4_out0, n16bit_registry_1_1_4_out1, n16bit_registry_1_1_4_out2,
       n16bit_registry_1_1_4_out3, n16bit_registry_1_1_4_out4, n16bit_registry_1_1_4_out5,
       n16bit_registry_1_1_4_out6, n16bit_registry_1_1_4_out7, n16bit_registry_1_1_4_out8,
       n16bit_registry_1_1_4_out9, n16bit_registry_1_1_4_out10, n16bit_registry_1_1_4_out11,
       n16bit_registry_1_1_4_out12, n16bit_registry_1_1_4_out13, n16bit_registry_1_1_4_out14,
       n16bit_registry_1_1_4_out15, n16bit_registry_1_1_5_out0, n16bit_registry_1_1_5_out1,
       n16bit_registry_1_1_5_out2, n16bit_registry_1_1_5_out3, n16bit_registry_1_1_5_out4,
       n16bit_registry_1_1_5_out5, n16bit_registry_1_1_5_out6, n16bit_registry_1_1_5_out7,
       n16bit_registry_1_1_5_out8, n16bit_registry_1_1_5_out9, n16bit_registry_1_1_5_out10,
       n16bit_registry_1_1_5_out11, n16bit_registry_1_1_5_out12, n16bit_registry_1_1_5_out13,
       n16bit_registry_1_1_5_out14, n16bit_registry_1_1_5_out15, n16bit_registry_1_1_6_out0,
       n16bit_registry_1_1_6_out1, n16bit_registry_1_1_6_out2, n16bit_registry_1_1_6_out3,
       n16bit_registry_1_1_6_out4, n16bit_registry_1_1_6_out5, n16bit_registry_1_1_6_out6,
       n16bit_registry_1_1_6_out7, n16bit_registry_1_1_6_out8, n16bit_registry_1_1_6_out9,
       n16bit_registry_1_1_6_out10, n16bit_registry_1_1_6_out11, n16bit_registry_1_1_6_out12,
       n16bit_registry_1_1_6_out13, n16bit_registry_1_1_6_out14, n16bit_registry_1_1_6_out15,
       n16bit_registry_1_1_7_out0, n16bit_registry_1_1_7_out1, n16bit_registry_1_1_7_out2,
       n16bit_registry_1_1_7_out3, n16bit_registry_1_1_7_out4, n16bit_registry_1_1_7_out5,
       n16bit_registry_1_1_7_out6, n16bit_registry_1_1_7_out7, n16bit_registry_1_1_7_out8,
       n16bit_registry_1_1_7_out9, n16bit_registry_1_1_7_out10, n16bit_registry_1_1_7_out11,
       n16bit_registry_1_1_7_out12, n16bit_registry_1_1_7_out13, n16bit_registry_1_1_7_out14,
       n16bit_registry_1_1_7_out15, n16bit_registry_1_1_8_out0, n16bit_registry_1_1_8_out1,
       n16bit_registry_1_1_8_out2, n16bit_registry_1_1_8_out3, n16bit_registry_1_1_8_out4,
       n16bit_registry_1_1_8_out5, n16bit_registry_1_1_8_out6, n16bit_registry_1_1_8_out7,
       n16bit_registry_1_1_8_out8, n16bit_registry_1_1_8_out9, n16bit_registry_1_1_8_out10,
       n16bit_registry_1_1_8_out11, n16bit_registry_1_1_8_out12, n16bit_registry_1_1_8_out13,
       n16bit_registry_1_1_8_out14, n16bit_registry_1_1_8_out15;
  wire [15:0] n16bit_registry_selector_1_out, n16bit_registry_selector_2_out, n16bit_registry_selector_3_out,
       n16bit_registry_selector_4_out, n16bit_registry_selector_5_out, n16bit_registry_selector_6_out,
       n16bit_registry_selector_7_out, n16bit_registry_selector_8_out;

  and and_1 (and_1_out, ~Address[0], ~Address[1], ~Address[2]);  // AND_Gate
  and and_2 (and_2_out, and_1_out, in_3);
  and and_3 (and_3_out, Address[0], ~Address[1], ~Address[2]);  // AND_Gate
  and and_4 (and_4_out, and_3_out, in_3);
  and and_5 (and_5_out, ~Address[0], Address[1], ~Address[2]);  // AND_Gate
  and and_6 (and_6_out, and_5_out, in_3);
  and and_7 (and_7_out, Address[0], Address[1], ~Address[2]);  // AND_Gate
  and and_8 (and_8_out, and_7_out, in_3);
  and and_9 (and_9_out, ~Address[0], ~Address[1], Address[2]);  // AND_Gate
  and and_10 (and_10_out, and_9_out, in_3);
  and and_11 (and_11_out, Address[0], ~Address[1], Address[2]);  // AND_Gate
  and and_12 (and_12_out, and_11_out, in_3);
  and and_13 (and_13_out, ~Address[0], Address[1], Address[2]);  // AND_Gate
  and and_14 (and_14_out, and_13_out, in_3);
  and and_15 (and_15_out, Address[0], Address[1], Address[2]);
  and and_16 (and_16_out, and_15_out, in_3);
  _16bit_Registry__1_1 u_16bit_registry_1_1_1 (
    .WE(and_2_out), .In(Data_In), .Out15(n16bit_registry_1_1_1_out15), .Out14(n16bit_registry_1_1_1_out14),
    .Out13(n16bit_registry_1_1_1_out13), .Out12(n16bit_registry_1_1_1_out12),
    .Out11(n16bit_registry_1_1_1_out11), .Out10(n16bit_registry_1_1_1_out10),
    .Out9(n16bit_registry_1_1_1_out9), .Out8(n16bit_registry_1_1_1_out8), .Out7(n16bit_registry_1_1_1_out7),
    .Out6(n16bit_registry_1_1_1_out6), .Out5(n16bit_registry_1_1_1_out5), .Out4(n16bit_registry_1_1_1_out4),
    .Out3(n16bit_registry_1_1_1_out3), .Out2(n16bit_registry_1_1_1_out2), .Out1(n16bit_registry_1_1_1_out1),
    .Out0(n16bit_registry_1_1_1_out0));
  _16bit_Registry_Selector u_16bit_registry_selector_1 (
    .WE(and_1_out), .In(n16bit_registry_1_1_1_out15), .In_2(n16bit_registry_1_1_1_out14),
    .In_3(n16bit_registry_1_1_1_out13), .In_4(n16bit_registry_1_1_1_out12),
    .In_5(n16bit_registry_1_1_1_out11), .In_6(n16bit_registry_1_1_1_out10),
    .In_7(n16bit_registry_1_1_1_out9), .In_8(n16bit_registry_1_1_1_out8), .In_9(n16bit_registry_1_1_1_out7),
    .In_10(n16bit_registry_1_1_1_out6), .In_11(n16bit_registry_1_1_1_out5),
    .In_12(n16bit_registry_1_1_1_out4), .In_13(n16bit_registry_1_1_1_out3),
    .In_14(n16bit_registry_1_1_1_out2), .In_15(n16bit_registry_1_1_1_out1),
    .In_16(n16bit_registry_1_1_1_out0), .Out(n16bit_registry_selector_1_out));
  _16bit_Registry__1_1 u_16bit_registry_1_1_2 (
    .WE(and_4_out), .In(Data_In), .Out15(n16bit_registry_1_1_2_out15), .Out14(n16bit_registry_1_1_2_out14),
    .Out13(n16bit_registry_1_1_2_out13), .Out12(n16bit_registry_1_1_2_out12),
    .Out11(n16bit_registry_1_1_2_out11), .Out10(n16bit_registry_1_1_2_out10),
    .Out9(n16bit_registry_1_1_2_out9), .Out8(n16bit_registry_1_1_2_out8), .Out7(n16bit_registry_1_1_2_out7),
    .Out6(n16bit_registry_1_1_2_out6), .Out5(n16bit_registry_1_1_2_out5), .Out4(n16bit_registry_1_1_2_out4),
    .Out3(n16bit_registry_1_1_2_out3), .Out2(n16bit_registry_1_1_2_out2), .Out1(n16bit_registry_1_1_2_out1),
    .Out0(n16bit_registry_1_1_2_out0));
  _16bit_Registry_Selector u_16bit_registry_selector_2 (
    .WE(and_3_out), .In(n16bit_registry_1_1_2_out15), .In_2(n16bit_registry_1_1_2_out14),
    .In_3(n16bit_registry_1_1_2_out13), .In_4(n16bit_registry_1_1_2_out12),
    .In_5(n16bit_registry_1_1_2_out11), .In_6(n16bit_registry_1_1_2_out10),
    .In_7(n16bit_registry_1_1_2_out9), .In_8(n16bit_registry_1_1_2_out8), .In_9(n16bit_registry_1_1_2_out7),
    .In_10(n16bit_registry_1_1_2_out6), .In_11(n16bit_registry_1_1_2_out5),
    .In_12(n16bit_registry_1_1_2_out4), .In_13(n16bit_registry_1_1_2_out3),
    .In_14(n16bit_registry_1_1_2_out2), .In_15(n16bit_registry_1_1_2_out1),
    .In_16(n16bit_registry_1_1_2_out0), .Out(n16bit_registry_selector_2_out));
  _16bit_Registry__1_1 u_16bit_registry_1_1_3 (
    .WE(and_6_out), .In(Data_In), .Out15(n16bit_registry_1_1_3_out15), .Out14(n16bit_registry_1_1_3_out14),
    .Out13(n16bit_registry_1_1_3_out13), .Out12(n16bit_registry_1_1_3_out12),
    .Out11(n16bit_registry_1_1_3_out11), .Out10(n16bit_registry_1_1_3_out10),
    .Out9(n16bit_registry_1_1_3_out9), .Out8(n16bit_registry_1_1_3_out8), .Out7(n16bit_registry_1_1_3_out7),
    .Out6(n16bit_registry_1_1_3_out6), .Out5(n16bit_registry_1_1_3_out5), .Out4(n16bit_registry_1_1_3_out4),
    .Out3(n16bit_registry_1_1_3_out3), .Out2(n16bit_registry_1_1_3_out2), .Out1(n16bit_registry_1_1_3_out1),
    .Out0(n16bit_registry_1_1_3_out0));
  _16bit_Registry_Selector u_16bit_registry_selector_3 (
    .WE(and_5_out), .In(n16bit_registry_1_1_3_out15), .In_2(n16bit_registry_1_1_3_out14),
    .In_3(n16bit_registry_1_1_3_out13), .In_4(n16bit_registry_1_1_3_out12),
    .In_5(n16bit_registry_1_1_3_out11), .In_6(n16bit_registry_1_1_3_out10),
    .In_7(n16bit_registry_1_1_3_out9), .In_8(n16bit_registry_1_1_3_out8), .In_9(n16bit_registry_1_1_3_out7),
    .In_10(n16bit_registry_1_1_3_out6), .In_11(n16bit_registry_1_1_3_out5),
    .In_12(n16bit_registry_1_1_3_out4), .In_13(n16bit_registry_1_1_3_out3),
    .In_14(n16bit_registry_1_1_3_out2), .In_15(n16bit_registry_1_1_3_out1),
    .In_16(n16bit_registry_1_1_3_out0), .Out(n16bit_registry_selector_3_out));
  _16bit_Registry__1_1 u_16bit_registry_1_1_4 (
    .WE(and_8_out), .In(Data_In), .Out15(n16bit_registry_1_1_4_out15), .Out14(n16bit_registry_1_1_4_out14),
    .Out13(n16bit_registry_1_1_4_out13), .Out12(n16bit_registry_1_1_4_out12),
    .Out11(n16bit_registry_1_1_4_out11), .Out10(n16bit_registry_1_1_4_out10),
    .Out9(n16bit_registry_1_1_4_out9), .Out8(n16bit_registry_1_1_4_out8), .Out7(n16bit_registry_1_1_4_out7),
    .Out6(n16bit_registry_1_1_4_out6), .Out5(n16bit_registry_1_1_4_out5), .Out4(n16bit_registry_1_1_4_out4),
    .Out3(n16bit_registry_1_1_4_out3), .Out2(n16bit_registry_1_1_4_out2), .Out1(n16bit_registry_1_1_4_out1),
    .Out0(n16bit_registry_1_1_4_out0));
  _16bit_Registry_Selector u_16bit_registry_selector_4 (
    .WE(and_7_out), .In(n16bit_registry_1_1_4_out15), .In_2(n16bit_registry_1_1_4_out14),
    .In_3(n16bit_registry_1_1_4_out13), .In_4(n16bit_registry_1_1_4_out12),
    .In_5(n16bit_registry_1_1_4_out11), .In_6(n16bit_registry_1_1_4_out10),
    .In_7(n16bit_registry_1_1_4_out9), .In_8(n16bit_registry_1_1_4_out8), .In_9(n16bit_registry_1_1_4_out7),
    .In_10(n16bit_registry_1_1_4_out6), .In_11(n16bit_registry_1_1_4_out5),
    .In_12(n16bit_registry_1_1_4_out4), .In_13(n16bit_registry_1_1_4_out3),
    .In_14(n16bit_registry_1_1_4_out2), .In_15(n16bit_registry_1_1_4_out1),
    .In_16(n16bit_registry_1_1_4_out0), .Out(n16bit_registry_selector_4_out));
  _16bit_Registry__1_1 u_16bit_registry_1_1_5 (
    .WE(and_10_out), .In(Data_In), .Out15(n16bit_registry_1_1_5_out15), .Out14(n16bit_registry_1_1_5_out14),
    .Out13(n16bit_registry_1_1_5_out13), .Out12(n16bit_registry_1_1_5_out12),
    .Out11(n16bit_registry_1_1_5_out11), .Out10(n16bit_registry_1_1_5_out10),
    .Out9(n16bit_registry_1_1_5_out9), .Out8(n16bit_registry_1_1_5_out8), .Out7(n16bit_registry_1_1_5_out7),
    .Out6(n16bit_registry_1_1_5_out6), .Out5(n16bit_registry_1_1_5_out5), .Out4(n16bit_registry_1_1_5_out4),
    .Out3(n16bit_registry_1_1_5_out3), .Out2(n16bit_registry_1_1_5_out2), .Out1(n16bit_registry_1_1_5_out1),
    .Out0(n16bit_registry_1_1_5_out0));
  _16bit_Registry_Selector u_16bit_registry_selector_5 (
    .WE(and_9_out), .In(n16bit_registry_1_1_5_out15), .In_2(n16bit_registry_1_1_5_out14),
    .In_3(n16bit_registry_1_1_5_out13), .In_4(n16bit_registry_1_1_5_out12),
    .In_5(n16bit_registry_1_1_5_out11), .In_6(n16bit_registry_1_1_5_out10),
    .In_7(n16bit_registry_1_1_5_out9), .In_8(n16bit_registry_1_1_5_out8), .In_9(n16bit_registry_1_1_5_out7),
    .In_10(n16bit_registry_1_1_5_out6), .In_11(n16bit_registry_1_1_5_out5),
    .In_12(n16bit_registry_1_1_5_out4), .In_13(n16bit_registry_1_1_5_out3),
    .In_14(n16bit_registry_1_1_5_out2), .In_15(n16bit_registry_1_1_5_out1),
    .In_16(n16bit_registry_1_1_5_out0), .Out(n16bit_registry_selector_5_out));
  _16bit_Registry__1_1 u_16bit_registry_1_1_6 (
    .WE(and_12_out), .In(Data_In), .Out15(n16bit_registry_1_1_6_out15), .Out14(n16bit_registry_1_1_6_out14),
    .Out13(n16bit_registry_1_1_6_out13), .Out12(n16bit_registry_1_1_6_out12),
    .Out11(n16bit_registry_1_1_6_out11), .Out10(n16bit_registry_1_1_6_out10),
    .Out9(n16bit_registry_1_1_6_out9), .Out8(n16bit_registry_1_1_6_out8), .Out7(n16bit_registry_1_1_6_out7),
    .Out6(n16bit_registry_1_1_6_out6), .Out5(n16bit_registry_1_1_6_out5), .Out4(n16bit_registry_1_1_6_out4),
    .Out3(n16bit_registry_1_1_6_out3), .Out2(n16bit_registry_1_1_6_out2), .Out1(n16bit_registry_1_1_6_out1),
    .Out0(n16bit_registry_1_1_6_out0));
  _16bit_Registry_Selector u_16bit_registry_selector_6 (
    .WE(and_11_out), .In(n16bit_registry_1_1_6_out15), .In_2(n16bit_registry_1_1_6_out14),
    .In_3(n16bit_registry_1_1_6_out13), .In_4(n16bit_registry_1_1_6_out12),
    .In_5(n16bit_registry_1_1_6_out11), .In_6(n16bit_registry_1_1_6_out10),
    .In_7(n16bit_registry_1_1_6_out9), .In_8(n16bit_registry_1_1_6_out8), .In_9(n16bit_registry_1_1_6_out7),
    .In_10(n16bit_registry_1_1_6_out6), .In_11(n16bit_registry_1_1_6_out5),
    .In_12(n16bit_registry_1_1_6_out4), .In_13(n16bit_registry_1_1_6_out3),
    .In_14(n16bit_registry_1_1_6_out2), .In_15(n16bit_registry_1_1_6_out1),
    .In_16(n16bit_registry_1_1_6_out0), .Out(n16bit_registry_selector_6_out));
  _16bit_Registry__1_1 u_16bit_registry_1_1_7 (
    .WE(and_14_out), .In(Data_In), .Out15(n16bit_registry_1_1_7_out15), .Out14(n16bit_registry_1_1_7_out14),
    .Out13(n16bit_registry_1_1_7_out13), .Out12(n16bit_registry_1_1_7_out12),
    .Out11(n16bit_registry_1_1_7_out11), .Out10(n16bit_registry_1_1_7_out10),
    .Out9(n16bit_registry_1_1_7_out9), .Out8(n16bit_registry_1_1_7_out8), .Out7(n16bit_registry_1_1_7_out7),
    .Out6(n16bit_registry_1_1_7_out6), .Out5(n16bit_registry_1_1_7_out5), .Out4(n16bit_registry_1_1_7_out4),
    .Out3(n16bit_registry_1_1_7_out3), .Out2(n16bit_registry_1_1_7_out2), .Out1(n16bit_registry_1_1_7_out1),
    .Out0(n16bit_registry_1_1_7_out0));
  _16bit_Registry_Selector u_16bit_registry_selector_7 (
    .WE(and_13_out), .In(n16bit_registry_1_1_7_out15), .In_2(n16bit_registry_1_1_7_out14),
    .In_3(n16bit_registry_1_1_7_out13), .In_4(n16bit_registry_1_1_7_out12),
    .In_5(n16bit_registry_1_1_7_out11), .In_6(n16bit_registry_1_1_7_out10),
    .In_7(n16bit_registry_1_1_7_out9), .In_8(n16bit_registry_1_1_7_out8), .In_9(n16bit_registry_1_1_7_out7),
    .In_10(n16bit_registry_1_1_7_out6), .In_11(n16bit_registry_1_1_7_out5),
    .In_12(n16bit_registry_1_1_7_out4), .In_13(n16bit_registry_1_1_7_out3),
    .In_14(n16bit_registry_1_1_7_out2), .In_15(n16bit_registry_1_1_7_out1),
    .In_16(n16bit_registry_1_1_7_out0), .Out(n16bit_registry_selector_7_out));
  _16bit_Registry__1_1 u_16bit_registry_1_1_8 (
    .WE(and_16_out), .In(Data_In), .Out15(n16bit_registry_1_1_8_out15), .Out14(n16bit_registry_1_1_8_out14),
    .Out13(n16bit_registry_1_1_8_out13), .Out12(n16bit_registry_1_1_8_out12),
    .Out11(n16bit_registry_1_1_8_out11), .Out10(n16bit_registry_1_1_8_out10),
    .Out9(n16bit_registry_1_1_8_out9), .Out8(n16bit_registry_1_1_8_out8), .Out7(n16bit_registry_1_1_8_out7),
    .Out6(n16bit_registry_1_1_8_out6), .Out5(n16bit_registry_1_1_8_out5), .Out4(n16bit_registry_1_1_8_out4),
    .Out3(n16bit_registry_1_1_8_out3), .Out2(n16bit_registry_1_1_8_out2), .Out1(n16bit_registry_1_1_8_out1),
    .Out0(n16bit_registry_1_1_8_out0));
  _16bit_Registry_Selector u_16bit_registry_selector_8 (
    .WE(and_15_out), .In(n16bit_registry_1_1_8_out15), .In_2(n16bit_registry_1_1_8_out14),
    .In_3(n16bit_registry_1_1_8_out13), .In_4(n16bit_registry_1_1_8_out12),
    .In_5(n16bit_registry_1_1_8_out11), .In_6(n16bit_registry_1_1_8_out10),
    .In_7(n16bit_registry_1_1_8_out9), .In_8(n16bit_registry_1_1_8_out8), .In_9(n16bit_registry_1_1_8_out7),
    .In_10(n16bit_registry_1_1_8_out6), .In_11(n16bit_registry_1_1_8_out5),
    .In_12(n16bit_registry_1_1_8_out4), .In_13(n16bit_registry_1_1_8_out3),
    .In_14(n16bit_registry_1_1_8_out2), .In_15(n16bit_registry_1_1_8_out1),
    .In_16(n16bit_registry_1_1_8_out0), .Out(n16bit_registry_selector_8_out));
  assign Data_Out = n16bit_registry_selector_1_out | n16bit_registry_selector_2_out | n16bit_registry_selector_3_out | n16bit_registry_selector_4_out | n16bit_registry_selector_5_out | n16bit_registry_selector_6_out | n16bit_registry_selector_7_out | n16bit_registry_selector_8_out;  // OR_Gate or_1, 16 bits wide
endmodule

module Program_Pointer__PP (
  input  [15:0] In,
  input  WE,
  input  Read_Enable,
  output [15:0] Data_Out
);

  wire nand_1_out, nand_2_out, nand_3_out, nand_4_out, nand_5_out, nand_6_out, nand_7_out, nand_8_out,
       nand_9_out, nand_10_out, nand_11_out, nand_12_out, nand_13_out, nand_14_out, nand_15_out, nand_16_out,
       nand_17_out, nand_18_out, nand_19_out, nand_20_out, nand_21_out, nand_22_out, nand_23_out,
       nand_24_out, nand_25_out, nand_26_out, nand_27_out, nand_28_out, nand_29_out, nand_30_out,
       nand_31_out, nand_32_out, nand_33_out, nand_34_out, nand_35_out, nand_36_out, nand_37_out,
       nand_38_out, nand_39_out, nand_40_out, nand_41_out, nand_42_out, nand_43_out, nand_44_out,
       nand_45_out, nand_46_out, nand_47_out, nand_48_out, nand_49_out, nand_50_out, nand_51_out,
       nand_52_out, nand_53_out, nand_54_out, nand_55_out, nand_56_out, nand_57_out, nand_58_out,
       nand_59_out, nand_60_out, nand_61_out, nand_62_out, nand_63_out, nand_64_out;

  nand nand_1 (nand_1_out, WE, ~In[15]);  // NAND_Gate
  nand nand_2 (nand_2_out, nand_1_out, nand_5_out);
  nand nand_3 (nand_3_out, In[15], WE);
  nand nand_4 (nand_4_out, WE, ~In[14]);  // NAND_Gate
  nand nand_5 (nand_5_out, nand_2_out, nand_3_out);
  nand nand_6 (nand_6_out, nand_4_out, nand_9_out);
  nand nand_7 (nand_7_out, WE, ~In[13]);  // NAND_Gate
  nand nand_8 (nand_8_out, In[14], WE);
  nand nand_9 (nand_9_out, nand_6_out, nand_8_out);
  nand nand_10 (nand_10_out, nand_7_out, nand_13_out);
  nand nand_11 (nand_11_out, In[13], WE);
  nand nand_12 (nand_12_out, WE, ~In[12]);  // NAND_Gate
  nand nand_13 (nand_13_out, nand_10_out, nand_11_out);
  nand nand_14 (nand_14_out, nand_12_out, nand_17_out);
  nand nand_15 (nand_15_out, WE, ~In[11]);  // NAND_Gate
  nand nand_16 (nand_16_out, In[12], WE);
  nand nand_17 (nand_17_out, nand_14_out, nand_16_out);
  nand nand_18 (nand_18_out, nand_15_out, nand_20_out);
  nand nand_19 (nand_19_out, In[11], WE);
  nand nand_20 (nand_20_out, nand_18_out, nand_19_out);
  nand nand_21 (nand_21_out, WE, ~In[10]);  // NAND_Gate
  nand nand_22 (nand_22_out, In[10], WE);
  nand nand_23 (nand_23_out, nand_24_out, nand_22_out);
  nand nand_24 (nand_24_out, nand_21_out, nand_23_out);
  nand nand_25 (nand_25_out, WE, ~In[9]);  // NAND_Gate
  nand nand_26 (nand_26_out, In[9], WE);
  nand nand_27 (nand_27_out, nand_25_out, nand_28_out);
  nand nand_28 (nand_28_out, nand_27_out, nand_26_out);
  nand nand_29 (nand_29_out, WE, ~In[8]);  // NAND_Gate
  nand nand_30 (nand_30_out, In[8], WE);
  nand nand_31 (nand_31_out, nand_29_out, nand_32_out);
  nand nand_32 (nand_32_out, nand_31_out, nand_30_out);
  nand nand_33 (nand_33_out, WE, ~In[7]);  // NAND_Gate
  nand nand_34 (nand_34_out, nand_33_out, nand_38_out);
  nand nand_35 (nand_35_out, In[7], WE);
  nand nand_36 (nand_36_out, WE, ~In[6]);  // NAND_Gate
  nand nand_37 (nand_37_out, nand_36_out, nand_41_out);
  nand nand_38 (nand_38_out, nand_34_out, nand_35_out);
  nand nand_39 (nand_39_out, WE, ~In[5]);  // NAND_Gate
  nand nand_40 (nand_40_out, In[6], WE);
  nand nand_41 (nand_41_out, nand_37_out, nand_40_out);
  nand nand_42 (nand_42_out, nand_39_out, nand_45_out);
  nand nand_43 (nand_43_out, WE, ~In[4]);  // NAND_Gate
  nand nand_44 (nand_44_out, In[5], WE);
  nand nand_45 (nand_45_out, nand_42_out, nand_44_out);
  nand nand_46 (nand_46_out, nand_43_out, nand_50_out);
  nand nand_47 (nand_47_out, In[4], WE);
  nand nand_48 (nand_48_out, WE, ~In[3]);  // NAND_Gate
  nand nand_49 (nand_49_out, nand_48_out, nand_52_out);
  nand nand_50 (nand_50_out, nand_46_out, nand_47_out);
  nand nand_51 (nand_51_out, In[3], WE);
  nand nand_52 (nand_52_out, nand_49_out, nand_51_out);
  nand nand_53 (nand_53_out, In[2], WE);
  nand nand_54 (nand_54_out, WE, ~In[2]);  // NAND_Gate
  nand nand_55 (nand_55_out, nand_56_out, nand_53_out);
  nand nand_56 (nand_56_out, nand_54_out, nand_55_out);
  nand nand_57 (nand_57_out, In[1], WE);
  nand nand_58 (nand_58_out, WE, ~In[1]);  // NAND_Gate
  nand nand_59 (nand_59_out, nand_58_out, nand_60_out);
  nand nand_60 (nand_60_out, nand_59_out, nand_57_out);
  _16bit_Registry_Selector u_16bit_registry_selector_1 (
    .WE(Read_Enable), .In(nand_5_out), .In_2(nand_9_out), .In_3(nand_13_out), .In_4(nand_17_out),
    .In_5(nand_20_out), .In_6(nand_23_out), .In_7(nand_28_out), .In_8(nand_32_out), .In_9(nand_38_out),
    .In_10(nand_41_out), .In_11(nand_45_out), .In_12(nand_50_out), .In_13(nand_52_out), .In_14(nand_55_out),
    .In_15(nand_60_out), .In_16(nand_64_out), .Out(Data_Out));
  nand nand_61 (nand_61_out, WE, ~In[0]);  // NAND_Gate
  nand nand_62 (nand_62_out, In[0], WE);
  nand nand_63 (nand_63_out, nand_61_out, nand_64_out);
  nand nand_64 (nand_64_out, nand_63_out, nand_62_out);
endmodule

module Memory_Address_Registry__MAR (
  input  [15:0] In,
  input  WE,
  input  Read_Enable,
  output [15:0] Data_Out
);

  wire nand_1_out, nand_2_out, nand_3_out, nand_4_out, nand_5_out, nand_6_out, nand_7_out, nand_8_out,
       nand_9_out, nand_10_out, nand_11_out, nand_12_out, nand_13_out, nand_14_out, nand_15_out, nand_16_out,
       nand_17_out, nand_18_out, nand_19_out, nand_20_out, nand_21_out, nand_22_out, nand_23_out,
       nand_24_out, nand_25_out, nand_26_out, nand_27_out, nand_28_out, nand_29_out, nand_30_out,
       nand_31_out, nand_32_out, nand_33_out, nand_34_out, nand_35_out, nand_36_out, nand_37_out,
       nand_38_out, nand_39_out, nand_40_out, nand_41_out, nand_42_out, nand_43_out, nand_44_out,
       nand_45_out, nand_46_out, nand_47_out, nand_48_out, nand_49_out, nand_50_out, nand_51_out,
       nand_52_out, nand_53_out, nand_54_out, nand_55_out, nand_56_out, nand_57_out, nand_58_out,
       nand_59_out, nand_60_out, nand_61_out, nand_62_out, nand_63_out, nand_64_out;

  nand nand_1 (nand_1_out, WE, ~In[15]);  // NAND_Gate
  nand nand_2 (nand_2_out, nand_1_out, nand_5_out);
  nand nand_3 (nand_3_out, In[15], WE);
  nand nand_4 (nand_4_out, WE, ~In[14]);  // NAND_Gate
  nand nand_5 (nand_5_out, nand_2_out, nand_3_out);
  nand nand_6 (nand_6_out, nand_4_out, nand_9_out);
  nand nand_7 (nand_7_out, WE, ~In[13]);  // NAND_Gate
  nand nand_8 (nand_8_out, In[14], WE);
  nand nand_9 (nand_9_out, nand_6_out, nand_8_out);
  nand nand_10 (nand_10_out, nand_7_out, nand_14_out);
  nand nand_11 (nand_11_out, WE, ~In[12]);  // NAND_Gate
  nand nand_12 (nand_12_out, In[13], WE);
  nand nand_13 (nand_13_out, nand_11_out, nand_18_out);
  nand nand_14 (nand_14_out, nand_10_out, nand_12_out);
  nand nand_15 (nand_15_out, WE, ~In[11]);  // NAND_Gate
  nand nand_16 (nand_16_out, In[12], WE);
  nand nand_17 (nand_17_out, nand_15_out, nand_20_out);
  nand nand_18 (nand_18_out, nand_13_out, nand_16_out);
  nand nand_19 (nand_19_out, In[11], WE);
  nand nand_20 (nand_20_out, nand_17_out, nand_19_out);
  nand nand_21 (nand_21_out, In[10], WE);
  nand nand_22 (nand_22_out, WE, ~In[10]);  // NAND_Gate
  nand nand_23 (nand_23_out, nand_24_out, nand_21_out);
  nand nand_24 (nand_24_out, nand_22_out, nand_23_out);
  nand nand_25 (nand_25_out, In[9], WE);
  nand nand_26 (nand_26_out, WE, ~In[9]);  // NAND_Gate
  nand nand_27 (nand_27_out, nand_28_out, nand_25_out);
  nand nand_28 (nand_28_out, nand_26_out, nand_27_out);
  nand nand_29 (nand_29_out, WE, ~In[8]);  // NAND_Gate
  nand nand_30 (nand_30_out, In[8], WE);
  nand nand_31 (nand_31_out, nand_32_out, nand_30_out);
  nand nand_32 (nand_32_out, nand_29_out, nand_31_out);
  nand nand_33 (nand_33_out, WE, ~In[7]);  // NAND_Gate
  nand nand_34 (nand_34_out, nand_33_out, nand_37_out);
  nand nand_35 (nand_35_out, WE, ~In[6]);  // NAND_Gate
  nand nand_36 (nand_36_out, In[7], WE);
  nand nand_37 (nand_37_out, nand_34_out, nand_36_out);
  nand nand_38 (nand_38_out, nand_35_out, nand_42_out);
  nand nand_39 (nand_39_out, In[6], WE);
  nand nand_40 (nand_40_out, WE, ~In[5]);  // NAND_Gate
  nand nand_41 (nand_41_out, nand_40_out, nand_45_out);
  nand nand_42 (nand_42_out, nand_38_out, nand_39_out);
  nand nand_43 (nand_43_out, WE, ~In[4]);  // NAND_Gate
  nand nand_44 (nand_44_out, In[5], WE);
  nand nand_45 (nand_45_out, nand_41_out, nand_44_out);
  nand nand_46 (nand_46_out, nand_43_out, nand_49_out);
  nand nand_47 (nand_47_out, In[4], WE);
  nand nand_48 (nand_48_out, WE, ~In[3]);  // NAND_Gate
  nand nand_49 (nand_49_out, nand_46_out, nand_47_out);
  nand nand_50 (nand_50_out, nand_48_out, nand_52_out);
  nand nand_51 (nand_51_out, In[3], WE);
  nand nand_52 (nand_52_out, nand_50_out, nand_51_out);
  nand nand_53 (nand_53_out, WE, ~In[2]);  // NAND_Gate
  nand nand_54 (nand_54_out, In[2], WE);
  nand nand_55 (nand_55_out, nand_53_out, nand_56_out);
  nand nand_56 (nand_56_out, nand_55_out, nand_54_out);
  nand nand_57 (nand_57_out, In[1], WE);
  nand nand_58 (nand_58_out, WE, ~In[1]);  // NAND_Gate
  nand nand_59 (nand_59_out, nand_58_out, nand_60_out);
  nand nand_60 (nand_60_out, nand_59_out, nand_57_out);
  _16bit_Registry_Selector u_16bit_registry_selector_1 (
    .WE(Read_Enable), .In(nand_5_out), .In_2(nand_9_out), .In_3(nand_14_out), .In_4(nand_18_out),
    .In_5(nand_20_out), .In_6(nand_23_out), .In_7(nand_27_out), .In_8(nand_31_out), .In_9(nand_37_out),
    .In_10(nand_42_out), .In_11(nand_45_out), .In_12(nand_49_out), .In_13(nand_52_out), .In_14(nand_56_out),
    .In_15(nand_60_out), .In_16(nand_64_out), .Out(Data_Out));
  nand nand_61 (nand_61_out, WE, ~In[0]);  // NAND_Gate
  nand nand_62 (nand_62_out, In[0], WE);
  nand nand_63 (nand_63_out, nand_61_out, nand_64_out);
  nand nand_64 (nand_64_out, nand_63_out, nand_62_out);
endmodule

module Memory_Data_Registry__MDR (
  input  [15:0] In,
  input  WE,
  output [15:0] out_3
);

  wire nand_1_out, nand_2_out, nand_3_out, nand_4_out, nand_6_out, nand_7_out, nand_8_out, nand_10_out,
       nand_11_out, nand_12_out, nand_14_out, nand_15_out, nand_16_out, nand_17_out, nand_19_out,
       nand_21_out, nand_22_out, nand_23_out, nand_25_out, nand_26_out, nand_27_out, nand_29_out,
       nand_30_out, nand_32_out, nand_33_out, nand_34_out, nand_35_out, nand_36_out, nand_37_out,
       nand_39_out, nand_40_out, nand_41_out, nand_43_out, nand_44_out, nand_45_out, nand_47_out,
       nand_48_out, nand_50_out, nand_51_out, nand_53_out, nand_54_out, nand_55_out, nand_57_out,
       nand_58_out, nand_59_out, nand_61_out, nand_62_out, nand_63_out;

  nand nand_1 (nand_1_out, WE, ~In[15]);  // NAND_Gate
  nand nand_2 (nand_2_out, nand_1_out, out_3[15]);
  nand nand_3 (nand_3_out, In[15], WE);
  nand nand_4 (nand_4_out, WE, ~In[14]);  // NAND_Gate
  nand nand_5 (out_3[15], nand_2_out, nand_3_out);
  nand nand_6 (nand_6_out, nand_4_out, out_3[14]);
  nand nand_7 (nand_7_out, In[14], WE);
  nand nand_8 (nand_8_out, WE, ~In[13]);  // NAND_Gate
  nand nand_9 (out_3[14], nand_6_out, nand_7_out);
  nand nand_10 (nand_10_out, nand_8_out, out_3[13]);
  nand nand_11 (nand_11_out, In[13], WE);
  nand nand_12 (nand_12_out, WE, ~In[12]);  // NAND_Gate
  nand nand_13 (out_3[13], nand_10_out, nand_11_out);
  nand nand_14 (nand_14_out, nand_12_out, out_3[12]);
  nand nand_15 (nand_15_out, In[12], WE);
  nand nand_16 (nand_16_out, WE, ~In[11]);  // NAND_Gate
  nand nand_17 (nand_17_out, nand_16_out, out_3[11]);
  nand nand_18 (out_3[12], nand_14_out, nand_15_out);
  nand nand_19 (nand_19_out, In[11], WE);
  nand nand_20 (out_3[11], nand_17_out, nand_19_out);
  nand nand_21 (nand_21_out, In[10], WE);
  nand nand_22 (nand_22_out, WE, ~In[10]);  // NAND_Gate
  nand nand_23 (nand_23_out, nand_22_out, out_3[10]);
  nand nand_24 (out_3[10], nand_23_out, nand_21_out);
  nand nand_25 (nand_25_out, In[9], WE);
  nand nand_26 (nand_26_out, WE, ~In[9]);  // NAND_Gate
  nand nand_27 (nand_27_out, nand_26_out, out_3[9]);
  nand nand_28 (out_3[9], nand_27_out, nand_25_out);
  nand nand_29 (nand_29_out, In[8], WE);
  nand nand_30 (nand_30_out, WE, ~In[8]);  // NAND_Gate
  nand nand_31 (out_3[8], nand_32_out, nand_29_out);
  nand nand_32 (nand_32_out, nand_30_out, out_3[8]);
  nand nand_33 (nand_33_out, WE, ~In[7]);  // NAND_Gate
  nand nand_34 (nand_34_out, nand_33_out, out_3[7]);
  nand nand_35 (nand_35_out, In[7], WE);
  nand nand_36 (nand_36_out, WE, ~In[6]);  // NAND_Gate
  nand nand_37 (nand_37_out, nand_36_out, out_3[6]);
  nand nand_38 (out_3[7], nand_34_out, nand_35_out);
  nand nand_39 (nand_39_out, WE, ~In[5]);  // NAND_Gate
  nand nand_40 (nand_40_out, In[6], WE);
  nand nand_41 (nand_41_out, nand_39_out, out_3[5]);
  nand nand_42 (out_3[6], nand_37_out, nand_40_out);
  nand nand_43 (nand_43_out, In[5], WE);
  nand nand_44 (nand_44_out, WE, ~In[4]);  // NAND_Gate
  nand nand_45 (nand_45_out, nand_44_out, out_3[4]);
  nand nand_46 (out_3[5], nand_41_out, nand_43_out);
  nand nand_47 (nand_47_out, In[4], WE);
  nand nand_48 (nand_48_out, WE, ~In[3]);  // NAND_Gate
  nand nand_49 (out_3[4], nand_45_out, nand_47_out);
  nand nand_50 (nand_50_out, nand_48_out, out_3[3]);
  nand nand_51 (nand_51_out, In[3], WE);
  nand nand_52 (out_3[3], nand_50_out, nand_51_out);
  nand nand_53 (nand_53_out, In[2], WE);
  nand nand_54 (nand_54_out, WE, ~In[2]);  // NAND_Gate
  nand nand_55 (nand_55_out, nand_54_out, out_3[2]);
  nand nand_56 (out_3[2], nand_55_out, nand_53_out);
  nand nand_57 (nand_57_out, In[1], WE);
  nand nand_58 (nand_58_out, WE, ~In[1]);  // NAND_Gate
  nand nand_59 (nand_59_out, nand_58_out, out_3[1]);
  nand nand_60 (out_3[1], nand_59_out, nand_57_out);
  nand nand_61 (nand_61_out, WE, ~In[0]);  // NAND_Gate
  nand nand_62 (nand_62_out, In[0], WE);
  nand nand_63 (nand_63_out, nand_61_out, out_3[0]);
  nand nand_64 (out_3[0], nand_63_out, nand_62_out);
endmodule

module Instruction_Registry__IR (
  input  [15:0] In,
  input  WE,
  output [15:0] Data_Out
);

  wire nand_1_out, nand_2_out, nand_3_out, nand_4_out, nand_5_out, nand_7_out, nand_8_out, nand_10_out,
       nand_11_out, nand_12_out, nand_13_out, nand_15_out, nand_16_out, nand_18_out, nand_19_out,
       nand_21_out, nand_22_out, nand_24_out, nand_25_out, nand_26_out, nand_28_out, nand_29_out,
       nand_30_out, nand_31_out, nand_33_out, nand_34_out, nand_35_out, nand_36_out, nand_38_out,
       nand_39_out, nand_40_out, nand_42_out, nand_43_out, nand_44_out, nand_46_out, nand_47_out,
       nand_48_out, nand_50_out, nand_51_out, nand_53_out, nand_54_out, nand_55_out, nand_57_out,
       nand_58_out, nand_60_out, nand_61_out, nand_62_out, nand_63_out;

  nand nand_1 (nand_1_out, WE, ~In[15]);  // NAND_Gate
  nand nand_2 (nand_2_out, nand_1_out, Data_Out[15]);
  nand nand_3 (nand_3_out, WE, ~In[14]);  // NAND_Gate
  nand nand_4 (nand_4_out, In[15], WE);
  nand nand_5 (nand_5_out, nand_3_out, Data_Out[14]);
  nand nand_6 (Data_Out[15], nand_2_out, nand_4_out);
  nand nand_7 (nand_7_out, WE, ~In[13]);  // NAND_Gate
  nand nand_8 (nand_8_out, In[14], WE);
  nand nand_9 (Data_Out[14], nand_5_out, nand_8_out);
  nand nand_10 (nand_10_out, nand_7_out, Data_Out[13]);
  nand nand_11 (nand_11_out, In[13], WE);
  nand nand_12 (nand_12_out, WE, ~In[12]);  // NAND_Gate
  nand nand_13 (nand_13_out, nand_12_out, Data_Out[12]);
  nand nand_14 (Data_Out[13], nand_10_out, nand_11_out);
  nand nand_15 (nand_15_out, In[12], WE);
  nand nand_16 (nand_16_out, WE, ~In[11]);  // NAND_Gate
  nand nand_17 (Data_Out[12], nand_13_out, nand_15_out);
  nand nand_18 (nand_18_out, nand_16_out, Data_Out[11]);
  nand nand_19 (nand_19_out, In[11], WE);
  nand nand_20 (Data_Out[11], nand_18_out, nand_19_out);
  nand nand_21 (nand_21_out, WE, ~In[10]);  // NAND_Gate
  nand nand_22 (nand_22_out, In[10], WE);
  nand nand_23 (Data_Out[10], nand_24_out, nand_22_out);
  nand nand_24 (nand_24_out, nand_21_out, Data_Out[10]);
  nand nand_25 (nand_25_out, WE, ~In[9]);  // NAND_Gate
  nand nand_26 (nand_26_out, In[9], WE);
  nand nand_27 (Data_Out[9], nand_28_out, nand_26_out);
  nand nand_28 (nand_28_out, nand_25_out, Data_Out[9]);
  nand nand_29 (nand_29_out, In[8], WE);
  nand nand_30 (nand_30_out, WE, ~In[8]);  // NAND_Gate
  nand nand_31 (nand_31_out, nand_30_out, Data_Out[8]);
  nand nand_32 (Data_Out[8], nand_31_out, nand_29_out);
  nand nand_33 (nand_33_out, WE, ~In[7]);  // NAND_Gate
  nand nand_34 (nand_34_out, nand_33_out, Data_Out[7]);
  nand nand_35 (nand_35_out, In[7], WE);
  nand nand_36 (nand_36_out, WE, ~In[6]);  // NAND_Gate
  nand nand_37 (Data_Out[7], nand_34_out, nand_35_out);
  nand nand_38 (nand_38_out, nand_36_out, Data_Out[6]);
  nand nand_39 (nand_39_out, WE, ~In[5]);  // NAND_Gate
  nand nand_40 (nand_40_out, In[6], WE);
  nand nand_41 (Data_Out[6], nand_38_out, nand_40_out);
  nand nand_42 (nand_42_out, nand_39_out, Data_Out[5]);
  nand nand_43 (nand_43_out, In[5], WE);
  nand nand_44 (nand_44_out, WE, ~In[4]);  // NAND_Gate
  nand nand_45 (Data_Out[5], nand_42_out, nand_43_out);
  nand nand_46 (nand_46_out, nand_44_out, Data_Out[4]);
  nand nand_47 (nand_47_out, WE, ~In[3]);  // NAND_Gate
  nand nand_48 (nand_48_out, In[4], WE);
  nand nand_49 (Data_Out[4], nand_46_out, nand_48_out);
  nand nand_50 (nand_50_out, nand_47_out, Data_Out[3]);
  nand nand_51 (nand_51_out, In[3], WE);
  nand nand_52 (Data_Out[3], nand_50_out, nand_51_out);
  nand nand_53 (nand_53_out, In[2], WE);
  nand nand_54 (nand_54_out, WE, ~In[2]);  // NAND_Gate
  nand nand_55 (nand_55_out, nand_54_out, Data_Out[2]);
  nand nand_56 (Data_Out[2], nand_55_out, nand_53_out);
  nand nand_57 (nand_57_out, In[1], WE);
  nand nand_58 (nand_58_out, WE, ~In[1]);  // NAND_Gate
  nand nand_59 (Data_Out[1], nand_60_out, nand_57_out);
  nand nand_60 (nand_60_out, nand_58_out, Data_Out[1]);
  nand nand_61 (nand_61_out, In[0], WE);
  nand nand_62 (nand_62_out, WE, ~In[0]);  // NAND_Gate
  nand nand_63 (nand_63_out, nand_62_out, Data_Out[0]);
  nand nand_64 (Data_Out[0], nand_63_out, nand_61_out);
endmodule

module Instruction_Decoder (
  input  [15:0] Decoder_In,
  output [3:0] Opcode,
  output [2:0] DR,
  output [2:0] SR1,
  output [5:0] OpDepndnt
);


  assign DR = Decoder_In[11:9];
  assign Opcode = Decoder_In[15:12];
  assign OpDepndnt = Decoder_In[5:0];
  assign SR1 = Decoder_In[8:6];
endmodule

module Operation_Multiplexer (
  input  [3:0] Op_In,
  output LDR_Out,
  output ADD_Out
);

  and and_1 (LDR_Out, ~Op_In[3], Op_In[2], Op_In[1], ~Op_In[0]);  // AND_Gate
  and and_2 (ADD_Out, ~Op_In[3], ~Op_In[2], ~Op_In[1], Op_In[0]);  // AND_Gate
endmodule

module Evaluate_Address (
  input  [2:0] SR,
  input  [5:0] _2s_Comp_Offset,
  input  Activate,
  input  Evaluate,
  output [15:0] out_5
);

  wire adder_1_cout, n16bit_registry_1_1_1_out0, n16bit_registry_1_1_1_out1, n16bit_registry_1_1_1_out2,
       n16bit_registry_1_1_1_out3, n16bit_registry_1_1_1_out4, n16bit_registry_1_1_1_out5,
       n16bit_registry_1_1_1_out6, n16bit_registry_1_1_1_out7, n16bit_registry_1_1_1_out8,
       n16bit_registry_1_1_1_out9, n16bit_registry_1_1_1_out10, n16bit_registry_1_1_1_out11,
       n16bit_registry_1_1_1_out12, n16bit_registry_1_1_1_out13, n16bit_registry_1_1_1_out14,
       n16bit_registry_1_1_1_out15;
  wire [5:0] adder_1_out, and_4_out, and_12_out;

  and and_1 (and_4_out[3], Activate, Evaluate, 1'b0);
  and and_2 (and_4_out[4], Activate, Evaluate, 1'b0);
  and and_3 (and_4_out[5], Activate, Evaluate, 1'b0);
  and and_4 (and_4_out[0], Activate, Evaluate, SR[0]);
  and and_5 (and_4_out[2], Activate, Evaluate, SR[2]);
  and and_6 (and_4_out[1], Activate, Evaluate, SR[1]);
  and and_7 (and_12_out[4], Activate, Evaluate, _2s_Comp_Offset[4]);
  and and_8 (and_12_out[5], Activate, Evaluate, _2s_Comp_Offset[5]);
  and and_9 (and_12_out[2], Activate, Evaluate, _2s_Comp_Offset[2]);
  and and_10 (and_12_out[1], Activate, Evaluate, _2s_Comp_Offset[1]);
  and and_11 (and_12_out[3], Activate, Evaluate, _2s_Comp_Offset[3]);
  Adder #(.width(6)) adder_1 (.a(and_4_out), .b(and_12_out), .out(adder_1_out), .cin(1'b0), .cout(adder_1_cout));
  and and_12 (and_12_out[0], Activate, Evaluate, _2s_Comp_Offset[0]);
  _16bit_Registry__1_1 u_16bit_registry_1_1_1 (
    .WE(Evaluate), .In({{10{1'b0}}, adder_1_out}), .Out15(n16bit_registry_1_1_1_out15),
    .Out14(n16bit_registry_1_1_1_out14), .Out13(n16bit_registry_1_1_1_out13),
    .Out12(n16bit_registry_1_1_1_out12), .Out11(n16bit_registry_1_1_1_out11),
    .Out10(n16bit_registry_1_1_1_out10), .Out9(n16bit_registry_1_1_1_out9),
    .Out8(n16bit_registry_1_1_1_out8), .Out7(n16bit_registry_1_1_1_out7), .Out6(n16bit_registry_1_1_1_out6),
    .Out5(n16bit_registry_1_1_1_out5), .Out4(n16bit_registry_1_1_1_out4), .Out3(n16bit_registry_1_1_1_out3),
    .Out2(n16bit_registry_1_1_1_out2), .Out1(n16bit_registry_1_1_1_out1), .Out0(n16bit_registry_1_1_1_out0));
  _16bit_Registry_Selector u_16bit_registry_selector_1 (
    .WE(Evaluate), .In(n16bit_registry_1_1_1_out15), .In_2(n16bit_registry_1_1_1_out14),
    .In_3(n16bit_registry_1_1_1_out13), .In_4(n16bit_registry_1_1_1_out12),
    .In_5(n16bit_registry_1_1_1_out11), .In_6(n16bit_registry_1_1_1_out10),
    .In_7(n16bit_registry_1_1_1_out9), .In_8(n16bit_registry_1_1_1_out8), .In_9(n16bit_registry_1_1_1_out7),
    .In_10(n16bit_registry_1_1_1_out6), .In_11(n16bit_registry_1_1_1_out5),
    .In_12(n16bit_registry_1_1_1_out4), .In_13(n16bit_registry_1_1_1_out3),
    .In_14(n16bit_registry_1_1_1_out2), .In_15(n16bit_registry_1_1_1_out1),
    .In_16(n16bit_registry_1_1_1_out0), .Out(out_5));
  // also tied to GND on the sheet: adder_1_cout
endmodule

module _16bit_Multiplexer (
  input  [15:0] In_1,
  input  [15:0] In_2,
  input  in_3,
  output [15:0] Out
);

  wire not_1_out;
  wire [15:0] n16bit_registry_selector_1_out, n16bit_registry_selector_2_out;

  not not_1 (not_1_out, in_3);
  _16bit_Registry_Selector u_16bit_registry_selector_1 (
    .WE(not_1_out), .In(In_1[15]), .In_2(In_1[14]), .In_3(In_1[13]), .In_4(In_1[12]), .In_5(In_1[11]),
    .In_6(In_1[10]), .In_7(In_1[9]), .In_8(In_1[8]), .In_9(In_1[7]), .In_10(In_1[6]), .In_11(In_1[5]),
    .In_12(In_1[4]), .In_13(In_1[3]), .In_14(In_1[2]), .In_15(In_1[1]), .In_16(In_1[0]),
    .Out(n16bit_registry_selector_1_out));
  _16bit_Registry_Selector u_16bit_registry_selector_2 (
    .WE(in_3), .In(In_2[15]), .In_2(In_2[14]), .In_3(In_2[13]), .In_4(In_2[12]), .In_5(In_2[11]),
    .In_6(In_2[10]), .In_7(In_2[9]), .In_8(In_2[8]), .In_9(In_2[7]), .In_10(In_2[6]), .In_11(In_2[5]),
    .In_12(In_2[4]), .In_13(In_2[3]), .In_14(In_2[2]), .In_15(In_2[1]), .In_16(In_2[0]),
    .Out(n16bit_registry_selector_2_out));
  assign Out = n16bit_registry_selector_1_out | n16bit_registry_selector_2_out;  // OR_Gate or_1, 16 bits wide
endmodule

module _16bit_Decoder (
  input  [15:0] In,
  input  To_IR,
  input  To_Reg,
  output [15:0] Out,
  output [15:0] Out_2
);

  _16bit_Registry__1_1 u_16bit_registry_1_1_1 (
    .WE(To_IR), .In(In), .Out15(Out[15]), .Out14(Out[14]), .Out13(Out[13]), .Out12(Out[12]), .Out11(Out[11]),
    .Out10(Out[10]), .Out9(Out[9]), .Out8(Out[8]), .Out7(Out[7]), .Out6(Out[6]), .Out5(Out[5]),
    .Out4(Out[4]), .Out3(Out[3]), .Out2(Out[2]), .Out1(Out[1]), .Out0(Out[0]));
  _16bit_Registry__1_1 u_16bit_registry_1_1_2 (
    .WE(To_Reg), .In(In), .Out15(Out_2[15]), .Out14(Out_2[14]), .Out13(Out_2[13]), .Out12(Out_2[12]),
    .Out11(Out_2[11]), .Out10(Out_2[10]), .Out9(Out_2[9]), .Out8(Out_2[8]), .Out7(Out_2[7]), .Out6(Out_2[6]),
    .Out5(Out_2[5]), .Out4(Out_2[4]), .Out3(Out_2[3]), .Out2(Out_2[2]), .Out1(Out_2[1]), .Out0(Out_2[0]));
endmodule

module N (
  input  In,
  input  WE,
  output out_3
);

  wire nand_1_out, nand_2_out, nand_3_out;

  nand nand_1 (nand_1_out, WE, ~In);  // NAND_Gate
  nand nand_2 (nand_2_out, nand_1_out, out_3);
  nand nand_3 (nand_3_out, In, WE);
  nand nand_4 (out_3, nand_2_out, nand_3_out);
endmodule

module Z (
  input  In,
  input  WE,
  output out_3
);

  wire nand_1_out, nand_2_out, nand_3_out;

  nand nand_1 (nand_1_out, WE, ~In);  // NAND_Gate
  nand nand_2 (nand_2_out, nand_1_out, out_3);
  nand nand_3 (nand_3_out, In, WE);
  nand nand_4 (out_3, nand_2_out, nand_3_out);
endmodule

module P (
  input  In,
  input  WE,
  output out_3
);

  wire nand_1_out, nand_2_out, nand_3_out;

  nand nand_1 (nand_1_out, WE, ~In);  // NAND_Gate
  nand nand_2 (nand_2_out, nand_1_out, out_3);
  nand nand_3 (nand_3_out, In, WE);
  nand nand_4 (out_3, nand_2_out, nand_3_out);
endmodule

module Control_Unit (
  input  Activate,
  input  Clock,
  output out_3,
  output out_4,
  output out_5,
  output out_6,
  output out_7,
  output out_8,
  output out_9,
  output out_10,
  output BLANK
);

  wire nand_1_out, nand_2_out, nand_3_out, nand_4_out, nand_5_out, nand_6_out, nand_7_out, nand_8_out,
       nand_9_out, nand_10_out, nand_11_out, nand_12_out, nand_13_out, nand_14_out, nand_15_out, nand_16_out,
       nand_17_out, nand_18_out, nand_19_out, nand_20_out, nand_21_out, nand_22_out, nand_23_out,
       nand_24_out, nand_25_out, nand_26_out, nand_27_out, nand_28_out, nand_29_out, nand_30_out,
       nand_31_out, nand_32_out, nand_33_out, nand_34_out, nand_35_out, nand_36_out, nand_37_out,
       nand_38_out, nand_39_out, nand_40_out, nand_41_out, nand_42_out, nand_43_out, nand_44_out,
       nand_45_out, nand_46_out, nand_47_out, nand_48_out, nand_49_out, nand_50_out, nand_51_out,
       nand_52_out, nand_53_out, nand_54_out, nand_55_out, nand_56_out, nand_57_out, nand_58_out,
       nand_59_out, nand_60_out, nand_61_out, nand_62_out, nand_63_out, nand_64_out, not_1_out;

  nand nand_1 (nand_1_out, nand_17_out, nand_2_out);
  nand nand_2 (nand_2_out, nand_1_out, nand_18_out);
  nand nand_3 (nand_3_out, nand_19_out, nand_4_out);
  nand nand_4 (nand_4_out, nand_3_out, nand_20_out);
  nand nand_5 (nand_5_out, nand_21_out, nand_6_out);
  nand nand_6 (nand_6_out, nand_5_out, nand_22_out);
  nand nand_7 (nand_7_out, nand_23_out, nand_8_out);
  nand nand_8 (nand_8_out, nand_7_out, nand_24_out);
  nand nand_9 (nand_9_out, nand_25_out, nand_10_out);
  nand nand_10 (nand_10_out, nand_9_out, nand_26_out);
  nand nand_11 (nand_11_out, nand_27_out, nand_12_out);
  nand nand_12 (nand_12_out, nand_11_out, nand_28_out);
  nand nand_13 (nand_13_out, nand_29_out, nand_14_out);
  nand nand_14 (nand_14_out, nand_13_out, nand_30_out);
  nand nand_15 (nand_15_out, nand_31_out, nand_16_out);
  nand nand_16 (nand_16_out, nand_15_out, nand_32_out);
  nand nand_17 (nand_17_out, nand_34_out, Clock);
  nand nand_18 (nand_18_out, Clock, ~nand_34_out);  // NAND_Gate
  nand nand_19 (nand_19_out, nand_38_out, Clock);
  nand nand_20 (nand_20_out, Clock, ~nand_38_out);  // NAND_Gate
  nand nand_21 (nand_21_out, nand_41_out, Clock);
  nand nand_22 (nand_22_out, Clock, ~nand_41_out);  // NAND_Gate
  nand nand_23 (nand_23_out, nand_46_out, Clock);
  nand nand_24 (nand_24_out, Clock, ~nand_46_out);  // NAND_Gate
  nand nand_25 (nand_25_out, nand_50_out, Clock);
  nand nand_26 (nand_26_out, Clock, ~nand_50_out);  // NAND_Gate
  nand nand_27 (nand_27_out, nand_54_out, Clock);
  nand nand_28 (nand_28_out, Clock, ~nand_54_out);  // NAND_Gate
  nand nand_29 (nand_29_out, nand_57_out, Clock);
  nand nand_30 (nand_30_out, Clock, ~nand_57_out);  // NAND_Gate
  nand nand_31 (nand_31_out, nand_62_out, Clock);
  nand nand_32 (nand_32_out, Clock, ~nand_62_out);  // NAND_Gate
  and and_1 (out_3, Activate, ~nand_1_out, ~nand_3_out, ~nand_5_out, ~nand_7_out, ~nand_9_out, ~nand_11_out, ~nand_13_out, ~nand_15_out);  // AND_Gate
  and and_2 (out_4, Activate, nand_1_out, ~nand_3_out, ~nand_5_out, ~nand_7_out, ~nand_9_out, ~nand_11_out, ~nand_13_out, ~nand_15_out);  // AND_Gate
  and and_3 (out_5, Activate, ~nand_1_out, nand_3_out, ~nand_5_out, ~nand_7_out, ~nand_9_out, ~nand_11_out, ~nand_13_out, ~nand_15_out);  // AND_Gate
  and and_4 (out_6, Activate, ~nand_1_out, ~nand_3_out, nand_5_out, ~nand_7_out, ~nand_9_out, ~nand_11_out, ~nand_13_out, ~nand_15_out);  // AND_Gate
  and and_5 (out_7, Activate, ~nand_1_out, ~nand_3_out, ~nand_5_out, nand_7_out, ~nand_9_out, ~nand_11_out, ~nand_13_out, ~nand_15_out);  // AND_Gate
  and and_6 (out_8, Activate, ~nand_1_out, ~nand_3_out, ~nand_5_out, ~nand_7_out, nand_9_out, ~nand_11_out, ~nand_13_out, ~nand_15_out);  // AND_Gate
  and and_7 (out_9, Activate, ~nand_1_out, ~nand_3_out, ~nand_5_out, ~nand_7_out, ~nand_9_out, nand_11_out, ~nand_13_out, ~nand_15_out);  // AND_Gate
  and and_8 (out_10, Activate, ~nand_1_out, ~nand_3_out, ~nand_5_out, ~nand_7_out, ~nand_9_out, ~nand_11_out, nand_13_out, ~nand_15_out);  // AND_Gate
  and and_9 (BLANK, Activate, ~nand_1_out, ~nand_3_out, ~nand_5_out, ~nand_7_out, ~nand_9_out, ~nand_11_out, ~nand_13_out, nand_15_out);  // AND_Gate
  nand nand_33 (nand_33_out, out_3, not_1_out);
  nand nand_34 (nand_34_out, nand_33_out, nand_35_out);
  nand nand_35 (nand_35_out, nand_34_out, nand_36_out);
  nand nand_36 (nand_36_out, not_1_out, ~out_3);  // NAND_Gate
  nand nand_37 (nand_37_out, out_4, not_1_out);
  nand nand_38 (nand_38_out, nand_37_out, nand_40_out);
  nand nand_39 (nand_39_out, not_1_out, ~out_4);  // NAND_Gate
  nand nand_40 (nand_40_out, nand_38_out, nand_39_out);
  nand nand_41 (nand_41_out, nand_42_out, nand_44_out);
  nand nand_42 (nand_42_out, out_5, not_1_out);
  nand nand_43 (nand_43_out, not_1_out, ~out_5);  // NAND_Gate
  nand nand_44 (nand_44_out, nand_41_out, nand_43_out);
  nand nand_45 (nand_45_out, out_6, not_1_out);
  nand nand_46 (nand_46_out, nand_45_out, nand_48_out);
  nand nand_47 (nand_47_out, not_1_out, ~out_6);  // NAND_Gate
  nand nand_48 (nand_48_out, nand_46_out, nand_47_out);
  nand nand_49 (nand_49_out, out_7, not_1_out);
  nand nand_50 (nand_50_out, nand_49_out, nand_52_out);
  nand nand_51 (nand_51_out, not_1_out, ~out_7);  // NAND_Gate
  nand nand_52 (nand_52_out, nand_50_out, nand_51_out);
  nand nand_53 (nand_53_out, out_8, not_1_out);
  nand nand_54 (nand_54_out, nand_53_out, nand_56_out);
  nand nand_55 (nand_55_out, not_1_out, ~out_8);  // NAND_Gate
  nand nand_56 (nand_56_out, nand_54_out, nand_55_out);
  nand nand_57 (nand_57_out, nand_58_out, nand_59_out);
  nand nand_58 (nand_58_out, out_9, not_1_out);
  nand nand_59 (nand_59_out, nand_57_out, nand_60_out);
  nand nand_60 (nand_60_out, not_1_out, ~out_9);  // NAND_Gate
  nand nand_61 (nand_61_out, out_10, not_1_out);
  nand nand_62 (nand_62_out, nand_61_out, nand_64_out);
  nand nand_63 (nand_63_out, not_1_out, ~out_10);  // NAND_Gate
  nand nand_64 (nand_64_out, nand_62_out, nand_63_out);
  not not_1 (not_1_out, Clock);
  not not_2 (not_1_out, Clock);
  not not_3 (not_1_out, Clock);
  not not_4 (not_1_out, Clock);
  not not_5 (not_1_out, Clock);
  not not_6 (not_1_out, Clock);
  not not_7 (not_1_out, Clock);
  not not_8 (not_1_out, Clock);
endmodule
