// Logisim project project_3_equalto.circ as structural Verilog: 1 circuit, main circuit main
module main (
  input  in_1,
  input  in_2,
  input  in_3,
  input  in_4,
  input  in_5,
  input  in_6,
  input  in_7,
  input  in_8,
  input  in_9,
  input  in_10,
  input  in_11,
  input  in_12,
  input  in_13,
  input  in_14,
  input  in_15,
  input  in_16,
  input  in_17,
  input  in_18,
  input  in_19,
  input  in_20,
  input  in_21,
  input  in_22,
  input  in_23,
  input  in_24,
  input  in_25,
  input  in_26,
  input  in_27,
  input  in_28,
  input  in_29,
  input  in_30,
  input  in_31,
  input  in_32,
  input  in_33,
  input  in_34,
  input  in_35,
  input  in_36,
  input  in_37,
  input  in_38,
  input  in_39,
  input  in_40,
  input  in_41,
  input  in_42,
  input  in_43,
  input  in_44,
  input  in_45,
  input  in_46,
  input  in_47,
  input  in_48,
  input  in_49,
  input  in_50,
  input  in_51,
  input  in_52,
  input  in_53,
  input  in_54,
  input  in_55,
  input  in_56,
  input  in_57,
  input  in_58,
  input  in_59,
  input  in_60,
  input  in_61,
  input  in_62,
  input  ColA,
  input  ColB,
  output out_65
);

  wire xnor_1_out, xnor_2_out, xnor_3_out, xnor_4_out, xnor_5_out, xnor_6_out, xnor_7_out, xnor_8_out,
       xnor_9_out, xnor_10_out, xnor_11_out, xnor_12_out, xnor_13_out, xnor_14_out, xnor_15_out, xnor_16_out,
       xnor_17_out, xnor_18_out, xnor_19_out, xnor_20_out, xnor_21_out, xnor_22_out, xnor_23_out,
       xnor_24_out, xnor_25_out, xnor_26_out, xnor_27_out, xnor_28_out, xnor_29_out, xnor_30_out,
       xnor_31_out, xnor_32_out;

  xnor xnor_1 (xnor_1_out, in_55, in_56);
  xnor xnor_2 (xnor_2_out, in_57, in_58);
  xnor xnor_3 (xnor_3_out, in_59, in_60);
  xnor xnor_4 (xnor_4_out, in_61, in_62);
  xnor xnor_5 (xnor_5_out, ColA, ColB);
  xnor xnor_6 (xnor_6_out, in_39, in_40);
  xnor xnor_7 (xnor_7_out, in_41, in_42);
  xnor xnor_8 (xnor_8_out, in_43, in_44);
  xnor xnor_9 (xnor_9_out, in_45, in_46);
  xnor xnor_10 (xnor_10_out, in_47, in_48);
  xnor xnor_11 (xnor_11_out, in_49, in_50);
  xnor xnor_12 (xnor_12_out, in_51, in_52);
  xnor xnor_13 (xnor_13_out, in_53, in_54);
  xnor xnor_14 (xnor_14_out, in_25, in_26);
  xnor xnor_15 (xnor_15_out, in_27, in_28);
  xnor xnor_16 (xnor_16_out, in_29, in_30);
  xnor xnor_17 (xnor_17_out, in_31, in_32);
  xnor xnor_18 (xnor_18_out, in_33, in_34);
  xnor xnor_19 (xnor_19_out, in_35, in_36);
  xnor xnor_20 (xnor_20_out, in_37, in_38);
  and and_1 (out_65, xnor_5_out, xnor_4_out, xnor_3_out, xnor_2_out, xnor_1_out, xnor_13_out, xnor_12_out, xnor_11_out, xnor_10_out, xnor_9_out, xnor_8_out, xnor_7_out, xnor_6_out, xnor_20_out, xnor_19_out, xnor_18_out, xnor_17_out, xnor_16_out, xnor_15_out, xnor_14_out, xnor_28_out, xnor_27_out, xnor_26_out, xnor_25_out, xnor_24_out, xnor_23_out, xnor_22_out, xnor_21_out, xnor_32_out, xnor_31_out, xnor_30_out, xnor_29_out);
  xnor xnor_21 (xnor_21_out, in_9, in_10);
  xnor xnor_22 (xnor_22_out, in_11, in_12);
  xnor xnor_23 (xnor_23_out, in_13, in_14);
  xnor xnor_24 (xnor_24_out, in_15, in_16);
  xnor xnor_25 (xnor_25_out, in_17, in_18);
  xnor xnor_26 (xnor_26_out, in_19, in_20);
  xnor xnor_27 (xnor_27_out, in_21, in_22);
  xnor xnor_28 (xnor_28_out, in_23, in_24);
  xnor xnor_29 (xnor_29_out, in_1, in_2);
  xnor xnor_30 (xnor_30_out, in_3, in_4);
  xnor xnor_31 (xnor_31_out, in_5, in_6);
  xnor xnor_32 (xnor_32_out, in_7, in_8);
endmodule
